// Logisim project Reveil_NMorand_FRamirez.circ as structural Verilog: 24 circuits, main circuit powerOnReset
module main (
  input  POR,
  input  click,
  input  CHA,
  input  CHB,
  output VCC,
  output GND,
  output buzzer
);

  wire alarmHandlerDisplayOveride, alarmHorloge, alarmTimer, and_1_out, and_2_out, and_4_out, and_5_out,
       bipMenu, blinkHeure, blinkHeureAlarm, blinkHeureTimer, blinkMinute, blinkMinuteAlarm,
       blinkMinuteTimer, blinkSecond, blinkSecondAlarm, blinkSecondTimer, BUSYChrono, BUSYMelodie,
       busyPlayingMelody, BUSYSetAlarm, BUSYSetHeure, BUSYsetMessage, BUSYTimer, BUSYTimerIdle, CCW,
       chronoEnable, CLK, clock_2_out, clock_3_out, clock_4_out, clock_5_out, clock_6_out, clock_7_out, CW,
       d_ff_1_q, d_ff_2_q, d_ff_3_q, debouncer_1_debounced, debouncer_2_debounced, debouncer_3_debounced,
       decoder_1_out1, decoder_1_out2, decoder_1_out3, decoder_2_out1, decoder_2_out2, decoder_2_out3,
       decoder_3_out1, decoder_3_out2, decoder_3_out3, doubleClick, driver7seg_1_a, driver7seg_1_b,
       driver7seg_1_c, driver7seg_1_d, driver7seg_1_e, driver7seg_1_f, driver7seg_1_g, driver7seg_1_h,
       driver7seg_2_a, driver7seg_2_b, driver7seg_2_c, driver7seg_2_d, driver7seg_2_e, driver7seg_2_f,
       driver7seg_2_g, driver7seg_2_h, driver7seg_3_a, driver7seg_3_b, driver7seg_3_c, driver7seg_3_d,
       driver7seg_3_e, driver7seg_3_f, driver7seg_3_g, driver7seg_3_h, driver7seg_4_a, driver7seg_4_b,
       driver7seg_4_c, driver7seg_4_d, driver7seg_4_e, driver7seg_4_f, driver7seg_4_g, driver7seg_4_h,
       driver7seg_5_a, driver7seg_5_b, driver7seg_5_c, driver7seg_5_d, driver7seg_5_e, driver7seg_5_f,
       driver7seg_5_g, driver7seg_5_h, driver7seg_6_a, driver7seg_6_b, driver7seg_6_c, driver7seg_6_d,
       driver7seg_6_e, driver7seg_6_f, driver7seg_6_g, driver7seg_6_h, enHourAlarm, enTimerAlarm,
       jingleNotSet, longClick, menuDisplayOveride, menuSetMelody_1_play, menuSetMelody_1_rec, not_1_out,
       not_2_out, not_6_out, not_7_out, not_11_out, not_12_out, or_1_out, or_2_out, or_4_out, or_5_out,
       or_6_out, or_7_out, play, POR_t, powerOnReset_1_gen_por, requestAlarmMessage, resetChronoTime,
       s_r_ff_1_q, setCstmChar, simpleAlarm, simpleClick;
  wire [1:0] setHeure_1_statehms, setTimeMenu_1_statehms, setTimeMenu_2_statehms;
  wire [3:0] cstmCharADR, currentHourHSet, currentHourHSetAlarm, currentHourHSetTimer, currentHourLSet,
       currentHourLSetAlarm, currentHourLSetTimer, currentMinuteHSet, currentMinuteHSetAlarm,
       currentMinuteHSetTimer, currentMinuteLSet, currentMinuteLSetAlarm, currentMinuteLSetTimer,
       currentSecondHSet, currentSecondHSetAlarm, currentSecondHSetTimer, currentSecondLSet,
       currentSecondLSetAlarm, currentSecondLSetTimer, menuSelect, menuSelectPreview, menuSetMelody_1_bpm;
  wire [4:0] menuSetMelody_1_adress, multiplexer_1_out, notePreview, tone;
  wire [5:0] cstmChar;
  wire [35:0] alarmDisplay, DisplayChrono, DisplayClock, DisplayOut, DisplaySetMelody, DisplaySetMessage,
       DisplayTimer, DisplayTimeSet, DisplayTimeSetAlarm, DisplayTimeSetTimer, menuTitle, multiplexer_20_out,
       multiplexer_21_out;

  Clock clock_1 (.out(CLK));
  not not_1 (not_1_out, click);
  or or_1 (or_1_out, POR_t, bipMenu);
  or or_2 (or_2_out, doubleClick, simpleAlarm);
  not not_2 (not_2_out, BUSYSetHeure);
  Multiplexer #(.width(5)) multiplexer_1 (.in0(tone), .in1(notePreview), .out(multiplexer_1_out), .sel(and_1_out));
  and and_1 (and_1_out, BUSYMelodie, ~busyPlayingMelody);  // AND_Gate
  Clock #(.lowDuration(99999)) clock_2 (.out(clock_2_out));
  powerOnReset powerOnReset_1 (.CLK(CLK), .GEN_POR(powerOnReset_1_gen_por));
  debouncer debouncer_1 (.rawInput(not_1_out), .CLK(CLK), .POR(POR_t), .debounced(debouncer_1_debounced));
  debouncer debouncer_2 (.rawInput(CHA), .CLK(CLK), .POR(POR_t), .debounced(debouncer_2_debounced));
  debouncer debouncer_3 (.rawInput(CHB), .CLK(CLK), .POR(POR_t), .debounced(debouncer_3_debounced));
  or or_3 (POR_t, POR, powerOnReset_1_gen_por);
  clockDCB clockDCB2_1 (
    .setTime(BUSYSetHeure), .reverseCount(1'b0), .clockInput(clock_2_out), .enCount(not_2_out), .POR(POR_t),
    .setHourH(currentHourHSet), .setHourL(currentHourLSet), .setMinuteH(currentMinuteHSet),
    .setMinuteL(currentMinuteLSet), .setSecondH(currentSecondHSet), .setSecondL(currentSecondLSet),
    .hourH(DisplayClock[5:0]), .hourL(DisplayClock[11:6]), .minuteH(DisplayClock[17:12]),
    .minuteL(DisplayClock[23:18]), .secondH(DisplayClock[29:24]), .secondL(DisplayClock[35:30]));
  menuSetTime setHeure_1 (
    .clickSimple(simpleClick), .clickDouble(doubleClick), .clickLong(longClick), .CCW(CCW), .CW(CW),
    .CLK(CLK), .POR(POR_t), .selectMenu(menuSelect), .ADDR(4'b0010), .BUSY(BUSYSetHeure),
    .stateHMS(setHeure_1_statehms), .currentHourH(currentHourHSet), .currentHourL(currentHourLSet),
    .currentMinuteH(currentMinuteHSet), .currentMinuteL(currentMinuteLSet),
    .currentSecondH(currentSecondHSet), .currentSecondL(currentSecondLSet));
  driverBuzzerTone driverBuzzerTone_1 (
    .POR(POR_t), .CLK(CLK), .bip(or_1_out), .longBip(longClick), .doubleBip(or_2_out),
    .TONE(multiplexer_1_out), .Buzzer(buzzer));
  clickSimpleLongAndDouble clickSimpleLongAndDouble_1 (
    .click(debouncer_1_debounced), .POR(POR_t), .CLK(CLK), .clickSimple(simpleClick),
    .doubleClick(doubleClick), .longClick(longClick));
  driverRotaryEncoder rotaryEncoder_1 (
    .POR(POR_t), .CLK(CLK), .CHA(debouncer_2_debounced), .CHB(debouncer_3_debounced), .CCW(CCW), .CW(CW));
  Clock #(.highDuration(50000), .lowDuration(50000)) clock_3 (.out(clock_3_out));
  Decoder #(.select(2)) decoder_1 (
    .out1(decoder_1_out1), .out2(decoder_1_out2), .out3(decoder_1_out3), .sel(setHeure_1_statehms),
    .en(clock_3_out));  // open: out0
  Multiplexer #(.width(6)) multiplexer_2 (
    .in0(6'b010000), .in1({2'b00, currentHourHSet}), .out(DisplayTimeSet[5:0]), .sel(blinkHeure));
  Multiplexer #(.width(6)) multiplexer_3 (
    .in0(6'b010000), .in1({2'b00, currentHourLSet}), .out(DisplayTimeSet[11:6]), .sel(blinkHeure));
  Multiplexer #(.width(6)) multiplexer_4 (
    .in0(6'b010000), .in1({2'b00, currentMinuteHSet}), .out(DisplayTimeSet[17:12]), .sel(blinkMinute));
  Multiplexer #(.width(6)) multiplexer_5 (
    .in0(6'b010000), .in1({2'b00, currentMinuteLSet}), .out(DisplayTimeSet[23:18]), .sel(blinkMinute));
  Multiplexer #(.width(6)) multiplexer_6 (
    .in0(6'b010000), .in1({2'b00, currentSecondHSet}), .out(DisplayTimeSet[29:24]), .sel(blinkSecond));
  Multiplexer #(.width(6)) multiplexer_7 (
    .in0(6'b010000), .in1({2'b00, currentSecondLSet}), .out(DisplayTimeSet[35:30]), .sel(blinkSecond));
  not not_3 (blinkHeure, decoder_1_out1);
  not not_4 (blinkMinute, decoder_1_out2);
  not not_5 (blinkSecond, decoder_1_out3);
  or or_4 (or_4_out, BUSYSetHeure, BUSYSetAlarm, BUSYTimer, BUSYTimerIdle, BUSYChrono, BUSYMelodie, BUSYsetMessage);
  D_Flip_Flop d_ff_1 (.D(BUSYSetAlarm), .clk(CLK), .Q(d_ff_1_q), .reset(POR_t));  // open: Qn, preset
  not not_6 (not_6_out, BUSYSetAlarm);
  S_R_Flip_Flop s_r_ff_1 (.S(and_2_out), .clk(CLK), .Q(s_r_ff_1_q), .reset(POR_t));  // open: R, Qn, preset
  and and_2 (and_2_out, not_6_out, d_ff_1_q);
  menuMain stateMachineMenu_1 (
    .CW(CW), .CCW(CCW), .doubleClick(doubleClick), .longClick(longClick), .simpleClick(simpleClick),
    .POR(POR_t), .clk(CLK), .BUSY(or_4_out), .selectMenu(menuSelect), .menuPreview(menuSelectPreview),
    .bipOut(bipMenu));
  not not_7 (not_7_out, BUSYSetHeure);
  and and_3 (enHourAlarm, s_r_ff_1_q, not_7_out);
  menuSetTime setTimeMenu_2 (
    .clickSimple(simpleClick), .clickDouble(doubleClick), .clickLong(longClick), .CCW(CCW), .CW(CW),
    .CLK(CLK), .POR(POR_t), .selectMenu(menuSelect), .ADDR(4'b0001), .BUSY(BUSYSetAlarm),
    .stateHMS(setTimeMenu_2_statehms), .currentHourH(currentHourHSetAlarm),
    .currentHourL(currentHourLSetAlarm), .currentMinuteH(currentMinuteHSetAlarm),
    .currentMinuteL(currentMinuteLSetAlarm), .currentSecondH(currentSecondHSetAlarm),
    .currentSecondL(currentSecondLSetAlarm));
  Clock #(.highDuration(50000), .lowDuration(50000)) clock_4 (.out(clock_4_out));
  Decoder #(.select(2)) decoder_2 (
    .out1(decoder_2_out1), .out2(decoder_2_out2), .out3(decoder_2_out3), .sel(setTimeMenu_2_statehms),
    .en(clock_4_out));  // open: out0
  Multiplexer #(.width(6)) multiplexer_8 (
    .in0(6'b010000), .in1({2'b00, currentHourHSetAlarm}), .out(DisplayTimeSetAlarm[5:0]),
    .sel(blinkHeureAlarm));
  Multiplexer #(.width(6)) multiplexer_9 (
    .in0(6'b010000), .in1({2'b00, currentHourLSetAlarm}), .out(DisplayTimeSetAlarm[11:6]),
    .sel(blinkHeureAlarm));
  Multiplexer #(.width(6)) multiplexer_10 (
    .in0(6'b010000), .in1({2'b00, currentMinuteHSetAlarm}), .out(DisplayTimeSetAlarm[17:12]),
    .sel(blinkMinuteAlarm));
  Multiplexer #(.width(6)) multiplexer_11 (
    .in0(6'b010000), .in1({2'b00, currentMinuteLSetAlarm}), .out(DisplayTimeSetAlarm[23:18]),
    .sel(blinkMinuteAlarm));
  Multiplexer #(.width(6)) multiplexer_12 (
    .in0(6'b010000), .in1({2'b00, currentSecondHSetAlarm}), .out(DisplayTimeSetAlarm[29:24]),
    .sel(blinkSecondAlarm));
  Multiplexer #(.width(6)) multiplexer_13 (
    .in0(6'b010000), .in1({2'b00, currentSecondLSetAlarm}), .out(DisplayTimeSetAlarm[35:30]),
    .sel(blinkSecondAlarm));
  TimeComparator TimeComparator_2 (
    .CLK(CLK), .POR(POR_t), .en(enHourAlarm), .currentHourH(DisplayClock[5:0]),
    .currentHourL(DisplayClock[11:6]), .currentMinuteH(DisplayClock[17:12]),
    .currentMinuteL(DisplayClock[23:18]), .currentSecondH(DisplayClock[29:24]),
    .currentSecondL(DisplayClock[35:30]), .compareHourH(currentHourHSetAlarm),
    .compareHourL(currentHourLSetAlarm), .compareMinuteH(currentMinuteHSetAlarm),
    .compareMinuteL(currentMinuteLSetAlarm), .compareSecondH(currentSecondHSetAlarm),
    .compareSecondL(currentSecondLSetAlarm), .equal(alarmHorloge));
  not not_8 (blinkHeureAlarm, decoder_2_out1);
  not not_9 (blinkMinuteAlarm, decoder_2_out2);
  not not_10 (blinkSecondAlarm, decoder_2_out3);
  menuSetMelody menuSetMelody_1 (
    .clickSimple(simpleClick), .clickDouble(doubleClick), .clickLong(longClick), .CCW(CCW), .CW(CW),
    .CLK(CLK), .POR(POR_t), .selectMenu(menuSelect), .ADDR(4'b0110), .BUSY(BUSYMelodie),
    .PLAY(menuSetMelody_1_play), .REC(menuSetMelody_1_rec), .adress(menuSetMelody_1_adress),
    .tone(notePreview), .BPM(menuSetMelody_1_bpm), .displayOut(DisplaySetMelody));
  or or_5 (or_5_out, play, menuSetMelody_1_play);
  menuSetMessage menuSetMessage_1 (
    .POR(POR_t), .CLK(CLK), .ClickSimple(simpleClick), .LongClick(longClick), .CW(CW), .CCW(CCW),
    .selectMenu(menuSelect), .ADRESS(4'b0111), .displayIn(alarmDisplay), .BUSY(BUSYsetMessage),
    .displayCM(requestAlarmMessage), .setChar(setCstmChar), .char(cstmChar), .charPos(cstmCharADR),
    .displayOut(DisplaySetMessage));
  D_Flip_Flop d_ff_2 (.D(BUSYMelodie), .clk(CLK), .Q(d_ff_2_q), .reset(POR_t));  // open: Qn, preset
  not not_11 (not_11_out, BUSYMelodie);
  D_Flip_Flop d_ff_3 (.D(BUSYTimer), .clk(CLK), .Q(d_ff_3_q), .reset(POR_t));  // open: Qn, preset
  songPlayer songPlayer_1 (
    .POR(POR_t), .CLK(CLK), .play(or_5_out), .rec(menuSetMelody_1_rec), .addr(menuSetMelody_1_adress),
    .TONE(notePreview), .BPM(menuSetMelody_1_bpm), .noteOut(tone), .BUSY(busyPlayingMelody));
  S_R_Flip_Flop s_r_ff_2 (.S(and_4_out), .clk(CLK), .reset(POR_t), .Qn(jingleNotSet));  // open: R, Q, preset
  and and_4 (and_4_out, not_11_out, d_ff_2_q);
  Clock #(.lowDuration(99999)) clock_5 (.out(clock_5_out));
  not not_12 (not_12_out, BUSYTimer);
  and and_5 (and_5_out, not_12_out, d_ff_3_q);
  S_R_Flip_Flop s_r_ff_3 (.S(and_5_out), .clk(CLK), .Q(enTimerAlarm), .reset(or_6_out));  // open: R, Qn, preset
  or or_6 (or_6_out, alarmTimer, POR_t);
  and and_6 (simpleAlarm, play, jingleNotSet);
  menuIdle idleMenu_1 (
    .clickSimple(simpleClick), .CLK(CLK), .POR(POR_t), .selectMenu(menuSelect), .ADDR(4'b0100),
    .BUSY(BUSYTimerIdle));
  clockDCB clockDCB2_3 (
    .setTime(BUSYTimer), .reverseCount(1'b1), .clockInput(clock_5_out), .enCount(enTimerAlarm), .POR(POR_t),
    .setHourH(currentHourHSetTimer), .setHourL(currentHourLSetTimer), .setMinuteH(currentMinuteHSetTimer),
    .setMinuteL(currentMinuteLSetTimer), .setSecondH(currentSecondHSetTimer),
    .setSecondL(currentSecondLSetTimer), .hourH(DisplayTimer[5:0]), .hourL(DisplayTimer[11:6]),
    .minuteH(DisplayTimer[17:12]), .minuteL(DisplayTimer[23:18]), .secondH(DisplayTimer[29:24]),
    .secondL(DisplayTimer[35:30]));
  menuSetTime setTimeMenu_1 (
    .clickSimple(simpleClick), .clickDouble(doubleClick), .clickLong(longClick), .CCW(CCW), .CW(CW),
    .CLK(CLK), .POR(POR_t), .selectMenu(menuSelect), .ADDR(4'b0011), .BUSY(BUSYTimer),
    .stateHMS(setTimeMenu_1_statehms), .currentHourH(currentHourHSetTimer),
    .currentHourL(currentHourLSetTimer), .currentMinuteH(currentMinuteHSetTimer),
    .currentMinuteL(currentMinuteLSetTimer), .currentSecondH(currentSecondHSetTimer),
    .currentSecondL(currentSecondLSetTimer));
  Decoder #(.select(2)) decoder_3 (
    .out1(decoder_3_out1), .out2(decoder_3_out2), .out3(decoder_3_out3), .sel(setTimeMenu_1_statehms),
    .en(clock_6_out));  // open: out0
  Clock #(.highDuration(50000), .lowDuration(50000)) clock_6 (.out(clock_6_out));
  not not_13 (blinkHeureTimer, decoder_3_out1);
  not not_14 (blinkMinuteTimer, decoder_3_out2);
  not not_15 (blinkSecondTimer, decoder_3_out3);
  Multiplexer #(.width(6)) multiplexer_14 (
    .in0(6'b010000), .in1({2'b00, currentHourHSetTimer}), .out(DisplayTimeSetTimer[5:0]),
    .sel(blinkHeureTimer));
  Multiplexer #(.width(6)) multiplexer_15 (
    .in0(6'b010000), .in1({2'b00, currentHourLSetTimer}), .out(DisplayTimeSetTimer[11:6]),
    .sel(blinkHeureTimer));
  Multiplexer #(.width(6)) multiplexer_16 (
    .in0(6'b010000), .in1({2'b00, currentMinuteHSetTimer}), .out(DisplayTimeSetTimer[17:12]),
    .sel(blinkMinuteTimer));
  Multiplexer #(.width(6)) multiplexer_17 (
    .in0(6'b010000), .in1({2'b00, currentMinuteLSetTimer}), .out(DisplayTimeSetTimer[23:18]),
    .sel(blinkMinuteTimer));
  Multiplexer #(.width(6)) multiplexer_18 (
    .in0(6'b010000), .in1({2'b00, currentSecondHSetTimer}), .out(DisplayTimeSetTimer[29:24]),
    .sel(blinkSecondTimer));
  Multiplexer #(.width(6)) multiplexer_19 (
    .in0(6'b010000), .in1({2'b00, currentSecondLSetTimer}), .out(DisplayTimeSetTimer[35:30]),
    .sel(blinkSecondTimer));
  menuTitleHandler menuTitleHandle_1 (
    .CLK(CLK), .POR(POR_t), .alarmHorloge(alarmHorloge), .alarmTimer(alarmTimer), .setCstmChar(setCstmChar),
    .cstmChar(cstmChar), .cstmCharADR(cstmCharADR), .menuSelected(menuSelect),
    .menuSelectPreview(menuSelectPreview), .displayCM(requestAlarmMessage),
    .menudisplayOveride(menuDisplayOveride), .alarmOveride(alarmHandlerDisplayOveride),
    .menuTitle(menuTitle), .alarmMessage(alarmDisplay), .simpleAlarm(simpleAlarm), .customAlarm(play));
  TimeComparator TimeComparator_1 (
    .CLK(CLK), .POR(POR_t), .en(enTimerAlarm), .currentHourH(DisplayTimer[5:0]),
    .currentHourL(DisplayTimer[11:6]), .currentMinuteH(DisplayTimer[17:12]),
    .currentMinuteL(DisplayTimer[23:18]), .currentSecondH(DisplayTimer[29:24]),
    .currentSecondL(DisplayTimer[35:30]), .compareHourH(4'b0000), .compareHourL(4'b0000),
    .compareMinuteH(4'b0000), .compareMinuteL(4'b0000), .compareSecondH(4'b0000), .compareSecondL(4'b0000),
    .equal(alarmTimer));
  Multiplexer #(.width(36)) multiplexer_20 (
    .in0(DisplayClock), .in1(menuTitle), .out(multiplexer_20_out), .sel(menuDisplayOveride));
  Multiplexer #(.width(36)) multiplexer_21 (
    .in0(multiplexer_20_out), .in1(alarmDisplay), .out(multiplexer_21_out), .sel(alarmHandlerDisplayOveride));
  Clock #(.lowDuration(99999)) clock_7 (.out(clock_7_out));
  or or_7 (or_7_out, POR_t, resetChronoTime);
  Multiplexer #(.select(4), .width(36)) multiplexer_22 (
    .in0(multiplexer_21_out), .in1(DisplayTimeSetAlarm), .in2(DisplayTimeSet), .in3(DisplayTimeSetTimer),
    .in4(DisplayTimer), .in5(DisplayChrono), .in6(DisplaySetMelody), .in7(DisplaySetMessage),
    .out(DisplayOut), .sel(menuSelect));  // open: in8, in9, in10, in11, in12, in13, in14, in15
  driver7seg driver7seg_1 (
    .B(driver7seg_1_b), .C(driver7seg_1_c), .D(driver7seg_1_d), .E(driver7seg_1_e), .F(driver7seg_1_f),
    .G(driver7seg_1_g), .H(driver7seg_1_h), .A(driver7seg_1_a), .bcd(DisplayOut[5:0]));
  _7_Segment_Display L_7_Segment_Display_1 (
    .g(driver7seg_1_g), .f(driver7seg_1_f), .a(driver7seg_1_a), .b(driver7seg_1_b), .e(driver7seg_1_e),
    .d(driver7seg_1_d), .c(driver7seg_1_c), .dp(driver7seg_1_h));
  clockDCB clockDCB2_2 (
    .setTime(1'b0), .reverseCount(1'b0), .clockInput(clock_7_out), .enCount(chronoEnable), .POR(or_7_out),
    .hourH(DisplayChrono[5:0]), .hourL(DisplayChrono[11:6]), .minuteH(DisplayChrono[17:12]),
    .minuteL(DisplayChrono[23:18]), .secondH(DisplayChrono[29:24]), .secondL(DisplayChrono[35:30]));  // open: setHourH, setHourL, setMinuteH, setMinuteL, setSecondH, setSecondL
  menuChrono chronoMenu_1 (
    .clickSimple(simpleClick), .clickDouble(doubleClick), .clickLong(longClick), .CLK(CLK), .POR(POR_t),
    .selectMenu(menuSelect), .ADDR(4'b0101), .BUSY(BUSYChrono), .chronoReset(resetChronoTime),
    .chronoEnabled(chronoEnable));
  driver7seg driver7seg_2 (
    .B(driver7seg_2_b), .C(driver7seg_2_c), .D(driver7seg_2_d), .E(driver7seg_2_e), .F(driver7seg_2_f),
    .G(driver7seg_2_g), .H(driver7seg_2_h), .A(driver7seg_2_a), .bcd(DisplayOut[11:6]));
  _7_Segment_Display L_7_Segment_Display_2 (
    .g(driver7seg_2_g), .f(driver7seg_2_f), .a(driver7seg_2_a), .b(driver7seg_2_b), .e(driver7seg_2_e),
    .d(driver7seg_2_d), .c(driver7seg_2_c), .dp(driver7seg_2_h));
  driver7seg driver7seg_3 (
    .B(driver7seg_3_b), .C(driver7seg_3_c), .D(driver7seg_3_d), .E(driver7seg_3_e), .F(driver7seg_3_f),
    .G(driver7seg_3_g), .H(driver7seg_3_h), .A(driver7seg_3_a), .bcd(DisplayOut[17:12]));
  _7_Segment_Display L_7_Segment_Display_3 (
    .g(driver7seg_3_g), .f(driver7seg_3_f), .a(driver7seg_3_a), .b(driver7seg_3_b), .e(driver7seg_3_e),
    .d(driver7seg_3_d), .c(driver7seg_3_c), .dp(driver7seg_3_h));
  driver7seg driver7seg_4 (
    .B(driver7seg_4_b), .C(driver7seg_4_c), .D(driver7seg_4_d), .E(driver7seg_4_e), .F(driver7seg_4_f),
    .G(driver7seg_4_g), .H(driver7seg_4_h), .A(driver7seg_4_a), .bcd(DisplayOut[23:18]));
  driver7seg driver7seg_5 (
    .B(driver7seg_5_b), .C(driver7seg_5_c), .D(driver7seg_5_d), .E(driver7seg_5_e), .F(driver7seg_5_f),
    .G(driver7seg_5_g), .H(driver7seg_5_h), .A(driver7seg_5_a), .bcd(DisplayOut[29:24]));
  _7_Segment_Display L_7_Segment_Display_4 (
    .g(driver7seg_4_g), .f(driver7seg_4_f), .a(driver7seg_4_a), .b(driver7seg_4_b), .e(driver7seg_4_e),
    .d(driver7seg_4_d), .c(driver7seg_4_c), .dp(driver7seg_4_h));
  driver7seg driver7seg_6 (
    .B(driver7seg_6_b), .C(driver7seg_6_c), .D(driver7seg_6_d), .E(driver7seg_6_e), .F(driver7seg_6_f),
    .G(driver7seg_6_g), .H(driver7seg_6_h), .A(driver7seg_6_a), .bcd(DisplayOut[35:30]));
  _7_Segment_Display L_7_Segment_Display_5 (
    .g(driver7seg_5_g), .f(driver7seg_5_f), .a(driver7seg_5_a), .b(driver7seg_5_b), .e(driver7seg_5_e),
    .d(driver7seg_5_d), .c(driver7seg_5_c), .dp(driver7seg_5_h));
  _7_Segment_Display L_7_Segment_Display_6 (
    .g(driver7seg_6_g), .f(driver7seg_6_f), .a(driver7seg_6_a), .b(driver7seg_6_b), .e(driver7seg_6_e),
    .d(driver7seg_6_d), .c(driver7seg_6_c), .dp(driver7seg_6_h));

  assign GND = 1'b0;
  assign VCC = 1'b1;

  // Notes on the sheet:
  //   Constantes :
  //   MasterClock 100kHz :
  //   Clock 1 sec :
  //   Horloge :
  //   IO section :
  //   Click :
  //   Encodeur Rotatif :
  //   Buzzer :
  //   Make the select digits blink :
  //   See note in menuMain regarding the BUSY
  //   Désactive l'alarme si pas set
  //   Menu Control Section :
  //   ou si l'heure est modifié :
  //   0 -> Hour
  //   1 -> Set Sunrise
  //   2 -> Set Hour
  //   4 -> Hourglass
  //   5 -> Chrono
  //   7 -> Set display
  //   3 -> Set Hourglass
  //   6 -> Set ringtone
  //   Set Alarme :
  //   Make the select digits blink :
  //   Menu Custom Melody  :
  //   Menu Custom Message :
  //   Custom alarm player :
  //   fallback Alarm if not set
  //   Clock 1 sec :
  //   Désactive l'alarme si pas set :
  //   Timer :
  //   Make the select digits blink :
  //   Display Handler Menu/Alarm :
  //   Clock 1 sec :
  //   7 Seg driver :
  //   Chrono :
endmodule

module powerOnReset (
  input  CLK,
  output GEN_POR
);

  wire counter_1_carry;

  Counter #(.max('h8fff), .width(16)) counter_1 (
    .clr(1'b0), .load(1'b0), .up(1'b1), .count(GEN_POR), .clk(CLK), .carry(counter_1_carry));  // open: D, Q
  not not_1 (GEN_POR, counter_1_carry);

  // Other names for the same wires on the sheet: POR = GEN_POR

  // Notes on the sheet:
  //   Variables :
  //   low probabilities of starting close to overflow
endmodule

module driver7seg (
  input  [5:0] bcd,
  output A,
  output B,
  output C,
  output D,
  output E,
  output F,
  output G,
  output H
);

  wire and_1_out, and_2_out, and_3_out, and_4_out, and_5_out, and_6_out, and_7_out, and_8_out, and_9_out,
       and_10_out, and_11_out, and_12_out, and_13_out, and_14_out, and_15_out, and_16_out, and_17_out,
       and_18_out, and_19_out, and_20_out, and_21_out, and_22_out, and_23_out, and_24_out, and_25_out,
       and_26_out, and_27_out, and_28_out, and_29_out, and_30_out, and_31_out, and_32_out, and_33_out,
       and_34_out, and_35_out, and_36_out, and_37_out, and_38_out, and_39_out, and_40_out, and_41_out,
       and_42_out, and_43_out, and_44_out, and_45_out, and_46_out, and_47_out, and_48_out, and_49_out,
       and_50_out, and_51_out, and_52_out, and_53_out, and_54_out, and_55_out, and_56_out, and_57_out,
       and_58_out, and_59_out, not_1_out, not_2_out, not_3_out, not_4_out, not_5_out;

  not not_1 (not_1_out, bcd[4]);
  not not_2 (not_2_out, bcd[3]);
  not not_3 (not_3_out, bcd[2]);
  not not_4 (not_4_out, bcd[1]);
  not not_5 (not_5_out, bcd[0]);
  and and_1 (and_1_out, not_1_out, not_3_out, not_5_out);
  and and_2 (and_2_out, not_1_out, not_2_out, bcd[1]);
  and and_3 (and_3_out, not_1_out, not_2_out, bcd[2], bcd[0]);
  and and_4 (and_4_out, not_1_out, bcd[2], bcd[1]);
  and and_5 (and_5_out, not_2_out, bcd[2], bcd[1], bcd[0]);
  and and_6 (and_6_out, not_1_out, bcd[3], not_3_out, not_4_out);
  and and_7 (and_7_out, not_1_out, bcd[3], not_5_out);
  and and_8 (and_8_out, bcd[4], bcd[3], not_4_out, bcd[0]);
  and and_9 (and_9_out, not_1_out, not_2_out, not_4_out, not_5_out);
  and and_10 (and_10_out, not_1_out, not_3_out, not_4_out);
  and and_11 (and_11_out, not_1_out, not_3_out, not_5_out);
  and and_12 (and_12_out, not_2_out, not_3_out, bcd[0]);
  and and_13 (and_13_out, not_2_out, bcd[1], bcd[0]);
  and and_14 (and_14_out, not_1_out, bcd[3], not_4_out, bcd[0]);
  and and_15 (and_15_out, bcd[4], bcd[3], bcd[2], not_4_out);
  and and_16 (and_16_out, not_1_out, not_2_out, not_4_out);
  and and_17 (and_17_out, not_1_out, not_4_out, bcd[0]);
  and and_18 (and_18_out, not_2_out, not_4_out, bcd[0]);
  and and_19 (and_19_out, not_3_out, bcd[0]);
  and and_20 (and_20_out, not_1_out, not_2_out, bcd[2]);
  and and_21 (and_21_out, not_2_out, bcd[2], bcd[1], not_5_out);
  and and_22 (and_22_out, not_1_out, bcd[3], not_3_out);
  and and_23 (and_23_out, bcd[4], bcd[3], bcd[2], not_4_out, not_5_out);
  and and_24 (and_24_out, not_1_out, not_3_out, not_4_out, not_5_out);
  and and_25 (and_25_out, not_1_out, not_2_out, bcd[1], not_5_out);
  and and_26 (and_26_out, not_3_out, bcd[1], bcd[0]);
  and and_27 (and_27_out, not_1_out, bcd[2], not_4_out, bcd[0]);
  and and_28 (and_28_out, bcd[3], not_3_out, bcd[0]);
  and and_29 (and_29_out, not_1_out, bcd[3], bcd[2], not_5_out);
  and and_30 (and_30_out, bcd[3], bcd[2], not_4_out, not_5_out);
  and and_31 (and_31_out, bcd[4], not_2_out, bcd[2], not_5_out);
  and and_32 (and_32_out, bcd[4], bcd[3], not_3_out, bcd[1]);
  and and_33 (and_33_out, not_1_out, not_3_out, not_5_out);
  and and_34 (and_34_out, bcd[1], not_5_out);
  and and_35 (and_35_out, bcd[3], not_3_out, not_5_out);
  and and_36 (and_36_out, bcd[3], not_3_out, bcd[1]);
  and and_37 (and_37_out, not_1_out, bcd[3], bcd[2]);
  and and_38 (and_38_out, bcd[4], not_2_out, not_4_out, bcd[0]);
  and and_39 (and_39_out, bcd[4], not_2_out, bcd[2]);
  and and_40 (and_40_out, not_1_out, not_4_out, not_5_out);
  and and_41 (and_41_out, not_1_out, not_2_out, bcd[2], not_4_out);
  and and_42 (and_42_out, not_1_out, bcd[2], not_5_out);
  and and_43 (and_43_out, bcd[2], not_4_out, not_5_out);
  and and_44 (and_44_out, not_1_out, bcd[3], not_3_out);
  and and_45 (and_45_out, not_1_out, bcd[3], bcd[1]);
  and and_46 (and_46_out, bcd[4], not_3_out, not_4_out, bcd[0]);
  and and_47 (and_47_out, bcd[4], not_3_out, bcd[1], not_5_out);
  and and_48 (and_48_out, bcd[4], not_2_out, bcd[2], bcd[1], bcd[0]);
  and and_49 (and_49_out, bcd[4], bcd[3], bcd[2], not_4_out);
  and and_50 (and_50_out, not_1_out, not_3_out, bcd[1]);
  and and_51 (and_51_out, not_1_out, bcd[1], not_5_out);
  and and_52 (and_52_out, not_1_out, not_2_out, bcd[2], not_4_out);
  and and_53 (and_53_out, not_2_out, bcd[2], bcd[1], not_5_out);
  and and_54 (and_54_out, not_1_out, bcd[3], not_3_out);
  and and_55 (and_55_out, bcd[3], not_3_out, not_5_out);
  and and_56 (and_56_out, bcd[3], bcd[2], bcd[0]);
  and and_57 (and_57_out, bcd[4], not_4_out, bcd[0]);
  and and_58 (and_58_out, bcd[4], bcd[2], bcd[0]);
  and and_59 (and_59_out, bcd[4], bcd[3], not_4_out);
  or or_1 (A, and_1_out, and_2_out, and_3_out, and_4_out, and_5_out, and_6_out, and_7_out, and_8_out);
  or or_2 (B, and_9_out, and_10_out, and_11_out, and_12_out, and_13_out, and_14_out, and_15_out);
  or or_3 (C, and_16_out, and_17_out, and_18_out, and_19_out, and_20_out, and_21_out, and_22_out, and_23_out);
  or or_4 (D, and_24_out, and_25_out, and_26_out, and_27_out, and_28_out, and_29_out, and_30_out, and_31_out, and_32_out);
  or or_5 (E, and_33_out, and_34_out, and_35_out, and_36_out, and_37_out, and_38_out, and_39_out);
  or or_6 (F, and_40_out, and_41_out, and_42_out, and_43_out, and_44_out, and_45_out, and_46_out, and_47_out, and_48_out, and_49_out);
  or or_7 (G, and_50_out, and_51_out, and_52_out, and_53_out, and_54_out, and_55_out, and_56_out, and_57_out, and_58_out, and_59_out);

  assign H = bcd[5];

  // Notes on the sheet:
  //   bit 5 = dot
  //   bit 4 = ADV_Mode
  //   bit 0-3 = DCB / display code
endmodule

module driverRotaryEncoder (
  input  POR,
  input  CLK,
  input  CHA,
  input  CHB,
  output CCW,
  output CW
);

  wire and_1_out, and_2_out, and_3_out, and_4_out, and_5_out, and_6_out, and_7_out, and_8_out, and_9_out,
       and_10_out, CHA_OUT, CHB_OUT, not_1_out, not_2_out, not_3_out, not_4_out, PREV_CHA, PREV_CHB;

  D_Flip_Flop d_ff_1 (.D(CHA_OUT), .clk(CLK), .Q(PREV_CHA), .reset(POR));  // open: Qn, preset
  not not_1 (not_1_out, PREV_CHA);
  not not_2 (not_2_out, PREV_CHB);
  not not_3 (not_3_out, CHA);
  not not_4 (not_4_out, CHB);
  D_Flip_Flop d_ff_2 (.D(CHB_OUT), .clk(CLK), .Q(PREV_CHB), .reset(POR));  // open: Qn, preset
  and and_1 (and_1_out, PREV_CHA, not_2_out, CHA, CHB);
  or or_1 (CW, and_1_out, and_2_out);
  and and_2 (and_2_out, PREV_CHA, PREV_CHB, not_3_out, CHB);
  and and_3 (and_3_out, not_1_out, PREV_CHB, CHA, CHB);
  or or_2 (CCW, and_3_out, and_4_out);
  and and_4 (and_4_out, PREV_CHA, PREV_CHB, CHA, not_4_out);
  and and_5 (and_5_out, not_2_out, CHA, not_4_out);
  and and_6 (and_6_out, PREV_CHB, CHA, CHB);
  or or_3 (CHA_OUT, and_5_out, and_6_out, and_7_out);
  and and_7 (and_7_out, PREV_CHA, CHA);
  and and_8 (and_8_out, not_1_out, not_3_out, CHB);
  and and_9 (and_9_out, PREV_CHB, CHB);
  or or_4 (CHB_OUT, and_8_out, and_9_out, and_10_out);
  and and_10 (and_10_out, PREV_CHA, CHA, CHB);

  // Other names for the same wires on the sheet: RST = POR

  // Notes on the sheet:
  //   Variables :
  //   This module convert the debounced input of the rotary encoder and output a click for each step up or down
  //   Memory
  //   Etat de la machine :
  //   State machine decoder :
endmodule

module driverBuzzerTone (
  input  POR,
  input  CLK,
  input  bip,
  input  longBip,
  input  doubleBip,
  input  [4:0] TONE,
  output Buzzer
);

  wire and_1_out, and_2_out, and_3_out, blanc, clock_1_out, clock_2_out, clock_3_out, clock_4_out,
       clock_5_out, clock_6_out, clock_7_out, clock_8_out, clock_9_out, clock_10_out, clock_11_out,
       clock_12_out, clock_13_out, clock_14_out, clock_15_out, clock_16_out, clock_17_out, clock_18_out,
       clock_19_out, clock_20_out, clock_21_out, clock_22_out, clock_23_out, clock_24_out, clock_25_out,
       clock_26_out, clock_27_out, clock_28_out, clock_29_out, clock_30_out, clock_31_out, clock_32_out,
       clock_33_out, comparator_1_eq, comparator_4_eq, comparator_5_eq, multiplexer_1_out, nor_1_out,
       or_1_out, or_3_out, or_4_out, or_5_out, or_6_out, or_7_out, or_8_out, or_9_out, or_10_out, or_11_out,
       or_12_out, resetBlanc, resetDouble, resetLong, resetSecond, resetSimple, secondBip, triggerBlanc,
       triggerDoubleA, triggerDoubleB, triggerLong, triggerSimple;
  wire [15:0] counter_1_q, counter_2_q, counter_3_q, counter_4_q, counter_5_q;

  Clock #(.highDuration(227), .lowDuration(227)) clock_1 (.out(clock_1_out));
  Clock #(.highDuration(215), .lowDuration(215)) clock_2 (.out(clock_2_out));
  Clock #(.highDuration(203), .lowDuration(203)) clock_3 (.out(clock_3_out));
  Clock #(.highDuration(192), .lowDuration(192)) clock_4 (.out(clock_4_out));
  Clock #(.highDuration(181), .lowDuration(181)) clock_5 (.out(clock_5_out));
  Clock #(.highDuration(171), .lowDuration(171)) clock_6 (.out(clock_6_out));
  Clock #(.highDuration(161), .lowDuration(161)) clock_7 (.out(clock_7_out));
  Clock #(.highDuration(152), .lowDuration(152)) clock_8 (.out(clock_8_out));
  Clock #(.highDuration(143), .lowDuration(143)) clock_9 (.out(clock_9_out));
  Clock #(.highDuration(135), .lowDuration(135)) clock_10 (.out(clock_10_out));
  Clock #(.highDuration(120), .lowDuration(120)) clock_11 (.out(clock_11_out));
  Clock #(.highDuration(114), .lowDuration(114)) clock_12 (.out(clock_12_out));
  Clock #(.highDuration(107), .lowDuration(107)) clock_13 (.out(clock_13_out));
  Clock #(.highDuration(101), .lowDuration(101)) clock_14 (.out(clock_14_out));
  Clock #(.highDuration(96), .lowDuration(96)) clock_15 (.out(clock_15_out));
  Clock #(.highDuration(90), .lowDuration(90)) clock_16 (.out(clock_16_out));
  Clock #(.highDuration(85), .lowDuration(85)) clock_17 (.out(clock_17_out));
  Clock #(.highDuration(80), .lowDuration(80)) clock_18 (.out(clock_18_out));
  Clock #(.highDuration(76), .lowDuration(76)) clock_19 (.out(clock_19_out));
  Clock #(.highDuration(72), .lowDuration(72)) clock_20 (.out(clock_20_out));
  Clock #(.highDuration(68), .lowDuration(68)) clock_21 (.out(clock_21_out));
  Clock #(.highDuration(64), .lowDuration(64)) clock_22 (.out(clock_22_out));
  Clock #(.highDuration(60), .lowDuration(60)) clock_23 (.out(clock_23_out));
  Clock #(.highDuration(57), .lowDuration(57)) clock_24 (.out(clock_24_out));
  Clock #(.highDuration(54), .lowDuration(54)) clock_25 (.out(clock_25_out));
  Clock #(.highDuration(51), .lowDuration(51)) clock_26 (.out(clock_26_out));
  Clock #(.highDuration(48), .lowDuration(48)) clock_27 (.out(clock_27_out));
  Clock #(.highDuration(45), .lowDuration(45)) clock_28 (.out(clock_28_out));
  Clock #(.highDuration(43), .lowDuration(43)) clock_29 (.out(clock_29_out));
  Clock #(.highDuration(40), .lowDuration(40)) clock_30 (.out(clock_30_out));
  Clock #(.highDuration(36), .lowDuration(36)) clock_31 (.out(clock_31_out));
  Multiplexer #(.select(5)) multiplexer_1 (
    .in0(1'b0), .in1(clock_1_out), .in2(clock_2_out), .in3(clock_3_out), .in4(clock_4_out),
    .in5(clock_5_out), .in6(clock_6_out), .in7(clock_7_out), .in8(clock_8_out), .in9(clock_9_out),
    .in10(clock_10_out), .in11(clock_11_out), .in12(clock_12_out), .in13(clock_13_out), .in14(clock_14_out),
    .in15(clock_15_out), .in16(clock_16_out), .in17(clock_17_out), .in18(clock_18_out), .in19(clock_19_out),
    .in20(clock_20_out), .in21(clock_21_out), .in22(clock_22_out), .in23(clock_23_out), .in24(clock_24_out),
    .in25(clock_25_out), .in26(clock_26_out), .in27(clock_27_out), .in28(clock_28_out), .in29(clock_29_out),
    .in30(clock_30_out), .in31(clock_31_out), .out(multiplexer_1_out), .sel(TONE));
  or or_1 (or_1_out, triggerSimple, triggerDoubleA, triggerDoubleB, triggerLong);
  Clock #(.highDuration(50), .lowDuration(50)) clock_32 (.out(clock_32_out));
  and and_1 (and_1_out, or_1_out, clock_32_out);
  nor nor_1 (nor_1_out, triggerSimple, triggerDoubleA, triggerDoubleB, triggerLong);
  and and_2 (and_2_out, multiplexer_1_out, nor_1_out);
  Clock #(.highDuration(50), .lowDuration(50)) clock_33 (.out(clock_33_out));
  and and_3 (and_3_out, POR, clock_33_out);
  or or_2 (Buzzer, and_3_out, and_1_out, and_2_out);
  or or_3 (or_3_out, resetSimple, POR);
  Counter #(.max('hffff), .width(16)) counter_1 (
    .clr(or_3_out), .load(1'b0), .up(1'b1), .count(triggerSimple), .clk(CLK), .Q(counter_1_q));  // open: D, carry
  or or_4 (or_4_out, resetDouble, POR);
  S_R_Flip_Flop s_r_ff_1 (.S(bip), .clk(CLK), .Q(triggerSimple), .reset(or_5_out));  // open: R, Qn, preset
  or or_5 (or_5_out, POR, resetSimple);
  Counter #(.max('hffff), .width(16)) counter_2 (
    .clr(or_4_out), .load(1'b0), .up(1'b1), .count(triggerDoubleA), .clk(CLK), .Q(counter_2_q));  // open: D, carry
  S_R_Flip_Flop s_r_ff_2 (.S(doubleBip), .clk(CLK), .Q(triggerDoubleA), .reset(or_6_out));  // open: R, Qn, preset
  or or_6 (or_6_out, POR, resetDouble);
  Comparator #(.width(16)) comparator_1 (.a(16'h5dc), .b(counter_1_q), .eq(comparator_1_eq));  // open: gt, lt
  D_Flip_Flop d_ff_1 (.D(comparator_1_eq), .clk(CLK), .Q(resetSimple), .reset(POR));  // open: Qn, preset
  D_Flip_Flop d_ff_2 (.D(blanc), .clk(CLK), .Q(resetDouble), .reset(POR));  // open: Qn, preset
  Comparator #(.width(16)) comparator_2 (.a(16'h3a98), .b(counter_2_q), .eq(blanc));  // open: gt, lt
  or or_7 (or_7_out, resetLong, POR);
  or or_8 (or_8_out, resetBlanc, POR);
  S_R_Flip_Flop s_r_ff_3 (.S(longBip), .clk(CLK), .Q(triggerLong), .reset(or_9_out));  // open: R, Qn, preset
  Counter #(.max('hffff), .width(16)) counter_3 (
    .clr(or_7_out), .load(1'b0), .up(1'b1), .count(triggerLong), .clk(CLK), .Q(counter_3_q));  // open: D, carry
  S_R_Flip_Flop s_r_ff_4 (.S(blanc), .clk(CLK), .Q(triggerBlanc), .reset(or_10_out));  // open: R, Qn, preset
  Counter #(.max('hffff), .width(16)) counter_4 (
    .clr(or_8_out), .load(1'b0), .up(1'b1), .count(triggerBlanc), .clk(CLK), .Q(counter_4_q));  // open: D, carry
  or or_9 (or_9_out, POR, resetLong);
  or or_10 (or_10_out, POR, resetBlanc);
  Comparator #(.width(16)) comparator_3 (.a(16'h3a98), .b(counter_4_q), .eq(secondBip));  // open: gt, lt
  D_Flip_Flop d_ff_3 (.D(comparator_4_eq), .clk(CLK), .Q(resetLong), .reset(POR));  // open: Qn, preset
  Comparator #(.width(16)) comparator_4 (.a(16'h4e20), .b(counter_3_q), .eq(comparator_4_eq));  // open: gt, lt
  D_Flip_Flop d_ff_4 (.D(secondBip), .clk(CLK), .Q(resetBlanc), .reset(POR));  // open: Qn, preset
  or or_11 (or_11_out, resetSecond, POR);
  Counter #(.max('hffff), .width(16)) counter_5 (
    .clr(or_11_out), .load(1'b0), .up(1'b1), .count(triggerDoubleB), .clk(CLK), .Q(counter_5_q));  // open: D, carry
  S_R_Flip_Flop s_r_ff_5 (.S(secondBip), .clk(CLK), .Q(triggerDoubleB), .reset(or_12_out));  // open: R, Qn, preset
  or or_12 (or_12_out, POR, resetSecond);
  Comparator #(.width(16)) comparator_5 (.a(16'h3a98), .b(counter_5_q), .eq(comparator_5_eq));  // open: gt, lt
  D_Flip_Flop d_ff_5 (.D(comparator_5_eq), .clk(CLK), .Q(resetSecond), .reset(POR));  // open: Qn, preset

  // Other names for the same wires on the sheet: RST = POR

  // Notes on the sheet:
  //   la2=220
  //   la#2=233
  //   si2=246
  //   do3=261
  //   do#3=277
  //   ré3=293
  //   ré3#=311
  //   mi3=329
  //   fa3=349
  //   sol3=370
  //   sol#3=415
  //   la3=440
  //   la#3=466
  //   do4=523
  //   do#4=554
  //   ré4=587
  //   ré#4=622
  //   mi4=659
  //   fa#4=740
  //   sol4=784
  //   sol#4=830
  //   la#4=932
  //   do#5=1108
  //   Variables :
  //   Human hearing seems to be 1-2Hz precise
  //   si3=494
  //   fa4=698
  //   la4=880
  //   si4=988
  //   do5=1046
  //   ré5=1174
  //   ré#5=1244
  //   m5=1397
  //   Input
  //   overide tone played to beep
  //   2.5 Octave, 32 tone
  //   12 note / Octave
  //   master clock @ 100 khz
  //   Machine simple bip :
  //   Memoire simple bip :
  //   Timeout generator :
  //   First bip :
  //   Machine double first-bip :
  //   Timeout generator :
  //   Memoire long bip :
  //   Machine long bip :
  //   Timeout generator :
  //   Memoire double bip :
  //   Silence btw 2 bips :
  //   Machine Double silence :
  //   Timeout generator :
  //   Second bip :
  //   Machine double second-bip :
  //   Timeout generator :
endmodule

module debouncer (
  input  rawInput,
  input  CLK,
  input  POR,
  output debounced
);

  wire d_ff_1_q, d_ff_2_q, d_ff_3_q, d_ff_4_q, d_ff_5_q, d_ff_6_q, d_ff_7_q, d_ff_8_q, d_ff_9_q, d_ff_10_q,
       d_ff_11_q, d_ff_12_q, d_ff_13_q, d_ff_14_q, d_ff_15_q, d_ff_16_q;

  D_Flip_Flop d_ff_1 (.D(rawInput), .clk(CLK), .Q(d_ff_1_q), .reset(POR));  // open: Qn, preset
  D_Flip_Flop d_ff_2 (.D(d_ff_1_q), .clk(CLK), .Q(d_ff_2_q), .reset(POR));  // open: Qn, preset
  D_Flip_Flop d_ff_3 (.D(d_ff_2_q), .clk(CLK), .Q(d_ff_3_q), .reset(POR));  // open: Qn, preset
  D_Flip_Flop d_ff_4 (.D(d_ff_3_q), .clk(CLK), .Q(d_ff_4_q), .reset(POR));  // open: Qn, preset
  D_Flip_Flop d_ff_5 (.D(d_ff_4_q), .clk(CLK), .Q(d_ff_5_q), .reset(POR));  // open: Qn, preset
  D_Flip_Flop d_ff_6 (.D(d_ff_5_q), .clk(CLK), .Q(d_ff_6_q), .reset(POR));  // open: Qn, preset
  D_Flip_Flop d_ff_7 (.D(d_ff_6_q), .clk(CLK), .Q(d_ff_7_q), .reset(POR));  // open: Qn, preset
  D_Flip_Flop d_ff_8 (.D(d_ff_7_q), .clk(CLK), .Q(d_ff_8_q), .reset(POR));  // open: Qn, preset
  D_Flip_Flop d_ff_9 (.D(d_ff_8_q), .clk(CLK), .Q(d_ff_9_q), .reset(POR));  // open: Qn, preset
  D_Flip_Flop d_ff_10 (.D(d_ff_9_q), .clk(CLK), .Q(d_ff_10_q), .reset(POR));  // open: Qn, preset
  D_Flip_Flop d_ff_11 (.D(d_ff_10_q), .clk(CLK), .Q(d_ff_11_q), .reset(POR));  // open: Qn, preset
  D_Flip_Flop d_ff_12 (.D(d_ff_11_q), .clk(CLK), .Q(d_ff_12_q), .reset(POR));  // open: Qn, preset
  D_Flip_Flop d_ff_13 (.D(d_ff_12_q), .clk(CLK), .Q(d_ff_13_q), .reset(POR));  // open: Qn, preset
  D_Flip_Flop d_ff_14 (.D(d_ff_13_q), .clk(CLK), .Q(d_ff_14_q), .reset(POR));  // open: Qn, preset
  D_Flip_Flop d_ff_15 (.D(d_ff_14_q), .clk(CLK), .Q(d_ff_15_q), .reset(POR));  // open: Qn, preset
  D_Flip_Flop d_ff_16 (.D(d_ff_15_q), .clk(CLK), .Q(d_ff_16_q), .reset(POR));  // open: Qn, preset
  and and_1 (debounced, d_ff_1_q, d_ff_2_q, d_ff_3_q, d_ff_4_q, d_ff_5_q, d_ff_6_q, d_ff_7_q, d_ff_8_q, d_ff_9_q, d_ff_10_q, d_ff_11_q, d_ff_12_q, d_ff_13_q, d_ff_14_q, d_ff_15_q, d_ff_16_q);

  // Notes on the sheet:
  //   20 us typical reboud duration
  //   clock = 100 khz -> 10 us
  //   + a safe margin of  80 us
endmodule

module clickLong (
  input  click,
  input  POR,
  input  clk,
  output click1,
  output clickLong
);

  wire and_1_out, and_2_out, and_5_out, and_6_out, clickFalling, clickRising, d_ff_2_qn, d_ff_3_q, mem,
       memOut, not_1_out, not_2_out, not_3_out, not_4_out, not_5_out, or_3_out, reset, timeOut, trigger;
  wire [15:0] counter_1_q;

  not not_1 (not_1_out, mem);
  not not_2 (not_2_out, timeOut);
  not not_3 (not_3_out, clickRising);
  not not_4 (not_4_out, clickFalling);
  and and_1 (and_1_out, not_1_out, clickRising, not_4_out);
  and and_2 (and_2_out, mem, not_2_out, not_3_out, not_4_out);
  and and_3 (click1, mem, not_3_out, clickFalling);
  and and_4 (clickLong, mem, timeOut, not_3_out, not_4_out);
  and and_5 (and_5_out, not_1_out, clickRising, not_4_out);
  and and_6 (and_6_out, mem, not_2_out, not_3_out, not_4_out);
  D_Flip_Flop d_ff_1 (.D(memOut), .clk(clk), .Q(mem), .reset(POR));  // open: Qn, preset
  or or_1 (trigger, and_1_out, and_2_out);
  or or_2 (memOut, and_5_out, and_6_out);
  D_Flip_Flop d_ff_2 (.D(click), .clk(clk), .Qn(d_ff_2_qn), .reset(POR));  // open: Q, preset
  or or_3 (or_3_out, reset, click1, POR);
  Counter #(.max('hffff), .width(16)) counter_1 (
    .clr(or_3_out), .load(1'b0), .up(1'b1), .count(trigger), .clk(clk), .Q(counter_1_q));  // open: D, carry
  and and_7 (clickRising, click, d_ff_2_qn);
  not not_5 (not_5_out, click);
  D_Flip_Flop d_ff_3 (.D(click), .clk(clk), .Q(d_ff_3_q), .reset(POR));  // open: Qn, preset
  Comparator #(.width(16)) comparator_1 (.a(16'hea60), .b(counter_1_q), .eq(timeOut));  // open: gt, lt
  and and_8 (clickFalling, not_5_out, d_ff_3_q);
  D_Flip_Flop d_ff_4 (.D(timeOut), .clk(clk), .Q(reset), .reset(POR));  // open: Qn, preset

  // Notes on the sheet:
  //   Variables :
  //   Machine Etat :
  //   Etat de la machine :
  //   Detecteur de flanc montant :
  //   Timeout generator :
  //   600 ms
  //   Detecteur de flanc descendant :
endmodule

module clickDouble (
  input  click,
  input  POR,
  input  clk,
  output click1,
  output clickDouble
);

  wire and_3_out, and_4_out, clickEdge, d_ff_2_qn, mem, memOut, not_1_out, not_2_out, not_3_out, or_3_out,
       reset, timeOut, trigger;
  wire [15:0] counter_1_q;

  not not_1 (not_1_out, mem);
  not not_2 (not_2_out, clickEdge);
  not not_3 (not_3_out, timeOut);
  or or_1 (trigger, clickEdge, mem);
  and and_1 (click1, mem, not_2_out, timeOut);
  and and_2 (clickDouble, mem, clickEdge);
  and and_3 (and_3_out, not_1_out, clickEdge);
  and and_4 (and_4_out, mem, not_2_out, not_3_out);
  D_Flip_Flop d_ff_1 (.D(memOut), .clk(clk), .Q(mem), .reset(POR));  // open: Qn, preset
  or or_2 (memOut, and_3_out, and_4_out);
  D_Flip_Flop d_ff_2 (.D(click), .clk(clk), .Qn(d_ff_2_qn), .reset(POR));  // open: Q, preset
  or or_3 (or_3_out, reset, clickDouble, POR);
  Counter #(.max('hffff), .width(16)) counter_1 (
    .clr(or_3_out), .load(1'b0), .up(1'b1), .count(trigger), .clk(clk), .Q(counter_1_q));  // open: D, carry
  and and_5 (clickEdge, click, d_ff_2_qn);
  Comparator #(.width(16)) comparator_1 (.a(16'h3a98), .b(counter_1_q), .eq(timeOut));  // open: gt, lt
  D_Flip_Flop d_ff_3 (.D(timeOut), .clk(clk), .Q(reset), .reset(POR));  // open: Qn, preset

  // Other names for the same wires on the sheet: click2 = clickDouble

  // Notes on the sheet:
  //   Variables :
  //   Machine Etat :
  //   Etat de la machine :
  //   Detecteur de flanc montant :
  //   Timeout generator :
  //   150 ms
endmodule

module clickSimpleLongAndDouble (
  input  click,
  input  POR,
  input  CLK,
  output clickSimple,
  output doubleClick,
  output longClick
);

  wire and_1_out, doubleClick1, longClick1, memDoubleClick1, memLongClick1, or_1_out, RST;

  D_Flip_Flop d_ff_1 (.D(1'b0), .clk(1'b0), .Q(memLongClick1), .preset(longClick1), .reset(or_1_out));  // open: Qn
  or or_1 (or_1_out, RST, POR);
  clickDouble clickDouble_1 (.click(click), .POR(POR), .clk(CLK), .click1(longClick1), .clickDouble(doubleClick));
  clickLong clickLong_1 (.click(click), .POR(POR), .clk(CLK), .click1(doubleClick1), .clickLong(longClick));
  D_Flip_Flop d_ff_2 (.D(1'b0), .clk(1'b0), .Q(memDoubleClick1), .preset(doubleClick1), .reset(or_1_out));  // open: Qn
  and and_1 (and_1_out, memLongClick1, memDoubleClick1);
  or or_2 (RST, clickSimple, doubleClick, longClick);
  D_Flip_Flop d_ff_3 (.D(and_1_out), .clk(CLK), .Q(clickSimple), .reset(POR));  // open: Qn, preset

  // Other names for the same wires on the sheet: click1 = clickSimple; double = doubleClick; long = longClick

  // Notes on the sheet:
  //   Variables :
  //   double long click -> .    -------- generate both event
  //   edge behaviour :
  //   Choose what type of click :
  //   Stockage infos :
  //   Verif Coherence click1 :
  //   Reset quand fini :
endmodule

module Counter4bit (
  input  CLK,
  input  en,
  input  RST,
  input  load,
  input  decrement,
  input  [3:0] target,
  input  [3:0] preset,
  output overflow,
  output [3:0] value
);

  wire and_1_out, and_2_out, and_3_out, and_4_out, and_5_out, and_6_out, and_7_out, and_8_out, and_9_out,
       and_10_out, and_11_out, and_12_out, and_13_out, and_14_out, and_15_out, and_16_out, and_17_out,
       and_18_out, and_19_out, and_20_out, and_21_out, comparator_1_gt, comparator_2_eq, not_1_out,
       not_2_out, not_3_out, not_4_out, not_5_out, not_6_out, not_7_out, not_8_out, not_9_out, not_10_out,
       not_11_out, not_12_out, not_13_out, not_14_out, not_15_out, not_16_out, not_17_out, or_5_out,
       or_6_out, or_7_out, or_8_out, or_9_out, xor_1_out, xor_2_out, xor_3_out;
  wire [3:0] multiplexer_1_out, multiplexer_2_out, or_1_out;

  not not_1 (not_1_out, en);
  not not_2 (not_2_out, value[0]);
  not not_3 (not_3_out, and_3_out);
  not not_4 (not_4_out, value[1]);
  not not_5 (not_5_out, and_6_out);
  not not_6 (not_6_out, value[2]);
  not not_7 (not_7_out, and_9_out);
  not not_8 (not_8_out, value[3]);
  and and_1 (and_1_out, not_1_out, value[0]);
  and and_2 (and_2_out, en, not_2_out);
  xor xor_1 (xor_1_out, value[0], decrement);
  and and_3 (and_3_out, xor_1_out, en);
  and and_4 (and_4_out, not_3_out, value[1]);
  and and_5 (and_5_out, and_3_out, not_4_out);
  xor xor_2 (xor_2_out, value[1], decrement);
  and and_6 (and_6_out, xor_2_out, and_3_out);
  and and_7 (and_7_out, not_5_out, value[2]);
  and and_8 (and_8_out, and_6_out, not_6_out);
  xor xor_3 (xor_3_out, value[2], decrement);
  and and_9 (and_9_out, xor_3_out, and_6_out);
  and and_10 (and_10_out, not_7_out, value[3]);
  and and_11 (and_11_out, and_9_out, not_8_out);
  or or_1 (or_1_out[0], and_1_out, and_2_out);
  or or_2 (or_1_out[1], and_4_out, and_5_out);
  or or_3 (or_1_out[2], and_7_out, and_8_out);
  or or_4 (or_1_out[3], and_10_out, and_11_out);
  not not_9 (not_9_out, decrement);
  Comparator #(.mode("unsigned"), .width(4)) comparator_1 (
    .a(or_1_out), .b(target), .gt(comparator_1_gt));  // open: eq, lt
  Comparator #(.mode("unsigned"), .width(4)) comparator_2 (
    .a(or_1_out), .b(4'b1111), .eq(comparator_2_eq));  // open: gt, lt
  and and_12 (and_12_out, not_9_out, comparator_1_gt);
  and and_13 (and_13_out, comparator_2_eq, decrement);
  Multiplexer #(.width(4)) multiplexer_1 (.in0(or_1_out), .in1(4'b0000), .out(multiplexer_1_out), .sel(and_12_out));
  Multiplexer #(.width(4)) multiplexer_2 (
    .in0(multiplexer_1_out), .in1(target), .out(multiplexer_2_out), .sel(and_13_out));
  or or_5 (or_5_out, and_12_out, and_13_out);
  D_Flip_Flop d_ff_1 (.D(or_5_out), .clk(CLK), .Q(overflow), .reset(RST));  // open: Qn, preset
  and and_14 (and_14_out, preset[3], load);
  S_R_Flip_Flop s_r_ff_1 (
    .S(multiplexer_2_out[3]), .R(not_10_out), .clk(CLK), .Q(value[3]), .reset(or_6_out), .preset(and_14_out));  // open: Qn
  not not_10 (not_10_out, multiplexer_2_out[3]);
  or or_6 (or_6_out, and_15_out, RST);
  and and_15 (and_15_out, load, not_11_out);
  not not_11 (not_11_out, preset[3]);
  and and_16 (and_16_out, preset[2], load);
  S_R_Flip_Flop s_r_ff_2 (
    .S(multiplexer_2_out[2]), .R(not_12_out), .clk(CLK), .Q(value[2]), .reset(or_7_out), .preset(and_16_out));  // open: Qn
  not not_12 (not_12_out, multiplexer_2_out[2]);
  or or_7 (or_7_out, and_17_out, RST);
  and and_17 (and_17_out, load, not_13_out);
  not not_13 (not_13_out, preset[2]);
  S_R_Flip_Flop s_r_ff_3 (
    .S(multiplexer_2_out[1]), .R(not_14_out), .clk(CLK), .Q(value[1]), .reset(or_8_out), .preset(and_19_out));  // open: Qn
  not not_14 (not_14_out, multiplexer_2_out[1]);
  and and_18 (and_18_out, load, not_15_out);
  and and_19 (and_19_out, preset[1], load);
  or or_8 (or_8_out, and_18_out, RST);
  not not_15 (not_15_out, preset[1]);
  not not_16 (not_16_out, multiplexer_2_out[0]);
  and and_20 (and_20_out, preset[0], load);
  S_R_Flip_Flop s_r_ff_4 (
    .S(multiplexer_2_out[0]), .R(not_16_out), .clk(CLK), .Q(value[0]), .reset(or_9_out), .preset(and_20_out));  // open: Qn
  or or_9 (or_9_out, and_21_out, RST);
  and and_21 (and_21_out, load, not_17_out);
  not not_17 (not_17_out, preset[0]);

  // Notes on the sheet:
  //   Variables :
  //   4 bit adder :
  //   Asynchronously setable register :
endmodule

module Counter6Bit (
  input  CLK,
  input  en,
  input  RST,
  input  load,
  input  decrement,
  input  [5:0] target,
  input  [5:0] preset,
  output overflow,
  output [5:0] value
);

  wire and_1_out, and_2_out, and_3_out, and_4_out, and_5_out, and_6_out, and_7_out, and_8_out, and_9_out,
       and_10_out, and_11_out, and_12_out, and_13_out, and_14_out, and_15_out, and_16_out, and_17_out,
       and_18_out, and_19_out, and_20_out, and_21_out, and_22_out, and_23_out, and_24_out, and_25_out,
       and_26_out, and_27_out, and_28_out, and_29_out, and_30_out, and_31_out, comparator_1_gt,
       comparator_2_eq, not_1_out, not_2_out, not_3_out, not_4_out, not_5_out, not_6_out, not_7_out,
       not_8_out, not_9_out, not_10_out, not_11_out, not_12_out, not_13_out, not_14_out, not_15_out,
       not_16_out, not_17_out, not_18_out, not_19_out, not_20_out, not_21_out, not_22_out, not_23_out,
       not_24_out, not_25_out, or_7_out, or_8_out, or_9_out, or_10_out, or_11_out, or_12_out, or_13_out,
       xor_1_out, xor_2_out, xor_3_out, xor_4_out, xor_5_out;
  wire [5:0] multiplexer_1_out, multiplexer_2_out, or_1_out;

  not not_1 (not_1_out, en);
  not not_2 (not_2_out, value[0]);
  not not_3 (not_3_out, and_3_out);
  not not_4 (not_4_out, value[1]);
  not not_5 (not_5_out, and_6_out);
  not not_6 (not_6_out, value[2]);
  not not_7 (not_7_out, and_9_out);
  not not_8 (not_8_out, value[3]);
  not not_9 (not_9_out, and_12_out);
  not not_10 (not_10_out, value[4]);
  not not_11 (not_11_out, and_15_out);
  not not_12 (not_12_out, value[5]);
  and and_1 (and_1_out, not_1_out, value[0]);
  or or_1 (or_1_out[0], and_1_out, and_2_out);
  and and_2 (and_2_out, en, not_2_out);
  xor xor_1 (xor_1_out, value[0], decrement);
  and and_3 (and_3_out, xor_1_out, en);
  and and_4 (and_4_out, not_3_out, value[1]);
  or or_2 (or_1_out[1], and_4_out, and_5_out);
  and and_5 (and_5_out, and_3_out, not_4_out);
  xor xor_2 (xor_2_out, value[1], decrement);
  and and_6 (and_6_out, xor_2_out, and_3_out);
  and and_7 (and_7_out, not_5_out, value[2]);
  or or_3 (or_1_out[2], and_7_out, and_8_out);
  and and_8 (and_8_out, and_6_out, not_6_out);
  xor xor_3 (xor_3_out, value[2], decrement);
  and and_9 (and_9_out, xor_3_out, and_6_out);
  and and_10 (and_10_out, not_7_out, value[3]);
  or or_4 (or_1_out[3], and_10_out, and_11_out);
  and and_11 (and_11_out, and_9_out, not_8_out);
  xor xor_4 (xor_4_out, value[3], decrement);
  and and_12 (and_12_out, xor_4_out, and_9_out);
  and and_13 (and_13_out, not_9_out, value[4]);
  or or_5 (or_1_out[4], and_13_out, and_14_out);
  and and_14 (and_14_out, and_12_out, not_10_out);
  xor xor_5 (xor_5_out, value[4], decrement);
  and and_15 (and_15_out, xor_5_out, and_12_out);
  and and_16 (and_16_out, not_11_out, value[5]);
  or or_6 (or_1_out[5], and_16_out, and_17_out);
  and and_17 (and_17_out, and_15_out, not_12_out);
  not not_13 (not_13_out, decrement);
  Comparator #(.mode("unsigned"), .width(6)) comparator_1 (
    .a(or_1_out), .b(target), .gt(comparator_1_gt));  // open: eq, lt
  Comparator #(.mode("unsigned"), .width(6)) comparator_2 (
    .a(or_1_out), .b({6{1'b1}}), .eq(comparator_2_eq));  // open: gt, lt
  Multiplexer #(.width(6)) multiplexer_1 (.in0(or_1_out), .in1({6{1'b0}}), .out(multiplexer_1_out), .sel(and_18_out));
  and and_18 (and_18_out, not_13_out, comparator_1_gt);
  and and_19 (and_19_out, comparator_2_eq, decrement);
  Multiplexer #(.width(6)) multiplexer_2 (
    .in0(multiplexer_1_out), .in1(target), .out(multiplexer_2_out), .sel(and_19_out));
  D_Flip_Flop d_ff_1 (.D(or_7_out), .clk(CLK), .Q(overflow), .reset(RST));  // open: Qn, preset
  or or_7 (or_7_out, and_18_out, and_19_out);
  and and_20 (and_20_out, preset[5], load);
  S_R_Flip_Flop s_r_ff_1 (
    .S(multiplexer_2_out[5]), .R(not_14_out), .clk(CLK), .Q(value[5]), .reset(or_8_out), .preset(and_20_out));  // open: Qn
  not not_14 (not_14_out, multiplexer_2_out[5]);
  or or_8 (or_8_out, and_21_out, RST);
  and and_21 (and_21_out, load, not_15_out);
  not not_15 (not_15_out, preset[5]);
  and and_22 (and_22_out, preset[4], load);
  S_R_Flip_Flop s_r_ff_2 (
    .S(multiplexer_2_out[4]), .R(not_16_out), .clk(CLK), .Q(value[4]), .reset(or_9_out), .preset(and_22_out));  // open: Qn
  not not_16 (not_16_out, multiplexer_2_out[4]);
  or or_9 (or_9_out, and_23_out, RST);
  and and_23 (and_23_out, load, not_17_out);
  not not_17 (not_17_out, preset[4]);
  S_R_Flip_Flop s_r_ff_3 (
    .S(multiplexer_2_out[3]), .R(not_18_out), .clk(CLK), .Q(value[3]), .reset(or_10_out), .preset(and_25_out));  // open: Qn
  not not_18 (not_18_out, multiplexer_2_out[3]);
  and and_24 (and_24_out, load, not_19_out);
  and and_25 (and_25_out, preset[3], load);
  or or_10 (or_10_out, and_24_out, RST);
  not not_19 (not_19_out, preset[3]);
  not not_20 (not_20_out, multiplexer_2_out[2]);
  and and_26 (and_26_out, preset[2], load);
  S_R_Flip_Flop s_r_ff_4 (
    .S(multiplexer_2_out[2]), .R(not_20_out), .clk(CLK), .Q(value[2]), .reset(or_11_out), .preset(and_26_out));  // open: Qn
  or or_11 (or_11_out, and_27_out, RST);
  and and_27 (and_27_out, load, not_21_out);
  not not_21 (not_21_out, preset[2]);
  and and_28 (and_28_out, preset[1], load);
  S_R_Flip_Flop s_r_ff_5 (
    .S(multiplexer_2_out[1]), .R(not_22_out), .clk(CLK), .Q(value[1]), .reset(or_12_out), .preset(and_28_out));  // open: Qn
  not not_22 (not_22_out, multiplexer_2_out[1]);
  or or_12 (or_12_out, and_29_out, RST);
  and and_29 (and_29_out, load, not_23_out);
  not not_23 (not_23_out, preset[1]);
  and and_30 (and_30_out, preset[0], load);
  S_R_Flip_Flop s_r_ff_6 (
    .S(multiplexer_2_out[0]), .R(not_24_out), .clk(CLK), .Q(value[0]), .reset(or_13_out), .preset(and_30_out));  // open: Qn
  not not_24 (not_24_out, multiplexer_2_out[0]);
  or or_13 (or_13_out, and_31_out, RST);
  and and_31 (and_31_out, load, not_25_out);
  not not_25 (not_25_out, preset[0]);

  // Notes on the sheet:
  //   Variables :
  //   6 bit adder :
  //   reset logic
  //   Asynchronously setable register :
endmodule

module menuMain (
  input  CW,
  input  CCW,
  input  doubleClick,
  input  longClick,
  input  simpleClick,
  input  POR,
  input  clk,
  input  BUSY,
  output [3:0] selectMenu,
  output [3:0] menuPreview,
  output bipOut
);

  wire and_1_out, and_2_out, d_ff_1_q, d_ff_2_q, d_ff_3_q, not_1_out, not_2_out, not_3_out, not_4_out,
       or_1_out, or_2_out, or_4_out, or_6_out, resetMenuTimeout, timeout;
  wire [31:0] counter_1_q;

  or or_1 (or_1_out, resetMenuTimeout, POR);
  not not_1 (not_1_out, BUSY);
  Counter #(.max('hffffffff), .width(32)) counter_1 (
    .clr(or_1_out), .load(1'b0), .up(1'b1), .count(not_1_out), .clk(clk), .Q(counter_1_q));  // open: D, carry
  Comparator #(.width(32)) comparator_1 (.a(32'hf4240), .b(counter_1_q), .eq(timeout));  // open: gt, lt
  D_Flip_Flop d_ff_1 (.D(or_2_out), .clk(clk), .Q(d_ff_1_q), .reset(POR));  // open: Qn, preset
  or or_2 (or_2_out, CW, CCW);
  D_Flip_Flop d_ff_2 (.D(timeout), .clk(clk), .Q(d_ff_2_q), .reset(POR));  // open: Qn, preset
  not not_2 (not_2_out, BUSY);
  not not_3 (not_3_out, or_2_out);
  or or_3 (resetMenuTimeout, CW, CCW, doubleClick, longClick, simpleClick, d_ff_2_q);
  or or_4 (or_4_out, timeout, POR);
  and and_1 (and_1_out, not_3_out, d_ff_1_q);
  Counter #(.max('h7), .width(4)) counter_2 (
    .clr(or_4_out), .load(1'b0), .up(CW), .count(not_2_out), .clk(and_1_out), .Q(menuPreview));  // open: D, carry
  or or_5 (bipOut, and_1_out, simpleClick);
  D_Flip_Flop d_ff_3 (.D(BUSY), .clk(clk), .Q(d_ff_3_q), .reset(POR));  // open: Qn, preset
  not not_4 (not_4_out, BUSY);
  Register #(.width(4)) register_1 (.D(menuPreview), .en(simpleClick), .clk(clk), .Q(selectMenu), .clr(or_6_out));
  and and_2 (and_2_out, not_4_out, d_ff_3_q);
  or or_6 (or_6_out, and_2_out, timeout, POR);

  // Other names for the same wires on the sheet: click = simpleClick; clickDouble = doubleClick;
  //   clickLong = longClick; codeMenu[3:0] = selectMenu; codeMenuPreview[3:0] = menuPreview

  // Notes on the sheet:
  //   Variables :
  //   BUSY input is high if any submodule is busy
  //   10 sec
  //   Falling edge detector so that the up/down pin settle before validation
  //   Reset the menu to the clock if no key is pressed for more than X seconds :
  //   Counter Menu Rotatif :
  //   0 -> Hour
  //   1 -> Set Sunrise
  //   2 -> Set Hour
  //   3 -> Set Hourglass
  //   4 -> Hourglass
  //   5 -> Chrono
  //   6 -> Set ringtone
  //   7 -> Set display
  //   Detecteur de flanc descendant :
  //   Menu selector :
  //   when a click occur the menu choice is validated
  //   one (clock) and accept command again
  //   each submodule check if that code is their and activate if yes
  //   each submodule maintain BUSY at TRUE as long as they are active
  //   once done they release BUSY and this circuit reset the code to the default
endmodule

module menuTitleHandler (
  input  CLK,
  input  POR,
  input  alarmHorloge,
  input  alarmTimer,
  input  setCstmChar,
  input  [5:0] cstmChar,
  input  [3:0] cstmCharADR,
  input  [3:0] menuSelected,
  input  [3:0] menuSelectPreview,
  input  displayCM,
  output menudisplayOveride,
  output alarmOveride,
  output [35:0] menuTitle,
  output [35:0] alarmMessage,
  output simpleAlarm,
  output customAlarm
);

  wire and_1_out, and_2_out, clock_1_out, comparator_1_eq, comparator_2_eq, comparator_3_eq, d_ff_1_qn,
       d_ff_2_qn, not_2_out, or_2_out, or_3_out, or_5_out, or_6_out, or_7_out, or_8_out, refreshDisplay,
       resetAlarmDuration, triggerHorloge, triggerTimer;
  wire [3:0] messageRegister_1_lengthmessage, multiplexer_1_out, multiplexer_2_out, register_1_q;
  wire [4:0] counter_1_q;
  wire [5:0] messageRegister_1_l1, messageRegister_1_l2, messageRegister_1_l3, messageRegister_1_l4,
       messageRegister_1_l5, messageRegister_1_l6, messageRegister_1_l7, messageRegister_1_l8,
       messageRegister_1_l9, messageRegister_1_l10, messageRegister_1_l11, messageRegister_1_l12,
       messageRegister_1_l13, messageRegister_1_l14;

  or or_1 (alarmOveride, triggerHorloge, triggerTimer);
  Comparator #(.width(4)) comparator_1 (.a(menuSelected), .b(menuSelectPreview), .eq(comparator_1_eq));  // open: gt, lt
  Multiplexer #(.width(4)) multiplexer_1 (.in0(4'b1111), .in1(4'b1110), .out(multiplexer_1_out), .sel(triggerTimer));
  not not_1 (menudisplayOveride, comparator_1_eq);
  Multiplexer #(.width(4)) multiplexer_2 (
    .in0(menuSelectPreview), .in1(multiplexer_1_out), .out(multiplexer_2_out), .sel(or_2_out));
  or or_2 (or_2_out, triggerHorloge, displayCM, triggerTimer);
  or or_3 (or_3_out, alarmHorloge, displayCM);
  Register #(.width(4)) register_1 (
    .D(menuSelectPreview), .en(menudisplayOveride), .clk(CLK), .Q(register_1_q), .clr(POR));
  messageRegister messageRegister_1 (
    .numMessage(multiplexer_2_out), .POR(POR), .CLK(CLK), .set(setCstmChar), .ADDR(cstmCharADR),
    .CHAR(cstmChar), .lengthMessage(messageRegister_1_lengthmessage), .L1(messageRegister_1_l1),
    .L2(messageRegister_1_l2), .L3(messageRegister_1_l3), .L4(messageRegister_1_l4),
    .L5(messageRegister_1_l5), .L6(messageRegister_1_l6), .L7(messageRegister_1_l7),
    .L8(messageRegister_1_l8), .L9(messageRegister_1_l9), .L10(messageRegister_1_l10),
    .L11(messageRegister_1_l11), .L12(messageRegister_1_l12), .L13(messageRegister_1_l13),
    .L14(messageRegister_1_l14));
  D_Flip_Flop d_ff_1 (.D(or_3_out), .clk(CLK), .Qn(d_ff_1_qn), .reset(POR));  // open: Q, preset
  D_Flip_Flop d_ff_2 (.D(alarmTimer), .clk(CLK), .Qn(d_ff_2_qn), .reset(POR));  // open: Q, preset
  and and_1 (and_1_out, or_3_out, d_ff_1_qn);
  and and_2 (and_2_out, alarmTimer, d_ff_2_qn);
  not not_2 (not_2_out, comparator_2_eq);
  Comparator #(.width(4)) comparator_2 (.a(menuSelectPreview), .b(register_1_q), .eq(comparator_2_eq));  // open: gt, lt
  or or_4 (refreshDisplay, and_1_out, and_2_out, not_2_out);
  messageCycleShifter messageCycleShifter_1 (
    .POR(POR), .load(refreshDisplay), .CLK(CLK), .mesLength(messageRegister_1_lengthmessage),
    .L1(messageRegister_1_l1), .L2(messageRegister_1_l2), .L3(messageRegister_1_l3),
    .L4(messageRegister_1_l4), .L5(messageRegister_1_l5), .L6(messageRegister_1_l6),
    .L7(messageRegister_1_l7), .L8(messageRegister_1_l8), .L9(messageRegister_1_l9),
    .L10(messageRegister_1_l10), .L11(messageRegister_1_l11), .L12(messageRegister_1_l12),
    .L13(messageRegister_1_l13), .L14(messageRegister_1_l14), .displayOut(alarmMessage));
  or or_5 (or_5_out, resetAlarmDuration, POR);
  or or_6 (or_6_out, triggerHorloge, triggerTimer);
  Counter #(.max('h1f), .width(5)) counter_1 (
    .clr(or_5_out), .load(1'b0), .up(1'b1), .count(or_6_out), .clk(clock_1_out), .Q(counter_1_q));  // open: D, carry
  Clock #(.lowDuration(100000)) clock_1 (.out(clock_1_out));
  S_R_Flip_Flop s_r_ff_1 (.S(alarmHorloge), .clk(CLK), .Q(triggerHorloge), .reset(or_7_out));  // open: R, Qn, preset
  or or_7 (or_7_out, POR, resetAlarmDuration);
  and and_3 (simpleAlarm, clock_1_out, triggerTimer);
  Comparator #(.mode("unsigned"), .width(5)) comparator_3 (
    .a(5'b10100), .b(counter_1_q), .eq(comparator_3_eq));  // open: gt, lt
  S_R_Flip_Flop s_r_ff_2 (.S(alarmTimer), .clk(CLK), .Q(triggerTimer), .reset(or_8_out));  // open: R, Qn, preset
  D_Flip_Flop d_ff_3 (.D(comparator_3_eq), .clk(CLK), .Q(resetAlarmDuration), .reset(POR));  // open: Qn, preset
  or or_8 (or_8_out, POR, resetAlarmDuration);

  assign customAlarm = alarmHorloge;
  assign menuTitle = alarmMessage;

  // Other names for the same wires on the sheet: alarmDisplayOveride = alarmOveride; menuSelect[3:0] = menuSelected

  // Notes on the sheet:
  //   Variables :
  //   Pass the alarm signal to the music box :
  //   Display the alarm message instead of the time or the menu
  //   Maintain the display mux on the menu title :
  //   display the message :
  //   Refresh the screen for each menu selected :
  //   1 sec clock
  //   Timeout generator :
  //   Keep the alarm condition active for 20 secs :
  //   send each second an impulse that will be fed to the double bip
  //   but ony for the simple timer, the other play the custom melody instead
  //   The sound and animation are played for 20 secs :
endmodule

module menuIdle (
  input  clickSimple,
  input  CLK,
  input  POR,
  input  [3:0] selectMenu,
  input  [3:0] ADDR,
  output BUSY
);

  wire and_1_out, and_2_out, en, mem1, not_1_out, not_2_out;

  Comparator #(.width(4)) comparator_1 (.a(selectMenu), .b(ADDR), .eq(en));  // open: gt, lt
  D_Flip_Flop d_ff_1 (.D(BUSY), .clk(CLK), .Q(mem1), .reset(POR));  // open: Qn, preset
  not not_1 (not_1_out, clickSimple);
  not not_2 (not_2_out, clickSimple);
  and and_1 (and_1_out, en, not_1_out);
  and and_2 (and_2_out, not_2_out, mem1);
  or or_1 (BUSY, and_1_out, and_2_out);

  // Other names for the same wires on the sheet: codeMenu[3:0] = selectMenu; mem1Out = BUSY

  // Notes on the sheet:
  //   Variables :
  //   On/Off :
  //   Etat de la machine :
  //   Machine Etat :
endmodule

module menuChrono (
  input  clickSimple,
  input  clickDouble,
  input  clickLong,
  input  CLK,
  input  POR,
  input  [3:0] selectMenu,
  input  [3:0] ADDR,
  output BUSY,
  output chronoReset,
  output chronoEnabled
);

  wire and_1_out, and_2_out, and_3_out, and_4_out, and_5_out, and_6_out, and_7_out, and_8_out, and_9_out,
       and_10_out, and_11_out, and_12_out, and_13_out, and_14_out, and_15_out, chronoEn, en, mem1, mem1Out,
       mem2Out, not_1_out, not_2_out, not_3_out, not_4_out, not_5_out, resetAllowed;

  not not_1 (not_1_out, en);
  not not_2 (not_2_out, clickLong);
  not not_3 (not_3_out, clickSimple);
  not not_4 (not_4_out, mem1);
  not not_5 (not_5_out, chronoEnabled);
  and and_1 (and_1_out, not_2_out, mem1);
  and and_2 (and_2_out, en, not_2_out);
  and and_3 (and_3_out, not_1_out, not_3_out, chronoEnabled);
  and and_4 (and_4_out, not_2_out, not_3_out, chronoEnabled);
  and and_5 (and_5_out, not_2_out, not_4_out, chronoEnabled);
  and and_6 (and_6_out, not_2_out, clickSimple, mem1, not_5_out);
  and and_7 (and_7_out, not_2_out, mem1);
  and and_8 (and_8_out, en, not_2_out);
  and and_9 (and_9_out, not_1_out, not_3_out, chronoEnabled);
  and and_10 (and_10_out, not_2_out, not_3_out, chronoEnabled);
  and and_11 (and_11_out, not_2_out, not_4_out, chronoEnabled);
  and and_12 (and_12_out, not_2_out, clickSimple, mem1, not_5_out);
  and and_13 (and_13_out, not_2_out, mem1);
  and and_14 (and_14_out, en, not_2_out);
  or or_1 (mem1Out, and_1_out, and_2_out);
  or or_2 (mem2Out, and_3_out, and_4_out, and_5_out, and_6_out);
  or or_3 (BUSY, and_7_out, and_8_out);
  or or_4 (chronoEn, and_9_out, and_10_out, and_11_out, and_12_out);
  or or_5 (resetAllowed, and_13_out, and_14_out);
  Comparator #(.width(4)) comparator_1 (.a(selectMenu), .b(ADDR), .eq(en));  // open: gt, lt
  D_Flip_Flop d_ff_1 (.D(mem1Out), .clk(CLK), .Q(mem1), .reset(POR));  // open: Qn, preset
  and and_15 (and_15_out, clickDouble, resetAllowed);
  D_Flip_Flop d_ff_2 (.D(mem2Out), .clk(CLK), .Q(chronoEnabled), .reset(POR));  // open: Qn, preset
  D_Flip_Flop d_ff_3 (.D(and_15_out), .clk(CLK), .Q(chronoReset), .reset(POR));  // open: Qn, preset

  // Other names for the same wires on the sheet: codeMenu[3:0] = selectMenu; mem2 = chronoEnabled

  // Notes on the sheet:
  //   Variables :
  //   Machine Etat :
  //   On/Off :
  //    menu active :
  //   Etat de la machine :
  //   Chrono reset if doubleClick :
  //   chrono counting :
endmodule

module menuSetTime (
  input  clickSimple,
  input  clickDouble,
  input  clickLong,
  input  CCW,
  input  CW,
  input  CLK,
  input  POR,
  input  [3:0] selectMenu,
  input  [3:0] ADDR,
  output BUSY,
  output [1:0] stateHMS,
  output [3:0] currentHourH,
  output [3:0] currentHourL,
  output [3:0] currentMinuteH,
  output [3:0] currentMinuteL,
  output [3:0] currentSecondH,
  output [3:0] currentSecondL
);

  wire and_1_out, and_2_out, and_3_out, and_4_out, and_5_out, and_6_out, and_7_out, and_8_out, and_9_out,
       and_10_out, and_11_out, and_12_out, d_ff_3_q, d_ff_4_q, d_ff_5_q, en, enH, enM, enS, mem1Out, mem2Out,
       not_1_out, not_2_out, not_3_out, not_4_out, not_5_out, not_6_out, not_7_out, or_4_out, or_5_out,
       or_6_out;
  wire [5:0] counter_1_q, counter_2_q, counter_3_q;

  not not_1 (not_1_out, clickSimple);
  not not_2 (not_2_out, clickLong);
  not not_3 (not_3_out, stateHMS[1]);
  not not_4 (not_4_out, stateHMS[0]);
  and and_1 (and_1_out, not_1_out, not_2_out, stateHMS[1]);
  and and_2 (and_2_out, not_2_out, stateHMS[1], not_4_out);
  and and_3 (and_3_out, clickSimple, not_2_out, not_3_out, stateHMS[0]);
  and and_4 (and_4_out, not_1_out, not_2_out, stateHMS[0]);
  and and_5 (and_5_out, clickSimple, not_2_out, stateHMS[1]);
  and and_6 (and_6_out, en, not_2_out, not_3_out, not_4_out);
  and and_7 (and_7_out, not_2_out, stateHMS[0]);
  and and_8 (and_8_out, not_2_out, stateHMS[1]);
  and and_9 (and_9_out, en, not_2_out);
  or or_1 (mem1Out, and_1_out, and_2_out, and_3_out);
  or or_2 (mem2Out, and_4_out, and_5_out, and_6_out);
  or or_3 (BUSY, and_7_out, and_8_out, and_9_out);
  Comparator #(.width(4)) comparator_1 (.a(selectMenu), .b(ADDR), .eq(en));  // open: gt, lt
  D_Flip_Flop d_ff_1 (.D(mem1Out), .clk(CLK), .Q(stateHMS[1]), .reset(POR));  // open: Qn, preset
  Decoder #(.select(2)) decoder_1 (.out1(enH), .out2(enM), .out3(enS), .sel(stateHMS), .en(1'b1));  // open: out0
  D_Flip_Flop d_ff_2 (.D(mem2Out), .clk(CLK), .Q(stateHMS[0]), .reset(POR));  // open: Qn, preset
  D_Flip_Flop d_ff_3 (.D(or_4_out), .clk(CLK), .Q(d_ff_3_q), .reset(POR));  // open: Qn, preset
  or or_4 (or_4_out, CW, CCW);
  D_Flip_Flop d_ff_4 (.D(or_5_out), .clk(CLK), .Q(d_ff_4_q), .reset(POR));  // open: Qn, preset
  or or_5 (or_5_out, CW, CCW);
  D_Flip_Flop d_ff_5 (.D(or_6_out), .clk(CLK), .Q(d_ff_5_q), .reset(POR));  // open: Qn, preset
  or or_6 (or_6_out, CW, CCW);
  not not_5 (not_5_out, or_4_out);
  not not_6 (not_6_out, or_5_out);
  not not_7 (not_7_out, or_6_out);
  and and_10 (and_10_out, not_5_out, d_ff_3_q);
  and and_11 (and_11_out, not_6_out, d_ff_4_q);
  and and_12 (and_12_out, not_7_out, d_ff_5_q);
  Counter #(.max('h17), .width(6)) counter_1 (
    .clr(POR), .load(1'b0), .up(CW), .count(enH), .clk(and_10_out), .Q(counter_1_q));  // open: D, carry
  Counter #(.max('h3b), .width(6)) counter_2 (
    .clr(POR), .load(1'b0), .up(CW), .count(enM), .clk(and_11_out), .Q(counter_2_q));  // open: D, carry
  Counter #(.max('h3b), .width(6)) counter_3 (
    .clr(POR), .load(1'b0), .up(CW), .count(enS), .clk(and_12_out), .Q(counter_3_q));  // open: D, carry
  // Binary_to_BCD_converter #(.binvalue(6)) binary_to_bcd_converter_1: pin names not known; wires that end beside it: counter_1_q, currentHourH, currentHourL
  // Binary_to_BCD_converter #(.binvalue(6)) binary_to_bcd_converter_2: pin names not known; wires that end beside it: counter_2_q, currentMinuteH, currentMinuteL
  // Binary_to_BCD_converter #(.binvalue(6)) binary_to_bcd_converter_3: pin names not known; wires that end beside it: counter_3_q, currentSecondH, currentSecondL

  // Other names for the same wires on the sheet: codeMenu[3:0] = selectMenu; mem2 = stateHMS[0];
  //   state[1:0] = stateHMS; mem1 = stateHMS[1]

  // Notes on the sheet:
  //   Variables :
  //   Anti horaire
  //   Horaire
  //   Machine Etat :
  //   On/Off :
  //   Etat de la machine :
  //   Aiguillage set Heure/Min/Sec :
  //   Counter Hours/Min/Sec :
  //   counter for hours :
  //   counter for minutes :
  //   couter for seconds :
endmodule

module menuSetMelody (
  input  clickSimple,
  input  clickDouble,
  input  clickLong,
  input  CCW,
  input  CW,
  input  CLK,
  input  POR,
  input  [3:0] selectMenu,
  input  [3:0] ADDR,
  output BUSY,
  output PLAY,
  output REC,
  output [4:0] adress,
  output [4:0] tone,
  output [3:0] BPM,
  output [35:0] displayOut
);

  wire and_1_out, and_2_out, and_3_out, and_4_out, and_5_out, and_6_out, and_7_out, and_8_out, and_9_out,
       and_10_out, and_11_out, and_12_out, and_13_out, and_14_out, and_17_out, and_18_out, and_19_out,
       BUSYin, d_ff_4_q, d_ff_5_q, d_ff_7_q, en, enA, enB, enN, mem1, mem1Out, mem2, mem2Out, mem3, mem3Out,
       not_1_out, not_2_out, not_3_out, not_4_out, not_5_out, not_6_out, not_7_out, not_8_out, or_5_out,
       or_6_out, or_7_out;
  wire [4:0] adder_1_out;
  wire [6:0] adder_2_out, multiplier_1_out;
  wire [27:18] BPMDisplay;
  wire [33:24] positionDisplay;
  wire [35:0] toneDisplay;

  not not_1 (not_1_out, clickSimple);
  not not_2 (not_2_out, clickLong);
  not not_3 (not_3_out, mem1);
  not not_4 (not_4_out, mem2);
  not not_5 (not_5_out, mem3);
  Comparator #(.width(4)) comparator_1 (.a(selectMenu), .b(ADDR), .eq(en));  // open: gt, lt
  and and_1 (and_1_out, not_1_out, not_2_out, mem1, not_4_out, not_5_out);
  or or_1 (mem1Out, and_1_out, and_2_out);
  and and_2 (and_2_out, clickSimple, not_2_out, not_3_out, mem2, mem3);
  and and_3 (and_3_out, not_1_out, not_2_out, not_3_out, mem2);
  and and_4 (and_4_out, not_2_out, not_3_out, mem2, not_5_out);
  or or_2 (mem2Out, and_3_out, and_4_out, and_5_out);
  and and_5 (and_5_out, clickSimple, not_2_out, not_3_out, not_4_out, mem3);
  and and_6 (and_6_out, not_1_out, not_2_out, not_3_out, mem3);
  and and_7 (and_7_out, clickSimple, not_2_out, not_3_out, mem2, not_5_out);
  and and_8 (and_8_out, clickSimple, not_2_out, mem1, not_4_out, not_5_out);
  and and_9 (and_9_out, en, not_2_out, not_3_out, not_4_out, not_5_out);
  and and_10 (and_10_out, en, clickSimple, not_2_out, not_4_out, not_5_out);
  and and_11 (and_11_out, not_2_out, not_3_out, mem3);
  and and_12 (and_12_out, not_2_out, not_3_out, mem2);
  and and_13 (and_13_out, not_2_out, mem1, not_4_out, not_5_out);
  and and_14 (and_14_out, en, not_2_out, not_3_out);
  and and_15 (PLAY, clickSimple, not_2_out, not_3_out, mem2, mem3);
  and and_16 (REC, clickSimple, not_2_out, not_3_out, mem2, mem3);
  or or_3 (mem3Out, and_6_out, and_7_out, and_8_out, and_9_out, and_10_out);
  or or_4 (BUSYin, and_11_out, and_12_out, and_13_out, and_14_out);
  D_Flip_Flop d_ff_1 (.D(mem1Out), .clk(CLK), .Q(mem1), .reset(POR));  // open: Qn, preset
  Multiplexer #(.select(2), .width(36)) multiplexer_1 (
    .in0(36'h394255493), .in1({2'b00, positionDisplay[33:30], 2'b00, positionDisplay[27:24], 24'h419597}),
    .in2(toneDisplay), .in3({{8{1'b0}}, BPMDisplay[27:24], 2'b00, BPMDisplay[21:18], 18'h165da}),
    .out(displayOut), .sel({mem2, mem3}));
  D_Flip_Flop d_ff_2 (.D(mem2Out), .clk(CLK), .Q(mem2), .reset(POR));  // open: Qn, preset
  D_Flip_Flop d_ff_3 (.D(BUSYin), .clk(CLK), .Q(BUSY), .reset(POR));  // open: Qn, preset
  D_Flip_Flop d_ff_4 (.D(or_5_out), .clk(CLK), .Q(d_ff_4_q), .reset(POR));  // open: Qn, preset
  or or_5 (or_5_out, CW, PLAY, CCW);
  or or_6 (or_6_out, CW, CCW);
  D_Flip_Flop d_ff_5 (.D(or_7_out), .clk(CLK), .Q(d_ff_5_q), .reset(POR));  // open: Qn, preset
  or or_7 (or_7_out, CW, CCW);
  D_Flip_Flop d_ff_6 (.D(mem3Out), .clk(CLK), .Q(mem3), .reset(POR));  // open: Qn, preset
  not not_6 (not_6_out, or_5_out);
  not not_7 (not_7_out, or_6_out);
  D_Flip_Flop d_ff_7 (.D(or_6_out), .clk(CLK), .Q(d_ff_7_q), .reset(POR));  // open: Qn, preset
  not not_8 (not_8_out, or_7_out);
  Counter #(.max('h1f), .width(5)) counter_1 (
    .clr(POR), .load(1'b0), .up(CW), .count(enA), .clk(and_17_out), .Q(adress));  // open: D, carry
  and and_17 (and_17_out, not_6_out, d_ff_4_q);
  Counter #(.max('h1f), .width(5)) counter_2 (
    .clr(POR), .load(1'b0), .up(CW), .count(enN), .clk(and_18_out), .Q(tone));  // open: D, carry
  and and_18 (and_18_out, not_7_out, d_ff_7_q);
  Counter #(.max('hf), .width(4)) counter_3 (
    .clr(POR), .load(1'b0), .up(CW), .count(enB), .clk(and_19_out), .Q(BPM));  // open: D, carry
  and and_19 (and_19_out, not_8_out, d_ff_5_q);
  Decoder #(.select(2)) decoder_1 (.out1(enA), .out2(enN), .out3(enB), .sel({mem2, mem3}), .en(1'b1));  // open: out0
  Adder #(.width(5)) adder_1 (.a(adress), .b(5'b00001), .out(adder_1_out));  // open: cin, cout
  Multiplier #(.width(7)) multiplier_1 (.a({3'b000, BPM}), .b(7'b0000101), .out(multiplier_1_out));  // open: cin, cout
  // Binary_to_BCD_converter #(.binvalue(5)) binary_to_bcd_converter_1: pin names not known; wires that end beside it: adder_1_out, positionDisplay[27:24], positionDisplay[33:30]
  Adder #(.width(7)) adder_2 (.a(multiplier_1_out), .b(7'b0000101), .out(adder_2_out));  // open: cin, cout
  // Binary_to_BCD_converter #(.binvalue(7)) binary_to_bcd_converter_2: pin names not known; wires that end beside it: adder_2_out, BPMDisplay[21:18], BPMDisplay[27:24]
  Multiplexer #(.select(5), .width(36)) multiplexer_2 (
    .in0(36'h695394499), .in1(36'h90410294), .in2(36'h8d410294), .in3(36'h90410499), .in4(36'hd041058d),
    .in5(36'hcd41058d), .in6(36'hd0410398), .in7(36'hcd410398), .in8(36'hd0410495), .in9(36'hd041028f),
    .in10(36'hd0414599), .in11(36'hcd414599), .in12(36'hd0410294), .in13(36'hcd410294), .in14(36'hd0410499),
    .in15(36'h11041058d), .in16(36'h10d41058d), .in17(36'h110410398), .in18(36'h10d410398),
    .in19(36'h110410495), .in20(36'h11041028f), .in21(36'h10d41028f), .in22(36'h110414599),
    .in23(36'h10d414599), .in24(36'h110410294), .in25(36'h10d410294), .in26(36'h110410499),
    .in27(36'h15041058d), .in28(36'h10d41058d), .in29(36'h150410398), .in30(36'h14d410398),
    .in31(36'h150410495), .out(toneDisplay), .sel(tone));

  // Other names for the same wires on the sheet: setBPM[3:0] = BPM; addrNote[4:0] = adress;
  //   codeMenu[3:0] = selectMenu; setNote[4:0] = tone

  // Notes on the sheet:
  //   Variables :
  //   Anti horaire
  //   Horaire
  //   Machine Etat :
  //   On/Off :
  //   Aiguillage affichage sous menu :
  //   Etat de la machine :
  //   Counter Position/Tone/Duration :
  //   position
  //   Aiguillage set Heure/Min/Sec :
  //   tone
  //   duration
  //   convert 0-15 to 5-20 in DCB
  //   fa4=698
  //   r = 18
  //   o = 16
  //   L = 14
  //   i = 12
  //   silent
  //   la2=220
  //   la#2=233
  //   si2=246
  //   do3=261
  //   do#3=277
  //   ré3=293
  //   ré3#=311
  //   mi3=329
  //   fa3=349
  //   sol3=370
  //   sol#3=415
  //   la3=440
  //   la#3=466
  //   si3=494
  //   do4=523
  //   do#4=554
  //   ré4=587
  //   ré#4=622
  //   mi4=659
  //   fa#4=740
  //   sol4=784
  //   sol#4=830
  //   la4=880
  //   la#4=932
  //   si4=988
  //   do5=1046
  //   do#5=1108
  //   ré5=1174
  //   ré#5=1244
  //   mi5=1397
  //   Display Render :
  //   n = 15
  //   s = 19
  //   Jingle
  //   Pos XX
  //   TPoXXX
  //   Display Note Title :
  //   16 increment, range : 50-800 ms
endmodule

module menuSetMessage (
  input  POR,
  input  CLK,
  input  ClickSimple,
  input  LongClick,
  input  CW,
  input  CCW,
  input  [3:0] selectMenu,
  input  [3:0] ADRESS,
  input  [35:0] displayIn,
  output BUSY,
  output displayCM,
  output setChar,
  output [5:0] char,
  output [3:0] charPos,
  output [35:0] displayOut
);

  wire and_1_out, and_2_out, and_3_out, and_4_out, and_5_out, and_6_out, and_7_out, and_8_out, and_9_out,
       and_12_out, and_13_out, comparator_2_eq, comparator_3_eq, d_ff_3_q, d_ff_4_q, en, mem1, mem1Out, mem2,
       mem2Out, not_1_out, not_2_out, not_3_out, not_4_out, not_5_out, not_6_out, or_4_out, or_5_out;
  wire [3:0] adder_1_out, binary_to_bcd_converter_1_p2, binary_to_bcd_converter_1_p3;

  not not_1 (not_1_out, ClickSimple);
  not not_2 (not_2_out, LongClick);
  not not_3 (not_3_out, mem1);
  not not_4 (not_4_out, mem2);
  and and_1 (and_1_out, en, not_1_out, not_2_out, mem1);
  and and_2 (and_2_out, en, not_2_out, mem1, not_4_out);
  or or_1 (mem1Out, and_1_out, and_2_out, and_3_out);
  and and_3 (and_3_out, en, ClickSimple, not_2_out, not_3_out, mem2);
  and and_4 (and_4_out, en, not_1_out, not_2_out, not_3_out);
  and and_5 (and_5_out, en, not_2_out, mem1, mem2);
  or or_2 (mem2Out, and_4_out, and_5_out, and_6_out);
  and and_6 (and_6_out, en, ClickSimple, not_2_out, not_4_out);
  and and_7 (and_7_out, not_1_out, not_2_out, mem2);
  and and_8 (and_8_out, not_1_out, not_2_out, mem1);
  or or_3 (BUSY, and_7_out, and_8_out, and_9_out);
  and and_9 (and_9_out, en, not_2_out);
  Comparator #(.width(4)) comparator_1 (.a(selectMenu), .b(ADRESS), .eq(en));  // open: gt, lt
  D_Flip_Flop d_ff_1 (.D(mem1Out), .clk(CLK), .Q(mem1), .reset(POR));  // open: Qn, preset
  and and_10 (displayCM, mem2, mem1);
  and and_11 (setChar, BUSY, ClickSimple);
  D_Flip_Flop d_ff_2 (.D(mem2Out), .clk(CLK), .Q(mem2), .reset(POR));  // open: Qn, preset
  D_Flip_Flop d_ff_3 (.D(or_4_out), .clk(CLK), .Q(d_ff_3_q), .reset(POR));  // open: Qn, preset
  or or_4 (or_4_out, CW, displayCM, CCW);
  D_Flip_Flop d_ff_4 (.D(or_5_out), .clk(CLK), .Q(d_ff_4_q), .reset(POR));  // open: Qn, preset
  or or_5 (or_5_out, CW, CCW);
  Comparator #(.width(2)) comparator_2 (.a({mem1, mem2}), .b(2'b01), .eq(comparator_2_eq));  // open: gt, lt
  not not_5 (not_5_out, or_4_out);
  and and_12 (and_12_out, not_5_out, d_ff_3_q);
  Comparator #(.width(2)) comparator_3 (.a({mem1, mem2}), .b(2'b10), .eq(comparator_3_eq));  // open: gt, lt
  not not_6 (not_6_out, or_5_out);
  and and_13 (and_13_out, not_6_out, d_ff_4_q);
  Adder #(.width(4)) adder_1 (.a(charPos), .b(4'b0001), .out(adder_1_out));  // open: cin, cout
  // Binary_to_BCD_converter #(.binvalue(4)) binary_to_bcd_converter_1: pin names not known; wires that end beside it: adder_1_out, binary_to_bcd_converter_1_p2, binary_to_bcd_converter_1_p3
  Counter4bit Counter4bit_1 (
    .value(charPos), .en(comparator_2_eq), .RST(POR), .load(1'b0), .decrement(CCW), .target(4'b1101),
    .preset(4'b0000), .CLK(and_12_out));  // open: overflow
  Counter6Bit Counter6Bit_1 (
    .value(char), .en(comparator_3_eq), .RST(POR), .load(1'b0), .decrement(CCW), .target(6'b100000),
    .preset({6{1'b0}}), .CLK(and_13_out));  // open: overflow
  Multiplexer #(.select(2), .width(36)) multiplexer_1 (
    .in1({2'b00, binary_to_bcd_converter_1_p3, 2'b00, binary_to_bcd_converter_1_p2, 24'h419017}),
    .in2({char, 30'h1061a394}), .in3(displayIn), .out(displayOut), .sel({mem1, mem2}));  // open: in0

  // Other names for the same wires on the sheet: lettre[5:0] = char; codeMenu[3:0] = selectMenu;
  //   requestCustomMessage = displayCM

  // Notes on the sheet:
  //   Variables :
  //   Machine Etat :
  //   On/Off :
  //   Etat de la machine :
  //   Conditions de sortie :
  //   Counter Position/Lettre :
  //   Etat 01 :
  //   Position
  //   Etat 10 :
  //   Lettre
  //   Aiguillage affichage :
endmodule

module clockDCB (
  input  setTime,
  input  reverseCount,
  input  clockInput,
  input  enCount,
  input  POR,
  input  [3:0] setHourH,
  input  [3:0] setHourL,
  input  [3:0] setMinuteH,
  input  [3:0] setMinuteL,
  input  [3:0] setSecondH,
  input  [3:0] setSecondL,
  output [5:0] hourH,
  output [5:0] hourL,
  output [5:0] minuteH,
  output [5:0] minuteL,
  output [5:0] secondH,
  output [5:0] secondL
);

  wire comparator_1_gt, comparator_2_gt, comparator_3_gt, comparator_4_gt, comparator_5_gt, comparator_6_gt,
       comparator_7_gt, comparator_8_gt, comparator_9_gt, comparator_10_gt, comparator_11_gt,
       comparator_12_gt, comparator_13_gt, comparator_14_gt, comparator_15_gt, comparator_16_gt,
       comparator_17_gt, comparator_18_gt, comparator_19_gt, comparator_20_gt, comparator_21_gt,
       comparator_22_gt, comparator_23_gt, not_1_out, not_2_out, not_3_out;
  wire [4:0] multiplexer_1_out, multiplexer_2_out, multiplexer_3_out, multiplexer_4_out, multiplexer_5_out,
       multiplexer_6_out, multiplexer_7_out, multiplexer_8_out, multiplexer_9_out, multiplexer_10_out,
       multiplexer_11_out, multiplexer_12_out, multiplexer_13_out, multiplexer_14_out, multiplexer_15_out,
       multiplexer_16_out, multiplexer_17_out, multiplexer_18_out, multiplexer_19_out, multiplexer_20_out,
       multiplexer_21_out, multiplexer_22_out, multiplexer_23_out;
  wire [5:0] adder_1_out, adder_2_out, adder_3_out, adder_6_out, counter_3_q, multiplier_1_out,
       multiplier_2_out, multiplier_3_out, multiplier_6_out;
  wire [11:0] counter_2_q, minAndSec, multiplier_5_out;
  wire [16:0] adder_4_out, counter_1_q, multiplier_4_out;

  // Probe on hourH[3:0]
  // Probe on hourL[3:0]
  // Probe on minuteH[3:0]
  // Probe on minuteL[3:0]
  // Probe on secondH[3:0]
  // Probe on secondL[3:0]
  Multiplier #(.width(6)) multiplier_1 (
    .a({2'b00, setHourH}), .b(6'b001010), .out(multiplier_1_out));  // open: cin, cout
  Multiplier #(.width(6)) multiplier_2 (
    .a({2'b00, setMinuteH}), .b(6'b001010), .out(multiplier_2_out));  // open: cin, cout
  Multiplier #(.width(6)) multiplier_3 (
    .a({2'b00, setSecondH}), .b(6'b001010), .out(multiplier_3_out));  // open: cin, cout
  Adder #(.width(6)) adder_1 (.a(multiplier_1_out), .b({2'b00, setHourL}), .out(adder_1_out));  // open: cin, cout
  Adder #(.width(6)) adder_2 (.a(multiplier_2_out), .b({2'b00, setMinuteL}), .out(adder_2_out));  // open: cin, cout
  Adder #(.width(6)) adder_3 (.a(multiplier_3_out), .b({2'b00, setSecondL}), .out(adder_3_out));  // open: cin, cout
  Multiplier #(.width(17)) multiplier_4 (
    .a({{11{1'b0}}, adder_1_out}), .b(17'he10), .out(multiplier_4_out));  // open: cin, cout
  Multiplier #(.width(12)) multiplier_5 (
    .a({{6{1'b0}}, adder_2_out}), .b(12'h3c), .out(multiplier_5_out));  // open: cin, cout
  Multiplier #(.width(6)) multiplier_6 (
    .a({2'b00, setSecondH}), .b(6'b001010), .out(multiplier_6_out));  // open: cin, cout
  Counter #(.max('h1517f), .width(17)) counter_1 (
    .clr(POR), .load(setTime), .up(not_1_out), .count(enCount), .clk(clockInput), .D(adder_4_out),
    .Q(counter_1_q));  // open: carry
  not not_1 (not_1_out, reverseCount);
  Adder #(.width(17)) adder_4 (.a(multiplier_4_out), .b({{5{1'b0}}, minAndSec}), .out(adder_4_out));  // open: cin, cout
  Counter #(.max('he0f), .width(12)) counter_2 (
    .clr(POR), .load(setTime), .up(not_2_out), .count(enCount), .clk(clockInput), .D(minAndSec),
    .Q(counter_2_q));  // open: carry
  not not_2 (not_2_out, reverseCount);
  Adder #(.width(12)) adder_5 (.a(multiplier_5_out), .b({{6{1'b0}}, adder_3_out}), .out(minAndSec));  // open: cin, cout
  Counter #(.max('h3b), .width(6)) counter_3 (
    .clr(POR), .load(setTime), .up(not_3_out), .count(enCount), .clk(clockInput), .D(adder_6_out),
    .Q(counter_3_q));  // open: carry
  not not_3 (not_3_out, reverseCount);
  Adder #(.width(6)) adder_6 (.a(multiplier_6_out), .b({2'b00, setSecondL}), .out(adder_6_out));  // open: cin, cout
  // Binary_to_BCD_converter #(.binvalue(6)) binary_to_bcd_converter_1: pin names not known; wires that end beside it: counter_3_q, secondH[3:0], secondL[3:0]
  Comparator #(.mode("unsigned"), .width(17)) comparator_1 (
    .a(counter_1_q), .b(17'he10), .gt(comparator_1_gt));  // open: eq, lt
  Comparator #(.mode("unsigned"), .width(17)) comparator_2 (
    .a(counter_1_q), .b(17'h1c20), .gt(comparator_2_gt));  // open: eq, lt
  Comparator #(.mode("unsigned"), .width(17)) comparator_3 (
    .a(counter_1_q), .b(17'h2a30), .gt(comparator_3_gt));  // open: eq, lt
  Comparator #(.mode("unsigned"), .width(17)) comparator_4 (
    .a(counter_1_q), .b(17'h3840), .gt(comparator_4_gt));  // open: eq, lt
  Comparator #(.mode("unsigned"), .width(17)) comparator_5 (
    .a(counter_1_q), .b(17'h4650), .gt(comparator_5_gt));  // open: eq, lt
  Comparator #(.mode("unsigned"), .width(17)) comparator_6 (
    .a(counter_1_q), .b(17'h5460), .gt(comparator_6_gt));  // open: eq, lt
  Comparator #(.mode("unsigned"), .width(17)) comparator_7 (
    .a(counter_1_q), .b(17'h6270), .gt(comparator_7_gt));  // open: eq, lt
  Comparator #(.mode("unsigned"), .width(17)) comparator_8 (
    .a(counter_1_q), .b(17'h7080), .gt(comparator_8_gt));  // open: eq, lt
  Comparator #(.mode("unsigned"), .width(17)) comparator_9 (
    .a(counter_1_q), .b(17'h7e90), .gt(comparator_9_gt));  // open: eq, lt
  Comparator #(.mode("unsigned"), .width(17)) comparator_10 (
    .a(counter_1_q), .b(17'h8ca0), .gt(comparator_10_gt));  // open: eq, lt
  Comparator #(.mode("unsigned"), .width(17)) comparator_11 (
    .a(counter_1_q), .b(17'h9ab0), .gt(comparator_11_gt));  // open: eq, lt
  Comparator #(.mode("unsigned"), .width(17)) comparator_12 (
    .a(counter_1_q), .b(17'ha8c0), .gt(comparator_12_gt));  // open: eq, lt
  Comparator #(.mode("unsigned"), .width(17)) comparator_13 (
    .a(counter_1_q), .b(17'hb6d0), .gt(comparator_13_gt));  // open: eq, lt
  Comparator #(.mode("unsigned"), .width(17)) comparator_14 (
    .a(counter_1_q), .b(17'hc4e0), .gt(comparator_14_gt));  // open: eq, lt
  Comparator #(.mode("unsigned"), .width(17)) comparator_15 (
    .a(counter_1_q), .b(17'hd2f0), .gt(comparator_15_gt));  // open: eq, lt
  Comparator #(.mode("unsigned"), .width(17)) comparator_16 (
    .a(counter_1_q), .b(17'he100), .gt(comparator_16_gt));  // open: eq, lt
  Comparator #(.mode("unsigned"), .width(17)) comparator_17 (
    .a(counter_1_q), .b(17'hef10), .gt(comparator_17_gt));  // open: eq, lt
  Comparator #(.mode("unsigned"), .width(17)) comparator_18 (
    .a(counter_1_q), .b(17'hfd20), .gt(comparator_18_gt));  // open: eq, lt
  Comparator #(.mode("unsigned"), .width(17)) comparator_19 (
    .a(counter_1_q), .b(17'h10b30), .gt(comparator_19_gt));  // open: eq, lt
  Comparator #(.mode("unsigned"), .width(17)) comparator_20 (
    .a(counter_1_q), .b(17'h11940), .gt(comparator_20_gt));  // open: eq, lt
  Comparator #(.mode("unsigned"), .width(17)) comparator_21 (
    .a(counter_1_q), .b(17'h12750), .gt(comparator_21_gt));  // open: eq, lt
  Comparator #(.mode("unsigned"), .width(17)) comparator_22 (
    .a(counter_1_q), .b(17'h13560), .gt(comparator_22_gt));  // open: eq, lt
  Comparator #(.mode("unsigned"), .width(17)) comparator_23 (
    .a(counter_1_q), .b(17'h14370), .gt(comparator_23_gt));  // open: eq, lt
  secondToMinuteDCB secondToMinuteDCB_1 (.sec(counter_2_q), .minuteH(minuteH[3:0]), .minuteL(minuteL[3:0]));
  Multiplexer #(.width(5)) multiplexer_1 (
    .in0(5'b10110), .in1(5'b10111), .out(multiplexer_1_out), .sel(comparator_23_gt));
  Multiplexer #(.width(5)) multiplexer_2 (
    .in0(5'b10101), .in1(multiplexer_1_out), .out(multiplexer_2_out), .sel(comparator_22_gt));
  Multiplexer #(.width(5)) multiplexer_3 (
    .in0(5'b10100), .in1(multiplexer_2_out), .out(multiplexer_3_out), .sel(comparator_21_gt));
  Multiplexer #(.width(5)) multiplexer_4 (
    .in0(5'b10011), .in1(multiplexer_3_out), .out(multiplexer_4_out), .sel(comparator_20_gt));
  Multiplexer #(.width(5)) multiplexer_5 (
    .in0(5'b10010), .in1(multiplexer_4_out), .out(multiplexer_5_out), .sel(comparator_19_gt));
  Multiplexer #(.width(5)) multiplexer_6 (
    .in0(5'b10001), .in1(multiplexer_5_out), .out(multiplexer_6_out), .sel(comparator_18_gt));
  Multiplexer #(.width(5)) multiplexer_7 (
    .in0(5'b10000), .in1(multiplexer_6_out), .out(multiplexer_7_out), .sel(comparator_17_gt));
  Multiplexer #(.width(5)) multiplexer_8 (
    .in0(5'b01111), .in1(multiplexer_7_out), .out(multiplexer_8_out), .sel(comparator_16_gt));
  Multiplexer #(.width(5)) multiplexer_9 (
    .in0(5'b01110), .in1(multiplexer_8_out), .out(multiplexer_9_out), .sel(comparator_15_gt));
  Multiplexer #(.width(5)) multiplexer_10 (
    .in0(5'b01101), .in1(multiplexer_9_out), .out(multiplexer_10_out), .sel(comparator_14_gt));
  Multiplexer #(.width(5)) multiplexer_11 (
    .in0(5'b01100), .in1(multiplexer_10_out), .out(multiplexer_11_out), .sel(comparator_13_gt));
  Multiplexer #(.width(5)) multiplexer_12 (
    .in0(5'b01011), .in1(multiplexer_11_out), .out(multiplexer_12_out), .sel(comparator_12_gt));
  Multiplexer #(.width(5)) multiplexer_13 (
    .in0(5'b01010), .in1(multiplexer_12_out), .out(multiplexer_13_out), .sel(comparator_11_gt));
  Multiplexer #(.width(5)) multiplexer_14 (
    .in0(5'b01001), .in1(multiplexer_13_out), .out(multiplexer_14_out), .sel(comparator_10_gt));
  Multiplexer #(.width(5)) multiplexer_15 (
    .in0(5'b01000), .in1(multiplexer_14_out), .out(multiplexer_15_out), .sel(comparator_9_gt));
  Multiplexer #(.width(5)) multiplexer_16 (
    .in0(5'b00111), .in1(multiplexer_15_out), .out(multiplexer_16_out), .sel(comparator_8_gt));
  Multiplexer #(.width(5)) multiplexer_17 (
    .in0(5'b00110), .in1(multiplexer_16_out), .out(multiplexer_17_out), .sel(comparator_7_gt));
  Multiplexer #(.width(5)) multiplexer_18 (
    .in0(5'b00101), .in1(multiplexer_17_out), .out(multiplexer_18_out), .sel(comparator_6_gt));
  Multiplexer #(.width(5)) multiplexer_19 (
    .in0(5'b00100), .in1(multiplexer_18_out), .out(multiplexer_19_out), .sel(comparator_5_gt));
  Multiplexer #(.width(5)) multiplexer_20 (
    .in0(5'b00011), .in1(multiplexer_19_out), .out(multiplexer_20_out), .sel(comparator_4_gt));
  Multiplexer #(.width(5)) multiplexer_21 (
    .in0(5'b00010), .in1(multiplexer_20_out), .out(multiplexer_21_out), .sel(comparator_3_gt));
  Multiplexer #(.width(5)) multiplexer_22 (
    .in0(5'b00001), .in1(multiplexer_21_out), .out(multiplexer_22_out), .sel(comparator_2_gt));
  Multiplexer #(.width(5)) multiplexer_23 (
    .in0({5{1'b0}}), .in1(multiplexer_22_out), .out(multiplexer_23_out), .sel(comparator_1_gt));
  // Binary_to_BCD_converter #(.binvalue(5)) binary_to_bcd_converter_2: pin names not known; wires that end beside it: multiplexer_23_out, hourH[3:0], hourL[3:0]

  assign hourH[5:4] = 2'b00;
  assign hourL[5:4] = 2'b10;
  assign minuteH[5:4] = 2'b00;
  assign minuteL[5:4] = 2'b10;
  assign secondH[5:4] = 2'b00;
  assign secondL[5:4] = 2'b00;

  // Other names for the same wires on the sheet: clock = clockInput; en = enCount; currentHourH[3:0] = hourH[3:0];
  //   currentHourL[3:0] = hourL[3:0]; currentMinuteH[3:0] = minuteH[3:0]; currentMinuteL[3:0] = minuteL[3:0];
  //   reset = POR; reverse = reverseCount; currentSecondH[3:0] = secondH[3:0]; currentSecondL[3:0] = secondL[3:0]

  // Notes on the sheet:
  //   it can count and decount time
  //   settings
  //   This module receive a 1Hz clock and output the time in BCD mode
  //   time preset
  //   time output
  //   counter for hours
  //   counter for minutes
  //   counter for seconds
  //   reset @ 23
  //   1
  //   2
  //   3
  //   4
  //   5
  //   6
  //   7
  //   8
  //   9
  //   10
  //   11
  //   12
  //   13
  //   14
  //   15
  //   16
  //   17
  //   18
  //   19
  //   20
  //   21
  //   22
  //   23
  //   reset @ 59
  //   reset @ 59
  //   this configuration has the advantage of being easy to manage in term of set, reset as it is fully synchronous and parrallel
endmodule

module TimeComparator (
  input  CLK,
  input  POR,
  input  en,
  input  [5:0] currentHourH,
  input  [5:0] currentHourL,
  input  [5:0] currentMinuteH,
  input  [5:0] currentMinuteL,
  input  [5:0] currentSecondH,
  input  [5:0] currentSecondL,
  input  [3:0] compareHourH,
  input  [3:0] compareHourL,
  input  [3:0] compareMinuteH,
  input  [3:0] compareMinuteL,
  input  [3:0] compareSecondH,
  input  [3:0] compareSecondL,
  output equal
);

  wire and_1_out, comparator_1_eq, comparator_2_eq, comparator_3_eq, comparator_4_eq, comparator_5_eq,
       comparator_6_eq, d_ff_1_qn;

  Comparator #(.width(4)) comparator_1 (.a(currentHourH[3:0]), .b(compareHourH), .eq(comparator_1_eq));  // open: gt, lt
  Comparator #(.width(4)) comparator_2 (.a(currentHourL[3:0]), .b(compareHourL), .eq(comparator_2_eq));  // open: gt, lt
  Comparator #(.width(4)) comparator_3 (
    .a(currentMinuteH[3:0]), .b(compareMinuteH), .eq(comparator_3_eq));  // open: gt, lt
  Comparator #(.width(4)) comparator_4 (
    .a(currentMinuteL[3:0]), .b(compareMinuteL), .eq(comparator_4_eq));  // open: gt, lt
  Comparator #(.width(4)) comparator_5 (
    .a(currentSecondH[3:0]), .b(compareSecondH), .eq(comparator_5_eq));  // open: gt, lt
  Comparator #(.width(4)) comparator_6 (
    .a(currentSecondL[3:0]), .b(compareSecondL), .eq(comparator_6_eq));  // open: gt, lt
  and and_1 (and_1_out, comparator_1_eq, comparator_2_eq, comparator_3_eq, en, comparator_4_eq, comparator_5_eq, comparator_6_eq);
  D_Flip_Flop d_ff_1 (.D(and_1_out), .clk(CLK), .Qn(d_ff_1_qn), .reset(POR));  // open: Q, preset
  and and_2 (equal, and_1_out, d_ff_1_qn);

  // Notes on the sheet:
  //   Variables :
  //   si l'horloge s'arrete
  //   Detecteur de flanc montant :
  //   empeche l'alarme de rester active
endmodule
module songPlayer (
  input  POR,
  input  CLK,
  input  play,
  input  rec,
  input  [4:0] addr,
  input  [4:0] TONE,
  input  [3:0] BPM,
  output [4:0] noteOut,
  output BUSY
);

  wire and_1_out, comparator_1_eq, comparator_2_eq, comparator_3_eq, comparator_4_eq, comparator_5_eq,
       comparator_6_eq, comparator_7_eq, comparator_8_eq, comparator_9_eq, comparator_10_eq,
       comparator_11_eq, comparator_12_eq, comparator_13_eq, comparator_14_eq, comparator_15_eq,
       comparator_16_eq, comparator_17_eq, comparator_18_eq, comparator_19_eq, comparator_20_eq,
       comparator_21_eq, comparator_22_eq, comparator_23_eq, comparator_24_eq, comparator_25_eq,
       comparator_26_eq, comparator_27_eq, comparator_28_eq, comparator_29_eq, comparator_30_eq,
       comparator_31_eq, comparator_32_eq, comparator_33_eq, decoder_1_out0, decoder_1_out1, decoder_1_out2,
       decoder_1_out3, decoder_1_out4, decoder_1_out5, decoder_1_out6, decoder_1_out7, decoder_1_out8,
       decoder_1_out9, decoder_1_out10, decoder_1_out11, decoder_1_out12, decoder_1_out13, decoder_1_out14,
       decoder_1_out15, decoder_1_out16, decoder_1_out17, decoder_1_out18, decoder_1_out19, decoder_1_out20,
       decoder_1_out21, decoder_1_out22, decoder_1_out23, decoder_1_out24, decoder_1_out25, decoder_1_out26,
       decoder_1_out27, decoder_1_out28, decoder_1_out29, decoder_1_out30, decoder_1_out31, not_2_out,
       overflow;
  wire [8:0] D0, D1, D2, D3, D4, D5, D6, D7, D8, D9, D10, D11, D12, D13, D14, D15, D16, D17, D18, D19, D20,
       D21, D22, D23, D24, D25, D26, D27, D28, D29, D30, D31, shift_register_1_p17, shift_register_1_p18,
       shift_register_1_p19, shift_register_1_p20, shift_register_1_p21, shift_register_1_p22,
       shift_register_1_p23, shift_register_1_p24, shift_register_1_p25, shift_register_1_p26,
       shift_register_1_p27, shift_register_1_p28, undriven, undriven_2, undriven_3, undriven_4, undriven_5,
       undriven_6, undriven_7, undriven_8, undriven_9, undriven_10, undriven_11, undriven_12, undriven_13,
       undriven_14, undriven_15, undriven_16, undriven_17, undriven_18, undriven_19;
  wire [8:5] undriven_20;
  wire [16:0] counter_1_q, multiplexer_1_out, multiplexer_2_out;

  Decoder #(.select(5)) decoder_1 (
    .out0(decoder_1_out0), .out1(decoder_1_out1), .out2(decoder_1_out2), .out3(decoder_1_out3),
    .out4(decoder_1_out4), .out5(decoder_1_out5), .out6(decoder_1_out6), .out7(decoder_1_out7),
    .out8(decoder_1_out8), .out9(decoder_1_out9), .out10(decoder_1_out10), .out11(decoder_1_out11),
    .out12(decoder_1_out12), .out13(decoder_1_out13), .out14(decoder_1_out14), .out15(decoder_1_out15),
    .out16(decoder_1_out16), .out17(decoder_1_out17), .out18(decoder_1_out18), .out19(decoder_1_out19),
    .out20(decoder_1_out20), .out21(decoder_1_out21), .out22(decoder_1_out22), .out23(decoder_1_out23),
    .out24(decoder_1_out24), .out25(decoder_1_out25), .out26(decoder_1_out26), .out27(decoder_1_out27),
    .out28(decoder_1_out28), .out29(decoder_1_out29), .out30(decoder_1_out30), .out31(decoder_1_out31),
    .sel(addr), .en(rec));
  Register #(.width(9)) register_1 (.D({BPM, TONE}), .en(decoder_1_out0), .clk(CLK), .Q(D0), .clr(POR));
  Register #(.width(9)) register_2 (.D({BPM, TONE}), .en(decoder_1_out2), .clk(CLK), .Q(D2), .clr(POR));
  Register #(.width(9)) register_3 (.D({BPM, TONE}), .en(decoder_1_out4), .clk(CLK), .Q(D4), .clr(POR));
  Register #(.width(9)) register_4 (.D({BPM, TONE}), .en(decoder_1_out6), .clk(CLK), .Q(D6), .clr(POR));
  Register #(.width(9)) register_5 (.D({BPM, TONE}), .en(decoder_1_out8), .clk(CLK), .Q(D8), .clr(POR));
  Register #(.width(9)) register_6 (.D({BPM, TONE}), .en(decoder_1_out10), .clk(CLK), .Q(D10), .clr(POR));
  Register #(.width(9)) register_7 (.D({BPM, TONE}), .en(decoder_1_out12), .clk(CLK), .Q(D12), .clr(POR));
  Register #(.width(9)) register_8 (.D({BPM, TONE}), .en(decoder_1_out14), .clk(CLK), .Q(D14), .clr(POR));
  Register #(.width(9)) register_9 (.D({BPM, TONE}), .en(decoder_1_out16), .clk(CLK), .Q(D16), .clr(POR));
  Register #(.width(9)) register_10 (.D({BPM, TONE}), .en(decoder_1_out18), .clk(CLK), .Q(D18), .clr(POR));
  Register #(.width(9)) register_11 (.D({BPM, TONE}), .en(decoder_1_out20), .clk(CLK), .Q(D20), .clr(POR));
  Register #(.width(9)) register_12 (.D({BPM, TONE}), .en(decoder_1_out22), .clk(CLK), .Q(D22), .clr(POR));
  Register #(.width(9)) register_13 (.D({BPM, TONE}), .en(decoder_1_out24), .clk(CLK), .Q(D24), .clr(POR));
  Register #(.width(9)) register_14 (.D({BPM, TONE}), .en(decoder_1_out26), .clk(CLK), .Q(D26), .clr(POR));
  Register #(.width(9)) register_15 (.D({BPM, TONE}), .en(decoder_1_out28), .clk(CLK), .Q(D28), .clr(POR));
  Register #(.width(9)) register_16 (.D({BPM, TONE}), .en(decoder_1_out30), .clk(CLK), .Q(D30), .clr(POR));
  Register #(.width(9)) register_17 (.D({BPM, TONE}), .en(decoder_1_out1), .clk(CLK), .Q(D1), .clr(POR));
  Register #(.width(9)) register_18 (.D({BPM, TONE}), .en(decoder_1_out3), .clk(CLK), .Q(D3), .clr(POR));
  Register #(.width(9)) register_19 (.D({BPM, TONE}), .en(decoder_1_out5), .clk(CLK), .Q(D5), .clr(POR));
  Register #(.width(9)) register_20 (.D({BPM, TONE}), .en(decoder_1_out7), .clk(CLK), .Q(D7), .clr(POR));
  Register #(.width(9)) register_21 (.D({BPM, TONE}), .en(decoder_1_out9), .clk(CLK), .Q(D9), .clr(POR));
  Register #(.width(9)) register_22 (.D({BPM, TONE}), .en(decoder_1_out11), .clk(CLK), .Q(D11), .clr(POR));
  Register #(.width(9)) register_23 (.D({BPM, TONE}), .en(decoder_1_out13), .clk(CLK), .Q(D13), .clr(POR));
  Register #(.width(9)) register_24 (.D({BPM, TONE}), .en(decoder_1_out15), .clk(CLK), .Q(D15), .clr(POR));
  Register #(.width(9)) register_25 (.D({BPM, TONE}), .en(decoder_1_out17), .clk(CLK), .Q(D17), .clr(POR));
  Register #(.width(9)) register_26 (.D({BPM, TONE}), .en(decoder_1_out19), .clk(CLK), .Q(D19), .clr(POR));
  Register #(.width(9)) register_27 (.D({BPM, TONE}), .en(decoder_1_out21), .clk(CLK), .Q(D21), .clr(POR));
  Register #(.width(9)) register_28 (.D({BPM, TONE}), .en(decoder_1_out23), .clk(CLK), .Q(D23), .clr(POR));
  Register #(.width(9)) register_29 (.D({BPM, TONE}), .en(decoder_1_out25), .clk(CLK), .Q(D25), .clr(POR));
  Register #(.width(9)) register_30 (.D({BPM, TONE}), .en(decoder_1_out27), .clk(CLK), .Q(D27), .clr(POR));
  Register #(.width(9)) register_31 (.D({BPM, TONE}), .en(decoder_1_out29), .clk(CLK), .Q(D29), .clr(POR));
  Register #(.width(9)) register_32 (.D({BPM, TONE}), .en(decoder_1_out31), .clk(CLK), .Q(D31), .clr(POR));
  // Shift_Register #(.length(32), .width(9)) shift_register_1: pin names not known; wires that end beside it: POR, play, overflow, CLK, D31, D30, D29, D28, D27, D26, D25, D24, D23, D22, D21, D20, shift_register_1_p17, shift_register_1_p18, shift_register_1_p19, shift_register_1_p20, shift_register_1_p21, shift_register_1_p22, shift_register_1_p23, shift_register_1_p24, shift_register_1_p25, shift_register_1_p26, shift_register_1_p27, shift_register_1_p28
  Comparator #(.mode("unsigned"), .width(9)) comparator_1 (
    .a(shift_register_1_p17), .b({9{1'b0}}), .eq(comparator_1_eq));  // open: gt, lt
  Comparator #(.mode("unsigned"), .width(9)) comparator_2 (
    .a(shift_register_1_p19), .b({9{1'b0}}), .eq(comparator_2_eq));  // open: gt, lt
  Comparator #(.mode("unsigned"), .width(9)) comparator_3 (
    .a(shift_register_1_p21), .b({9{1'b0}}), .eq(comparator_3_eq));  // open: gt, lt
  Comparator #(.mode("unsigned"), .width(9)) comparator_4 (
    .a(shift_register_1_p23), .b({9{1'b0}}), .eq(comparator_4_eq));  // open: gt, lt
  Comparator #(.mode("unsigned"), .width(9)) comparator_5 (
    .a(shift_register_1_p25), .b({9{1'b0}}), .eq(comparator_5_eq));  // open: gt, lt
  Comparator #(.mode("unsigned"), .width(9)) comparator_6 (
    .a(shift_register_1_p27), .b({9{1'b0}}), .eq(comparator_6_eq));  // open: gt, lt
  Comparator #(.mode("unsigned"), .width(9)) comparator_7 (
    .a(undriven), .b({9{1'b0}}), .eq(comparator_7_eq));  // open: gt, lt
  Comparator #(.mode("unsigned"), .width(9)) comparator_8 (
    .a(undriven_3), .b({9{1'b0}}), .eq(comparator_8_eq));  // open: gt, lt
  Comparator #(.mode("unsigned"), .width(9)) comparator_9 (
    .a(undriven_5), .b({9{1'b0}}), .eq(comparator_9_eq));  // open: gt, lt
  Comparator #(.mode("unsigned"), .width(9)) comparator_10 (
    .a(undriven_7), .b({9{1'b0}}), .eq(comparator_10_eq));  // open: gt, lt
  Comparator #(.mode("unsigned"), .width(9)) comparator_11 (
    .a(undriven_9), .b({9{1'b0}}), .eq(comparator_11_eq));  // open: gt, lt
  Comparator #(.mode("unsigned"), .width(9)) comparator_12 (
    .a(undriven_11), .b({9{1'b0}}), .eq(comparator_12_eq));  // open: gt, lt
  Comparator #(.mode("unsigned"), .width(9)) comparator_13 (
    .a(undriven_13), .b({9{1'b0}}), .eq(comparator_13_eq));  // open: gt, lt
  Comparator #(.mode("unsigned"), .width(9)) comparator_14 (
    .a(undriven_15), .b({9{1'b0}}), .eq(comparator_14_eq));  // open: gt, lt
  Comparator #(.mode("unsigned"), .width(9)) comparator_15 (
    .a(undriven_17), .b({9{1'b0}}), .eq(comparator_15_eq));  // open: gt, lt
  Comparator #(.mode("unsigned"), .width(9)) comparator_16 (
    .a(undriven_19), .b({9{1'b0}}), .eq(comparator_16_eq));  // open: gt, lt
  Comparator #(.mode("unsigned"), .width(9)) comparator_17 (
    .a(shift_register_1_p18), .b({9{1'b0}}), .eq(comparator_17_eq));  // open: gt, lt
  Comparator #(.mode("unsigned"), .width(9)) comparator_18 (
    .a(shift_register_1_p20), .b({9{1'b0}}), .eq(comparator_18_eq));  // open: gt, lt
  Comparator #(.mode("unsigned"), .width(9)) comparator_19 (
    .a(shift_register_1_p22), .b({9{1'b0}}), .eq(comparator_19_eq));  // open: gt, lt
  Comparator #(.mode("unsigned"), .width(9)) comparator_20 (
    .a(shift_register_1_p24), .b({9{1'b0}}), .eq(comparator_20_eq));  // open: gt, lt
  Comparator #(.mode("unsigned"), .width(9)) comparator_21 (
    .a(shift_register_1_p26), .b({9{1'b0}}), .eq(comparator_21_eq));  // open: gt, lt
  Comparator #(.mode("unsigned"), .width(9)) comparator_22 (
    .a(shift_register_1_p28), .b({9{1'b0}}), .eq(comparator_22_eq));  // open: gt, lt
  Comparator #(.mode("unsigned"), .width(9)) comparator_23 (
    .a(undriven_2), .b({9{1'b0}}), .eq(comparator_23_eq));  // open: gt, lt
  Comparator #(.mode("unsigned"), .width(9)) comparator_24 (
    .a(undriven_4), .b({9{1'b0}}), .eq(comparator_24_eq));  // open: gt, lt
  Comparator #(.mode("unsigned"), .width(9)) comparator_25 (
    .a(undriven_6), .b({9{1'b0}}), .eq(comparator_25_eq));  // open: gt, lt
  Comparator #(.mode("unsigned"), .width(9)) comparator_26 (
    .a(undriven_8), .b({9{1'b0}}), .eq(comparator_26_eq));  // open: gt, lt
  Comparator #(.mode("unsigned"), .width(9)) comparator_27 (
    .a(undriven_10), .b({9{1'b0}}), .eq(comparator_27_eq));  // open: gt, lt
  Comparator #(.mode("unsigned"), .width(9)) comparator_28 (
    .a(undriven_12), .b({9{1'b0}}), .eq(comparator_28_eq));  // open: gt, lt
  Comparator #(.mode("unsigned"), .width(9)) comparator_29 (
    .a(undriven_14), .b({9{1'b0}}), .eq(comparator_29_eq));  // open: gt, lt
  Comparator #(.mode("unsigned"), .width(9)) comparator_30 (
    .a(undriven_16), .b({9{1'b0}}), .eq(comparator_30_eq));  // open: gt, lt
  Comparator #(.mode("unsigned"), .width(9)) comparator_31 (
    .a(undriven_18), .b({9{1'b0}}), .eq(comparator_31_eq));  // open: gt, lt
  Comparator #(.mode("unsigned"), .width(9)) comparator_32 (
    .a({undriven_20, noteOut}), .b({9{1'b0}}), .eq(comparator_32_eq));  // open: gt, lt
  and and_1 (and_1_out, comparator_1_eq, comparator_17_eq, comparator_2_eq, comparator_18_eq, comparator_3_eq, comparator_19_eq, comparator_4_eq, comparator_20_eq, comparator_5_eq, comparator_21_eq, comparator_6_eq, comparator_22_eq, comparator_7_eq, comparator_23_eq, comparator_8_eq, comparator_24_eq, comparator_9_eq, comparator_25_eq, comparator_10_eq, comparator_26_eq, comparator_11_eq, comparator_27_eq, comparator_12_eq, comparator_28_eq, comparator_13_eq, comparator_29_eq, comparator_14_eq, comparator_30_eq, comparator_15_eq, comparator_31_eq, comparator_16_eq, comparator_32_eq);
  not not_1 (BUSY, and_1_out);
  Counter #(.max('h1ffff), .width(17)) counter_1 (
    .clr(overflow), .load(1'b0), .up(1'b1), .count(1'b1), .clk(CLK), .Q(counter_1_q));  // open: D, carry
  Multiplexer #(.width(17)) multiplexer_1 (
    .in0(multiplexer_2_out), .in1(17'h64), .out(multiplexer_1_out), .sel(not_2_out));
  not not_2 (not_2_out, BUSY);
  Comparator #(.width(17)) comparator_33 (
    .a(counter_1_q), .b(multiplexer_1_out), .eq(comparator_33_eq));  // open: gt, lt
  Multiplexer #(.select(4), .width(17)) multiplexer_2 (
    .in0(17'h13880), .in1(17'h124f8), .in2(17'h11170), .in3(17'hfde8), .in4(17'hea60), .in5(17'hd6d8),
    .in6(17'hc350), .in7(17'hafc8), .in8(17'h9c40), .in9(17'h88b8), .in10(17'h7530), .in11(17'h61a8),
    .in12(17'h4e20), .in13(17'h3a98), .in14(17'h2710), .in15(17'h1338), .out(multiplexer_2_out),
    .sel(undriven_20));
  D_Flip_Flop d_ff_1 (.D(comparator_33_eq), .clk(CLK), .Q(overflow), .reset(POR));  // open: Qn, preset

  // Other names for the same wires on the sheet: RST = POR

  // Notes on the sheet:
  //   Variables :
  //   Memory Song :
  //   Play each note :
  //   Compute if done playing :
  //   Add a set delay between each note :
  //   le tempo drive le compteur pour la durée
  //   16 increment, range : 50-800 ms
endmodule

module messageCycleShifter (
  input  POR,
  input  load,
  input  CLK,
  input  [3:0] mesLength,
  input  [5:0] L1,
  input  [5:0] L2,
  input  [5:0] L3,
  input  [5:0] L4,
  input  [5:0] L5,
  input  [5:0] L6,
  input  [5:0] L7,
  input  [5:0] L8,
  input  [5:0] L9,
  input  [5:0] L10,
  input  [5:0] L11,
  input  [5:0] L12,
  input  [5:0] L13,
  input  [5:0] L14,
  output [35:0] displayOut
);

  wire CLKSlow, comparator_1_eq, comparator_2_eq, engage, not_1_out, or_1_out, or_2_out, RST, shift;
  wire [3:0] counter_1_q;
  wire [41:0] register_1_q, register_2_q;

  Clock #(.highDuration(2), .lowDuration(39998)) u_CLKSlow (.out(CLKSlow));
  Comparator #(.width(4)) comparator_1 (.a(mesLength), .b(4'b0110), .eq(comparator_1_eq));  // open: gt, lt
  S_R_Flip_Flop s_r_ff_1 (.R(CLKSlow), .clk(CLK), .Q(engage), .reset(POR), .preset(load));  // open: S, Qn
  not not_1 (not_1_out, comparator_1_eq);
  and and_1 (shift, not_1_out, CLKSlow);
  or or_1 (or_1_out, POR, RST);
  Counter #(.max('hf), .width(4)) counter_1 (
    .clr(or_1_out), .load(1'b0), .up(1'b1), .count(shift), .clk(CLK), .Q(counter_1_q));  // open: D, carry
  Register #(.width(42)) register_1 (
    .D({L8, L9, L10, L11, L12, L13, L14}), .en(load), .clk(CLK), .Q(register_1_q), .clr(POR));
  Register #(.width(42)) register_2 (
    .D({L1, L2, L3, L4, L5, L6, L7}), .en(load), .clk(CLK), .Q(register_2_q), .clr(POR));
  or or_2 (or_2_out, RST, engage);
  Comparator #(.width(4)) comparator_2 (.a(counter_1_q), .b(mesLength), .eq(comparator_2_eq));  // open: gt, lt
  // Shift_Register #(.length(14), .width(6)) shift_register_1: pin names not known; wires that end beside it: POR, or_2_out, shift, CLK, 6'b010000, register_1_q[5:0], register_1_q[11:6], register_1_q[17:12], register_1_q[23:18], register_1_q[29:24], register_1_q[35:30], register_1_q[41:36], register_2_q[5:0], register_2_q[11:6], register_2_q[17:12], register_2_q[23:18], register_2_q[29:24], displayOut[35:30], displayOut[29:24], displayOut[23:18], displayOut[17:12]
  S_R_Flip_Flop s_r_ff_2 (.R(1'b1), .clk(CLK), .Q(RST), .reset(POR), .preset(comparator_2_eq));  // open: S, Qn

  // Other names for the same wires on the sheet: length[3:0] = mesLength

  // Notes on the sheet:
  //   Variables :
  //   Shifter On/Off :
  //   Restart Shifter :
  //   Register Shifter :
endmodule

module messageRegister (
  input  [3:0] numMessage,
  input  POR,
  input  CLK,
  input  set,
  input  [3:0] ADDR,
  input  [5:0] CHAR,
  output [3:0] lengthMessage,
  output [5:0] L1,
  output [5:0] L2,
  output [5:0] L3,
  output [5:0] L4,
  output [5:0] L5,
  output [5:0] L6,
  output [5:0] L7,
  output [5:0] L8,
  output [5:0] L9,
  output [5:0] L10,
  output [5:0] L11,
  output [5:0] L12,
  output [5:0] L13,
  output [5:0] L14
);

  wire and_1_out, and_2_out, and_3_out, and_4_out, and_5_out, and_6_out, and_7_out, comparator_1_eq,
       comparator_2_eq, comparator_3_eq, comparator_4_eq, comparator_5_eq, comparator_6_eq, comparator_7_eq,
       comparator_8_eq, decoder_1_out0, decoder_1_out1, decoder_1_out2, decoder_1_out3, decoder_1_out4,
       decoder_1_out5, decoder_1_out6, decoder_1_out7, decoder_1_out8, decoder_1_out9, decoder_1_out10,
       decoder_1_out11, decoder_1_out12, decoder_1_out13;
  wire [3:0] messageLenght, multiplexer_6_out, multiplexer_7_out, multiplexer_8_out, multiplexer_13_out,
       multiplexer_14_out, multiplexer_19_out, multiplexer_20_out;
  wire [5:0] M0, M1, M2, M3, M4, M5, M6, M7, M8, M9, M10, M11, M12, M13;

  Decoder #(.select(4)) decoder_1 (
    .out0(decoder_1_out0), .out1(decoder_1_out1), .out2(decoder_1_out2), .out3(decoder_1_out3),
    .out4(decoder_1_out4), .out5(decoder_1_out5), .out6(decoder_1_out6), .out7(decoder_1_out7),
    .out8(decoder_1_out8), .out9(decoder_1_out9), .out10(decoder_1_out10), .out11(decoder_1_out11),
    .out12(decoder_1_out12), .out13(decoder_1_out13), .sel(ADDR), .en(set));  // open: out14, out15
  Register #(.width(6)) register_1 (.D(CHAR), .en(decoder_1_out0), .clk(CLK), .Q(M0), .clr(POR));
  Register #(.width(6)) register_2 (.D(CHAR), .en(decoder_1_out2), .clk(CLK), .Q(M2), .clr(POR));
  Register #(.width(6)) register_3 (.D(CHAR), .en(decoder_1_out4), .clk(CLK), .Q(M4), .clr(POR));
  Register #(.width(6)) register_4 (.D(CHAR), .en(decoder_1_out6), .clk(CLK), .Q(M6), .clr(POR));
  Register #(.width(6)) register_5 (.D(CHAR), .en(decoder_1_out8), .clk(CLK), .Q(M8), .clr(POR));
  Register #(.width(6)) register_6 (.D(CHAR), .en(decoder_1_out10), .clk(CLK), .Q(M10), .clr(POR));
  Register #(.width(6)) register_7 (.D(CHAR), .en(decoder_1_out12), .clk(CLK), .Q(M12), .clr(POR));
  Multiplexer #(.select(4), .width(4)) multiplexer_1 (
    .in0(4'b0100), .in1(4'b1001), .in2(4'b0111), .in3(4'b1110), .in4(4'b0111), .in5(4'b0110), .in6(4'b1010),
    .in7(4'b1010), .in8(4'b0000), .in9(4'b0000), .in10(4'b0000), .in11(4'b0000), .in12(4'b0000),
    .in13(4'b0000), .in14(4'b1011), .in15(messageLenght), .out(lengthMessage), .sel(numMessage));
  Register #(.width(6)) register_8 (.D(CHAR), .en(decoder_1_out1), .clk(CLK), .Q(M1), .clr(POR));
  Register #(.width(6)) register_9 (.D(CHAR), .en(decoder_1_out3), .clk(CLK), .Q(M3), .clr(POR));
  Register #(.width(6)) register_10 (.D(CHAR), .en(decoder_1_out5), .clk(CLK), .Q(M5), .clr(POR));
  Register #(.width(6)) register_11 (.D(CHAR), .en(decoder_1_out7), .clk(CLK), .Q(M7), .clr(POR));
  Register #(.width(6)) register_12 (.D(CHAR), .en(decoder_1_out9), .clk(CLK), .Q(M9), .clr(POR));
  Register #(.width(6)) register_13 (.D(CHAR), .en(decoder_1_out11), .clk(CLK), .Q(M11), .clr(POR));
  Register #(.width(6)) register_14 (.D(CHAR), .en(decoder_1_out13), .clk(CLK), .Q(M13), .clr(POR));
  Multiplexer #(.select(4), .width(6)) multiplexer_2 (
    .in0(6'b010001), .in1(6'b011001), .in2(6'b011001), .in3(6'b011001), .in4(6'b010001), .in5(6'b001100),
    .in6(6'b011001), .in7(6'b011001), .in8(6'b010000), .in9(6'b010000), .in10(6'b010000), .in11(6'b010000),
    .in12(6'b010000), .in13(6'b010000), .in14(6'b001011), .in15(M0), .out(L1), .sel(numMessage));
  Multiplexer #(.select(4), .width(6)) multiplexer_3 (
    .in0(6'b010110), .in1(6'b001110), .in2(6'b001110), .in3(6'b001110), .in4(6'b010110), .in5(6'b010001),
    .in6(6'b001110), .in7(6'b001110), .in8(6'b010000), .in9(6'b010000), .in10(6'b010000), .in11(6'b010000),
    .in12(6'b010000), .in13(6'b010000), .in14(6'b010010), .in15(M1), .out(L2), .sel(numMessage));
  Multiplexer #(.select(4), .width(6)) multiplexer_4 (
    .in0(6'b011011), .in1(6'b011010), .in2(6'b011010), .in3(6'b011010), .in4(6'b011011), .in5(6'b011000),
    .in6(6'b011010), .in7(6'b011010), .in8(6'b010000), .in9(6'b010000), .in10(6'b010000), .in11(6'b010000),
    .in12(6'b010000), .in13(6'b010000), .in14(6'b010111), .in15(M2), .out(L3), .sel(numMessage));
  Multiplexer #(.select(4), .width(6)) multiplexer_5 (
    .in0(6'b011000), .in1(6'b010000), .in2(6'b010000), .in3(6'b010000), .in4(6'b011000), .in5(6'b010110),
    .in6(6'b010000), .in7(6'b010000), .in8(6'b010000), .in9(6'b010000), .in10(6'b010000), .in11(6'b010000),
    .in12(6'b010000), .in13(6'b010000), .in14(6'b010000), .in15(M3), .out(L4), .sel(numMessage));
  Comparator #(.width(6)) comparator_1 (.a(M6), .b({6{1'b0}}), .eq(comparator_1_eq));  // open: gt, lt
  Comparator #(.width(6)) comparator_2 (.a(M7), .b({6{1'b0}}), .eq(comparator_2_eq));  // open: gt, lt
  Comparator #(.width(6)) comparator_3 (.a(M8), .b({6{1'b0}}), .eq(comparator_3_eq));  // open: gt, lt
  Comparator #(.width(6)) comparator_4 (.a(M9), .b({6{1'b0}}), .eq(comparator_4_eq));  // open: gt, lt
  Comparator #(.width(6)) comparator_5 (.a(M10), .b({6{1'b0}}), .eq(comparator_5_eq));  // open: gt, lt
  Comparator #(.width(6)) comparator_6 (.a(M11), .b({6{1'b0}}), .eq(comparator_6_eq));  // open: gt, lt
  Comparator #(.width(6)) comparator_7 (.a(M12), .b({6{1'b0}}), .eq(comparator_7_eq));  // open: gt, lt
  Comparator #(.width(6)) comparator_8 (.a(M13), .b({6{1'b0}}), .eq(comparator_8_eq));  // open: gt, lt
  and and_1 (and_1_out, comparator_1_eq, comparator_2_eq, comparator_3_eq, comparator_4_eq, comparator_5_eq, comparator_6_eq, comparator_7_eq, comparator_8_eq);
  and and_2 (and_2_out, comparator_2_eq, comparator_3_eq, comparator_4_eq, comparator_5_eq, comparator_6_eq, comparator_7_eq, comparator_8_eq);
  Multiplexer #(.width(4)) multiplexer_6 (.in0(4'b0111), .in1(4'b0110), .out(multiplexer_6_out), .sel(and_1_out));
  and and_3 (and_3_out, comparator_3_eq, comparator_4_eq, comparator_5_eq, comparator_6_eq, comparator_7_eq, comparator_8_eq);
  Multiplexer #(.width(4)) multiplexer_7 (
    .in0(4'b1000), .in1(multiplexer_6_out), .out(multiplexer_7_out), .sel(and_2_out));
  and and_4 (and_4_out, comparator_4_eq, comparator_5_eq, comparator_6_eq, comparator_7_eq, comparator_8_eq);
  Multiplexer #(.width(4)) multiplexer_8 (
    .in0(4'b1001), .in1(multiplexer_7_out), .out(multiplexer_8_out), .sel(and_3_out));
  Multiplexer #(.select(4), .width(6)) multiplexer_9 (
    .in0(6'b010000), .in1(6'b011001), .in2(6'b010001), .in3(6'b010001), .in4(6'b001001), .in5(6'b010101),
    .in6(6'b011000), .in7(6'b001101), .in8(6'b010000), .in9(6'b010000), .in10(6'b010000), .in11(6'b010000),
    .in12(6'b010000), .in13(6'b010000), .in14(6'b001011), .in15(M4), .out(L5), .sel(numMessage));
  Multiplexer #(.select(4), .width(6)) multiplexer_10 (
    .in0(6'b010000), .in1(6'b011011), .in2(6'b010110), .in3(6'b010110), .in4(6'b010100), .in5(6'b010110),
    .in6(6'b011110), .in7(6'b010010), .in8(6'b010000), .in9(6'b010000), .in10(6'b010000), .in11(6'b010000),
    .in12(6'b010000), .in13(6'b010000), .in14(6'b010010), .in15(M5), .out(L6), .sel(numMessage));
  Multiplexer #(.select(4), .width(6)) multiplexer_11 (
    .in0(6'b010000), .in1(6'b010101), .in2(6'b011011), .in3(6'b011011), .in4(6'b001010), .in5(6'b010000),
    .in6(6'b010101), .in7(6'b011001), .in8(6'b010000), .in9(6'b010000), .in10(6'b010000), .in11(6'b010000),
    .in12(6'b010000), .in13(6'b010000), .in14(6'b010111), .in15(M6), .out(L7), .sel(numMessage));
  Multiplexer #(.select(4), .width(6)) multiplexer_12 (
    .in0(6'b010000), .in1(6'b011000), .in2(6'b011000), .in3(6'b011000), .in4(6'b011001), .in5(6'b010000),
    .in6(6'b001001), .in7(6'b010111), .in8(6'b010000), .in9(6'b010000), .in10(6'b010000), .in11(6'b010000),
    .in12(6'b010000), .in13(6'b010000), .in14(6'b100000), .in15(M7), .out(L8), .sel(numMessage));
  and and_5 (and_5_out, comparator_5_eq, comparator_6_eq, comparator_7_eq, comparator_8_eq);
  Multiplexer #(.width(4)) multiplexer_13 (
    .in0(4'b1010), .in1(multiplexer_8_out), .out(multiplexer_13_out), .sel(and_4_out));
  and and_6 (and_6_out, comparator_6_eq, comparator_7_eq, comparator_8_eq);
  and and_7 (and_7_out, comparator_7_eq, comparator_8_eq);
  Multiplexer #(.width(4)) multiplexer_14 (
    .in0(4'b1011), .in1(multiplexer_13_out), .out(multiplexer_14_out), .sel(and_5_out));
  Multiplexer #(.select(4), .width(6)) multiplexer_15 (
    .in0(6'b010000), .in1(6'b011110), .in2(6'b010000), .in3(6'b001001), .in4(6'b011001), .in5(6'b010000),
    .in6(6'b011010), .in7(6'b010100), .in8(6'b010000), .in9(6'b010000), .in10(6'b010000), .in11(6'b010000),
    .in12(6'b010000), .in13(6'b010000), .in14(6'b100000), .in15(M8), .out(L9), .sel(numMessage));
  Multiplexer #(.select(4), .width(6)) multiplexer_16 (
    .in0(6'b010000), .in1(6'b011001), .in2(6'b010000), .in3(6'b010100), .in4(6'b010000), .in5(6'b010000),
    .in6(6'b010110), .in7(6'b001010), .in8(6'b010000), .in9(6'b010000), .in10(6'b010000), .in11(6'b010000),
    .in12(6'b010000), .in13(6'b010000), .in14(6'b100000), .in15(M9), .out(L10), .sel(numMessage));
  Multiplexer #(.select(4), .width(6)) multiplexer_17 (
    .in0(6'b010000), .in1(6'b001110), .in2(6'b010000), .in3(6'b001010), .in4(6'b010000), .in5(6'b010000),
    .in6(6'b010101), .in7(6'b011100), .in8(6'b010000), .in9(6'b010000), .in10(6'b010000), .in11(6'b010000),
    .in12(6'b010000), .in13(6'b010000), .in14(6'b010000), .in15(M10), .out(L11), .sel(numMessage));
  Multiplexer #(.select(4), .width(6)) multiplexer_18 (
    .in0(6'b010000), .in1(6'b010000), .in2(6'b010000), .in3(6'b011001), .in4(6'b010000), .in5(6'b010000),
    .in6(6'b001110), .in7(6'b010000), .in8(6'b010000), .in9(6'b010000), .in10(6'b010000), .in11(6'b010000),
    .in12(6'b010000), .in13(6'b010000), .in14(6'b010000), .in15(M11), .out(L12), .sel(numMessage));
  Multiplexer #(.width(4)) multiplexer_19 (
    .in0(4'b1100), .in1(multiplexer_14_out), .out(multiplexer_19_out), .sel(and_6_out));
  Multiplexer #(.width(4)) multiplexer_20 (
    .in0(4'b1101), .in1(multiplexer_19_out), .out(multiplexer_20_out), .sel(and_7_out));
  Multiplexer #(.width(4)) multiplexer_21 (
    .in0(4'b1110), .in1(multiplexer_20_out), .out(messageLenght), .sel(comparator_8_eq));
  Multiplexer #(.select(4), .width(6)) multiplexer_22 (
    .in0(6'b010000), .in1(6'b010000), .in2(6'b010000), .in3(6'b011001), .in4(6'b010000), .in5(6'b010000),
    .in6(6'b010000), .in7(6'b010000), .in8(6'b010000), .in9(6'b010000), .in10(6'b010000), .in11(6'b010000),
    .in12(6'b010000), .in13(6'b010000), .in14(6'b010000), .in15(M12), .out(L13), .sel(numMessage));
  Multiplexer #(.select(4), .width(6)) multiplexer_23 (
    .in0(6'b010000), .in1(6'b010000), .in2(6'b010000), .in3(6'b010000), .in4(6'b010000), .in5(6'b010000),
    .in6(6'b010000), .in7(6'b010000), .in8(6'b010000), .in9(6'b010000), .in10(6'b010000), .in11(6'b010000),
    .in12(6'b010000), .in13(6'b010000), .in14(6'b010000), .in15(M13), .out(L14), .sel(numMessage));

  // Other names for the same wires on the sheet: RST = POR

  // Notes on the sheet:
  //   Variables :
  //   Safe Custom Messages :
  //   Length Messages :
  //   0 -> Hour
  //   1 -> Set Sunrise
  //   2 -> Set Hour
  //   4 -> Hourglass
  //   5 -> Chrono
  //   6 -> Set ringtone
  //   7 -> Set display
  //   3 -> Set Hourglass
  //   15 -> chrono alarm message : Bip Bip...
  //   16 -> User set Message
  //   Calcul Size Custom Message : 
  //   Display Messages :
endmodule

module secondToMinuteDCB (
  input  [11:0] sec,
  output [3:0] minuteH,
  output [3:0] minuteL
);

  wire and_7_out, and_8_out, not_1_out, not_2_out, not_3_out, not_4_out, not_5_out, not_6_out, not_7_out,
       not_8_out, not_9_out, or_1_out, or_2_out, or_3_out, or_4_out, or_5_out, or_6_out, or_7_out, or_8_out,
       or_9_out, or_10_out, or_11_out, or_12_out, or_13_out, or_14_out, or_15_out, or_16_out, or_17_out,
       or_18_out, or_19_out, or_20_out, or_21_out, or_22_out, or_23_out, or_24_out, or_25_out, or_26_out,
       or_27_out, or_28_out, or_29_out, or_30_out, or_31_out, or_32_out, or_33_out, or_34_out, or_35_out,
       or_36_out, or_37_out, or_38_out, or_39_out, or_40_out, or_41_out, or_42_out, or_43_out, or_44_out,
       or_45_out, or_46_out, or_47_out, or_48_out, or_49_out, or_50_out, or_51_out, or_52_out, or_53_out,
       or_54_out, or_55_out, or_56_out, or_57_out, or_58_out, or_59_out, or_60_out, or_61_out, or_62_out,
       or_63_out, or_64_out, or_65_out, or_66_out, or_67_out, or_68_out, or_69_out, or_70_out, or_71_out,
       or_72_out, or_73_out, or_74_out, or_75_out, or_76_out, or_77_out, or_78_out, or_79_out, or_80_out,
       or_81_out, or_82_out, or_83_out, or_84_out, or_85_out, or_86_out, or_87_out, or_88_out, or_89_out,
       or_90_out, or_91_out, or_92_out, or_93_out, or_94_out, or_95_out, or_96_out, or_97_out, or_98_out,
       or_99_out, or_100_out, or_101_out, or_102_out, or_103_out, or_104_out, or_105_out, or_106_out,
       or_107_out, or_108_out, or_109_out, or_110_out, or_111_out, or_112_out, or_113_out, or_114_out,
       or_115_out, or_116_out, or_117_out, or_118_out, or_119_out, or_120_out, or_121_out, or_122_out,
       or_123_out, or_124_out, or_125_out, or_126_out, or_127_out, or_128_out, or_129_out, or_130_out,
       or_131_out, or_132_out, or_133_out, or_134_out, or_135_out, or_136_out, or_137_out, or_138_out,
       or_139_out, or_140_out, or_141_out, or_142_out, or_143_out, or_144_out, or_145_out, or_146_out,
       or_147_out, or_148_out, or_149_out, or_150_out, or_151_out, or_152_out, or_153_out, or_154_out,
       or_155_out, or_156_out, or_157_out, or_158_out, or_159_out, or_160_out, or_161_out, or_162_out,
       or_163_out, or_164_out, or_165_out, or_166_out, or_167_out, or_168_out, or_169_out, or_170_out,
       or_171_out, or_172_out, or_173_out, or_174_out, or_175_out, or_176_out, or_177_out, or_178_out,
       or_179_out, or_180_out, or_181_out, or_182_out, or_183_out, or_184_out, or_185_out, or_186_out,
       or_187_out, or_188_out, or_189_out, or_190_out, or_191_out, or_192_out, or_193_out, or_194_out,
       or_195_out, or_196_out, or_197_out, or_198_out, or_199_out, or_200_out, or_201_out, or_202_out,
       or_203_out, or_204_out, or_205_out, or_206_out, or_207_out, or_208_out, or_209_out, or_210_out,
       or_211_out, or_212_out, or_213_out, or_214_out, or_215_out, or_216_out, or_217_out, or_218_out,
       or_219_out, or_220_out, or_221_out, or_222_out, or_223_out, or_224_out, or_225_out, or_226_out,
       or_227_out, or_228_out, or_229_out, or_230_out, or_231_out, or_232_out, or_233_out, or_234_out,
       or_235_out, or_236_out, or_237_out, or_238_out, or_239_out, or_240_out, or_241_out, or_242_out,
       or_243_out, or_244_out, or_245_out, or_246_out, or_247_out, or_248_out, or_249_out, or_250_out,
       or_251_out, or_252_out, or_253_out, or_254_out, or_255_out, or_256_out, or_257_out, or_258_out,
       or_259_out, or_260_out, or_261_out, or_262_out, or_263_out, or_264_out, or_265_out, or_266_out;

  not not_1 (not_1_out, sec[11]);
  not not_2 (not_2_out, sec[10]);
  not not_3 (not_3_out, sec[9]);
  not not_4 (not_4_out, sec[8]);
  not not_5 (not_5_out, sec[7]);
  not not_6 (not_6_out, sec[6]);
  not not_7 (not_7_out, sec[5]);
  not not_8 (not_8_out, sec[4]);
  not not_9 (not_9_out, sec[3]);
  or or_1 (or_1_out, sec[10], sec[9], sec[8]);
  or or_2 (or_2_out, sec[10], sec[9], sec[7], sec[6]);
  or or_3 (or_3_out, sec[10], sec[9], sec[7], sec[5]);
  or or_4 (or_4_out, sec[11], sec[10]);
  or or_5 (or_5_out, not_1_out, not_2_out);
  or or_6 (or_6_out, sec[11], sec[9], sec[8], sec[6], sec[5]);
  or or_7 (or_7_out, sec[11], sec[9], sec[8], sec[6], sec[4]);
  or or_8 (or_8_out, not_2_out, sec[9], sec[8], sec[7]);
  or or_9 (or_9_out, sec[10], not_4_out, not_6_out, not_7_out);
  or or_10 (or_10_out, not_1_out, not_4_out, not_5_out);
  or or_11 (or_11_out, not_1_out, not_3_out);
  or or_12 (or_12_out, sec[11], sec[10], sec[9]);
  or or_13 (or_13_out, sec[11], sec[9], not_4_out);
  or or_14 (or_14_out, sec[10], sec[9], not_4_out, not_5_out);
  or or_15 (or_15_out, sec[11], not_2_out, sec[8], not_5_out, not_7_out, not_8_out);
  or or_16 (or_16_out, sec[11], not_2_out, sec[8], not_5_out, not_6_out);
  or or_17 (or_17_out, sec[11], not_2_out, not_3_out, sec[8]);
  or or_18 (or_18_out, sec[11], not_2_out, not_3_out, sec[7], sec[6], sec[5], sec[4], sec[3]);
  or or_19 (or_19_out, not_1_out, sec[10], not_4_out, sec[7], not_6_out, not_7_out);
  or or_20 (or_20_out, not_1_out, sec[10], not_3_out, sec[8]);
  or or_21 (or_21_out, not_1_out, sec[10], not_3_out, sec[7]);
  or or_22 (or_22_out, not_1_out, sec[10], not_3_out, sec[6], sec[5]);
  or or_23 (or_23_out, not_1_out, sec[10], not_3_out, sec[6], sec[4]);
  or or_24 (or_24_out, not_1_out, sec[10], not_3_out, sec[6], sec[3]);
  or or_25 (or_25_out, sec[11], not_3_out, sec[8], sec[7], sec[6]);
  or or_26 (or_26_out, sec[10], not_3_out, sec[8], sec[7], sec[5], sec[4]);
  or or_27 (or_27_out, sec[10], not_3_out, sec[8], sec[7], sec[5], sec[3]);
  or or_28 (or_28_out, sec[9], sec[8], sec[7], sec[6], sec[5]);
  or or_29 (or_29_out, sec[9], sec[8], sec[7], sec[6], sec[4]);
  or or_30 (or_30_out, sec[9], sec[8], sec[7], sec[6], sec[3]);
  or or_31 (or_31_out, sec[10], sec[9], sec[8], sec[7]);
  or or_32 (or_32_out, sec[10], sec[9], sec[8], sec[6]);
  or or_33 (or_33_out, sec[9], sec[8], not_5_out, not_6_out, sec[5]);
  or or_34 (or_34_out, sec[10], sec[8], not_6_out, not_7_out, sec[4], sec[3]);
  or or_35 (or_35_out, sec[11], sec[9], sec[8], not_5_out, not_6_out);
  or or_36 (or_36_out, sec[11], sec[9], sec[7], sec[6], sec[5]);
  or or_37 (or_37_out, sec[11], sec[9], sec[7], sec[6], sec[4]);
  or or_38 (or_38_out, sec[11], sec[9], sec[7], sec[6], sec[3]);
  or or_39 (or_39_out, sec[11], sec[10], sec[9], sec[7]);
  or or_40 (or_40_out, sec[9], not_4_out, not_5_out, sec[6], sec[5], sec[4]);
  or or_41 (or_41_out, sec[9], not_4_out, not_5_out, sec[6], sec[5], sec[3]);
  or or_42 (or_42_out, sec[11], not_4_out, not_5_out, sec[6]);
  or or_43 (or_43_out, sec[11], sec[9], not_5_out, not_6_out, sec[5]);
  or or_44 (or_44_out, sec[10], sec[8], sec[7], not_6_out, not_8_out, not_9_out);
  or or_45 (or_45_out, sec[10], sec[8], sec[7], not_6_out, not_7_out);
  or or_46 (or_46_out, not_3_out, sec[8], not_5_out, sec[6], sec[5], sec[4]);
  or or_47 (or_47_out, sec[10], sec[8], not_5_out, sec[6]);
  or or_48 (or_48_out, sec[10], sec[8], not_5_out, sec[5]);
  or or_49 (or_49_out, sec[11], sec[10], sec[8], not_6_out, not_7_out);
  or or_50 (or_50_out, sec[10], not_3_out, not_4_out, sec[7], sec[6]);
  or or_51 (or_51_out, sec[11], sec[10], not_4_out, sec[7]);
  or or_52 (or_52_out, sec[10], not_5_out, not_6_out, sec[5]);
  or or_53 (or_53_out, sec[11], not_3_out, not_4_out, not_5_out);
  or or_54 (or_54_out, sec[9], sec[8], sec[6], not_7_out, not_8_out, sec[3]);
  or or_55 (or_55_out, sec[9], sec[8], not_5_out, sec[6], not_7_out, not_8_out);
  or or_56 (or_56_out, sec[11], sec[9], not_4_out, sec[7]);
  or or_57 (or_57_out, sec[11], not_2_out, not_4_out, not_5_out);
  or or_58 (or_58_out, sec[11], not_2_out, sec[8], sec[7], sec[6], sec[5]);
  or or_59 (or_59_out, sec[11], not_2_out, sec[8], sec[7], sec[6], sec[4]);
  or or_60 (or_60_out, sec[11], not_2_out, sec[8], sec[7], sec[6], sec[3]);
  or or_61 (or_61_out, sec[11], not_2_out, not_3_out, sec[8], sec[7]);
  or or_62 (or_62_out, sec[11], not_2_out, sec[7], sec[6], sec[5], not_9_out);
  or or_63 (or_63_out, not_2_out, sec[7], sec[6], sec[5], not_8_out);
  or or_64 (or_64_out, not_2_out, sec[7], sec[6], not_7_out, sec[4]);
  or or_65 (or_65_out, not_2_out, sec[7], sec[6], not_8_out, sec[3]);
  or or_66 (or_66_out, not_3_out, not_4_out, sec[7], sec[6], not_9_out);
  or or_67 (or_67_out, not_2_out, not_4_out, sec[7], not_6_out);
  or or_68 (or_68_out, not_1_out, sec[9], sec[7], not_6_out, not_7_out);
  or or_69 (or_69_out, sec[10], sec[9], not_5_out, sec[6]);
  or or_70 (or_70_out, not_1_out, sec[10], sec[9], not_6_out, not_7_out, sec[4], sec[3]);
  or or_71 (or_71_out, not_1_out, sec[10], not_4_out, not_5_out, not_6_out);
  or or_72 (or_72_out, not_1_out, sec[10], sec[8], sec[7]);
  or or_73 (or_73_out, sec[10], not_3_out, sec[8], not_6_out, not_7_out);
  or or_74 (or_74_out, not_1_out, not_3_out, sec[6], not_7_out, not_8_out, not_9_out);
  or or_75 (or_75_out, not_1_out, sec[9], sec[8], sec[7]);
  or or_76 (or_76_out, not_1_out, sec[8], not_5_out, sec[6]);
  or or_77 (or_77_out, not_1_out, sec[8], not_7_out, sec[4], sec[3]);
  or or_78 (or_78_out, not_2_out, sec[9], sec[8], not_5_out, not_6_out);
  or or_79 (or_79_out, not_2_out, sec[9], sec[7], sec[6], sec[5]);
  or or_80 (or_80_out, not_1_out, not_2_out, sec[9], sec[7]);
  or or_81 (or_81_out, sec[10], sec[9], not_4_out, not_5_out, not_6_out, not_7_out);
  or or_82 (or_82_out, sec[11], not_2_out, not_4_out, sec[7]);
  or or_83 (or_83_out, not_1_out, sec[10], sec[9], not_5_out, not_6_out, not_7_out, not_8_out);
  or or_84 (or_84_out, not_1_out, sec[10], sec[9], not_4_out);
  or or_85 (or_85_out, not_1_out, not_2_out, sec[8], sec[7]);
  or or_86 (or_86_out, not_1_out, not_4_out, not_5_out, not_7_out);
  or or_87 (or_87_out, not_1_out, not_4_out, not_5_out, not_6_out);
  or or_88 (or_88_out, sec[11], sec[10], not_3_out, sec[7], sec[6]);
  or or_89 (or_89_out, sec[10], sec[9], not_5_out, not_6_out, not_7_out, sec[4], not_9_out);
  or or_90 (or_90_out, sec[10], not_3_out, sec[8], sec[7], sec[6]);
  or or_91 (or_91_out, not_2_out, sec[9], sec[8], not_5_out, sec[6], sec[5]);
  or or_92 (or_92_out, sec[10], not_3_out, sec[7], not_6_out, sec[5], sec[4], sec[3]);
  or or_93 (or_93_out, sec[11], not_2_out, not_4_out, sec[6], sec[5]);
  or or_94 (or_94_out, not_2_out, sec[8], not_5_out, sec[6], not_7_out, sec[4], sec[3]);
  or or_95 (or_95_out, sec[11], sec[10], sec[8], sec[6]);
  or or_96 (or_96_out, sec[11], sec[9], sec[8], not_6_out, sec[5]);
  or or_97 (or_97_out, sec[11], sec[9], sec[8], not_6_out, sec[4]);
  or or_98 (or_98_out, sec[11], sec[9], sec[8], sec[7], not_6_out);
  or or_99 (or_99_out, sec[10], not_3_out, sec[8], sec[7], sec[5], sec[4]);
  or or_100 (or_100_out, sec[11], sec[10], sec[8], sec[5]);
  or or_101 (or_101_out, sec[11], sec[10], sec[8], sec[4]);
  or or_102 (or_102_out, sec[11], sec[10], sec[8], sec[7]);
  or or_103 (or_103_out, sec[11], not_3_out, sec[8], not_5_out, not_6_out);
  or or_104 (or_104_out, sec[11], sec[9], sec[8], sec[6], not_7_out, not_8_out, not_9_out);
  or or_105 (or_105_out, sec[11], sec[8], not_5_out, sec[6], not_7_out);
  or or_106 (or_106_out, sec[11], not_2_out, sec[9], sec[8], not_5_out);
  or or_107 (or_107_out, sec[11], sec[8], not_5_out, sec[6], not_8_out);
  or or_108 (or_108_out, not_2_out, not_3_out, not_5_out, sec[6], not_7_out);
  or or_109 (or_109_out, not_2_out, not_3_out, not_5_out, not_6_out, sec[5]);
  or or_110 (or_110_out, not_2_out, not_3_out, not_4_out, sec[4]);
  or or_111 (or_111_out, not_2_out, not_3_out, not_5_out, not_8_out, sec[3]);
  or or_112 (or_112_out, not_1_out, not_3_out, sec[7], not_6_out, sec[5], sec[4]);
  or or_113 (or_113_out, not_1_out, sec[10], not_4_out, not_6_out);
  or or_114 (or_114_out, not_1_out, sec[10], not_4_out, not_5_out);
  or or_115 (or_115_out, not_2_out, not_5_out, sec[6], sec[5], not_8_out, not_9_out);
  or or_116 (or_116_out, sec[10], sec[9], sec[7], sec[6]);
  or or_117 (or_117_out, sec[11], sec[9], not_4_out, not_5_out, not_6_out, not_7_out);
  or or_118 (or_118_out, sec[10], not_3_out, not_5_out, sec[6]);
  or or_119 (or_119_out, sec[11], not_2_out, sec[9], sec[8], not_5_out);
  or or_120 (or_120_out, not_2_out, sec[9], not_5_out, not_6_out);
  or or_121 (or_121_out, not_2_out, not_3_out, not_4_out, sec[7]);
  or or_122 (or_122_out, sec[9], sec[8], not_5_out, not_6_out, not_7_out, not_8_out);
  or or_123 (or_123_out, sec[11], sec[10], not_3_out, sec[8], sec[7]);
  or or_124 (or_124_out, sec[11], not_2_out, sec[9], sec[8], not_7_out, not_8_out, not_9_out);
  or or_125 (or_125_out, not_2_out, not_5_out, not_6_out, not_7_out, not_8_out, not_9_out);
  or or_126 (or_126_out, not_1_out, sec[10], sec[9], sec[8], not_6_out, not_7_out, sec[4], not_9_out);
  or or_127 (or_127_out, not_1_out, sec[10], not_4_out, sec[7], not_6_out);
  or or_128 (or_128_out, not_1_out, not_3_out, not_4_out, not_6_out);
  or or_129 (or_129_out, not_1_out, not_2_out, sec[7], sec[6], sec[5]);
  or or_130 (or_130_out, not_1_out, not_2_out, sec[8], sec[7], sec[6], sec[4]);
  or or_131 (or_131_out, sec[11], sec[9], sec[8], sec[7], not_6_out, sec[3]);
  or or_132 (or_132_out, sec[11], not_3_out, sec[8], not_5_out, not_6_out, sec[5], sec[4]);
  or or_133 (or_133_out, not_3_out, sec[8], not_5_out, not_6_out, sec[5], sec[4], sec[3]);
  or or_134 (or_134_out, not_1_out, not_4_out, not_5_out, sec[6], not_8_out, not_9_out);
  or or_135 (or_135_out, sec[11], sec[9], sec[8], sec[7], not_6_out, sec[5]);
  or or_136 (or_136_out, sec[11], sec[9], sec[8], sec[7], not_6_out, sec[4]);
  or or_137 (or_137_out, sec[10], sec[9], sec[7], sec[5]);
  or or_138 (or_138_out, sec[10], sec[7], not_6_out, not_7_out, sec[4], sec[3]);
  or or_139 (or_139_out, sec[11], sec[10], sec[7], not_6_out, sec[5], not_9_out);
  or or_140 (or_140_out, sec[10], sec[7], not_6_out, sec[5], not_8_out);
  or or_141 (or_141_out, sec[11], sec[10], not_3_out, sec[7], not_6_out, not_9_out);
  or or_142 (or_142_out, sec[10], not_3_out, sec[7], not_6_out, not_8_out);
  or or_143 (or_143_out, sec[9], not_4_out, sec[7], sec[6], sec[5]);
  or or_144 (or_144_out, sec[11], sec[9], not_4_out, sec[7], sec[6], sec[4], sec[3]);
  or or_145 (or_145_out, sec[11], not_2_out, sec[9], not_4_out, sec[6], not_7_out, sec[4], sec[3]);
  or or_146 (or_146_out, not_2_out, sec[9], not_5_out, not_7_out, not_9_out);
  or or_147 (or_147_out, not_2_out, sec[9], not_5_out, not_7_out, not_8_out);
  or or_148 (or_148_out, sec[11], not_3_out, sec[8], sec[7], sec[6], sec[5], sec[4]);
  or or_149 (or_149_out, sec[11], not_3_out, sec[8], sec[7], sec[6], sec[5], sec[3]);
  or or_150 (or_150_out, sec[11], not_3_out, sec[8], sec[6], sec[5], not_8_out, sec[3]);
  or or_151 (or_151_out, sec[11], not_2_out, sec[8], not_5_out, not_8_out);
  or or_152 (or_152_out, sec[11], not_2_out, sec[8], not_5_out, not_7_out);
  or or_153 (or_153_out, not_1_out, sec[10], sec[9], not_4_out, sec[6]);
  or or_154 (or_154_out, not_1_out, sec[10], sec[9], not_4_out, sec[5], sec[4]);
  or or_155 (or_155_out, not_1_out, sec[10], sec[9], not_4_out, sec[5], sec[3]);
  or or_156 (or_156_out, sec[10], sec[8], sec[7], not_6_out, not_7_out, sec[4]);
  or or_157 (or_157_out, not_1_out, not_4_out, not_5_out, sec[6], not_7_out);
  or or_158 (or_158_out, sec[11], sec[10], sec[9], sec[8], sec[7], sec[6], sec[3]);
  or or_159 (or_159_out, sec[11], sec[10], sec[9], sec[8], sec[6], sec[4]);
  or or_160 (or_160_out, sec[11], sec[10], sec[9], sec[7], sec[6], sec[4], sec[3]);
  or or_161 (or_161_out, sec[11], sec[10], sec[9], sec[6], sec[5]);
  or or_162 (or_162_out, sec[11], sec[10], sec[8], sec[7], sec[6], sec[5], sec[3]);
  or or_163 (or_163_out, sec[11], sec[10], sec[8], sec[6], sec[5], sec[4]);
  or or_164 (or_164_out, sec[11], sec[10], sec[7], sec[6], sec[5], sec[4], sec[3]);
  or or_165 (or_165_out, sec[11], not_2_out, sec[9], sec[8], sec[7], not_6_out, sec[4]);
  or or_166 (or_166_out, sec[11], not_2_out, sec[9], sec[8], sec[7], not_6_out, sec[3], sec[2]);
  or or_167 (or_167_out, not_2_out, sec[9], sec[8], not_6_out, sec[5]);
  or or_168 (or_168_out, sec[11], not_2_out, sec[9], sec[8], not_6_out, sec[4], sec[3]);
  or or_169 (or_169_out, sec[11], not_2_out, sec[9], sec[8], not_6_out, sec[4], sec[2]);
  or or_170 (or_170_out, sec[11], not_2_out, sec[9], sec[7], not_6_out, sec[5]);
  or or_171 (or_171_out, sec[11], not_2_out, sec[9], sec[7], not_6_out, sec[4], sec[3], sec[2]);
  or or_172 (or_172_out, not_2_out, sec[9], not_6_out, sec[5], sec[4]);
  or or_173 (or_173_out, sec[11], not_2_out, sec[9], not_6_out, sec[5], sec[3]);
  or or_174 (or_174_out, sec[11], not_2_out, sec[9], not_6_out, sec[5], sec[2]);
  or or_175 (or_175_out, not_2_out, sec[8], sec[7], not_6_out, sec[5], sec[4]);
  or or_176 (or_176_out, not_2_out, sec[8], sec[7], not_6_out, sec[5], sec[3], sec[2]);
  or or_177 (or_177_out, not_2_out, sec[8], not_6_out, sec[5], sec[4], sec[3]);
  or or_178 (or_178_out, not_2_out, sec[8], not_6_out, sec[5], sec[4], sec[2]);
  or or_179 (or_179_out, not_2_out, sec[7], not_6_out, sec[5], sec[4], sec[3], sec[2]);
  or or_180 (or_180_out, not_2_out, not_3_out, not_4_out, not_5_out, not_6_out, not_7_out, not_8_out, not_9_out);
  or or_181 (or_181_out, sec[10], sec[9], sec[8], sec[7], sec[6], sec[4]);
  or or_182 (or_182_out, sec[10], sec[9], sec[8], sec[6], sec[5]);
  or or_183 (or_183_out, sec[10], sec[9], sec[8], sec[6], sec[4], sec[3]);
  or or_184 (or_184_out, sec[10], sec[9], sec[7], sec[6], sec[5]);
  or or_185 (or_185_out, sec[10], sec[9], sec[6], sec[5], sec[4]);
  or or_186 (or_186_out, sec[10], sec[9], sec[6], sec[5], sec[3]);
  or or_187 (or_187_out, sec[10], sec[8], sec[7], sec[6], sec[5], sec[4]);
  or or_188 (or_188_out, not_1_out, not_3_out, not_4_out, not_5_out, sec[6], not_7_out, not_8_out, not_9_out);
  or or_189 (or_189_out, not_1_out, not_2_out, sec[6], not_7_out, not_8_out);
  or or_190 (or_190_out, not_1_out, not_2_out, not_5_out, sec[6], not_7_out, not_9_out);
  or or_191 (or_191_out, not_1_out, not_2_out, not_4_out, sec[6], not_7_out);
  or or_192 (or_192_out, not_1_out, not_2_out, not_4_out, not_5_out, sec[6], not_8_out, not_9_out);
  or or_193 (or_193_out, not_1_out, sec[10], sec[9], sec[8], sec[7], not_7_out, not_8_out, sec[3], sec[2]);
  or or_194 (or_194_out, not_1_out, sec[10], sec[9], sec[8], not_5_out, not_7_out, sec[4], not_9_out, sec[2]);
  or or_195 (or_195_out, not_1_out, sec[10], sec[9], not_4_out, sec[7], not_7_out, sec[4], sec[3], sec[2]);
  or or_196 (or_196_out, not_1_out, sec[10], sec[9], not_4_out, not_5_out, sec[5], not_8_out, not_9_out, sec[2]);
  or or_197 (or_197_out, not_1_out, not_3_out, sec[8], sec[7], sec[5], not_8_out, sec[3], sec[2]);
  or or_198 (or_198_out, not_1_out, not_3_out, not_4_out, sec[7], sec[5], sec[4], sec[3], sec[2]);
  or or_199 (or_199_out, sec[11], sec[9], sec[8], sec[7], sec[6], not_7_out, not_8_out, not_9_out, sec[2]);
  or or_200 (or_200_out, sec[11], sec[10], sec[9], sec[8], sec[7], not_7_out, not_8_out, not_9_out, sec[2]);
  or or_201 (or_201_out, sec[10], sec[8], not_6_out, not_7_out, not_8_out, not_9_out);
  or or_202 (or_202_out, sec[11], sec[9], sec[8], not_5_out, sec[6], not_7_out, not_8_out, sec[3], sec[2]);
  or or_203 (or_203_out, sec[11], sec[10], sec[9], sec[8], not_5_out, not_7_out, not_8_out, sec[3], sec[2]);
  or or_204 (or_204_out, sec[10], sec[8], not_5_out, not_6_out, not_7_out, not_8_out);
  or or_205 (or_205_out, sec[11], sec[9], not_4_out, sec[7], sec[6], not_7_out, sec[4], not_9_out, sec[2]);
  or or_206 (or_206_out, sec[11], sec[10], sec[9], not_4_out, sec[7], not_7_out, sec[4], not_9_out, sec[2]);
  or or_207 (or_207_out, sec[11], sec[10], not_4_out, sec[7], not_6_out, not_7_out, not_9_out);
  or or_208 (or_208_out, sec[10], not_4_out, sec[7], not_6_out, not_7_out, not_8_out, sec[3]);
  or or_209 (or_209_out, sec[11], sec[9], not_4_out, not_5_out, sec[6], not_7_out, sec[4], sec[3], sec[2]);
  or or_210 (or_210_out, sec[11], sec[10], sec[9], not_4_out, not_5_out, not_7_out, sec[4], sec[3], sec[2]);
  or or_211 (or_211_out, sec[10], not_4_out, not_5_out, not_6_out, not_7_out, sec[4]);
  or or_212 (or_212_out, sec[10], not_4_out, not_5_out, not_6_out, not_7_out, sec[3], sec[2]);
  or or_213 (or_213_out, sec[11], sec[10], not_4_out, not_5_out, not_6_out, not_7_out, sec[3]);
  or or_214 (or_214_out, sec[11], sec[10], not_4_out, not_6_out, not_7_out, not_8_out, sec[2]);
  or or_215 (or_215_out, sec[10], sec[9], not_5_out, not_6_out, not_7_out, not_8_out);
  or or_216 (or_216_out, sec[11], not_3_out, sec[8], sec[7], sec[6], sec[5], not_8_out, not_9_out, sec[2]);
  or or_217 (or_217_out, sec[11], sec[10], not_3_out, sec[8], sec[7], sec[5], not_8_out, not_9_out, sec[2]);
  or or_218 (or_218_out, sec[10], not_3_out, sec[8], not_6_out, not_8_out, not_9_out);
  or or_219 (or_219_out, sec[10], not_3_out, sec[8], not_6_out, not_7_out);
  or or_220 (or_220_out, sec[11], not_3_out, sec[8], not_5_out, sec[6], sec[5], not_8_out, sec[3], sec[2]);
  or or_221 (or_221_out, sec[11], sec[10], not_3_out, sec[8], not_5_out, sec[5], not_8_out, sec[3], sec[2]);
  or or_222 (or_222_out, sec[10], not_3_out, sec[8], not_5_out, not_6_out, not_8_out);
  or or_223 (or_223_out, sec[11], not_3_out, not_4_out, sec[7], sec[6], sec[5], sec[4], not_9_out, sec[2]);
  or or_224 (or_224_out, sec[11], sec[10], not_3_out, not_4_out, sec[7], sec[5], sec[4], not_9_out, sec[2]);
  or or_225 (or_225_out, sec[11], sec[10], not_3_out, not_4_out, sec[7], not_6_out, not_9_out);
  or or_226 (or_226_out, sec[10], not_3_out, not_4_out, sec[7], not_6_out, not_8_out, sec[3]);
  or or_227 (or_227_out, sec[10], not_3_out, sec[7], not_6_out, not_7_out, sec[3]);
  or or_228 (or_228_out, sec[11], not_3_out, not_4_out, not_5_out, sec[6], sec[5], sec[4], sec[3], sec[2]);
  or or_229 (or_229_out, sec[11], sec[10], not_3_out, not_4_out, not_5_out, sec[5], sec[4], sec[3], sec[2]);
  or or_230 (or_230_out, sec[10], not_3_out, not_4_out, not_5_out, not_6_out, sec[5]);
  or or_231 (or_231_out, not_2_out, sec[8], sec[6], not_7_out, not_8_out, not_9_out);
  or or_232 (or_232_out, not_2_out, sec[8], not_5_out, sec[6], not_7_out, not_8_out);
  or or_233 (or_233_out, not_2_out, not_4_out, sec[7], sec[6], not_7_out, not_9_out);
  or or_234 (or_234_out, not_2_out, not_4_out, sec[7], sec[6], not_7_out, not_8_out);
  or or_235 (or_235_out, not_2_out, not_4_out, not_5_out, sec[6], not_7_out, sec[4]);
  or or_236 (or_236_out, not_2_out, not_5_out, sec[6], not_7_out, not_8_out, sec[3]);
  or or_237 (or_237_out, not_2_out, not_4_out, sec[6], not_7_out, not_8_out, sec[2]);
  or or_238 (or_238_out, not_2_out, sec[9], not_4_out, not_5_out, sec[6], not_7_out);
  or or_239 (or_239_out, not_2_out, not_3_out, sec[8], sec[6], not_8_out, not_9_out);
  or or_240 (or_240_out, not_2_out, not_3_out, sec[8], sec[6], not_7_out);
  or or_241 (or_241_out, not_2_out, not_3_out, sec[8], not_5_out, sec[6], not_8_out);
  or or_242 (or_242_out, not_2_out, not_3_out, not_4_out, sec[7], sec[6], not_9_out);
  or or_243 (or_243_out, not_2_out, not_3_out, not_4_out, sec[7], sec[6], not_8_out);
  or or_244 (or_244_out, not_2_out, not_3_out, sec[7], sec[6], not_7_out);
  or or_245 (or_245_out, not_2_out, not_3_out, not_4_out, not_5_out, sec[6], sec[5]);
  or or_246 (or_246_out, not_1_out, sec[10], sec[8], not_6_out, not_7_out, not_8_out);
  or or_247 (or_247_out, not_1_out, sec[10], sec[8], not_5_out, not_6_out, not_7_out, not_9_out);
  or or_248 (or_248_out, not_1_out, sec[10], not_4_out, sec[7], not_6_out, not_7_out, sec[3]);
  or or_249 (or_249_out, not_1_out, sec[10], not_4_out, sec[7], not_6_out, not_7_out, sec[2]);
  or or_250 (or_250_out, sec[10], not_4_out, not_6_out, not_7_out, sec[4], not_9_out);
  or or_251 (or_251_out, sec[10], sec[9], not_4_out, not_6_out, not_7_out, not_9_out);
  or or_252 (or_252_out, not_1_out, sec[10], not_4_out, not_5_out, not_6_out, sec[5], not_8_out, not_9_out);
  or or_253 (or_253_out, not_1_out, not_3_out, sec[8], not_6_out, not_8_out);
  or or_254 (or_254_out, not_1_out, not_3_out, sec[8], not_5_out, sec[6], sec[5], sec[4], sec[3]);
  or or_255 (or_255_out, not_1_out, not_3_out, sec[8], not_5_out, sec[6], sec[5], sec[4], sec[2]);
  or or_256 (or_256_out, not_1_out, not_3_out, sec[8], not_5_out, sec[5], sec[4], not_9_out, sec[2]);
  or or_257 (or_257_out, not_1_out, not_3_out, sec[8], not_5_out, not_6_out, not_9_out);
  or or_258 (or_258_out, not_1_out, not_3_out, not_4_out, sec[7], not_6_out, sec[3]);
  or or_259 (or_259_out, not_1_out, not_3_out, not_4_out, sec[7], not_6_out, sec[2]);
  or or_260 (or_260_out, sec[10], not_3_out, not_4_out, not_6_out, sec[5], not_9_out);
  or or_261 (or_261_out, not_2_out, sec[9], sec[8], sec[7], not_6_out, sec[4], sec[3]);
  or or_262 (or_262_out, not_2_out, sec[9], sec[8], sec[7], not_6_out, sec[4], sec[2]);
  or or_263 (or_263_out, not_2_out, sec[9], sec[8], not_6_out, sec[4], sec[3], sec[2]);
  or or_264 (or_264_out, not_2_out, sec[9], sec[7], not_6_out, sec[5], sec[3]);
  or or_265 (or_265_out, not_2_out, sec[9], sec[7], not_6_out, sec[5], sec[2]);
  or or_266 (or_266_out, not_2_out, sec[9], not_6_out, sec[5], sec[3], sec[2]);
  and and_1 (minuteH[2], sec[11], or_1_out, or_2_out, or_3_out);
  and and_2 (minuteH[1], or_4_out, or_5_out, or_6_out, or_7_out, or_8_out, or_9_out, or_10_out, or_11_out);
  and and_3 (minuteH[0], or_12_out, or_13_out, or_14_out, or_15_out, or_16_out, or_17_out, or_18_out, or_19_out, or_20_out, or_21_out, or_22_out, or_23_out, or_24_out, or_25_out, or_26_out, or_27_out);
  and and_4 (minuteL[2], or_81_out, or_82_out, or_83_out, or_84_out, or_85_out, or_86_out, or_87_out, or_88_out, or_89_out, or_90_out, or_91_out, or_92_out, or_93_out, or_94_out, or_95_out, or_96_out, or_97_out, or_98_out, or_99_out, or_100_out, or_101_out, or_102_out, or_103_out, or_104_out, or_105_out, or_106_out, or_107_out, or_108_out, or_109_out, or_110_out, or_111_out, or_112_out, or_113_out, or_114_out, or_115_out);
  and and_5 (minuteL[3], or_28_out, or_29_out, or_30_out, or_31_out, or_32_out, or_33_out, or_34_out, or_35_out, or_36_out, or_37_out, or_38_out, or_39_out, or_40_out, or_41_out, or_42_out, or_43_out, or_44_out, or_45_out, or_46_out, or_47_out, or_48_out, or_49_out, or_50_out, or_51_out, or_52_out, or_53_out, or_54_out, or_55_out, or_56_out, or_57_out, or_58_out, or_59_out, or_60_out, or_61_out, or_62_out, or_63_out, or_64_out, or_65_out, or_66_out, or_67_out, or_68_out, or_69_out, or_70_out, or_71_out, or_72_out, or_73_out, or_74_out, or_75_out, or_76_out, or_77_out, or_78_out, or_79_out, or_80_out);
  and and_6 (minuteL[1], or_116_out, or_117_out, or_118_out, or_119_out, or_120_out, or_121_out, or_122_out, or_123_out, or_124_out, or_125_out, or_126_out, or_127_out, or_128_out, or_129_out, or_130_out, or_131_out, or_132_out, or_133_out, or_134_out, or_135_out, or_136_out, or_137_out, or_138_out, or_139_out, or_140_out, or_141_out, or_142_out, or_143_out, or_144_out, or_145_out, or_146_out, or_147_out, or_148_out, or_149_out, or_150_out, or_151_out, or_152_out, or_153_out, or_154_out, or_155_out, or_156_out, or_157_out);
  and and_7 (and_7_out, or_158_out, or_159_out, or_160_out, or_161_out, or_162_out, or_163_out, or_164_out, or_165_out, or_166_out, or_167_out, or_168_out, or_169_out, or_170_out, or_171_out, or_172_out, or_173_out, or_174_out, or_175_out, or_176_out, or_177_out, or_178_out, or_179_out, or_180_out, or_181_out, or_182_out, or_183_out, or_184_out, or_185_out, or_186_out, or_187_out, or_188_out, or_189_out, or_190_out, or_191_out, or_192_out, or_193_out, or_194_out, or_195_out, or_196_out, or_197_out, or_198_out, or_199_out, or_200_out, or_201_out, or_202_out, or_203_out, or_204_out, or_205_out, or_206_out, or_207_out, or_208_out, or_209_out, or_210_out, or_211_out, or_212_out);
  and and_8 (and_8_out, or_213_out, or_214_out, or_215_out, or_216_out, or_217_out, or_218_out, or_219_out, or_220_out, or_221_out, or_222_out, or_223_out, or_224_out, or_225_out, or_226_out, or_227_out, or_228_out, or_229_out, or_230_out, or_231_out, or_232_out, or_233_out, or_234_out, or_235_out, or_236_out, or_237_out, or_238_out, or_239_out, or_240_out, or_241_out, or_242_out, or_243_out, or_244_out, or_245_out, or_246_out, or_247_out, or_248_out, or_249_out, or_250_out, or_251_out, or_252_out, or_253_out, or_254_out, or_255_out, or_256_out, or_257_out, or_258_out, or_259_out, or_260_out, or_261_out, or_262_out, or_263_out, or_264_out, or_265_out, or_266_out);
  and and_9 (minuteL[0], and_7_out, and_8_out);

  assign minuteH[3] = 1'b0;

  // Notes on the sheet:
  //   this circuit take in 12 bit representing the ammount of second
  //   and output 2*4 bit representing the time in DCB for the minute elapsed
  //   the truthtable was generated with a python script as it was faster than laying out 59 comparator and a 2^6 priority encoder that is not available anyway
endmodule
