// Logisim project Add1second.circ as structural Verilog: 2 circuits, main circuit main
module main (
);

  Add1 add1_1 ();  // open: ValEntree, Plus1, ValSortie, Retenue
endmodule

module Add1 (
  input  ValEntree,
  input  Plus1,
  output ValSortie,
  output Retenue
);

  wire not_1_out;

  not not_1 (not_1_out, Plus1);
  or or_1 (ValSortie, ValEntree, not_1_out);
  and and_1 (Retenue, ValEntree, Plus1);
endmodule
