// Logisim project Chrono2.circ as structural Verilog: 19 circuits, main circuit main
module main (
);

  wire clock_1_out, clock_2_out, compte24_1_adec, compte24_1_aunite, compte24_1_bdec, compte24_1_bunite,
       compte24_1_cdec, compte24_1_cunite, compte24_1_ddec, compte24_1_dunite, compte60_1_adec,
       compte60_1_aunite, compte60_1_bdec, compte60_1_bunite, compte60_1_cdec, compte60_1_cunite,
       compte60_1_ddec, compte60_1_dunite, compte60_1_plus1, compte60_2_adec, compte60_2_aunite,
       compte60_2_bdec, compte60_2_bunite, compte60_2_cdec, compte60_2_cunite, compte60_2_ddec,
       compte60_2_dunite, segmentdisplaycontroller_1_a, segmentdisplaycontroller_1_b,
       segmentdisplaycontroller_1_c, segmentdisplaycontroller_1_d, segmentdisplaycontroller_1_e,
       segmentdisplaycontroller_1_f, segmentdisplaycontroller_1_g, segmentdisplaycontroller_2_a,
       segmentdisplaycontroller_2_b, segmentdisplaycontroller_2_c, segmentdisplaycontroller_2_d,
       segmentdisplaycontroller_2_e, segmentdisplaycontroller_2_f, segmentdisplaycontroller_2_g,
       segmentdisplaycontroller_3_a, segmentdisplaycontroller_3_b, segmentdisplaycontroller_3_c,
       segmentdisplaycontroller_3_d, segmentdisplaycontroller_3_e, segmentdisplaycontroller_3_f,
       segmentdisplaycontroller_3_g, segmentdisplaycontroller_4_a, segmentdisplaycontroller_4_b,
       segmentdisplaycontroller_4_c, segmentdisplaycontroller_4_d, segmentdisplaycontroller_4_e,
       segmentdisplaycontroller_4_f, segmentdisplaycontroller_4_g, segmentdisplaycontroller_5_a,
       segmentdisplaycontroller_5_b, segmentdisplaycontroller_5_c, segmentdisplaycontroller_5_d,
       segmentdisplaycontroller_5_e, segmentdisplaycontroller_5_f, segmentdisplaycontroller_5_g,
       segmentdisplaycontroller_6_a, segmentdisplaycontroller_6_b, segmentdisplaycontroller_6_c,
       segmentdisplaycontroller_6_d, segmentdisplaycontroller_6_e, segmentdisplaycontroller_6_f,
       segmentdisplaycontroller_6_g;

  Clock clock_1 (.out(clock_1_out));
  Clock clock_2 (.out(clock_2_out));
  compte60 compte60_1 (
    .EN(clock_1_out), .Bunite(compte60_1_bunite), .Aunite(compte60_1_aunite), .Dunite(compte60_1_dunite),
    .Cunite(compte60_1_cunite), .Bdec(compte60_1_bdec), .Adec(compte60_1_adec), .Ddec(compte60_1_ddec),
    .Cdec(compte60_1_cdec), .plus1(compte60_1_plus1));  // open: reset
  compte24 compte24_1 (
    .EN(clock_2_out), .Aunite(compte24_1_aunite), .Bunite(compte24_1_bunite), .Cunite(compte24_1_cunite),
    .Dunite(compte24_1_dunite), .Adec(compte24_1_adec), .Bdec(compte24_1_bdec), .Cdec(compte24_1_cdec),
    .Ddec(compte24_1_ddec));  // open: reset, plus1
  compte60 compte60_2 (
    .EN(compte60_1_plus1), .Bunite(compte60_2_bunite), .Aunite(compte60_2_aunite),
    .Dunite(compte60_2_dunite), .Cunite(compte60_2_cunite), .Bdec(compte60_2_bdec), .Adec(compte60_2_adec),
    .Ddec(compte60_2_ddec), .Cdec(compte60_2_cdec));  // open: reset, plus1
  SegmentDisplayController segmentdisplaycontroller_1 (
    .B_B(compte60_1_bunite), .B_A(compte60_1_aunite), .B_D(compte60_1_dunite), .B_C(compte60_1_cunite),
    .A(segmentdisplaycontroller_1_a), .B(segmentdisplaycontroller_1_b), .C(segmentdisplaycontroller_1_c),
    .D(segmentdisplaycontroller_1_d), .E(segmentdisplaycontroller_1_e), .F(segmentdisplaycontroller_1_f),
    .G(segmentdisplaycontroller_1_g));
  _7_Segment_Display u_7_segment_display_1 (
    .g(segmentdisplaycontroller_1_g), .f(segmentdisplaycontroller_1_f), .a(segmentdisplaycontroller_1_a),
    .b(segmentdisplaycontroller_1_b), .e(segmentdisplaycontroller_1_e), .d(segmentdisplaycontroller_1_d),
    .c(segmentdisplaycontroller_1_c));  // open: dp
  SegmentDisplayController segmentdisplaycontroller_2 (
    .B_B(compte60_1_bdec), .B_A(compte60_1_adec), .B_D(compte60_1_ddec), .B_C(compte60_1_cdec),
    .A(segmentdisplaycontroller_2_a), .B(segmentdisplaycontroller_2_b), .C(segmentdisplaycontroller_2_c),
    .D(segmentdisplaycontroller_2_d), .E(segmentdisplaycontroller_2_e), .F(segmentdisplaycontroller_2_f),
    .G(segmentdisplaycontroller_2_g));
  _7_Segment_Display u_7_segment_display_2 (
    .g(segmentdisplaycontroller_2_g), .f(segmentdisplaycontroller_2_f), .a(segmentdisplaycontroller_2_a),
    .b(segmentdisplaycontroller_2_b), .e(segmentdisplaycontroller_2_e), .d(segmentdisplaycontroller_2_d),
    .c(segmentdisplaycontroller_2_c));  // open: dp
  SegmentDisplayController segmentdisplaycontroller_3 (
    .B_B(compte60_2_bunite), .B_A(compte60_2_aunite), .B_D(compte60_2_dunite), .B_C(compte60_2_cunite),
    .A(segmentdisplaycontroller_3_a), .B(segmentdisplaycontroller_3_b), .C(segmentdisplaycontroller_3_c),
    .D(segmentdisplaycontroller_3_d), .E(segmentdisplaycontroller_3_e), .F(segmentdisplaycontroller_3_f),
    .G(segmentdisplaycontroller_3_g));
  _7_Segment_Display u_7_segment_display_3 (
    .g(segmentdisplaycontroller_3_g), .f(segmentdisplaycontroller_3_f), .a(segmentdisplaycontroller_3_a),
    .b(segmentdisplaycontroller_3_b), .e(segmentdisplaycontroller_3_e), .d(segmentdisplaycontroller_3_d),
    .c(segmentdisplaycontroller_3_c));  // open: dp
  SegmentDisplayController segmentdisplaycontroller_4 (
    .B_B(compte60_2_bdec), .B_A(compte60_2_adec), .B_D(compte60_2_ddec), .B_C(compte60_2_cdec),
    .A(segmentdisplaycontroller_4_a), .B(segmentdisplaycontroller_4_b), .C(segmentdisplaycontroller_4_c),
    .D(segmentdisplaycontroller_4_d), .E(segmentdisplaycontroller_4_e), .F(segmentdisplaycontroller_4_f),
    .G(segmentdisplaycontroller_4_g));
  _7_Segment_Display u_7_segment_display_4 (
    .g(segmentdisplaycontroller_4_g), .f(segmentdisplaycontroller_4_f), .a(segmentdisplaycontroller_4_a),
    .b(segmentdisplaycontroller_4_b), .e(segmentdisplaycontroller_4_e), .d(segmentdisplaycontroller_4_d),
    .c(segmentdisplaycontroller_4_c));  // open: dp
  SegmentDisplayController segmentdisplaycontroller_5 (
    .B_B(compte24_1_bunite), .B_A(compte24_1_aunite), .B_D(compte24_1_dunite), .B_C(compte24_1_cunite),
    .A(segmentdisplaycontroller_5_a), .B(segmentdisplaycontroller_5_b), .C(segmentdisplaycontroller_5_c),
    .D(segmentdisplaycontroller_5_d), .E(segmentdisplaycontroller_5_e), .F(segmentdisplaycontroller_5_f),
    .G(segmentdisplaycontroller_5_g));
  _7_Segment_Display u_7_segment_display_5 (
    .g(segmentdisplaycontroller_5_g), .f(segmentdisplaycontroller_5_f), .a(segmentdisplaycontroller_5_a),
    .b(segmentdisplaycontroller_5_b), .e(segmentdisplaycontroller_5_e), .d(segmentdisplaycontroller_5_d),
    .c(segmentdisplaycontroller_5_c));  // open: dp
  SegmentDisplayController segmentdisplaycontroller_6 (
    .B_B(compte24_1_bdec), .B_A(compte24_1_adec), .B_D(compte24_1_ddec), .B_C(compte24_1_cdec),
    .A(segmentdisplaycontroller_6_a), .B(segmentdisplaycontroller_6_b), .C(segmentdisplaycontroller_6_c),
    .D(segmentdisplaycontroller_6_d), .E(segmentdisplaycontroller_6_e), .F(segmentdisplaycontroller_6_f),
    .G(segmentdisplaycontroller_6_g));
  _7_Segment_Display u_7_segment_display_6 (
    .g(segmentdisplaycontroller_6_g), .f(segmentdisplaycontroller_6_f), .a(segmentdisplaycontroller_6_a),
    .b(segmentdisplaycontroller_6_b), .e(segmentdisplaycontroller_6_e), .d(segmentdisplaycontroller_6_d),
    .c(segmentdisplaycontroller_6_c));  // open: dp
endmodule

module SegmentDisplayController (
  input  B_B,
  input  B_A,
  input  B_D,
  input  B_C,
  output A,
  output B,
  output C,
  output D,
  output E,
  output F,
  output G
);

  wire not_1_out, not_2_out, not_3_out, not_4_out;

  not not_1 (not_1_out, B_D);
  not not_2 (not_2_out, B_C);
  not not_3 (not_3_out, B_B);
  not not_4 (not_4_out, B_A);
  SegmentA_AUTO segmenta_auto_1 (.W(B_D), .X(B_C), .Y(B_B), .Z(B_A), .O(A));
  SegmentB_AUTO segmentb_auto_1 (.W(B_D), .X(B_C), .Y(B_B), .Z(B_A), .O(B));
  SegmentC_AUTO segmentc_auto_1 (.W(B_D), .X(B_C), .Y(B_B), .Z(B_A), .O(C));
  SegmentD segmentd_1 (.W(B_D), .X(B_C), .Y(B_B), .Z(B_A), .O(D));
  SegmentE segmente_1 (.W(B_D), .X(B_C), .Y(B_B), .Z(B_A), .O(E));
  SegmentF segmentf_1 (.W(B_D), .X(B_C), .Y(B_B), .Z(B_A), .O(F));
  SegmentG segmentg_1 (.W(B_D), .X(B_C), .Y(B_B), .Z(B_A), .O(G));
  _7_Segment_Display u_7_segment_display_1 (.g(G), .f(F), .a(A), .b(B), .e(E), .d(D), .c(C));  // open: dp
endmodule

module SegmentD (
  input  W,
  input  X,
  input  Y,
  input  Z,
  output O
);

  wire and_1_out, and_2_out, and_3_out, and_4_out, and_5_out, not_1_out, not_2_out, not_3_out, not_4_out,
       not_5_out, not_6_out, not_7_out;

  not not_1 (not_1_out, W);
  not not_2 (not_2_out, X);
  not not_3 (not_3_out, Z);
  not not_4 (not_4_out, X);
  not not_5 (not_5_out, Y);
  not not_6 (not_6_out, Z);
  not not_7 (not_7_out, Y);
  and and_1 (and_1_out, not_1_out, not_2_out, not_3_out);
  and and_2 (and_2_out, not_4_out, Y, Z);
  and and_3 (and_3_out, X, not_5_out, Z);
  and and_4 (and_4_out, X, Y, not_6_out);
  and and_5 (and_5_out, W, not_7_out);
  or or_1 (O, and_1_out, and_2_out, and_3_out, and_4_out, and_5_out);
endmodule

module SegmentG (
  input  W,
  input  X,
  input  Y,
  input  Z,
  output O
);

  wire and_1_out, and_2_out, and_3_out, and_4_out, and_5_out, not_1_out, not_2_out, not_3_out, not_4_out,
       not_5_out;

  not not_1 (not_1_out, X);
  not not_2 (not_2_out, Z);
  not not_3 (not_3_out, W);
  not not_4 (not_4_out, Y);
  not not_5 (not_5_out, X);
  and and_1 (and_1_out, not_1_out, Y);
  and and_2 (and_2_out, Y, not_2_out);
  and and_3 (and_3_out, not_3_out, X, not_4_out);
  and and_4 (and_4_out, W, not_5_out);
  and and_5 (and_5_out, W, Z);
  or or_1 (O, and_1_out, and_2_out, and_3_out, and_4_out, and_5_out);
endmodule

module SegmentE (
  input  W,
  input  X,
  input  Y,
  input  Z,
  output O
);

  wire and_1_out, and_2_out, and_3_out, and_4_out, not_1_out, not_2_out, not_3_out;

  not not_1 (not_1_out, X);
  not not_2 (not_2_out, Z);
  not not_3 (not_3_out, Z);
  and and_1 (and_1_out, not_1_out, not_2_out);
  and and_2 (and_2_out, Y, not_3_out);
  and and_3 (and_3_out, W, Y);
  and and_4 (and_4_out, W, X);
  or or_1 (O, and_1_out, and_2_out, and_3_out, and_4_out);
endmodule

module SegmentF (
  input  W,
  input  X,
  input  Y,
  input  Z,
  output O
);

  wire and_1_out, and_2_out, and_3_out, and_4_out, and_5_out, not_1_out, not_2_out, not_3_out, not_4_out,
       not_5_out, not_6_out;

  not not_1 (not_1_out, Y);
  not not_2 (not_2_out, Z);
  not not_3 (not_3_out, W);
  not not_4 (not_4_out, Y);
  not not_5 (not_5_out, Z);
  not not_6 (not_6_out, X);
  and and_1 (and_1_out, not_1_out, not_2_out);
  and and_2 (and_2_out, not_3_out, X, not_4_out);
  and and_3 (and_3_out, X, not_5_out);
  and and_4 (and_4_out, W, not_6_out);
  and and_5 (and_5_out, W, Y);
  or or_1 (O, and_1_out, and_2_out, and_3_out, and_4_out, and_5_out);
endmodule

module SegmentA_AUTO (
  input  W,
  input  X,
  input  Y,
  input  Z,
  output O
);

  wire not_1_out, not_2_out, not_3_out, not_4_out, not_5_out, not_6_out, not_7_out, not_8_out, or_1_out,
       or_2_out, or_3_out, or_4_out;

  not not_1 (not_1_out, Z);
  not not_2 (not_2_out, X);
  not not_3 (not_3_out, W);
  not not_4 (not_4_out, Y);
  not not_5 (not_5_out, Z);
  not not_6 (not_6_out, W);
  not not_7 (not_7_out, X);
  not not_8 (not_8_out, Z);
  or or_1 (or_1_out, W, X, Y, not_1_out);
  or or_2 (or_2_out, W, not_2_out, Y, Z);
  or or_3 (or_3_out, not_3_out, X, not_4_out, not_5_out);
  or or_4 (or_4_out, not_6_out, not_7_out, Y, not_8_out);
  and and_1 (O, or_1_out, or_2_out, or_3_out, or_4_out);
endmodule

module SegmentB_AUTO (
  input  W,
  input  X,
  input  Y,
  input  Z,
  output O
);

  wire nand_1_out, nand_2_out, nand_3_out, nand_4_out, nand_5_out, nand_6_out, nand_7_out, nand_8_out,
       nand_9_out;

  nand nand_1 (nand_1_out, W, W);
  nand nand_2 (nand_2_out, Y, Y);
  nand nand_3 (nand_3_out, Z, Z);
  nand nand_4 (nand_4_out, Z, Z);
  nand nand_5 (nand_5_out, nand_1_out, X, nand_2_out, Z);
  nand nand_6 (nand_6_out, X, Y, nand_3_out);
  nand nand_7 (nand_7_out, W, Y, Z);
  nand nand_8 (nand_8_out, W, X, nand_4_out);
  nand nand_9 (nand_9_out, nand_5_out, nand_6_out, nand_7_out, nand_8_out);
  nand nand_10 (O, nand_9_out, nand_9_out);
endmodule

module SegmentC_AUTO (
  input  W,
  input  X,
  input  Y,
  input  Z,
  output O
);

  wire nand_1_out, nand_2_out, nand_3_out, nand_4_out, nand_5_out, nand_6_out, nand_7_out, nand_8_out,
       nand_9_out, nand_10_out, nand_11_out, nand_12_out, nand_13_out, nand_14_out, nand_15_out, nand_16_out,
       nand_17_out, nand_18_out;

  nand nand_1 (nand_1_out, W, W);
  nand nand_2 (nand_2_out, X, X);
  nand nand_3 (nand_3_out, Z, Z);
  nand nand_4 (nand_4_out, nand_1_out, nand_2_out);
  nand nand_5 (nand_5_out, Y, nand_3_out);
  nand nand_6 (nand_6_out, W, X);
  nand nand_7 (nand_7_out, nand_4_out, nand_4_out);
  nand nand_8 (nand_8_out, nand_5_out, nand_5_out);
  nand nand_9 (nand_9_out, nand_6_out, nand_6_out);
  nand nand_10 (nand_10_out, Z, Z);
  nand nand_11 (nand_11_out, nand_7_out, nand_8_out);
  nand nand_12 (nand_12_out, nand_9_out, nand_10_out);
  nand nand_13 (nand_13_out, W, X);
  nand nand_14 (nand_14_out, nand_11_out, nand_12_out);
  nand nand_15 (nand_15_out, nand_13_out, nand_13_out);
  nand nand_16 (nand_16_out, nand_14_out, nand_14_out);
  nand nand_17 (nand_17_out, nand_15_out, Y);
  nand nand_18 (nand_18_out, nand_16_out, nand_17_out);
  nand nand_19 (O, nand_18_out, nand_18_out);
endmodule

module Add1 (
  input  Plus1,
  input  ValEntree,
  output ValSortie,
  output Retenue
);

  wire and_1_out, and_2_out, not_1_out, not_2_out;

  not not_1 (not_1_out, Plus1);
  not not_2 (not_2_out, ValEntree);
  and and_1 (and_1_out, not_1_out, ValEntree);
  and and_2 (and_2_out, Plus1, not_2_out);
  and and_3 (Retenue, ValEntree, Plus1);
  or or_1 (ValSortie, and_1_out, and_2_out);
endmodule

module conditionUnite (
  input  A1,
  input  A2,
  input  A3,
  input  A4,
  output A,
  output B,
  output C,
  output D,
  output EN
);

  wire and_1_out, not_1_out, not_2_out, not_3_out, or_1_out;

  not not_1 (not_1_out, A2);
  and and_1 (and_1_out, not_1_out, not_2_out);
  not not_2 (not_2_out, A3);
  not not_3 (not_3_out, A4);
  or or_1 (or_1_out, and_1_out, not_3_out);
  resultEnable resultenable_1 (.EN(or_1_out), .D(A4), .C(A3), .B(A2), .A(A1), .As(A), .Bs(B), .Cs(C), .Ds(D), .ENs(EN));
endmodule

module resultEnable (
  input  EN,
  input  D,
  input  C,
  input  B,
  input  A,
  output As,
  output Bs,
  output Cs,
  output Ds,
  output ENs
);

  wire and_1_out, and_2_out, and_3_out, and_4_out, and_6_out, and_7_out, not_1_out, not_2_out, not_3_out,
       not_4_out, not_5_out, not_6_out, not_7_out, not_8_out, not_9_out, not_10_out, not_11_out;

  not not_1 (not_1_out, D);
  not not_2 (not_2_out, C);
  not not_3 (not_3_out, B);
  not not_4 (not_4_out, D);
  not not_5 (not_5_out, C);
  not not_6 (not_6_out, A);
  not not_7 (not_7_out, D);
  not not_8 (not_8_out, C);
  not not_9 (not_9_out, B);
  not not_10 (not_10_out, C);
  not not_11 (not_11_out, A);
  and and_1 (and_1_out, EN, not_1_out, A);
  and and_2 (and_2_out, EN, not_2_out, not_3_out, A);
  and and_3 (and_3_out, EN, not_4_out, B);
  and and_4 (and_4_out, EN, not_5_out, B, not_6_out);
  and and_5 (Cs, EN, not_7_out, C);
  and and_6 (and_6_out, EN, D, not_8_out, not_9_out);
  and and_7 (and_7_out, EN, D, not_10_out, not_11_out);
  or or_1 (As, and_1_out, and_2_out);
  or or_2 (Bs, and_3_out, and_4_out);
  or or_3 (Ds, and_6_out, and_7_out);

  assign ENs = EN;
endmodule

module conditionDix (
  input  A,
  input  B,
  input  C,
  input  D,
  output As,
  output Bs,
  output Cs,
  output Ds,
  output EN
);

  wire and_1_out, and_2_out, and_3_out, not_1_out, not_2_out, not_3_out, not_4_out, not_5_out, not_6_out,
       or_1_out;

  not not_1 (not_1_out, D);
  not not_2 (not_2_out, C);
  not not_3 (not_3_out, D);
  not not_4 (not_4_out, B);
  not not_5 (not_5_out, D);
  not not_6 (not_6_out, A);
  and and_1 (and_1_out, not_1_out, not_2_out);
  and and_2 (and_2_out, not_3_out, not_4_out);
  or or_1 (or_1_out, and_1_out, and_2_out, and_3_out);
  and and_3 (and_3_out, not_5_out, not_6_out);
  resultEnable resultenable_1 (.EN(or_1_out), .D(D), .C(C), .B(B), .A(A), .As(As), .Bs(Bs), .Cs(Cs), .Ds(Ds), .ENs(EN));
endmodule

module compte60 (
  input  EN,
  input  reset,
  output Bunite,
  output Aunite,
  output Dunite,
  output Cunite,
  output Bdec,
  output Adec,
  output Ddec,
  output Cdec,
  output plus1
);

  wire add1_1_retenue, add1_1_valsortie, add1_2_retenue, add1_2_valsortie, add1_3_retenue, add1_3_valsortie,
       add1_4_valsortie, add1_5_retenue, add1_5_valsortie, add1_6_retenue, add1_6_valsortie, add1_7_retenue,
       add1_7_valsortie, add1_8_valsortie, and_1_out, and_2_out, conditiondix_1_en, conditionunite_1_en,
       d_ff_1_q, d_ff_2_q, d_ff_3_q, d_ff_4_q, d_ff_5_q, d_ff_6_q, d_ff_7_q, d_ff_8_q, d_ff_9_q, not_1_out,
       not_2_out, not_3_out;

  not not_1 (not_1_out, EN);
  Add1 add1_1 (.Plus1(not_1_out), .ValEntree(Aunite), .ValSortie(add1_1_valsortie), .Retenue(add1_1_retenue));
  Add1 add1_2 (.Plus1(add1_1_retenue), .ValEntree(Bunite), .ValSortie(add1_2_valsortie), .Retenue(add1_2_retenue));
  Add1 add1_3 (.Plus1(add1_2_retenue), .ValEntree(Cunite), .ValSortie(add1_3_valsortie), .Retenue(add1_3_retenue));
  Add1 add1_4 (.Plus1(add1_3_retenue), .ValEntree(Dunite), .ValSortie(add1_4_valsortie));  // open: Retenue
  Add1 add1_5 (.Plus1(d_ff_9_q), .ValEntree(Adec), .ValSortie(add1_5_valsortie), .Retenue(add1_5_retenue));
  Add1 add1_6 (.Plus1(add1_5_retenue), .ValEntree(Bdec), .ValSortie(add1_6_valsortie), .Retenue(add1_6_retenue));
  Add1 add1_7 (.Plus1(add1_6_retenue), .ValEntree(Cdec), .ValSortie(add1_7_valsortie), .Retenue(add1_7_retenue));
  Add1 add1_8 (.Plus1(add1_7_retenue), .ValEntree(Ddec), .ValSortie(add1_8_valsortie));  // open: Retenue
  D_Flip_Flop d_ff_1 (.D(add1_1_valsortie), .clk(EN), .Q(d_ff_1_q));  // open: Qn, preset, reset
  D_Flip_Flop d_ff_2 (.D(add1_2_valsortie), .clk(EN), .Q(d_ff_2_q));  // open: Qn, preset, reset
  D_Flip_Flop d_ff_3 (.D(add1_3_valsortie), .clk(EN), .Q(d_ff_3_q));  // open: Qn, preset, reset
  D_Flip_Flop d_ff_4 (.D(add1_4_valsortie), .clk(EN), .Q(d_ff_4_q));  // open: Qn, preset, reset
  D_Flip_Flop d_ff_5 (.D(add1_5_valsortie), .clk(EN), .Q(d_ff_5_q));  // open: Qn, preset, reset
  D_Flip_Flop d_ff_6 (.D(add1_6_valsortie), .clk(EN), .Q(d_ff_6_q));  // open: Qn, preset, reset
  D_Flip_Flop d_ff_7 (.D(add1_7_valsortie), .clk(EN), .Q(d_ff_7_q));  // open: Qn, preset, reset
  D_Flip_Flop d_ff_8 (.D(add1_8_valsortie), .clk(EN), .Q(d_ff_8_q));  // open: Qn, preset, reset
  conditionUnite conditionunite_1 (
    .A1(d_ff_1_q), .A2(d_ff_2_q), .A3(d_ff_3_q), .A4(d_ff_4_q), .A(Aunite), .B(Bunite), .C(Cunite),
    .D(Dunite), .EN(conditionunite_1_en));
  conditionDix conditiondix_1 (
    .A(d_ff_5_q), .B(d_ff_6_q), .C(d_ff_7_q), .D(d_ff_8_q), .As(Adec), .Bs(Bdec), .Cs(Cdec), .Ds(Ddec),
    .EN(conditiondix_1_en));
  and and_1 (and_1_out, conditionunite_1_en, Aunite, Dunite);
  not not_2 (not_2_out, EN);
  and and_2 (and_2_out, conditiondix_1_en, Ddec, Bdec);
  not not_3 (not_3_out, EN);
  D_Flip_Flop d_ff_9 (.D(and_1_out), .clk(not_2_out), .Q(d_ff_9_q));  // open: Qn, preset, reset
  D_Flip_Flop d_ff_10 (.D(and_2_out), .clk(not_3_out), .Q(plus1));  // open: Qn, preset, reset
endmodule

module compte24 (
  input  EN,
  input  reset,
  output Aunite,
  output Bunite,
  output Cunite,
  output Dunite,
  output Adec,
  output Bdec,
  output Cdec,
  output Ddec,
  output plus1
);

  wire add1_1_retenue, add1_1_valsortie, add1_2_retenue, add1_2_valsortie, add1_3_retenue, add1_3_valsortie,
       add1_4_valsortie, add1_5_retenue, add1_5_valsortie, add1_6_retenue, add1_6_valsortie, add1_7_retenue,
       add1_7_valsortie, add1_8_valsortie, and_1_out, and_2_out, conditionheure_1_conds,
       conditionheure_1_ens, conditionheurediix_1_en, d_ff_1_q, d_ff_2_q, d_ff_3_q, d_ff_4_q, d_ff_5_q,
       d_ff_6_q, d_ff_7_q, d_ff_8_q, d_ff_9_q, d_ff_10_q, not_1_out, not_2_out, not_3_out;

  not not_1 (not_1_out, EN);
  Add1 add1_1 (.Plus1(not_1_out), .ValEntree(Aunite), .ValSortie(add1_1_valsortie), .Retenue(add1_1_retenue));
  Add1 add1_2 (.Plus1(add1_1_retenue), .ValEntree(Bunite), .ValSortie(add1_2_valsortie), .Retenue(add1_2_retenue));
  Add1 add1_3 (.Plus1(add1_2_retenue), .ValEntree(Cunite), .ValSortie(add1_3_valsortie), .Retenue(add1_3_retenue));
  Add1 add1_4 (.Plus1(add1_3_retenue), .ValEntree(Dunite), .ValSortie(add1_4_valsortie));  // open: Retenue
  Add1 add1_5 (.Plus1(d_ff_10_q), .ValEntree(Adec), .ValSortie(add1_5_valsortie), .Retenue(add1_5_retenue));
  Add1 add1_6 (.Plus1(add1_5_retenue), .ValEntree(Bdec), .ValSortie(add1_6_valsortie), .Retenue(add1_6_retenue));
  Add1 add1_7 (.Plus1(add1_6_retenue), .ValEntree(Ddec), .ValSortie(add1_7_valsortie), .Retenue(add1_7_retenue));
  Add1 add1_8 (.Plus1(add1_7_retenue), .ValEntree(Cdec), .ValSortie(add1_8_valsortie));  // open: Retenue
  D_Flip_Flop d_ff_1 (.D(add1_1_valsortie), .clk(EN), .Q(d_ff_1_q));  // open: Qn, preset, reset
  D_Flip_Flop d_ff_2 (.D(add1_2_valsortie), .clk(EN), .Q(d_ff_2_q));  // open: Qn, preset, reset
  D_Flip_Flop d_ff_3 (.D(add1_3_valsortie), .clk(EN), .Q(d_ff_3_q));  // open: Qn, preset, reset
  D_Flip_Flop d_ff_4 (.D(add1_4_valsortie), .clk(EN), .Q(d_ff_4_q));  // open: Qn, preset, reset
  D_Flip_Flop d_ff_5 (.D(add1_5_valsortie), .clk(EN), .Q(d_ff_5_q));  // open: Qn, preset, reset
  D_Flip_Flop d_ff_6 (.D(add1_6_valsortie), .clk(EN), .Q(d_ff_6_q));  // open: Qn, preset, reset
  D_Flip_Flop d_ff_7 (.D(add1_7_valsortie), .clk(EN), .Q(d_ff_7_q));  // open: Qn, preset, reset
  D_Flip_Flop d_ff_8 (.D(add1_8_valsortie), .clk(EN), .Q(d_ff_8_q));  // open: Qn, preset, reset
  conditionHeure conditionheure_1 (
    .cond24(d_ff_9_q), .A(d_ff_1_q), .B(d_ff_2_q), .C(d_ff_3_q), .D(d_ff_4_q),
    .Conds(conditionheure_1_conds), .As(Aunite), .Bs(Bunite), .Cs(Cunite), .Ds(Dunite),
    .ENs(conditionheure_1_ens));
  conditionHeureDiix conditionheurediix_1 (
    .A(d_ff_5_q), .B(d_ff_6_q), .C(d_ff_7_q), .D(d_ff_8_q), .Ass(Adec), .Bss(Bdec), .Css(Ddec), .Dss(Cdec),
    .EN(conditionheurediix_1_en));
  D_Flip_Flop d_ff_9 (.D(conditionheure_1_conds), .clk(EN), .Q(d_ff_9_q));  // open: Qn, preset, reset
  and and_1 (and_1_out, conditionheure_1_ens, Aunite, Dunite);
  and and_2 (and_2_out, conditionheurediix_1_en, Adec, Cdec);
  D_Flip_Flop d_ff_10 (.D(and_1_out), .clk(not_2_out), .Q(d_ff_10_q));  // open: Qn, preset, reset
  not not_2 (not_2_out, EN);
  D_Flip_Flop d_ff_11 (.D(and_2_out), .clk(not_3_out), .Q(plus1));  // open: Qn, preset, reset
  not not_3 (not_3_out, EN);
endmodule

module conditionHeure (
  input  cond24,
  input  A,
  input  B,
  input  C,
  input  D,
  output Conds,
  output As,
  output Bs,
  output Cs,
  output Ds,
  output ENs
);

  wire and_1_out, and_2_out, and_3_out, and_4_out, and_5_out, and_6_out, and_7_out, and_8_out, and_9_out,
       and_10_out, and_11_out, not_1_out, not_2_out, not_3_out, not_4_out, not_5_out, not_6_out, not_7_out,
       not_8_out, not_9_out, not_10_out, not_11_out, not_12_out, not_13_out, not_14_out, not_15_out,
       not_16_out, not_17_out, not_18_out, not_19_out, not_20_out, or_1_out, or_2_out, or_3_out, or_4_out,
       or_5_out;

  not not_1 (not_1_out, A);
  not not_2 (not_2_out, B);
  not not_3 (not_3_out, D);
  not not_4 (not_4_out, C);
  not not_5 (not_5_out, D);
  not not_6 (not_6_out, C);
  not not_7 (not_7_out, cond24);
  not not_8 (not_8_out, C);
  not not_9 (not_9_out, D);
  not not_10 (not_10_out, cond24);
  not not_11 (not_11_out, C);
  not not_12 (not_12_out, D);
  not not_13 (not_13_out, cond24);
  not not_14 (not_14_out, A);
  not not_15 (not_15_out, B);
  not not_16 (not_16_out, D);
  not not_17 (not_17_out, cond24);
  not not_18 (not_18_out, B);
  not not_19 (not_19_out, C);
  and and_1 (and_1_out, cond24, not_1_out, not_2_out, not_3_out);
  and and_2 (and_2_out, cond24, not_4_out, not_5_out);
  and and_3 (and_3_out, cond24, B, not_6_out);
  and and_4 (and_4_out, not_7_out, A);
  and and_5 (and_5_out, A, not_8_out, not_9_out);
  and and_6 (and_6_out, not_10_out, B);
  and and_7 (and_7_out, B, not_11_out, not_12_out);
  and and_8 (and_8_out, not_13_out, C);
  and and_9 (and_9_out, not_14_out, not_15_out, C, not_16_out);
  and and_10 (and_10_out, not_17_out, D);
  and and_11 (and_11_out, not_18_out, not_19_out);
  not not_20 (not_20_out, D);
  or or_1 (or_1_out, and_1_out, and_2_out, and_3_out);
  or or_2 (or_2_out, and_4_out, and_5_out);
  or or_3 (or_3_out, and_6_out, and_7_out);
  or or_4 (or_4_out, and_8_out, and_9_out);
  or or_5 (or_5_out, and_11_out, not_20_out, cond24);
  resultEnableHeure resultenableheure_1 (
    .Con24(or_1_out), .A(or_2_out), .B(or_3_out), .C(or_4_out), .D(and_10_out), .EN(or_5_out),
    .Con24s(Conds), .As(As), .Bs(Bs), .Cs(Cs), .Ds(Ds), .ENs(ENs));
endmodule

module resultEnableHeure (
  input  Con24,
  input  A,
  input  B,
  input  C,
  input  D,
  input  EN,
  output Con24s,
  output As,
  output Bs,
  output Cs,
  output Ds,
  output ENs
);

  wire and_1_out, and_2_out, and_3_out, and_4_out, and_5_out, and_6_out, and_7_out, and_8_out, and_9_out,
       and_10_out, not_1_out, not_2_out, not_3_out, not_4_out, not_5_out, not_6_out, not_7_out, not_8_out,
       not_9_out, not_10_out, not_11_out, not_12_out, not_13_out, not_14_out, not_15_out, not_16_out,
       not_17_out, not_18_out, not_19_out, not_20_out, not_21_out, not_22_out, not_23_out, not_24_out,
       not_25_out, not_26_out, not_27_out;

  not not_1 (not_1_out, Con24);
  not not_2 (not_2_out, B);
  not not_3 (not_3_out, C);
  not not_4 (not_4_out, A);
  not not_5 (not_5_out, B);
  not not_6 (not_6_out, D);
  not not_7 (not_7_out, C);
  not not_8 (not_8_out, D);
  not not_9 (not_9_out, Con24);
  not not_10 (not_10_out, D);
  not not_11 (not_11_out, Con24);
  not not_12 (not_12_out, C);
  not not_13 (not_13_out, B);
  not not_14 (not_14_out, D);
  not not_15 (not_15_out, C);
  not not_16 (not_16_out, Con24);
  not not_17 (not_17_out, D);
  not not_18 (not_18_out, D);
  not not_19 (not_19_out, C);
  not not_20 (not_20_out, Con24);
  not not_21 (not_21_out, D);
  not not_22 (not_22_out, D);
  not not_23 (not_23_out, B);
  not not_24 (not_24_out, A);
  not not_25 (not_25_out, Con24);
  not not_26 (not_26_out, C);
  not not_27 (not_27_out, B);
  and and_1 (and_1_out, not_1_out, A, not_2_out, not_3_out, D);
  and and_2 (and_2_out, Con24, not_4_out, not_5_out, not_6_out, EN);
  and and_3 (and_3_out, Con24, not_7_out, not_8_out, EN);
  and and_4 (and_4_out, not_9_out, EN, not_10_out, A);
  and and_5 (and_5_out, not_11_out, EN, not_12_out, not_13_out, A);
  and and_6 (and_6_out, EN, not_14_out, not_15_out, A);
  and and_7 (and_7_out, not_16_out, EN, not_17_out, B);
  and and_8 (and_8_out, EN, not_18_out, not_19_out, B);
  and and_9 (and_9_out, not_20_out, EN, not_21_out, C);
  and and_10 (and_10_out, EN, not_22_out, C, not_23_out, not_24_out);
  and and_11 (Ds, not_25_out, EN, D, not_26_out, not_27_out);
  or or_1 (Con24s, and_1_out, and_2_out, and_3_out);
  or or_2 (As, and_4_out, and_5_out, and_6_out);
  or or_3 (Bs, and_7_out, and_8_out);
  or or_4 (Cs, and_9_out, and_10_out);

  assign ENs = EN;
endmodule

module autre (
  input  in_1,
  input  in_2,
  input  in_3,
  input  in_4,
  input  in_5,
  output out_6,
  output out_7,
  output out_8,
  output out_9,
  output out_10,
  output out_11
);

  wire and_1_out, and_2_out, and_3_out, and_4_out, and_5_out, and_6_out, and_7_out, and_8_out, and_9_out,
       not_1_out, not_2_out, not_3_out, not_4_out, not_5_out, not_6_out, not_7_out, not_8_out, not_9_out,
       not_10_out, not_11_out, not_12_out, not_13_out, not_14_out, not_15_out, not_16_out, or_1_out,
       or_2_out, or_3_out;

  not not_1 (not_1_out, in_2);
  not not_2 (not_2_out, in_3);
  not not_3 (not_3_out, in_2);
  not not_4 (not_4_out, in_4);
  not not_5 (not_5_out, in_5);
  not not_6 (not_6_out, in_3);
  not not_7 (not_7_out, in_4);
  not not_8 (not_8_out, in_5);
  not not_9 (not_9_out, in_1);
  not not_10 (not_10_out, in_2);
  not not_11 (not_11_out, in_3);
  not not_12 (not_12_out, in_1);
  not not_13 (not_13_out, in_2);
  not not_14 (not_14_out, in_3);
  not not_15 (not_15_out, in_1);
  not not_16 (not_16_out, in_1);
  and and_1 (and_1_out, in_1, not_1_out, not_2_out);
  and and_2 (and_2_out, not_3_out, in_3, not_4_out, not_5_out);
  and and_3 (and_3_out, in_2, not_6_out, not_7_out, not_8_out);
  and and_4 (and_4_out, not_9_out, in_5);
  and and_5 (and_5_out, not_10_out, not_11_out, in_5);
  and and_6 (and_6_out, not_12_out, in_4);
  and and_7 (and_7_out, not_13_out, not_14_out, in_4);
  and and_8 (and_8_out, not_15_out, in_3);
  and and_9 (and_9_out, not_16_out, in_2);
  or or_1 (or_1_out, and_2_out, and_3_out);
  or or_2 (or_2_out, and_4_out, and_5_out);
  or or_3 (or_3_out, and_6_out, and_7_out);
  resultEnableHeure resultenableheure_1 (
    .Con24(and_1_out), .A(or_1_out), .B(or_2_out), .C(or_3_out), .D(and_8_out), .EN(and_9_out),
    .Con24s(out_6), .As(out_7), .Bs(out_8), .Cs(out_9), .Ds(out_10), .ENs(out_11));
endmodule

module conditionHeureDiix (
  input  A,
  input  B,
  input  C,
  input  D,
  output Ass,
  output Bss,
  output Css,
  output Dss,
  output EN
);

  wire and_1_out, and_2_out, not_1_out, not_2_out, not_3_out, not_4_out, not_5_out, not_6_out, or_1_out;

  not not_1 (not_1_out, A);
  not not_2 (not_2_out, C);
  not not_3 (not_3_out, D);
  not not_4 (not_4_out, B);
  not not_5 (not_5_out, C);
  not not_6 (not_6_out, D);
  and and_1 (and_1_out, not_1_out, not_2_out, not_3_out);
  and and_2 (and_2_out, not_4_out, not_5_out, not_6_out);
  or or_1 (or_1_out, and_1_out, and_2_out);
  resultEnable resultenable_1 (
    .EN(or_1_out), .D(D), .C(C), .B(B), .A(A), .As(Ass), .Bs(Bss), .Cs(Css), .Ds(Dss), .ENs(EN));
endmodule
