// Logisim project compte60.circ as structural Verilog
module main (
  input  Enable,
  input  Reset,
  output Plus1
);

  wire add1_1_retenue, add1_1_valsortie, add1_2_retenue, add1_2_valsortie, add1_3_retenue, add1_3_valsortie,
       add1_4_valsortie, add1_5_retenue, add1_5_valsortie, add1_6_retenue, add1_6_valsortie, add1_7_retenue,
       add1_7_valsortie, add1_8_valsortie, and_1_out, and_2_out, conditiondix_1_out_5, conditiondix_1_out_6,
       conditiondix_1_out_7, conditiondix_1_out_8, conditiondix_1_out_9, conditionunite_1_a,
       conditionunite_1_b, conditionunite_1_c, conditionunite_1_d, conditionunite_1_en, d_ff_1_q, d_ff_2_q,
       d_ff_3_q, d_ff_4_q, d_ff_5_q, d_ff_6_q, d_ff_7_q, d_ff_8_q, d_ff_9_q, not_1_out, not_2_out, not_3_out,
       segmentdisplaycontroller_1_a, segmentdisplaycontroller_1_b, segmentdisplaycontroller_1_c,
       segmentdisplaycontroller_1_d, segmentdisplaycontroller_1_e, segmentdisplaycontroller_1_f,
       segmentdisplaycontroller_1_g, segmentdisplaycontroller_2_a, segmentdisplaycontroller_2_b,
       segmentdisplaycontroller_2_c, segmentdisplaycontroller_2_d, segmentdisplaycontroller_2_e,
       segmentdisplaycontroller_2_f, segmentdisplaycontroller_2_g;

  not not_1 (not_1_out, Enable);
  Add1 add1_1 (
    .Plus1(not_1_out), .ValEntree(conditionunite_1_a), .ValSortie(add1_1_valsortie), .Retenue(add1_1_retenue));
  Add1 add1_2 (
    .Plus1(add1_1_retenue), .ValEntree(conditionunite_1_b), .ValSortie(add1_2_valsortie),
    .Retenue(add1_2_retenue));
  Add1 add1_3 (
    .Plus1(add1_2_retenue), .ValEntree(conditionunite_1_c), .ValSortie(add1_3_valsortie),
    .Retenue(add1_3_retenue));
  Add1 add1_4 (.Plus1(add1_3_retenue), .ValEntree(conditionunite_1_d), .ValSortie(add1_4_valsortie));  // open: Retenue
  Add1 add1_5 (
    .Plus1(d_ff_9_q), .ValEntree(conditiondix_1_out_5), .ValSortie(add1_5_valsortie), .Retenue(add1_5_retenue));
  Add1 add1_6 (
    .Plus1(add1_5_retenue), .ValEntree(conditiondix_1_out_6), .ValSortie(add1_6_valsortie),
    .Retenue(add1_6_retenue));
  Add1 add1_7 (
    .Plus1(add1_6_retenue), .ValEntree(conditiondix_1_out_7), .ValSortie(add1_7_valsortie),
    .Retenue(add1_7_retenue));
  Add1 add1_8 (
    .Plus1(add1_7_retenue), .ValEntree(conditiondix_1_out_8), .ValSortie(add1_8_valsortie));  // open: Retenue
  D_Flip_Flop d_ff_1 (.D(add1_1_valsortie), .clk(Enable), .Q(d_ff_1_q));  // open: Qn, preset, reset
  D_Flip_Flop d_ff_2 (.D(add1_2_valsortie), .clk(Enable), .Q(d_ff_2_q));  // open: Qn, preset, reset
  D_Flip_Flop d_ff_3 (.D(add1_3_valsortie), .clk(Enable), .Q(d_ff_3_q));  // open: Qn, preset, reset
  D_Flip_Flop d_ff_4 (.D(add1_4_valsortie), .clk(Enable), .Q(d_ff_4_q));  // open: Qn, preset, reset
  D_Flip_Flop d_ff_5 (.D(add1_5_valsortie), .clk(Enable), .Q(d_ff_5_q));  // open: Qn, preset, reset
  D_Flip_Flop d_ff_6 (.D(add1_6_valsortie), .clk(Enable), .Q(d_ff_6_q));  // open: Qn, preset, reset
  D_Flip_Flop d_ff_7 (.D(add1_7_valsortie), .clk(Enable), .Q(d_ff_7_q));  // open: Qn, preset, reset
  D_Flip_Flop d_ff_8 (.D(add1_8_valsortie), .clk(Enable), .Q(d_ff_8_q));  // open: Qn, preset, reset
  conditionUnite conditionunite_1 (
    .A1(d_ff_1_q), .A2(d_ff_2_q), .A3(d_ff_3_q), .A4(d_ff_4_q), .A(conditionunite_1_a),
    .B(conditionunite_1_b), .C(conditionunite_1_c), .D(conditionunite_1_d), .EN(conditionunite_1_en));
  conditionDix conditiondix_1 (
    .A(d_ff_5_q), .B(d_ff_6_q), .C(d_ff_7_q), .D(d_ff_8_q), .out_5(conditiondix_1_out_5),
    .out_6(conditiondix_1_out_6), .out_7(conditiondix_1_out_7), .out_8(conditiondix_1_out_8),
    .out_9(conditiondix_1_out_9));
  and and_1 (and_1_out, conditionunite_1_en, conditionunite_1_a, conditionunite_1_d);
  and and_2 (and_2_out, conditiondix_1_out_9, conditiondix_1_out_5, conditiondix_1_out_8);
  D_Flip_Flop d_ff_9 (.D(and_1_out), .clk(not_2_out), .Q(d_ff_9_q));  // open: Qn, preset, reset
  not not_2 (not_2_out, Enable);
  D_Flip_Flop d_ff_10 (.D(and_2_out), .clk(not_3_out), .Q(Plus1));  // open: Qn, preset, reset
  not not_3 (not_3_out, Enable);
  SegmentDisplayController segmentdisplaycontroller_1 (
    .B_B(conditionunite_1_b), .B_A(conditionunite_1_a), .B_D(conditionunite_1_d), .B_C(conditionunite_1_c),
    .A(segmentdisplaycontroller_1_a), .B(segmentdisplaycontroller_1_b), .C(segmentdisplaycontroller_1_c),
    .D(segmentdisplaycontroller_1_d), .E(segmentdisplaycontroller_1_e), .F(segmentdisplaycontroller_1_f),
    .G(segmentdisplaycontroller_1_g));
  SegmentDisplayController segmentdisplaycontroller_2 (
    .B_B(conditiondix_1_out_6), .B_A(conditiondix_1_out_5), .B_D(conditiondix_1_out_8),
    .B_C(conditiondix_1_out_7), .A(segmentdisplaycontroller_2_a), .B(segmentdisplaycontroller_2_b),
    .C(segmentdisplaycontroller_2_c), .D(segmentdisplaycontroller_2_d), .E(segmentdisplaycontroller_2_e),
    .F(segmentdisplaycontroller_2_f), .G(segmentdisplaycontroller_2_g));
  _7_Segment_Display u_7_segment_display_1 (
    .g(segmentdisplaycontroller_1_g), .f(segmentdisplaycontroller_1_f), .a(segmentdisplaycontroller_1_a),
    .b(segmentdisplaycontroller_1_b), .e(segmentdisplaycontroller_1_e), .d(segmentdisplaycontroller_1_d),
    .c(segmentdisplaycontroller_1_c));  // open: dp
  _7_Segment_Display u_7_segment_display_2 (
    .g(segmentdisplaycontroller_2_g), .f(segmentdisplaycontroller_2_f), .a(segmentdisplaycontroller_2_a),
    .b(segmentdisplaycontroller_2_b), .e(segmentdisplaycontroller_2_e), .d(segmentdisplaycontroller_2_d),
    .c(segmentdisplaycontroller_2_c));  // open: dp
endmodule

module SegmentDisplayController (
  input  B_B,
  input  B_A,
  input  B_D,
  input  B_C,
  output A,
  output B,
  output C,
  output D,
  output E,
  output F,
  output G
);

  wire not_1_out, not_2_out, not_3_out, not_4_out;

  not not_1 (not_1_out, B_D);
  not not_2 (not_2_out, B_C);
  not not_3 (not_3_out, B_B);
  not not_4 (not_4_out, B_A);
  SegmentA_AUTO segmenta_auto_1 (.W(B_D), .X(B_C), .Y(B_B), .Z(B_A), .O(A));
  SegmentB_AUTO segmentb_auto_1 (.W(B_D), .X(B_C), .Y(B_B), .Z(B_A), .O(B));
  SegmentC_AUTO segmentc_auto_1 (.W(B_D), .X(B_C), .Y(B_B), .Z(B_A), .O(C));
  SegmentD segmentd_1 (.W(B_D), .X(B_C), .Y(B_B), .Z(B_A), .O(D));
  SegmentE segmente_1 (.W(B_D), .X(B_C), .Y(B_B), .Z(B_A), .O(E));
  SegmentF segmentf_1 (.W(B_D), .X(B_C), .Y(B_B), .Z(B_A), .O(F));
  SegmentG segmentg_1 (.W(B_D), .X(B_C), .Y(B_B), .Z(B_A), .O(G));
  _7_Segment_Display u_7_segment_display_1 (.g(G), .f(F), .a(A), .b(B), .e(E), .d(D), .c(C));  // open: dp
endmodule

module SegmentD (
  input  W,
  input  X,
  input  Y,
  input  Z,
  output O
);

  wire and_1_out, and_2_out, and_3_out, and_4_out, and_5_out, not_1_out, not_2_out, not_3_out, not_4_out,
       not_5_out, not_6_out, not_7_out;

  not not_1 (not_1_out, W);
  not not_2 (not_2_out, X);
  not not_3 (not_3_out, Z);
  not not_4 (not_4_out, X);
  not not_5 (not_5_out, Y);
  not not_6 (not_6_out, Z);
  not not_7 (not_7_out, Y);
  and and_1 (and_1_out, not_1_out, not_2_out, not_3_out);
  and and_2 (and_2_out, not_4_out, Y, Z);
  and and_3 (and_3_out, X, not_5_out, Z);
  and and_4 (and_4_out, X, Y, not_6_out);
  and and_5 (and_5_out, W, not_7_out);
  or or_1 (O, and_1_out, and_2_out, and_3_out, and_4_out, and_5_out);
endmodule

module SegmentG (
  input  W,
  input  X,
  input  Y,
  input  Z,
  output O
);

  wire and_1_out, and_2_out, and_3_out, and_4_out, and_5_out, not_1_out, not_2_out, not_3_out, not_4_out,
       not_5_out;

  not not_1 (not_1_out, X);
  not not_2 (not_2_out, Z);
  not not_3 (not_3_out, W);
  not not_4 (not_4_out, Y);
  not not_5 (not_5_out, X);
  and and_1 (and_1_out, not_1_out, Y);
  and and_2 (and_2_out, Y, not_2_out);
  and and_3 (and_3_out, not_3_out, X, not_4_out);
  and and_4 (and_4_out, W, not_5_out);
  and and_5 (and_5_out, W, Z);
  or or_1 (O, and_1_out, and_2_out, and_3_out, and_4_out, and_5_out);
endmodule

module SegmentE (
  input  W,
  input  X,
  input  Y,
  input  Z,
  output O
);

  wire and_1_out, and_2_out, and_3_out, and_4_out, not_1_out, not_2_out, not_3_out;

  not not_1 (not_1_out, X);
  not not_2 (not_2_out, Z);
  not not_3 (not_3_out, Z);
  and and_1 (and_1_out, not_1_out, not_2_out);
  and and_2 (and_2_out, Y, not_3_out);
  and and_3 (and_3_out, W, Y);
  and and_4 (and_4_out, W, X);
  or or_1 (O, and_1_out, and_2_out, and_3_out, and_4_out);
endmodule

module SegmentF (
  input  W,
  input  X,
  input  Y,
  input  Z,
  output O
);

  wire and_1_out, and_2_out, and_3_out, and_4_out, and_5_out, not_1_out, not_2_out, not_3_out, not_4_out,
       not_5_out, not_6_out;

  not not_1 (not_1_out, Y);
  not not_2 (not_2_out, Z);
  not not_3 (not_3_out, W);
  not not_4 (not_4_out, Y);
  not not_5 (not_5_out, Z);
  not not_6 (not_6_out, X);
  and and_1 (and_1_out, not_1_out, not_2_out);
  and and_2 (and_2_out, not_3_out, X, not_4_out);
  and and_3 (and_3_out, X, not_5_out);
  and and_4 (and_4_out, W, not_6_out);
  and and_5 (and_5_out, W, Y);
  or or_1 (O, and_1_out, and_2_out, and_3_out, and_4_out, and_5_out);
endmodule

module SegmentA_AUTO (
  input  W,
  input  X,
  input  Y,
  input  Z,
  output O
);

  wire not_1_out, not_2_out, not_3_out, not_4_out, not_5_out, not_6_out, not_7_out, not_8_out, or_1_out,
       or_2_out, or_3_out, or_4_out;

  not not_1 (not_1_out, Z);
  not not_2 (not_2_out, X);
  not not_3 (not_3_out, W);
  not not_4 (not_4_out, Y);
  not not_5 (not_5_out, Z);
  not not_6 (not_6_out, W);
  not not_7 (not_7_out, X);
  not not_8 (not_8_out, Z);
  or or_1 (or_1_out, W, X, Y, not_1_out);
  or or_2 (or_2_out, W, not_2_out, Y, Z);
  or or_3 (or_3_out, not_3_out, X, not_4_out, not_5_out);
  or or_4 (or_4_out, not_6_out, not_7_out, Y, not_8_out);
  and and_1 (O, or_1_out, or_2_out, or_3_out, or_4_out);
endmodule

module SegmentB_AUTO (
  input  W,
  input  X,
  input  Y,
  input  Z,
  output O
);

  wire nand_1_out, nand_2_out, nand_3_out, nand_4_out, nand_5_out, nand_6_out, nand_7_out, nand_8_out,
       nand_9_out;

  nand nand_1 (nand_1_out, W, W);
  nand nand_2 (nand_2_out, Y, Y);
  nand nand_3 (nand_3_out, Z, Z);
  nand nand_4 (nand_4_out, Z, Z);
  nand nand_5 (nand_5_out, nand_1_out, X, nand_2_out, Z);
  nand nand_6 (nand_6_out, X, Y, nand_3_out);
  nand nand_7 (nand_7_out, W, Y, Z);
  nand nand_8 (nand_8_out, W, X, nand_4_out);
  nand nand_9 (nand_9_out, nand_5_out, nand_6_out, nand_7_out, nand_8_out);
  nand nand_10 (O, nand_9_out, nand_9_out);
endmodule

module SegmentC_AUTO (
  input  W,
  input  X,
  input  Y,
  input  Z,
  output O
);

  wire nand_1_out, nand_2_out, nand_3_out, nand_4_out, nand_5_out, nand_6_out, nand_7_out, nand_8_out,
       nand_9_out, nand_10_out, nand_11_out, nand_12_out, nand_13_out, nand_14_out, nand_15_out, nand_16_out,
       nand_17_out, nand_18_out;

  nand nand_1 (nand_1_out, W, W);
  nand nand_2 (nand_2_out, X, X);
  nand nand_3 (nand_3_out, Z, Z);
  nand nand_4 (nand_4_out, nand_1_out, nand_2_out);
  nand nand_5 (nand_5_out, Y, nand_3_out);
  nand nand_6 (nand_6_out, W, X);
  nand nand_7 (nand_7_out, nand_4_out, nand_4_out);
  nand nand_8 (nand_8_out, nand_5_out, nand_5_out);
  nand nand_9 (nand_9_out, nand_6_out, nand_6_out);
  nand nand_10 (nand_10_out, Z, Z);
  nand nand_11 (nand_11_out, nand_7_out, nand_8_out);
  nand nand_12 (nand_12_out, nand_9_out, nand_10_out);
  nand nand_13 (nand_13_out, W, X);
  nand nand_14 (nand_14_out, nand_11_out, nand_12_out);
  nand nand_15 (nand_15_out, nand_13_out, nand_13_out);
  nand nand_16 (nand_16_out, nand_14_out, nand_14_out);
  nand nand_17 (nand_17_out, nand_15_out, Y);
  nand nand_18 (nand_18_out, nand_16_out, nand_17_out);
  nand nand_19 (O, nand_18_out, nand_18_out);
endmodule

module Add1 (
  input  Plus1,
  input  ValEntree,
  output ValSortie,
  output Retenue
);

  wire and_1_out, and_2_out, not_1_out, not_2_out;

  not not_1 (not_1_out, Plus1);
  not not_2 (not_2_out, ValEntree);
  and and_1 (and_1_out, not_1_out, ValEntree);
  and and_2 (and_2_out, Plus1, not_2_out);
  and and_3 (Retenue, ValEntree, Plus1);
  or or_1 (ValSortie, and_1_out, and_2_out);
endmodule

module conditionUnite (
  input  A1,
  input  A2,
  input  A3,
  input  A4,
  output A,
  output B,
  output C,
  output D,
  output EN
);

  wire and_1_out, not_1_out, not_2_out, not_3_out, or_1_out;

  not not_1 (not_1_out, A2);
  and and_1 (and_1_out, not_1_out, not_2_out);
  not not_2 (not_2_out, A3);
  not not_3 (not_3_out, A4);
  or or_1 (or_1_out, and_1_out, not_3_out);
  resultEnable resultenable_1 (.EN(or_1_out), .D(A4), .C(A3), .B(A2), .A(A1), .Ds(D), .Cs(C), .Bs(B), .As(A), .ENs(EN));
endmodule

module resultEnable (
  input  EN,
  input  D,
  input  C,
  input  B,
  input  A,
  output Ds,
  output Cs,
  output Bs,
  output As,
  output ENs
);

  wire and_1_out, and_2_out, and_4_out, and_5_out, and_6_out, and_7_out, not_1_out, not_2_out, not_3_out,
       not_4_out, not_5_out, not_6_out, not_7_out, not_8_out, not_9_out, not_10_out, not_11_out;

  not not_1 (not_1_out, C);
  not not_2 (not_2_out, B);
  not not_3 (not_3_out, C);
  not not_4 (not_4_out, A);
  not not_5 (not_5_out, D);
  not not_6 (not_6_out, D);
  not not_7 (not_7_out, C);
  not not_8 (not_8_out, A);
  not not_9 (not_9_out, D);
  not not_10 (not_10_out, C);
  not not_11 (not_11_out, B);
  and and_1 (and_1_out, EN, D, not_1_out, not_2_out);
  and and_2 (and_2_out, EN, D, not_3_out, not_4_out);
  and and_3 (Cs, EN, not_5_out, C);
  and and_4 (and_4_out, EN, not_6_out, B);
  and and_5 (and_5_out, EN, not_7_out, B, not_8_out);
  and and_6 (and_6_out, EN, not_9_out, A);
  and and_7 (and_7_out, EN, not_10_out, not_11_out, A);
  or or_1 (Ds, and_1_out, and_2_out);
  or or_2 (Bs, and_4_out, and_5_out);
  or or_3 (As, and_6_out, and_7_out);

  assign ENs = EN;
endmodule

module conditionDix (
  input  A,
  input  B,
  input  C,
  input  D,
  output out_5,
  output out_6,
  output out_7,
  output out_8,
  output out_9
);

  wire and_1_out, and_2_out, and_3_out, not_1_out, not_2_out, not_3_out, not_4_out, not_5_out, not_6_out,
       or_1_out;

  not not_1 (not_1_out, D);
  not not_2 (not_2_out, C);
  not not_3 (not_3_out, D);
  not not_4 (not_4_out, B);
  not not_5 (not_5_out, D);
  not not_6 (not_6_out, A);
  and and_1 (and_1_out, not_1_out, not_2_out);
  and and_2 (and_2_out, not_3_out, not_4_out);
  or or_1 (or_1_out, and_1_out, and_2_out, and_3_out);
  and and_3 (and_3_out, not_5_out, not_6_out);
  resultEnable resultenable_1 (
    .EN(or_1_out), .D(D), .C(C), .B(B), .A(A), .Ds(out_8), .Cs(out_7), .Bs(out_6), .As(out_5), .ENs(out_9));
endmodule
