// Logisim project soustration4bits.circ as structural Verilog: 2 circuits, main circuit main
module main (
  input  A1,
  input  B1,
  input  A2,
  input  B2,
  input  A3,
  input  B3,
  input  A4,
  input  B4,
  output P1,
  output P2,
  output P3,
  output P4,
  output U
);

  wire soustraction_1_u, soustraction_2_u, soustraction_3_u;

  Soustraction soustraction_1 (.A(A1), .B(B1), .C(1'b0), .P(P1), .U(soustraction_1_u));
  Soustraction soustraction_2 (.A(A2), .B(B2), .C(soustraction_1_u), .P(P2), .U(soustraction_2_u));
  Soustraction soustraction_3 (.A(A3), .B(B3), .C(soustraction_2_u), .P(P3), .U(soustraction_3_u));
  Soustraction soustraction_4 (.A(A4), .B(B4), .C(soustraction_3_u), .P(P4), .U(U));
endmodule

module Soustraction (
  input  A,
  input  B,
  input  C,
  output P,
  output U
);

  wire and_1_out, and_2_out, and_3_out, and_4_out, and_5_out, and_6_out, and_7_out, not_1_out, not_2_out,
       not_3_out, not_4_out, not_5_out, not_6_out;

  not not_1 (not_1_out, A);
  not not_2 (not_2_out, A);
  not not_3 (not_3_out, B);
  not not_4 (not_4_out, C);
  not not_5 (not_5_out, A);
  not not_6 (not_6_out, A);
  and and_1 (and_1_out, not_1_out, C);
  and and_2 (and_2_out, not_2_out, B);
  and and_3 (and_3_out, B, C);
  and and_4 (and_4_out, A, not_3_out, not_4_out);
  and and_5 (and_5_out, not_5_out, C);
  or or_1 (U, and_5_out, and_6_out, and_7_out);
  and and_6 (and_6_out, not_6_out, B);
  and and_7 (and_7_out, B, C);
  or or_2 (P, and_1_out, and_2_out, and_3_out, and_4_out);
endmodule
