// Logisim project MainMachine.circ as structural Verilog: 40 circuits, main circuit main
module main (
  input  y1,
  input  y2,
  input  y3,
  input  y4,
  output x1,
  output x2,
  output x3,
  output x4,
  output BUZZER
);

  wire ALARM_SWITCH, Button_1_out, Button_2_out, CHRONO_ENABLE, CHRONO_MSG_EN, ChronoButtonHandler_1_reset,
       ChronoButtonHandler_1_start_stop, clock_1_out, CLOCK_ENABLE, CLOCK_MSG_EN, comparator_1_eq,
       Countdown_1_timeout, COUNTDOWN_ENABLE, COUNTDOWN_MSG_EN, EN_ALARM, EN_COUNTDOWN_TIMEOUT,
       hexddec_example_1_data_ready, ImpulsOnRisingEdges_1_o, MSG_CLOCK, MUS_PLAY_REC_ENABLE,
       MUS_PLAY_SONG_ENABLE, MUS_REC_ENABLE, music_box_1_en, music_box_1_freq, or_1_out, or_2_out, or_3_out,
       or_4_out, or_5_out, or_6_out, or_7_out, PAD_DATA_READY, POR, s_r_ff_1_q, s_r_ff_3_q,
       segmentdisplaycontroller_1_output_1, segmentdisplaycontroller_1_output_2,
       segmentdisplaycontroller_1_output_3, segmentdisplaycontroller_1_output_4,
       segmentdisplaycontroller_1_output_5, segmentdisplaycontroller_1_output_6,
       segmentdisplaycontroller_1_output_7, segmentdisplaycontroller_1_output_8,
       segmentdisplaycontroller_2_output_1, segmentdisplaycontroller_2_output_2,
       segmentdisplaycontroller_2_output_3, segmentdisplaycontroller_2_output_4,
       segmentdisplaycontroller_2_output_5, segmentdisplaycontroller_2_output_6,
       segmentdisplaycontroller_2_output_7, segmentdisplaycontroller_2_output_8,
       segmentdisplaycontroller_3_output_1, segmentdisplaycontroller_3_output_2,
       segmentdisplaycontroller_3_output_3, segmentdisplaycontroller_3_output_4,
       segmentdisplaycontroller_3_output_5, segmentdisplaycontroller_3_output_6,
       segmentdisplaycontroller_3_output_7, segmentdisplaycontroller_3_output_8,
       segmentdisplaycontroller_4_output_1, segmentdisplaycontroller_4_output_2,
       segmentdisplaycontroller_4_output_3, segmentdisplaycontroller_4_output_4,
       segmentdisplaycontroller_4_output_5, segmentdisplaycontroller_4_output_6,
       segmentdisplaycontroller_4_output_7, segmentdisplaycontroller_4_output_8,
       segmentdisplaycontroller_5_output_1, segmentdisplaycontroller_5_output_2,
       segmentdisplaycontroller_5_output_3, segmentdisplaycontroller_5_output_4,
       segmentdisplaycontroller_5_output_5, segmentdisplaycontroller_5_output_7,
       segmentdisplaycontroller_5_output_8, segmentdisplaycontroller_6_output_1,
       segmentdisplaycontroller_6_output_2, segmentdisplaycontroller_6_output_3,
       segmentdisplaycontroller_6_output_4, segmentdisplaycontroller_6_output_5,
       segmentdisplaycontroller_6_output_6, segmentdisplaycontroller_6_output_7,
       segmentdisplaycontroller_6_output_8, SET_ALARM_EN, SET_ALARM_MSG_EN, SET_I_IMPULS, SET_II_IMPULS,
       SET_III_IMPULS, shift_register_1_p2, SYS_CLOCK, TIME_CLOCK, time_setter_1_set_time_impuls,
       time_setter_2_set_time_impuls, undriven, undriven_2;
  wire [3:0] hexddec_example_1_data, MainFSM_1_state, PAD_DATA, shift_register_1_p11, shift_register_1_p12,
       shift_register_1_p13, shift_register_1_p14, shift_register_1_p15, shift_register_1_p16;
  wire [23:0] adder_1_out, Chrono_1_hms, CLOCK_TIME, Countdown_1_hms, PAD_DATA_6REG;
  wire [29:0] CHRONO_MSG, CHRONO_SCR, CLOCK_MSG, CLOCK_SCR, COUNTDOWN_MSG, COUNTDOWN_SCR, multiplexer_1_out,
       PLAY_REC_MSG, PLAY_SONG_MSG, RECORDER_MSG, SET_ALARM_MSG, SET_ALARM_SCR;

  Button Button_1 (.out(Button_1_out));
  Button Button_2 (.out(Button_2_out));
  DipSwitch #(.number(10)) DipSwitch_1 (
    .sw1(ALARM_SWITCH), .sw10(POR));  // open: sw2, sw3, sw4, sw5, sw6, sw7, sw8, sw9
  // NOT_Gate not_1 has open pins: in=Button_1_out, out=open
  Clock #(.highDuration(32000), .lowDuration(32000)) clock_1 (.out(clock_1_out));
  Clock clock_2 (.out(SYS_CLOCK));
  Clock #(.highDuration(128000), .lowDuration(128000)) clock_3 (.out(TIME_CLOCK));
  Clock #(.highDuration(56000), .lowDuration(56000)) u_MSG_CLOCK (.out(MSG_CLOCK));
  Clock sysclk ();  // open: out
  Clock #(.highDuration(10), .lowDuration(10)) clk_16 ();  // open: out
  Clock #(.highDuration(100), .lowDuration(100)) clk_256 ();  // open: out
  or or_1 (or_1_out, SET_II_IMPULS, Countdown_1_timeout);
  or or_2 (or_2_out, EN_ALARM, EN_COUNTDOWN_TIMEOUT);
  Adder #(.width(24)) adder_1 (.a(PAD_DATA_6REG), .b(24'h1), .out(adder_1_out));  // open: cin, cout
  S_R_Flip_Flop #(.trigger("high")) s_r_ff_1 (
    .S(time_setter_2_set_time_impuls), .R(or_1_out), .clk(1'b1), .Q(s_r_ff_1_q), .reset(POR));  // open: Qn, preset
  ImpulsOnRisingEdges ImpulsOnRisingEdges_1 (
    .I(Button_2_out), .POR(POR), .CLOCK(TIME_CLOCK), .O(ImpulsOnRisingEdges_1_o));
  // Shift_Register #(.width(4), .length(6), .trigger("falling")) shift_register_1: pin names not known; wires that end beside it: POR, shift_register_1_p2, 1'b0, shift_register_1_p2, PAD_DATA_6REG[3:0], PAD_DATA_6REG[7:4], PAD_DATA_6REG[11:8], PAD_DATA_6REG[15:12], PAD_DATA_6REG[19:16], PAD_DATA_6REG[23:20], shift_register_1_p11, shift_register_1_p12, shift_register_1_p13, shift_register_1_p14, shift_register_1_p15, shift_register_1_p16
  or or_3 (or_3_out, POR, ImpulsOnRisingEdges_1_o);
  MainFSM MainFSM_1 (
    .BTN_CHGN(Button_1_out), .BTN_SE(Button_2_out), .TRIG(clock_1_out), .POR(POR), .STATE(MainFSM_1_state),
    .CLOCK_MSG_EN(CLOCK_MSG_EN), .CLOCK_ENABLE(CLOCK_ENABLE), .CHRONO_MSG_EN(CHRONO_MSG_EN),
    .CHRONO_ENABLE(CHRONO_ENABLE), .COUNTDOWN_MSG_EN(COUNTDOWN_MSG_EN), .COUNTDOWN_ENABLE(COUNTDOWN_ENABLE),
    .MUS_REC(MUS_REC_ENABLE), .MUS_REC_PLAY(MUS_PLAY_REC_ENABLE), .MUS_PLAY(MUS_PLAY_SONG_ENABLE),
    .SET_ALARM_MSG_EN(SET_ALARM_MSG_EN), .SET_ALARM_EN(SET_ALARM_EN));  // open: Output_7
  LED LED_1 (.in(CLOCK_ENABLE));
  LED LED_2 (.in(CHRONO_ENABLE));
  LED LED_3 (.in(COUNTDOWN_ENABLE));
  LED LED_4 (.in(MUS_REC_ENABLE));
  LED LED_5 (.in(MUS_PLAY_REC_ENABLE));
  LED LED_6 (.in(MUS_PLAY_SONG_ENABLE));
  LED LED_7 (.in(SET_ALARM_EN));
  time_setter time_setter_1 (
    .BTN(Button_2_out), .POR(POR), .TIME_CLOCK(TIME_CLOCK), .SET_EN(CLOCK_ENABLE), .VALUE(CLOCK_TIME),
    .SET_VALUE(PAD_DATA_6REG), .SET_MSG({30{1'b1}}), .MSG_CLOCK(MSG_CLOCK), .SET_M_ENT_IMPULS(SET_I_IMPULS),
    .SET_TIME_IMPULS(time_setter_1_set_time_impuls), .SCR_OUT(CLOCK_SCR));  // open: SET_M_EN
  Horloge Horloge_1 (
    .SET_TIME(adder_1_out), .SET_ENABLE(time_setter_1_set_time_impuls), .POR(POR), .TIME_CLOCK(TIME_CLOCK),
    .HMS(CLOCK_TIME));
  time_setter time_setter_3 (
    .BTN(Button_2_out), .POR(POR), .TIME_CLOCK(TIME_CLOCK), .SET_EN(SET_ALARM_EN),
    .VALUE({shift_register_1_p16, shift_register_1_p15, shift_register_1_p14, shift_register_1_p13, shift_register_1_p12, shift_register_1_p11}),
    .SET_VALUE(PAD_DATA_6REG), .SET_MSG({30{1'b1}}), .MSG_CLOCK(MSG_CLOCK),
    .SET_M_ENT_IMPULS(SET_III_IMPULS), .SET_TIME_IMPULS(shift_register_1_p2), .SCR_OUT(SET_ALARM_SCR));  // open: SET_M_EN
  // Probe on MainFSM_1_state
  time_setter time_setter_2 (
    .BTN(Button_2_out), .POR(POR), .TIME_CLOCK(TIME_CLOCK), .SET_EN(COUNTDOWN_ENABLE),
    .VALUE(Countdown_1_hms), .SET_VALUE(PAD_DATA_6REG), .SET_MSG({30{1'b1}}), .MSG_CLOCK(MSG_CLOCK),
    .SET_M_ENT_IMPULS(SET_II_IMPULS), .SET_TIME_IMPULS(time_setter_2_set_time_impuls), .SCR_OUT(COUNTDOWN_SCR));  // open: SET_M_EN
  Countdown Countdown_1 (
    .EN(s_r_ff_1_q), .SET_TIME(PAD_DATA_6REG), .SET_ENABLE(time_setter_2_set_time_impuls), .POR(POR),
    .TIME_CLOCK(TIME_CLOCK), .HMS(Countdown_1_hms), .TIMEOUT(Countdown_1_timeout));
  music_box music_box_1 (
    .key_button_pressed(PAD_DATA_READY), .key_button(PAD_DATA), .rec(MUS_REC_ENABLE),
    .play_recorder(MUS_PLAY_REC_ENABLE), .EN_alarm(or_2_out), .play_song(MUS_PLAY_SONG_ENABLE),
    .EN(music_box_1_en), .freq(music_box_1_freq));
  CountDownButtonHandler ChronoButtonHandler_1 (
    .ENABLE(CHRONO_ENABLE), .BTN(Button_2_out), .POR(POR), .TIME_CLOCK(TIME_CLOCK),
    .START_STOP(ChronoButtonHandler_1_start_stop), .RESET(ChronoButtonHandler_1_reset));
  Comparator #(.width(24), .mode("unsigned")) comparator_1 (
    .a({shift_register_1_p16, shift_register_1_p15, shift_register_1_p14, shift_register_1_p13, shift_register_1_p12, shift_register_1_p11}),
    .b(CLOCK_TIME), .eq(comparator_1_eq));  // open: gt, lt
  Multiplexer #(.select(4), .width(30), .enable("false")) multiplexer_1 (
    .in0(CLOCK_MSG), .in1(CLOCK_SCR), .in2(CHRONO_MSG), .in3(CHRONO_SCR), .in4(COUNTDOWN_MSG),
    .in5(COUNTDOWN_SCR), .in6(RECORDER_MSG), .in7(PLAY_REC_MSG), .in8(PLAY_SONG_MSG), .in9(SET_ALARM_MSG),
    .in10(SET_ALARM_SCR), .out(multiplexer_1_out), .sel(MainFSM_1_state));  // open: in11, in12, in13, in14, in15
  S_R_Flip_Flop #(.trigger("high")) s_r_ff_2 (
    .S(Countdown_1_timeout), .R(Button_2_out), .clk(1'b1), .Q(EN_COUNTDOWN_TIMEOUT), .reset(POR));  // open: Qn, preset
  S_R_Flip_Flop #(.trigger("high")) s_r_ff_3 (
    .S(comparator_1_eq), .R(Button_2_out), .clk(1'b1), .Q(s_r_ff_3_q), .reset(or_3_out));  // open: Qn, preset
  buzzer_sound buzzer_sound_1 (.EN(music_box_1_en), .signal_freq(music_box_1_freq), .buzzer_signal(BUZZER));
  Chrono Chrono_1 (
    .EN(ChronoButtonHandler_1_start_stop), .RESET(ChronoButtonHandler_1_reset), .POR(POR),
    .TIME_CLOCK(TIME_CLOCK), .HMS(Chrono_1_hms));  // open: overflow
  and and_1 (EN_ALARM, s_r_ff_3_q, ALARM_SWITCH);
  converter_24to30 converter_24to30_2 (.from_bits24(Chrono_1_hms), .to_30bits(CHRONO_SCR));
  or or_4 (or_4_out, POR, hexddec_example_1_data_ready);
  S_R_Flip_Flop #(.trigger("high")) s_r_ff_4 (
    .S(hexddec_example_1_data_ready), .R(MSG_CLOCK), .clk(1'b1), .Q(PAD_DATA_READY), .reset(POR));  // open: Qn, preset
  _7_Segment_Display u_7_segment_display_1 (
    .g(segmentdisplaycontroller_1_output_7), .f(segmentdisplaycontroller_1_output_6),
    .a(segmentdisplaycontroller_1_output_1), .b(segmentdisplaycontroller_1_output_2),
    .e(segmentdisplaycontroller_1_output_5), .d(segmentdisplaycontroller_1_output_4),
    .c(segmentdisplaycontroller_1_output_3), .dp(segmentdisplaycontroller_1_output_8));
  Register #(.width(4)) register_1 (
    .D(hexddec_example_1_data), .clk(hexddec_example_1_data_ready), .Q(PAD_DATA), .clr(POR));  // open: en
  SegmentDisplayController segmentdisplaycontroller_1 (
    .Input_bus_1(multiplexer_1_out[29:25]), .Output_1(segmentdisplaycontroller_1_output_1),
    .Output_2(segmentdisplaycontroller_1_output_2), .Output_3(segmentdisplaycontroller_1_output_3),
    .Output_4(segmentdisplaycontroller_1_output_4), .Output_5(segmentdisplaycontroller_1_output_5),
    .Output_6(segmentdisplaycontroller_1_output_6), .Output_7(segmentdisplaycontroller_1_output_7),
    .Output_8(segmentdisplaycontroller_1_output_8));  // open: POINT_EN
  hexddec_example hexddec_example_1 (
    .RESET(or_4_out), .y1(y1), .y2(y2), .y3(y3), .y4(y4), .x1(x1), .x2(x2), .x3(x3), .x4(x4),
    .data(hexddec_example_1_data), .data_ready(hexddec_example_1_data_ready));
  or or_5 (or_5_out, SET_I_IMPULS, SET_II_IMPULS, SET_II_IMPULS);
  _7_Segment_Display u_7_segment_display_2 (
    .g(segmentdisplaycontroller_2_output_7), .f(segmentdisplaycontroller_2_output_6),
    .a(segmentdisplaycontroller_2_output_1), .b(segmentdisplaycontroller_2_output_2),
    .e(segmentdisplaycontroller_2_output_5), .d(segmentdisplaycontroller_2_output_4),
    .c(segmentdisplaycontroller_2_output_3), .dp(segmentdisplaycontroller_2_output_8));
  or or_6 (or_6_out, hexddec_example_1_data_ready, or_5_out);
  SegmentDisplayController segmentdisplaycontroller_2 (
    .Input_bus_1(multiplexer_1_out[24:20]), .POINT_EN(or_7_out),
    .Output_1(segmentdisplaycontroller_2_output_1), .Output_2(segmentdisplaycontroller_2_output_2),
    .Output_3(segmentdisplaycontroller_2_output_3), .Output_4(segmentdisplaycontroller_2_output_4),
    .Output_5(segmentdisplaycontroller_2_output_5), .Output_6(segmentdisplaycontroller_2_output_6),
    .Output_7(segmentdisplaycontroller_2_output_7), .Output_8(segmentdisplaycontroller_2_output_8));
  // Shift_Register #(.width(4), .length(6)) shift_register_2: pin names not known; wires that end beside it: or_5_out, 1'b1, or_6_out, hexddec_example_1_data, PAD_DATA_6REG[3:0], PAD_DATA_6REG[7:4], PAD_DATA_6REG[11:8], PAD_DATA_6REG[15:12], PAD_DATA_6REG[19:16], PAD_DATA_6REG[23:20]
  _7_Segment_Display u_7_segment_display_3 (
    .g(segmentdisplaycontroller_3_output_7), .f(segmentdisplaycontroller_3_output_6),
    .a(segmentdisplaycontroller_3_output_1), .b(segmentdisplaycontroller_3_output_2),
    .e(segmentdisplaycontroller_3_output_5), .d(segmentdisplaycontroller_3_output_4),
    .c(segmentdisplaycontroller_3_output_3), .dp(segmentdisplaycontroller_3_output_8));
  SegmentDisplayController segmentdisplaycontroller_3 (
    .Input_bus_1(multiplexer_1_out[19:15]), .Output_1(segmentdisplaycontroller_3_output_1),
    .Output_2(segmentdisplaycontroller_3_output_2), .Output_3(segmentdisplaycontroller_3_output_3),
    .Output_4(segmentdisplaycontroller_3_output_4), .Output_5(segmentdisplaycontroller_3_output_5),
    .Output_6(segmentdisplaycontroller_3_output_6), .Output_7(segmentdisplaycontroller_3_output_7),
    .Output_8(segmentdisplaycontroller_3_output_8));  // open: POINT_EN
  state_messages state_messages_1 (
    .POR(POR), .Input_bus_1(5'b10100), .Input_bus_2(5'b01100), .Input_bus_3({5{1'b0}}),
    .Input_bus_4(5'b10101), .Input_bus_5(5'b01100), .Input_bus_6({5{1'b1}}), .Input_bus_7({5{1'b1}}),
    .Input_bus_8({5{1'b1}}), .Input_bus_9({5{1'b1}}), .Input_bus_10({5{1'b1}}), .EN(CLOCK_MSG_EN),
    .Output_bus_1(CLOCK_MSG));
  state_messages state_messages_3 (
    .POR(POR), .Input_bus_1(5'b10111), .Input_bus_2(5'b11010), .Input_bus_3({5{1'b0}}),
    .Input_bus_4(5'b01101), .Input_bus_5(5'b11101), .Input_bus_6(5'b10111), .Input_bus_7(5'b11110),
    .Input_bus_8({5{1'b0}}), .Input_bus_9(5'b01100), .Input_bus_10({5{1'b1}}), .EN(COUNTDOWN_MSG_EN),
    .Output_bus_1(COUNTDOWN_MSG));
  state_messages state_messages_5 (
    .POR(POR), .Input_bus_1(5'b01100), .Input_bus_2(5'b01110), .Input_bus_3(5'b11011),
    .Input_bus_4({5{1'b1}}), .Input_bus_5(5'b11000), .Input_bus_6(5'b01010), .Input_bus_7(5'b10101),
    .Input_bus_8(5'b11001), .Input_bus_9({5{1'b1}}), .Input_bus_10({5{1'b1}}), .EN(MUS_PLAY_REC_ENABLE),
    .Output_bus_1(PLAY_REC_MSG));
  state_messages state_messages_7 (
    .POR(POR), .Input_bus_1(5'b10110), .Input_bus_2(5'b11011), .Input_bus_3(5'b01010),
    .Input_bus_4(5'b10101), .Input_bus_5(5'b01010), .Input_bus_6({5{1'b1}}), .Input_bus_7(5'b11101),
    .Input_bus_8(5'b01110), .Input_bus_9(5'b11100), .Input_bus_10({5{1'b1}}), .EN(SET_ALARM_MSG_EN),
    .Output_bus_1(SET_ALARM_MSG));
  _7_Segment_Display u_7_segment_display_4 (
    .g(segmentdisplaycontroller_4_output_7), .f(segmentdisplaycontroller_4_output_6),
    .a(segmentdisplaycontroller_4_output_1), .b(segmentdisplaycontroller_4_output_2),
    .e(segmentdisplaycontroller_4_output_5), .d(segmentdisplaycontroller_4_output_4),
    .c(segmentdisplaycontroller_4_output_3), .dp(segmentdisplaycontroller_4_output_8));
  SegmentDisplayController segmentdisplaycontroller_4 (
    .Input_bus_1(multiplexer_1_out[14:10]), .POINT_EN(or_7_out),
    .Output_1(segmentdisplaycontroller_4_output_1), .Output_2(segmentdisplaycontroller_4_output_2),
    .Output_3(segmentdisplaycontroller_4_output_3), .Output_4(segmentdisplaycontroller_4_output_4),
    .Output_5(segmentdisplaycontroller_4_output_5), .Output_6(segmentdisplaycontroller_4_output_6),
    .Output_7(segmentdisplaycontroller_4_output_7), .Output_8(segmentdisplaycontroller_4_output_8));
  _7_Segment_Display u_7_segment_display_5 (
    .g(segmentdisplaycontroller_5_output_7), .f(undriven), .a(segmentdisplaycontroller_5_output_1),
    .b(segmentdisplaycontroller_5_output_2), .e(segmentdisplaycontroller_5_output_5),
    .d(segmentdisplaycontroller_5_output_4), .c(segmentdisplaycontroller_5_output_3),
    .dp(segmentdisplaycontroller_5_output_8));
  SegmentDisplayController segmentdisplaycontroller_5 (
    .Input_bus_1(multiplexer_1_out[9:5]), .Output_1(segmentdisplaycontroller_5_output_1),
    .Output_2(segmentdisplaycontroller_5_output_2), .Output_3(segmentdisplaycontroller_5_output_3),
    .Output_4(segmentdisplaycontroller_5_output_4), .Output_5(segmentdisplaycontroller_5_output_5),
    .Output_7(segmentdisplaycontroller_5_output_7), .Output_8(segmentdisplaycontroller_5_output_8));  // open: POINT_EN, Output_6
  state_messages state_messages_2 (
    .POR(POR), .Input_bus_1(5'b11011), .Input_bus_2(5'b01110), .Input_bus_3(5'b10110),
    .Input_bus_4(5'b10010), .Input_bus_5(5'b11101), .Input_bus_6({5{1'b1}}), .Input_bus_7({5{1'b1}}),
    .Input_bus_8({5{1'b1}}), .Input_bus_9({5{1'b1}}), .Input_bus_10({5{1'b1}}), .EN(CHRONO_MSG_EN),
    .Output_bus_1(CHRONO_MSG));
  state_messages state_messages_6 (
    .POR(POR), .Input_bus_1(5'b10000), .Input_bus_2(5'b10111), .Input_bus_3({5{1'b0}}),
    .Input_bus_4(5'b11100), .Input_bus_5({5{1'b1}}), .Input_bus_6(5'b11000), .Input_bus_7(5'b01010),
    .Input_bus_8(5'b10101), .Input_bus_9(5'b11001), .Input_bus_10({5{1'b1}}), .EN(MUS_PLAY_SONG_ENABLE),
    .Output_bus_1(PLAY_SONG_MSG));
  or or_7 (or_7_out, CLOCK_ENABLE, CHRONO_ENABLE, COUNTDOWN_ENABLE);
  state_messages state_messages_4 (
    .POR(POR), .Input_bus_1(5'b11011), .Input_bus_2(5'b01110), .Input_bus_3(5'b01101),
    .Input_bus_4(5'b11011), .Input_bus_5({5{1'b0}}), .Input_bus_6(5'b01100), .Input_bus_7(5'b01110),
    .Input_bus_8(5'b11011), .Input_bus_9({5{1'b1}}), .Input_bus_10({5{1'b1}}), .EN(MUS_REC_ENABLE),
    .Output_bus_1(RECORDER_MSG));
  _7_Segment_Display u_7_segment_display_6 (
    .g(segmentdisplaycontroller_6_output_7), .f(segmentdisplaycontroller_6_output_6),
    .a(segmentdisplaycontroller_6_output_1), .b(segmentdisplaycontroller_6_output_2),
    .e(segmentdisplaycontroller_6_output_5), .d(segmentdisplaycontroller_6_output_4), .c(undriven_2),
    .dp(segmentdisplaycontroller_6_output_8));
  SegmentDisplayController segmentdisplaycontroller_6 (
    .Input_bus_1(multiplexer_1_out[4:0]), .POINT_EN(or_7_out),
    .Output_1(segmentdisplaycontroller_6_output_1), .Output_2(segmentdisplaycontroller_6_output_2),
    .Output_3(segmentdisplaycontroller_6_output_3), .Output_4(segmentdisplaycontroller_6_output_4),
    .Output_5(segmentdisplaycontroller_6_output_5), .Output_6(segmentdisplaycontroller_6_output_6),
    .Output_7(segmentdisplaycontroller_6_output_7), .Output_8(segmentdisplaycontroller_6_output_8));

  // Other names for the same wires on the sheet: PLAY_REC_MSG_EN = MUS_PLAY_REC_ENABLE;
  //   PLAY_SONG_MSG_EN = MUS_PLAY_SONG_ENABLE; RECORDER_MSG_EN = MUS_REC_ENABLE

  // Notes on the sheet:
  //   may trig directly here but compiler
  //   complain  about gated and non gated use of same component
  //   horloge set time delay compensation
  //   Screen Management
  //   STATE MESSAGES
  //   POINT ENABLE ON
endmodule

module MainFSM (
  input  BTN_CHGN,
  input  BTN_SE,
  input  TRIG,
  input  POR,
  output [3:0] STATE,
  output CLOCK_MSG_EN,
  output CLOCK_ENABLE,
  output CHRONO_MSG_EN,
  output CHRONO_ENABLE,
  output COUNTDOWN_MSG_EN,
  output COUNTDOWN_ENABLE,
  output MUS_REC,
  output MUS_REC_PLAY,
  output MUS_PLAY,
  output SET_ALARM_MSG_EN,
  output SET_ALARM_EN,
  output Output_7
);

  wire demultiplexer_1_out12, demultiplexer_1_out13;

  nCounter4bitSeq nCounter4bitSeq_1 (
    .EN(BTN_CHGN), .TRIG(TRIG), .COUNT_TO_FROM(4'b1011), .SET(POR), .MODE_MOINS(1'b0), .COUNT_SET(4'b0000),
    .POR(POR), .O(STATE));  // open: R, R_DELAYED
  Demultiplexer #(.select(4), .enable("false")) demultiplexer_1 (
    .out0(CLOCK_MSG_EN), .out1(CLOCK_ENABLE), .out2(CHRONO_MSG_EN), .out3(CHRONO_ENABLE),
    .out4(COUNTDOWN_MSG_EN), .out5(COUNTDOWN_ENABLE), .out6(MUS_REC), .out7(MUS_REC_PLAY), .out8(MUS_PLAY),
    .out9(SET_ALARM_MSG_EN), .out10(SET_ALARM_EN), .out11(Output_7), .out12(demultiplexer_1_out12),
    .out13(demultiplexer_1_out13), .in(1'b1), .sel(STATE));  // open: out14, out15
endmodule

module Horloge (
  input  [23:0] SET_TIME,
  input  SET_ENABLE,
  input  POR,
  input  TIME_CLOCK,
  output [23:0] HMS
);

  wire or_1_out, TimeCounter_1_overflow;

  or or_1 (or_1_out, SET_ENABLE, TimeCounter_1_overflow);
  TimeCounter TimeCounter_1 (
    .EN(1'b1), .RES(or_1_out), .SET_TIME(SET_TIME), .MODE_MOINS(1'b0), .TIME_CLOCK(TIME_CLOCK), .POR(POR),
    .S0(HMS[3:0]), .S1(HMS[7:4]), .M0(HMS[11:8]), .M1(HMS[15:12]), .H0(HMS[19:16]), .H1(HMS[23:20]),
    .Overflow(TimeCounter_1_overflow));
endmodule

module Chrono (
  input  EN,
  input  RESET,
  input  POR,
  input  TIME_CLOCK,
  output [23:0] HMS,
  output overflow
);

  TimeCounter TimeCounter_1 (
    .EN(EN), .RES(RESET), .SET_TIME({24{1'b0}}), .MODE_MOINS(1'b0), .TIME_CLOCK(TIME_CLOCK), .POR(POR),
    .S0(HMS[3:0]), .S1(HMS[7:4]), .M0(HMS[11:8]), .M1(HMS[15:12]), .H0(HMS[19:16]), .H1(HMS[23:20]),
    .Overflow(overflow));
endmodule

module CountDownButtonHandler (
  input  ENABLE,
  input  BTN,
  input  POR,
  input  TIME_CLOCK,
  output START_STOP,
  output RESET
);

  wire and_1_out, LongPush_1_o, or_1_out, or_2_out, s_r_ff_2_q;

  and and_1 (and_1_out, ENABLE, BTN);
  or or_1 (or_1_out, RESET, POR);
  FlipOnEdges FlipOnEdges_1 (.Input_1(and_1_out), .POR(or_1_out), .Output_1(START_STOP));
  S_R_Flip_Flop #(.trigger("high")) s_r_ff_1 (
    .S(LongPush_1_o), .R(s_r_ff_2_q), .clk(1'b1), .Q(RESET), .reset(POR));  // open: Qn, preset
  LongPush LongPush_1 (.I(BTN), .TICK_NUMBER(4'b0100), .TIME_CLOCK(TIME_CLOCK), .POR(POR), .O(LongPush_1_o));
  S_R_Flip_Flop #(.trigger("falling")) s_r_ff_2 (
    .S(RESET), .R(1'b0), .clk(BTN), .Q(s_r_ff_2_q), .reset(or_2_out));  // open: Qn, preset
  or or_2 (or_2_out, s_r_ff_2_q, POR);
endmodule

module Countdown (
  input  EN,
  input  [23:0] SET_TIME,
  input  SET_ENABLE,
  input  POR,
  input  TIME_CLOCK,
  output [23:0] HMS,
  output TIMEOUT
);

  wire or_1_out;

  or or_1 (or_1_out, SET_ENABLE, TIMEOUT);
  TimeCounter TimeCounter_1 (
    .EN(EN), .RES(or_1_out), .SET_TIME(SET_TIME), .MODE_MOINS(1'b1), .TIME_CLOCK(TIME_CLOCK), .POR(POR),
    .S0(HMS[3:0]), .S1(HMS[7:4]), .M0(HMS[11:8]), .M1(HMS[15:12]), .H0(HMS[19:16]), .H1(HMS[23:20]),
    .Overflow(TIMEOUT));
endmodule

module TimeCounter (
  input  EN,
  input  RES,
  input  [23:0] SET_TIME,
  input  MODE_MOINS,
  input  TIME_CLOCK,
  input  POR,
  output [3:0] S0,
  output [3:0] S1,
  output [3:0] M0,
  output [3:0] M1,
  output [3:0] H0,
  output [3:0] H1,
  output Overflow
);

  wire comparator_1_eq, nCounter4bitSeq_1_r, nCounter4bitSeq_2_r, nCounter4bitSeq_3_r, nCounter4bitSeq_4_r,
       nCounter4bitSeq_5_r;
  wire [3:0] multiplexer_1_out;

  Comparator #(.width(4)) comparator_1 (.a(4'b0010), .b(H1), .eq(comparator_1_eq));  // open: gt, lt
  nCounter4bitSeq nCounter4bitSeq_1 (
    .EN(EN), .TRIG(TIME_CLOCK), .COUNT_TO_FROM(4'b1001), .SET(RES), .MODE_MOINS(MODE_MOINS),
    .COUNT_SET(SET_TIME[3:0]), .POR(POR), .O(S0), .R(nCounter4bitSeq_1_r));  // open: R_DELAYED
  nCounter4bitSeq nCounter4bitSeq_2 (
    .EN(nCounter4bitSeq_1_r), .TRIG(TIME_CLOCK), .COUNT_TO_FROM(4'b0101), .SET(RES), .MODE_MOINS(MODE_MOINS),
    .COUNT_SET(SET_TIME[7:4]), .POR(POR), .O(S1), .R(nCounter4bitSeq_2_r));  // open: R_DELAYED
  nCounter4bitSeq nCounter4bitSeq_3 (
    .EN(nCounter4bitSeq_2_r), .TRIG(TIME_CLOCK), .COUNT_TO_FROM(4'b1001), .SET(RES), .MODE_MOINS(MODE_MOINS),
    .COUNT_SET(SET_TIME[11:8]), .POR(POR), .O(M0), .R(nCounter4bitSeq_3_r));  // open: R_DELAYED
  nCounter4bitSeq nCounter4bitSeq_4 (
    .EN(nCounter4bitSeq_3_r), .TRIG(TIME_CLOCK), .COUNT_TO_FROM(4'b0101), .SET(RES), .MODE_MOINS(MODE_MOINS),
    .COUNT_SET(SET_TIME[15:12]), .POR(POR), .O(M1), .R(nCounter4bitSeq_4_r));  // open: R_DELAYED
  nCounter4bitSeq nCounter4bitSeq_5 (
    .EN(nCounter4bitSeq_4_r), .TRIG(TIME_CLOCK), .COUNT_TO_FROM(multiplexer_1_out), .SET(RES),
    .MODE_MOINS(MODE_MOINS), .COUNT_SET(SET_TIME[19:16]), .POR(POR), .O(H0), .R(nCounter4bitSeq_5_r));  // open: R_DELAYED
  Multiplexer #(.width(4), .enable("false")) multiplexer_1 (
    .in0(4'b1001), .in1(4'b0011), .out(multiplexer_1_out), .sel(comparator_1_eq));
  nCounter4bitSeq nCounter4bitSeq_6 (
    .EN(nCounter4bitSeq_5_r), .TRIG(TIME_CLOCK), .COUNT_TO_FROM(4'b0010), .SET(RES), .MODE_MOINS(MODE_MOINS),
    .COUNT_SET(SET_TIME[23:20]), .POR(POR), .O(H1), .R(Overflow));  // open: R_DELAYED
endmodule

module nCounter4bits (
  input  PLUS_MOINS_1,
  input  [3:0] I,
  input  [3:0] COUNT_TO_FROM,
  input  MODE_MOINS,
  output [3:0] O,
  output RETENU
);

  wire AddSous_1_1_retenue, AddSous_1_2_retenue, AddSous_1_3_retenue, and_1_out, and_2_out, comparator_1_eq,
       comparator_2_gt, not_1_out;
  wire [3:0] AddSous_1_1_valsortie, multiplexer_1_out;

  not not_1 (not_1_out, MODE_MOINS);
  AddSous_1 AddSous_1_1 (
    .PlusMoins1(PLUS_MOINS_1), .ValEntree(I[0]), .ModeMoins(MODE_MOINS),
    .ValSortie(AddSous_1_1_valsortie[0]), .Retenue(AddSous_1_1_retenue));
  AddSous_1 AddSous_1_2 (
    .PlusMoins1(AddSous_1_1_retenue), .ValEntree(I[1]), .ModeMoins(MODE_MOINS),
    .ValSortie(AddSous_1_1_valsortie[1]), .Retenue(AddSous_1_2_retenue));
  AddSous_1 AddSous_1_3 (
    .PlusMoins1(AddSous_1_2_retenue), .ValEntree(I[2]), .ModeMoins(MODE_MOINS),
    .ValSortie(AddSous_1_1_valsortie[2]), .Retenue(AddSous_1_3_retenue));
  AddSous_1 AddSous_1_4 (
    .PlusMoins1(AddSous_1_3_retenue), .ValEntree(I[3]), .ModeMoins(MODE_MOINS),
    .ValSortie(AddSous_1_1_valsortie[3]));  // open: Retenue
  // Probe on AddSous_1_1_valsortie
  Comparator #(.width(4), .mode("unsigned")) comparator_1 (
    .a(AddSous_1_1_valsortie), .b(4'b1111), .eq(comparator_1_eq));  // open: gt, lt
  Comparator #(.width(4), .mode("unsigned")) comparator_2 (
    .a(AddSous_1_1_valsortie), .b(COUNT_TO_FROM), .gt(comparator_2_gt));  // open: eq, lt
  and and_1 (and_1_out, comparator_2_gt, not_1_out);
  and and_2 (and_2_out, comparator_1_eq, MODE_MOINS);
  Multiplexer #(.width(4), .enable("false")) multiplexer_1 (
    .in0(AddSous_1_1_valsortie), .in1(4'b0000), .out(multiplexer_1_out), .sel(and_1_out));
  Multiplexer #(.width(4), .enable("false")) multiplexer_2 (
    .in0(multiplexer_1_out), .in1(COUNT_TO_FROM), .out(O), .sel(and_2_out));
  or or_1 (RETENU, and_1_out, and_2_out);
endmodule

module nCounter4bitSeq (
  input  EN,
  input  TRIG,
  input  [3:0] COUNT_TO_FROM,
  input  SET,
  input  MODE_MOINS,
  input  [3:0] COUNT_SET,
  input  POR,
  output [3:0] O,
  output R,
  output R_DELAYED
);

  wire ImpulsOnRisingEdges_1_o, not_1_out, or_1_out;
  wire [3:0] multiplexer_1_out, nCounter4bits_1_o;

  not not_1 (not_1_out, POR);
  // Probe on O
  ImpulsOnRisingEdges ImpulsOnRisingEdges_1 (.I(not_1_out), .POR(POR), .CLOCK(TRIG), .O(ImpulsOnRisingEdges_1_o));
  or or_1 (or_1_out, SET, ImpulsOnRisingEdges_1_o);
  nCounter4bits nCounter4bits_1 (
    .PLUS_MOINS_1(EN), .I(O), .COUNT_TO_FROM(COUNT_TO_FROM), .MODE_MOINS(MODE_MOINS), .O(nCounter4bits_1_o),
    .RETENU(R));
  // Probe on nCounter4bits_1_o
  Multiplexer #(.width(4), .enable("false")) multiplexer_1 (
    .in0(nCounter4bits_1_o), .in1(COUNT_SET), .out(multiplexer_1_out), .sel(or_1_out));
  Register #(.width(4)) register_1 (.D(multiplexer_1_out), .en(1'b1), .clk(TRIG), .Q(O), .clr(POR));
  D_Flip_Flop d_ff_1 (.D(R), .clk(TRIG), .Q(R_DELAYED), .reset(POR));  // open: Qn, preset

  // Notes on the sheet:
  //   COUNT_SET: pull=down
endmodule

module AddSous_1 (
  input  PlusMoins1,
  input  ValEntree,
  input  ModeMoins,
  output ValSortie,
  output Retenue
);

  wire and_1_out, and_2_out, not_1_out, not_2_out, xor_1_out;

  not not_1 (not_1_out, PlusMoins1);
  not not_2 (not_2_out, ValEntree);
  and and_1 (and_1_out, not_1_out, ValEntree);
  and and_2 (and_2_out, PlusMoins1, not_2_out);
  xor xor_1 (xor_1_out, ValEntree, ModeMoins);
  or or_1 (ValSortie, and_1_out, and_2_out);
  and and_3 (Retenue, xor_1_out, PlusMoins1);
endmodule

module SegmentDisplayController (
  input  [4:0] Input_bus_1,
  input  POINT_EN,
  output Output_1,
  output Output_2,
  output Output_3,
  output Output_4,
  output Output_5,
  output Output_6,
  output Output_7,
  output Output_8
);

  SegmentA SegmentA_1 (
    .Input_1(Input_bus_1[4]), .Input_2(Input_bus_1[3]), .Input_3(Input_bus_1[2]), .Input_4(Input_bus_1[1]),
    .Input_5(Input_bus_1[0]), .Output_1(Output_1));
  SegmentB SegmentB_1 (
    .Input_1(Input_bus_1[4]), .Input_2(Input_bus_1[3]), .Input_3(Input_bus_1[2]), .Input_4(Input_bus_1[1]),
    .Input_5(Input_bus_1[0]), .Output_1(Output_2));
  SegmentC SegmentC_1 (
    .Input_1(Input_bus_1[4]), .Input_2(Input_bus_1[3]), .Input_3(Input_bus_1[2]), .Input_4(Input_bus_1[1]),
    .Input_5(Input_bus_1[0]), .Output_1(Output_3));
  SegmentD SegmentD_1 (
    .Input_1(Input_bus_1[4]), .Input_2(Input_bus_1[3]), .Input_3(Input_bus_1[2]), .Input_4(Input_bus_1[1]),
    .Input_5(Input_bus_1[0]), .Output_1(Output_4));
  SegmentE SegmentE_1 (
    .Input_1(Input_bus_1[4]), .Input_2(Input_bus_1[3]), .Input_3(Input_bus_1[2]), .Input_4(Input_bus_1[1]),
    .Input_5(Input_bus_1[0]), .Output_1(Output_5));
  SegmentF SegmentF_1 (
    .Input_1(Input_bus_1[4]), .Input_2(Input_bus_1[3]), .Input_3(Input_bus_1[2]), .Input_4(Input_bus_1[1]),
    .Input_5(Input_bus_1[0]), .Output_1(Output_6));
  SegmentG SegmentG_1 (
    .Input_1(Input_bus_1[4]), .Input_2(Input_bus_1[3]), .Input_3(Input_bus_1[2]), .Input_4(Input_bus_1[1]),
    .Input_5(Input_bus_1[0]), .Output_1(Output_7));

  assign Output_8 = POINT_EN;
endmodule

module SegmentA (
  input  Input_1,
  input  Input_2,
  input  Input_3,
  input  Input_4,
  input  Input_5,
  output Output_1
);

  wire and_1_out, and_2_out, and_3_out, and_4_out, and_5_out, and_6_out, and_7_out, and_8_out, and_9_out,
       not_1_out, not_2_out, not_3_out, not_4_out, not_5_out, not_6_out, not_7_out, not_8_out, not_9_out,
       not_10_out, not_11_out, not_12_out, not_13_out, not_14_out, not_15_out, not_16_out, not_17_out,
       not_18_out;

  not not_1 (not_1_out, Input_1);
  not not_2 (not_2_out, Input_3);
  not not_3 (not_3_out, Input_5);
  not not_4 (not_4_out, Input_1);
  not not_5 (not_5_out, Input_2);
  not not_6 (not_6_out, Input_1);
  not not_7 (not_7_out, Input_2);
  not not_8 (not_8_out, Input_1);
  not not_9 (not_9_out, Input_2);
  not not_10 (not_10_out, Input_1);
  not not_11 (not_11_out, Input_3);
  not not_12 (not_12_out, Input_4);
  not not_13 (not_13_out, Input_4);
  not not_14 (not_14_out, Input_5);
  not not_15 (not_15_out, Input_2);
  not not_16 (not_16_out, Input_4);
  not not_17 (not_17_out, Input_5);
  not not_18 (not_18_out, Input_3);
  and and_1 (and_1_out, not_1_out, not_2_out, not_3_out);
  and and_2 (and_2_out, not_4_out, not_5_out, Input_4);
  and and_3 (and_3_out, not_6_out, not_7_out, Input_3, Input_5);
  and and_4 (and_4_out, not_8_out, Input_3, Input_4);
  and and_5 (and_5_out, not_9_out, Input_3, Input_4);
  and and_6 (and_6_out, not_10_out, Input_2, not_11_out, not_12_out);
  and and_7 (and_7_out, Input_2, Input_3, not_13_out, not_14_out);
  and and_8 (and_8_out, Input_1, not_15_out, not_16_out, not_17_out);
  and and_9 (and_9_out, Input_1, Input_2, not_18_out, Input_5);
  or or_1 (Output_1, and_1_out, and_2_out, and_3_out, and_4_out, and_5_out, and_6_out, and_7_out, and_8_out, and_9_out);
endmodule

module SegmentB (
  input  Input_1,
  input  Input_2,
  input  Input_3,
  input  Input_4,
  input  Input_5,
  output Output_1
);

  wire and_1_out, and_2_out, and_3_out, and_4_out, and_5_out, and_6_out, and_7_out, and_8_out, not_1_out,
       not_2_out, not_3_out, not_4_out, not_5_out, not_6_out, not_7_out, not_8_out, not_9_out, not_10_out,
       not_11_out, not_12_out, not_13_out, not_14_out, not_15_out, not_16_out, not_17_out, not_18_out;

  not not_1 (not_1_out, Input_1);
  not not_2 (not_2_out, Input_2);
  not not_3 (not_3_out, Input_3);
  not not_4 (not_4_out, Input_1);
  not not_5 (not_5_out, Input_2);
  not not_6 (not_6_out, Input_4);
  not not_7 (not_7_out, Input_5);
  not not_8 (not_8_out, Input_1);
  not not_9 (not_9_out, Input_3);
  not not_10 (not_10_out, Input_5);
  not not_11 (not_11_out, Input_2);
  not not_12 (not_12_out, Input_3);
  not not_13 (not_13_out, Input_2);
  not not_14 (not_14_out, Input_3);
  not not_15 (not_15_out, Input_4);
  not not_16 (not_16_out, Input_1);
  not not_17 (not_17_out, Input_4);
  not not_18 (not_18_out, Input_5);
  and and_1 (and_1_out, not_1_out, not_2_out, not_3_out);
  and and_2 (and_2_out, not_4_out, not_5_out, not_6_out, not_7_out);
  and and_3 (and_3_out, not_8_out, not_9_out, not_10_out);
  and and_4 (and_4_out, not_11_out, not_12_out, Input_5);
  and and_5 (and_5_out, not_13_out, Input_4, Input_5);
  and and_6 (and_6_out, Input_2, not_14_out, not_15_out);
  and and_7 (and_7_out, not_16_out, Input_2, not_17_out, Input_5);
  and and_8 (and_8_out, Input_1, Input_2, Input_4, not_18_out);
  or or_1 (Output_1, and_1_out, and_2_out, and_3_out, and_4_out, and_5_out, and_6_out, and_7_out, and_8_out);
endmodule

module SegmentC (
  input  Input_1,
  input  Input_2,
  input  Input_3,
  input  Input_4,
  input  Input_5,
  output Output_1
);

  wire and_1_out, and_2_out, and_3_out, and_4_out, and_5_out, and_6_out, and_7_out, not_1_out, not_2_out,
       not_3_out, not_4_out, not_5_out, not_6_out, not_7_out, not_8_out, not_9_out, not_10_out, not_11_out,
       not_12_out, not_13_out, not_14_out;

  not not_1 (not_1_out, Input_2);
  not not_2 (not_2_out, Input_3);
  not not_3 (not_3_out, Input_4);
  not not_4 (not_4_out, Input_3);
  not not_5 (not_5_out, Input_4);
  not not_6 (not_6_out, Input_5);
  not not_7 (not_7_out, Input_1);
  not not_8 (not_8_out, Input_4);
  not not_9 (not_9_out, Input_2);
  not not_10 (not_10_out, Input_1);
  not not_11 (not_11_out, Input_2);
  not not_12 (not_12_out, Input_1);
  not not_13 (not_13_out, Input_3);
  not not_14 (not_14_out, Input_5);
  and and_1 (and_1_out, not_1_out, not_2_out, not_3_out);
  and and_2 (and_2_out, not_4_out, not_5_out, not_6_out);
  and and_3 (and_3_out, not_7_out, not_8_out, Input_5);
  and and_4 (and_4_out, not_9_out, Input_4, Input_5);
  and and_5 (and_5_out, not_10_out, not_11_out, Input_3);
  and and_6 (and_6_out, not_12_out, Input_2, not_13_out);
  and and_7 (and_7_out, Input_1, Input_3, not_14_out);
  or or_1 (Output_1, and_1_out, and_2_out, and_3_out, and_4_out, and_5_out, and_6_out, and_7_out);
endmodule

module SegmentD (
  input  Input_1,
  input  Input_2,
  input  Input_3,
  input  Input_4,
  input  Input_5,
  output Output_1
);

  wire and_1_out, and_2_out, and_3_out, and_4_out, and_5_out, and_6_out, and_7_out, and_8_out, not_1_out,
       not_2_out, not_3_out, not_4_out, not_5_out, not_6_out, not_7_out, not_8_out, not_9_out, not_10_out,
       not_11_out, not_12_out, not_13_out, not_14_out, not_15_out;

  not not_1 (not_1_out, Input_3);
  not not_2 (not_2_out, Input_4);
  not not_3 (not_3_out, Input_5);
  not not_4 (not_4_out, Input_1);
  not not_5 (not_5_out, Input_2);
  not not_6 (not_6_out, Input_5);
  not not_7 (not_7_out, Input_2);
  not not_8 (not_8_out, Input_3);
  not not_9 (not_9_out, Input_4);
  not not_10 (not_10_out, Input_1);
  not not_11 (not_11_out, Input_4);
  not not_12 (not_12_out, Input_1);
  not not_13 (not_13_out, Input_3);
  not not_14 (not_14_out, Input_5);
  not not_15 (not_15_out, Input_5);
  and and_1 (and_1_out, not_1_out, not_2_out, not_3_out);
  and and_2 (and_2_out, not_4_out, not_5_out, Input_4, not_6_out);
  and and_3 (and_3_out, not_7_out, not_8_out, Input_4, Input_5);
  and and_4 (and_4_out, Input_3, not_9_out, Input_5);
  and and_5 (and_5_out, not_10_out, Input_2, not_11_out);
  and and_6 (and_6_out, not_12_out, Input_2, not_13_out, Input_5);
  and and_7 (and_7_out, Input_2, Input_3, not_14_out);
  and and_8 (and_8_out, Input_1, Input_2, not_15_out);
  or or_1 (Output_1, and_1_out, and_2_out, and_3_out, and_4_out, and_5_out, and_6_out, and_7_out, and_8_out);
endmodule

module SegmentG (
  input  Input_1,
  input  Input_2,
  input  Input_3,
  input  Input_4,
  input  Input_5,
  output Output_1
);

  wire and_1_out, and_2_out, and_3_out, and_4_out, and_5_out, and_6_out, and_7_out, and_8_out, not_1_out,
       not_2_out, not_3_out, not_4_out, not_5_out, not_6_out, not_7_out, not_8_out, not_9_out, not_10_out,
       not_11_out, not_12_out, not_13_out, not_14_out, not_15_out, not_16_out;

  not not_1 (not_1_out, Input_1);
  not not_2 (not_2_out, Input_3);
  not not_3 (not_3_out, Input_1);
  not not_4 (not_4_out, Input_5);
  not not_5 (not_5_out, Input_1);
  not not_6 (not_6_out, Input_2);
  not not_7 (not_7_out, Input_4);
  not not_8 (not_8_out, Input_1);
  not not_9 (not_9_out, Input_3);
  not not_10 (not_10_out, Input_4);
  not not_11 (not_11_out, Input_1);
  not not_12 (not_12_out, Input_2);
  not not_13 (not_13_out, Input_3);
  not not_14 (not_14_out, Input_4);
  not not_15 (not_15_out, Input_4);
  not not_16 (not_16_out, Input_5);
  and and_1 (and_1_out, not_1_out, not_2_out, Input_4);
  and and_2 (and_2_out, not_3_out, Input_4, not_4_out);
  and and_3 (and_3_out, not_5_out, not_6_out, Input_3, not_7_out);
  and and_4 (and_4_out, not_8_out, Input_2, not_9_out);
  and and_5 (and_5_out, Input_2, not_10_out, Input_5);
  and and_6 (and_6_out, not_11_out, Input_2, Input_4);
  and and_7 (and_7_out, Input_1, not_12_out, not_13_out, not_14_out);
  and and_8 (and_8_out, Input_1, Input_3, not_15_out, not_16_out);
  or or_1 (Output_1, and_1_out, and_2_out, and_3_out, and_4_out, and_5_out, and_6_out, and_7_out, and_8_out);
endmodule

module SegmentE (
  input  Input_1,
  input  Input_2,
  input  Input_3,
  input  Input_4,
  input  Input_5,
  output Output_1
);

  wire and_1_out, and_2_out, and_3_out, and_4_out, and_5_out, and_6_out, and_7_out, not_1_out, not_2_out,
       not_3_out, not_4_out, not_5_out, not_6_out, not_7_out, not_8_out, not_9_out;

  not not_1 (not_1_out, Input_1);
  not not_2 (not_2_out, Input_3);
  not not_3 (not_3_out, Input_5);
  not not_4 (not_4_out, Input_5);
  not not_5 (not_5_out, Input_1);
  not not_6 (not_6_out, Input_1);
  not not_7 (not_7_out, Input_2);
  not not_8 (not_8_out, Input_3);
  not not_9 (not_9_out, Input_4);
  and and_1 (and_1_out, not_1_out, not_2_out, not_3_out);
  and and_2 (and_2_out, Input_3, Input_4, not_4_out);
  and and_3 (and_3_out, not_5_out, Input_2, Input_4);
  and and_4 (and_4_out, not_6_out, Input_2, Input_3);
  and and_5 (and_5_out, Input_1, not_7_out);
  and and_6 (and_6_out, Input_1, not_8_out, Input_5);
  and and_7 (and_7_out, Input_1, not_9_out, Input_5);
  or or_1 (Output_1, and_1_out, and_2_out, and_3_out, and_4_out, and_5_out, and_6_out, and_7_out);
endmodule

module SegmentF (
  input  Input_1,
  input  Input_2,
  input  Input_3,
  input  Input_4,
  input  Input_5,
  output Output_1
);

  wire and_1_out, and_2_out, and_3_out, and_4_out, and_5_out, and_6_out, and_7_out, and_8_out, and_9_out,
       not_1_out, not_2_out, not_3_out, not_4_out, not_5_out, not_6_out, not_7_out, not_8_out, not_9_out,
       not_10_out, not_11_out, not_12_out, not_13_out;

  not not_1 (not_1_out, Input_4);
  not not_2 (not_2_out, Input_5);
  not not_3 (not_3_out, Input_1);
  not not_4 (not_4_out, Input_5);
  not not_5 (not_5_out, Input_2);
  not not_6 (not_6_out, Input_4);
  not not_7 (not_7_out, Input_3);
  not not_8 (not_8_out, Input_5);
  not not_9 (not_9_out, Input_1);
  not not_10 (not_10_out, Input_3);
  not not_11 (not_11_out, Input_5);
  not not_12 (not_12_out, Input_4);
  not not_13 (not_13_out, Input_2);
  and and_1 (and_1_out, not_1_out, not_2_out);
  and and_2 (and_2_out, not_3_out, Input_3, not_4_out);
  and and_3 (and_3_out, not_5_out, Input_3, not_6_out);
  and and_4 (and_4_out, Input_2, not_7_out);
  and and_5 (and_5_out, Input_2, not_8_out);
  and and_6 (and_6_out, not_9_out, Input_2, Input_4);
  and and_7 (and_7_out, Input_1, not_10_out, not_11_out);
  and and_8 (and_8_out, Input_1, not_12_out);
  and and_9 (and_9_out, Input_1, not_13_out, Input_3, Input_5);
  or or_1 (Output_1, and_1_out, and_2_out, and_3_out, and_4_out, and_5_out, and_6_out, and_7_out, and_8_out, and_9_out);
endmodule

module ImpulsOnRisingEdges (
  input  I,
  input  POR,
  input  CLOCK,
  output O
);

  wire d_ff_2_q, d_ff_3_q, d_ff_4_q, not_1_out, or_1_out;

  not not_1 (not_1_out, O);
  D_Flip_Flop d_ff_1 (.D(not_1_out), .clk(I), .Q(O), .reset(or_1_out));  // open: Qn, preset
  or or_1 (or_1_out, d_ff_4_q, POR);
  D_Flip_Flop d_ff_2 (.D(O), .clk(CLOCK), .Q(d_ff_2_q), .reset(POR));  // open: Qn, preset
  D_Flip_Flop d_ff_3 (.D(d_ff_2_q), .clk(CLOCK), .Q(d_ff_3_q), .reset(POR));  // open: Qn, preset
  D_Flip_Flop d_ff_4 (.D(d_ff_3_q), .clk(CLOCK), .Q(d_ff_4_q), .reset(POR));  // open: Qn, preset
endmodule

module FlipOnEdges (
  input  Input_1,
  input  POR,
  output Output_1
);

  wire d_ff_1_qn;

  D_Flip_Flop d_ff_1 (.D(d_ff_1_qn), .clk(Input_1), .Q(Output_1), .Qn(d_ff_1_qn), .reset(POR));  // open: preset
endmodule

module LongPush (
  input  I,
  input  [3:0] TICK_NUMBER,
  input  TIME_CLOCK,
  input  POR,
  output O
);

  wire not_1_out, or_1_out;
  wire [3:0] nCounter4bitSeq_1_o;

  not not_1 (not_1_out, I);
  or or_1 (or_1_out, O, not_1_out);
  nCounter4bitSeq nCounter4bitSeq_1 (
    .EN(I), .TRIG(TIME_CLOCK), .COUNT_TO_FROM(4'b1111), .SET(or_1_out), .MODE_MOINS(1'b0),
    .COUNT_SET(4'b0000), .POR(POR), .O(nCounter4bitSeq_1_o));  // open: R, R_DELAYED
  Comparator #(.width(4), .mode("unsigned")) comparator_1 (
    .a(TICK_NUMBER), .b(nCounter4bitSeq_1_o), .eq(O));  // open: gt, lt
endmodule

module hexddec_example (
  input  RESET,
  input  y1,
  input  y2,
  input  y3,
  input  y4,
  output x1,
  output x2,
  output x3,
  output x4,
  output [3:0] data,
  output data_ready
);

  wire column_debouncer_ch0_dout, column_debouncer_ch1_dout, column_debouncer_ch2_dout,
       column_debouncer_ch3_dout, FSM_main_output_1, FSM_main_output_2, FSM_main_output_3, FSM_main_output_4,
       not_1_out, not_2_out, not_3_out, not_4_out, not_5_out, not_6_out, not_7_out, not_8_out, or_1_out,
       result_register_output_1, result_register_output_2, result_register_output_3,
       result_register_output_4, result_register_output_5, result_register_output_6,
       result_register_output_7, result_register_output_8, state0_logic_hp_s0_detect,
       state2_logic_hp_s2_data_ready, state3_logic_timer_out, state_1_to_be_completed_1_hp_s0_detect;

  Clock sysclk ();  // open: out
  Clock #(.highDuration(10), .lowDuration(10)) clk_256 ();  // open: out
  Clock #(.highDuration(100), .lowDuration(100)) clk_16 ();  // open: out
  debounce_4 column_debouncer (
    .ch0(y1), .ch1(y2), .ch2(y3), .ch3(y4), .RESET(RESET), .ch0_dout(column_debouncer_ch0_dout),
    .ch1_dout(column_debouncer_ch1_dout), .ch2_dout(column_debouncer_ch2_dout),
    .ch3_dout(column_debouncer_ch3_dout));
  FSM_full FSM_main (
    .i01_Hpulse(state0_logic_hp_s0_detect), .i02_Hpulse(state_1_to_be_completed_1_hp_s0_detect),
    .i03_Hpulse(state2_logic_hp_s2_data_ready), .Input_1(state3_logic_timer_out), .RESET(RESET),
    .Output_1(FSM_main_output_1), .Output_2(FSM_main_output_2), .Output_3(FSM_main_output_3),
    .Output_4(FSM_main_output_4));
  state_0 state0_logic (
    .S0(FSM_main_output_1), .RESET(RESET), .y1(column_debouncer_ch0_dout), .y2(column_debouncer_ch1_dout),
    .y3(column_debouncer_ch2_dout), .y4(column_debouncer_ch3_dout), .HP_S0_detect(state0_logic_hp_s0_detect));
  state_1_to_be_completed state_1_to_be_completed_1 (
    .s1(FSM_main_output_2), .RESET(RESET), .y1(column_debouncer_ch0_dout), .y2(column_debouncer_ch1_dout),
    .y3(column_debouncer_ch2_dout), .y4(column_debouncer_ch3_dout),
    .HP_S0_detect(state_1_to_be_completed_1_hp_s0_detect), .coldriver0(x1), .coldriver1(x2), .coldriver2(x3),
    .coldriver3(x4));
  register_8bit result_register (
    .clk01(state0_logic_hp_s0_detect), .clk02(state_1_to_be_completed_1_hp_s0_detect), .RESET(RESET),
    .b0(column_debouncer_ch0_dout), .b1(column_debouncer_ch1_dout), .b2(column_debouncer_ch2_dout),
    .b3(column_debouncer_ch3_dout), .b4(x1), .b5(x2), .b6(x3), .b7(x4), .Output_1(result_register_output_1),
    .Output_2(result_register_output_2), .Output_3(result_register_output_3),
    .Output_4(result_register_output_4), .Output_5(result_register_output_5),
    .Output_6(result_register_output_6), .Output_7(result_register_output_7),
    .Output_8(result_register_output_8));
  state_2 state2_logic (.s2(FSM_main_output_3), .RESET(RESET), .HP_S2_data_ready(state2_logic_hp_s2_data_ready));
  state_3 state3_logic (.s3(FSM_main_output_4), .RESET(RESET), .timer_out(state3_logic_timer_out));
  not not_1 (not_1_out, result_register_output_1);
  not not_2 (not_2_out, result_register_output_2);
  not not_3 (not_3_out, result_register_output_3);
  not not_4 (not_4_out, result_register_output_4);
  not not_5 (not_5_out, result_register_output_5);
  not not_6 (not_6_out, result_register_output_6);
  not not_7 (not_7_out, result_register_output_7);
  not not_8 (not_8_out, result_register_output_8);
  or or_1 (or_1_out, state3_logic_timer_out, RESET);
  D_Flip_Flop d_ff_1 (
    .D(1'b0), .clk(1'b0), .Q(data_ready), .preset(state2_logic_hp_s2_data_ready), .reset(or_1_out));  // open: Qn
  ClavierTo4bit ClavierTo4bit_1 (
    .y1(not_1_out), .y2(not_2_out), .y3(not_3_out), .y4(not_4_out), .x1(not_5_out), .x2(not_6_out),
    .x3(not_7_out), .x4(not_8_out), .B0(data[0]), .B1(data[1]), .B2(data[2]), .B3(data[3]));
  // Probe on data

  // Notes on the sheet:
  //   y1: pull=up
  //   y2: pull=up
  //   y4: pull=up
  //   y3: pull=up
endmodule

module FSM_full (
  input  i01_Hpulse,
  input  i02_Hpulse,
  input  i03_Hpulse,
  input  Input_1,
  input  RESET,
  output Output_1,
  output Output_2,
  output Output_3,
  output Output_4
);

  wire or_1_out;

  Clock sysclk ();  // open: out
  or or_1 (or_1_out, i01_Hpulse, i02_Hpulse, i03_Hpulse, Input_1);
  D_Flip_Flop d_ff_1 (.D(Output_4), .clk(or_1_out), .Q(Output_1), .preset(RESET));  // open: Qn, reset
  D_Flip_Flop d_ff_2 (.D(Output_1), .clk(or_1_out), .Q(Output_2), .reset(RESET));  // open: Qn, preset
  D_Flip_Flop d_ff_3 (.D(Output_2), .clk(or_1_out), .Q(Output_3), .reset(RESET));  // open: Qn, preset
  D_Flip_Flop d_ff_4 (.D(Output_3), .clk(or_1_out), .Q(Output_4), .reset(RESET));  // open: Qn, preset

  // Notes on the sheet:
  //   Transition logic
  //   (active on a positive pulse)
  //   A Moore finite-state machine and its decoder are optimized into a simplified circuit presented here
  //   Counter and decoder
  //   (optimized/simplified into one circuit)
endmodule

module state_0 (
  input  S0,
  input  RESET,
  input  y1,
  input  y2,
  input  y3,
  input  y4,
  output HP_S0_detect
);

  wire and_1_out, and_2_out, clk_256_out, d_ff_1_q, d_ff_2_q, d_ff_3_q, not_1_out, or_1_out, xor_1_out;

  Clock sysclk ();  // open: out
  Clock #(.highDuration(50), .lowDuration(50)) clk_256 (.out(clk_256_out));
  not not_1 (not_1_out, S0);
  or or_1 (or_1_out, not_1_out, RESET);
  and and_1 (and_1_out, y1, y2, y3, y4);
  D_Flip_Flop d_ff_1 (.D(and_1_out), .clk(clk_256_out), .Q(d_ff_1_q), .reset(or_1_out));  // open: Qn, preset
  xor xor_1 (xor_1_out, and_1_out, d_ff_1_q);
  D_Flip_Flop d_ff_2 (.D(and_2_out), .clk(clk_256_out), .Q(d_ff_2_q), .reset(or_1_out));  // open: Qn, preset
  and and_2 (and_2_out, xor_1_out, d_ff_1_q);
  D_Flip_Flop d_ff_3 (.D(d_ff_2_q), .clk(clk_256_out), .Q(d_ff_3_q), .reset(or_1_out));  // open: Qn, preset
  xor xor_2 (HP_S0_detect, d_ff_2_q, d_ff_3_q);
endmodule

module state_1_to_be_completed (
  input  s1,
  input  RESET,
  input  y1,
  input  y2,
  input  y3,
  input  y4,
  output HP_S0_detect,
  output coldriver0,
  output coldriver1,
  output coldriver2,
  output coldriver3
);

  wire and_1_out, and_2_out, and_3_out, and_4_out, and_5_out, and_6_out, and_7_out, and_8_out, clk_16_out,
       clk_256_out, d_ff_1_qn, d_ff_2_qn, d_ff_3_q, d_ff_3_qn, d_ff_4_q, d_ff_5_q, d_ff_6_q, d_ff_7_q,
       d_ff_8_q, d_ff_9_q, d_ff_10_q, d_ff_11_q, d_ff_11_qn, demultiplexer_1_out0, demultiplexer_1_out1,
       demultiplexer_1_out2, demultiplexer_1_out3, not_1_out, or_1_out, or_2_out, xor_1_out, xor_2_out,
       xor_4_out;
  wire [3:0] nCounter4bitSeq_1_o;

  Clock sysclk ();  // open: out
  Clock #(.highDuration(10), .lowDuration(10)) clk_256 (.out(clk_256_out));
  Clock #(.highDuration(100), .lowDuration(100)) clk_16 (.out(clk_16_out));
  not not_1 (not_1_out, s1);
  or or_1 (or_1_out, not_1_out, RESET);
  and and_1 (and_1_out, y1, y2, y3, y4);
  and and_2 (and_2_out, d_ff_11_q, clk_16_out);
  D_Flip_Flop d_ff_1 (.D(d_ff_5_q), .clk(and_2_out), .Qn(d_ff_1_qn), .preset(or_1_out), .reset(xor_2_out));  // open: Q
  D_Flip_Flop d_ff_2 (.D(s1), .clk(clk_256_out), .Qn(d_ff_2_qn), .reset(or_1_out));  // open: Q, preset
  D_Flip_Flop d_ff_3 (
    .D(and_1_out), .clk(clk_256_out), .Q(d_ff_3_q), .Qn(d_ff_3_qn), .reset(or_2_out));  // open: preset
  or or_2 (or_2_out, or_1_out, d_ff_11_qn);
  D_Flip_Flop #(.trigger("falling")) d_ff_4 (
    .D(1'b0), .clk(clk_256_out), .Q(d_ff_4_q), .preset(d_ff_5_q), .reset(or_1_out));  // open: Qn
  D_Flip_Flop d_ff_5 (.D(and_3_out), .clk(clk_256_out), .Q(d_ff_5_q), .reset(or_1_out));  // open: Qn, preset
  and and_3 (and_3_out, s1, d_ff_2_qn);
  xor xor_1 (xor_1_out, and_1_out, d_ff_3_q);
  D_Flip_Flop d_ff_6 (.D(and_4_out), .clk(clk_256_out), .Q(d_ff_6_q), .reset(or_2_out));  // open: Qn, preset
  and and_4 (and_4_out, xor_1_out, d_ff_3_q);
  nCounter4bitSeq nCounter4bitSeq_1 (
    .EN(d_ff_1_qn), .TRIG(clk_256_out), .COUNT_TO_FROM(4'b0011), .SET(1'b0), .MODE_MOINS(1'b0),
    .COUNT_SET(4'b0000), .POR(RESET), .O(nCounter4bitSeq_1_o));  // open: R, R_DELAYED
  D_Flip_Flop d_ff_7 (.D(d_ff_5_q), .clk(clk_256_out), .Q(d_ff_7_q), .reset(or_1_out));  // open: Qn, preset
  D_Flip_Flop d_ff_8 (.D(d_ff_6_q), .clk(clk_256_out), .Q(d_ff_8_q), .reset(or_2_out));  // open: Qn, preset
  Demultiplexer #(.select(4), .enable("false")) demultiplexer_1 (
    .out0(demultiplexer_1_out0), .out1(demultiplexer_1_out1), .out2(demultiplexer_1_out2),
    .out3(demultiplexer_1_out3), .in(1'b1), .sel(nCounter4bitSeq_1_o));  // open: out4, out5, out6, out7, out8, out9, out10, out11, out12, out13, out14, out15
  xor xor_2 (xor_2_out, d_ff_5_q, d_ff_7_q);
  D_Flip_Flop d_ff_9 (.D(d_ff_7_q), .clk(clk_256_out), .Q(d_ff_9_q), .reset(or_1_out));  // open: Qn, preset
  D_Flip_Flop d_ff_10 (.D(d_ff_9_q), .clk(clk_256_out), .Q(d_ff_10_q), .reset(or_1_out));  // open: Qn, preset
  xor xor_3 (HP_S0_detect, d_ff_6_q, d_ff_8_q);
  or or_3 (coldriver0, d_ff_4_q, and_5_out);
  and and_5 (and_5_out, d_ff_1_qn, ~demultiplexer_1_out0);  // AND_Gate
  or or_4 (coldriver1, d_ff_4_q, and_6_out);
  and and_6 (and_6_out, d_ff_1_qn, ~demultiplexer_1_out1);  // AND_Gate
  or or_5 (coldriver2, d_ff_4_q, and_7_out);
  and and_7 (and_7_out, d_ff_1_qn, ~demultiplexer_1_out2);  // AND_Gate
  or or_6 (coldriver3, d_ff_4_q, and_8_out);
  and and_8 (and_8_out, d_ff_1_qn, ~demultiplexer_1_out3);  // AND_Gate
  xor xor_4 (xor_4_out, d_ff_9_q, d_ff_10_q);
  D_Flip_Flop d_ff_11 (.Q(d_ff_11_q), .Qn(d_ff_11_qn), .preset(xor_4_out), .reset(or_1_out));  // open: D, clk

  // Notes on the sheet:
  //   Your bubble-counter at this location
endmodule

module state_2 (
  input  s2,
  input  RESET,
  output HP_S2_data_ready
);

  wire clk_256_out, d_ff_1_q, d_ff_2_q, d_ff_3_q, not_1_out, or_1_out;

  Clock sysclk ();  // open: out
  Clock #(.highDuration(10), .lowDuration(10)) clk_256 (.out(clk_256_out));
  not not_1 (not_1_out, s2);
  or or_1 (or_1_out, not_1_out, RESET);
  D_Flip_Flop d_ff_1 (.D(1'b0), .clk(clk_256_out), .Q(d_ff_1_q), .preset(or_1_out));  // open: Qn, reset
  D_Flip_Flop d_ff_2 (.D(d_ff_1_q), .clk(clk_256_out), .Q(d_ff_2_q), .reset(or_1_out));  // open: Qn, preset
  D_Flip_Flop d_ff_3 (.D(d_ff_2_q), .clk(clk_256_out), .Q(d_ff_3_q), .reset(or_1_out));  // open: Qn, preset
  xor xor_1 (HP_S2_data_ready, d_ff_2_q, d_ff_3_q);
endmodule

module state_3 (
  input  s3,
  input  RESET,
  output timer_out
);

  wire clk_256_out, not_1_out, or_1_out;

  Clock sysclk ();  // open: out
  Clock #(.highDuration(10), .lowDuration(10)) clk_256 (.out(clk_256_out));
  not not_1 (not_1_out, s3);
  or or_1 (or_1_out, not_1_out, RESET);
  Counter counter_1 (.clr(or_1_out), .clk(clk_256_out), .carry(timer_out));  // open: load, up, count, D, Q
endmodule

module three_level_digfilter (
  input  button_in,
  input  RESET,
  output Output_1
);

  wire and_1_out, and_2_out, clk_256_t_out, d_ff_1_q, d_ff_2_q, d_ff_3_q, d_ff_4_q;

  Clock sysclk ();  // open: out
  Clock #(.highDuration(50), .lowDuration(50)) clk_256_t (.out(clk_256_t_out));
  D_Flip_Flop d_ff_1 (.D(button_in), .clk(clk_256_t_out), .Q(d_ff_1_q), .reset(RESET));  // open: Qn, preset
  D_Flip_Flop d_ff_2 (.D(d_ff_1_q), .clk(clk_256_t_out), .Q(d_ff_2_q), .reset(RESET));  // open: Qn, preset
  D_Flip_Flop d_ff_3 (.D(d_ff_2_q), .clk(clk_256_t_out), .Q(d_ff_3_q), .reset(RESET));  // open: Qn, preset
  D_Flip_Flop d_ff_4 (.D(d_ff_3_q), .clk(clk_256_t_out), .Q(d_ff_4_q), .reset(RESET));  // open: Qn, preset
  and and_1 (and_1_out, d_ff_2_q, d_ff_3_q, d_ff_4_q);
  and and_2 (and_2_out, ~d_ff_4_q, ~d_ff_3_q, ~d_ff_2_q);  // AND_Gate
  J_K_Flip_Flop j_k_ff_1 (.J(and_1_out), .K(and_2_out), .clk(clk_256_t_out), .Q(Output_1));  // open: Qn, preset, reset
endmodule

module debounce_4 (
  input  ch0,
  input  ch1,
  input  ch2,
  input  ch3,
  input  RESET,
  output ch0_dout,
  output ch1_dout,
  output ch2_dout,
  output ch3_dout
);

  Clock sysclk ();  // open: out
  three_level_digfilter debounce_ch0 (.button_in(ch0), .RESET(RESET), .Output_1(ch0_dout));
  three_level_digfilter debounce_ch1 (.button_in(ch1), .RESET(RESET), .Output_1(ch1_dout));
  three_level_digfilter debounce_ch2 (.button_in(ch2), .RESET(RESET), .Output_1(ch2_dout));
  three_level_digfilter debounce_ch3 (.button_in(ch3), .RESET(RESET), .Output_1(ch3_dout));
endmodule

module register_8bit (
  input  clk01,
  input  clk02,
  input  RESET,
  input  b0,
  input  b1,
  input  b2,
  input  b3,
  input  b4,
  input  b5,
  input  b6,
  input  b7,
  output Output_1,
  output Output_2,
  output Output_3,
  output Output_4,
  output Output_5,
  output Output_6,
  output Output_7,
  output Output_8
);

  Clock sysclk ();  // open: out
  D_Flip_Flop d_ff_1 (.D(b0), .clk(clk01), .Q(Output_1), .preset(RESET));  // open: Qn, reset
  D_Flip_Flop d_ff_2 (.D(b1), .clk(clk01), .Q(Output_2), .reset(RESET));  // open: Qn, preset
  D_Flip_Flop d_ff_3 (.D(b2), .clk(clk01), .Q(Output_3), .reset(RESET));  // open: Qn, preset
  D_Flip_Flop d_ff_4 (.D(b3), .clk(clk01), .Q(Output_4), .reset(RESET));  // open: Qn, preset
  D_Flip_Flop d_ff_5 (.D(b4), .clk(clk02), .Q(Output_5), .reset(RESET));  // open: Qn, preset
  D_Flip_Flop d_ff_6 (.D(b5), .clk(clk02), .Q(Output_6), .reset(RESET));  // open: Qn, preset
  D_Flip_Flop d_ff_7 (.D(b6), .clk(clk02), .Q(Output_7), .reset(RESET));  // open: Qn, preset
  D_Flip_Flop d_ff_8 (.D(b7), .clk(clk02), .Q(Output_8), .reset(RESET));  // open: Qn, preset
endmodule

module ClavierTo4bit (
  input  y1,
  input  y2,
  input  y3,
  input  y4,
  input  x1,
  input  x2,
  input  x3,
  input  x4,
  output B0,
  output B1,
  output B2,
  output B3
);

  wire and_1_out, and_2_out, and_3_out, and_4_out, and_5_out, and_6_out, and_7_out, and_8_out, and_9_out,
       and_10_out, and_11_out, and_12_out, and_13_out, and_14_out, and_15_out, and_16_out, and_17_out,
       and_18_out, and_19_out, and_20_out, and_21_out, and_22_out, and_23_out, and_24_out, and_25_out,
       and_26_out, and_27_out, and_28_out, and_29_out, and_30_out, and_31_out, and_32_out, and_33_out,
       and_34_out, and_35_out, and_36_out, and_37_out, and_38_out, and_39_out, and_40_out, and_41_out,
       and_42_out, and_43_out, and_44_out, and_45_out, and_46_out, and_47_out, and_48_out, and_49_out,
       and_50_out, and_51_out, and_52_out, and_53_out, and_54_out, and_55_out, and_56_out, and_57_out,
       and_58_out, and_59_out, and_60_out, and_61_out, and_62_out, and_63_out, and_64_out, and_65_out,
       and_66_out, and_67_out, and_68_out, and_69_out, and_70_out, and_71_out, and_72_out, not_1_out,
       not_2_out, not_3_out, not_4_out, not_5_out, not_6_out, not_7_out, not_8_out, not_9_out, not_10_out,
       not_11_out, not_12_out, not_13_out, not_14_out, not_15_out, not_16_out, not_17_out, not_18_out,
       not_19_out, not_20_out, not_21_out, not_22_out, not_23_out, not_24_out, not_25_out, not_26_out,
       not_27_out, not_28_out, not_29_out, not_30_out, not_31_out, not_32_out, not_33_out, not_34_out,
       not_35_out, not_36_out, not_37_out, not_38_out, not_39_out, not_40_out, not_41_out, not_42_out,
       not_43_out, not_44_out, not_45_out, not_46_out, not_47_out, not_48_out, not_49_out, not_50_out,
       not_51_out, not_52_out, not_53_out, not_54_out, not_55_out, not_56_out, not_57_out, not_58_out,
       not_59_out, not_60_out, not_61_out, not_62_out, not_63_out, not_64_out, not_65_out, not_66_out,
       not_67_out, not_68_out, not_69_out, not_70_out, not_71_out, not_72_out, not_73_out, not_74_out,
       not_75_out, not_76_out, not_77_out, not_78_out, not_79_out, not_80_out, not_81_out, not_82_out,
       not_83_out, not_84_out, not_85_out, not_86_out, not_87_out, not_88_out, not_89_out, not_90_out,
       not_91_out, not_92_out, not_93_out, not_94_out, not_95_out, not_96_out, not_97_out, not_98_out,
       not_99_out, not_100_out, not_101_out, not_102_out, not_103_out, not_104_out, not_105_out, not_106_out,
       not_107_out, not_108_out, not_109_out, not_110_out, not_111_out, not_112_out, not_113_out,
       not_114_out, not_115_out, not_116_out, not_117_out, not_118_out, not_119_out, not_120_out,
       not_121_out, not_122_out, not_123_out, not_124_out, not_125_out, not_126_out, not_127_out,
       not_128_out, not_129_out, not_130_out, not_131_out, not_132_out, not_133_out, not_134_out,
       not_135_out, not_136_out, not_137_out, not_138_out, not_139_out, not_140_out, not_141_out,
       not_142_out, not_143_out, not_144_out, not_145_out, not_146_out, not_147_out, not_148_out,
       not_149_out, not_150_out, not_151_out, not_152_out, not_153_out, not_154_out, not_155_out,
       not_156_out, not_157_out, not_158_out, not_159_out, not_160_out, not_161_out, not_162_out,
       not_163_out, not_164_out, not_165_out, not_166_out, not_167_out, not_168_out, not_169_out,
       not_170_out, not_171_out, not_172_out, not_173_out, not_174_out;

  not not_1 (not_1_out, y1);
  not not_2 (not_2_out, y3);
  not not_3 (not_3_out, y4);
  not not_4 (not_4_out, y4);
  not not_5 (not_5_out, y2);
  not not_6 (not_6_out, y3);
  not not_7 (not_7_out, y4);
  not not_8 (not_8_out, x2);
  not not_9 (not_9_out, x3);
  not not_10 (not_10_out, x2);
  not not_11 (not_11_out, x2);
  not not_12 (not_12_out, y1);
  not not_13 (not_13_out, y2);
  not not_14 (not_14_out, x2);
  not not_15 (not_15_out, x3);
  not not_16 (not_16_out, x4);
  not not_17 (not_17_out, x1);
  not not_18 (not_18_out, x2);
  not not_19 (not_19_out, x4);
  not not_20 (not_20_out, x1);
  not not_21 (not_21_out, y1);
  not not_22 (not_22_out, x2);
  not not_23 (not_23_out, x1);
  not not_24 (not_24_out, y1);
  not not_25 (not_25_out, y2);
  not not_26 (not_26_out, y1);
  not not_27 (not_27_out, y4);
  not not_28 (not_28_out, x1);
  not not_29 (not_29_out, x3);
  not not_30 (not_30_out, y3);
  not not_31 (not_31_out, x2);
  not not_32 (not_32_out, y1);
  not not_33 (not_33_out, y4);
  not not_34 (not_34_out, y2);
  not not_35 (not_35_out, x1);
  not not_36 (not_36_out, x2);
  not not_37 (not_37_out, y3);
  not not_38 (not_38_out, x2);
  not not_39 (not_39_out, y2);
  not not_40 (not_40_out, y3);
  not not_41 (not_41_out, x1);
  not not_42 (not_42_out, y2);
  not not_43 (not_43_out, x3);
  not not_44 (not_44_out, y3);
  not not_45 (not_45_out, y4);
  not not_46 (not_46_out, y1);
  not not_47 (not_47_out, y2);
  not not_48 (not_48_out, y3);
  not not_49 (not_49_out, x2);
  not not_50 (not_50_out, x4);
  not not_51 (not_51_out, y1);
  not not_52 (not_52_out, x1);
  not not_53 (not_53_out, x2);
  not not_54 (not_54_out, x3);
  not not_55 (not_55_out, x4);
  not not_56 (not_56_out, y2);
  not not_57 (not_57_out, y3);
  not not_58 (not_58_out, y4);
  not not_59 (not_59_out, x1);
  not not_60 (not_60_out, x2);
  not not_61 (not_61_out, x3);
  not not_62 (not_62_out, y3);
  not not_63 (not_63_out, y4);
  not not_64 (not_64_out, x1);
  not not_65 (not_65_out, x2);
  not not_66 (not_66_out, x4);
  not not_67 (not_67_out, y1);
  not not_68 (not_68_out, y2);
  not not_69 (not_69_out, x2);
  not not_70 (not_70_out, x3);
  not not_71 (not_71_out, y1);
  not not_72 (not_72_out, y2);
  not not_73 (not_73_out, x2);
  not not_74 (not_74_out, x3);
  not not_75 (not_75_out, x4);
  not not_76 (not_76_out, x4);
  not not_77 (not_77_out, x4);
  not not_78 (not_78_out, y3);
  not not_79 (not_79_out, y4);
  not not_80 (not_80_out, x1);
  not not_81 (not_81_out, x3);
  not not_82 (not_82_out, x4);
  not not_83 (not_83_out, x4);
  not not_84 (not_84_out, y1);
  not not_85 (not_85_out, y2);
  not not_86 (not_86_out, y3);
  not not_87 (not_87_out, y4);
  not not_88 (not_88_out, x1);
  not not_89 (not_89_out, x2);
  not not_90 (not_90_out, y1);
  not not_91 (not_91_out, y2);
  not not_92 (not_92_out, y3);
  not not_93 (not_93_out, x1);
  not not_94 (not_94_out, x2);
  not not_95 (not_95_out, x3);
  not not_96 (not_96_out, y3);
  not not_97 (not_97_out, x1);
  not not_98 (not_98_out, x2);
  not not_99 (not_99_out, x3);
  not not_100 (not_100_out, x4);
  not not_101 (not_101_out, y1);
  not not_102 (not_102_out, y3);
  not not_103 (not_103_out, y4);
  not not_104 (not_104_out, x1);
  not not_105 (not_105_out, x2);
  not not_106 (not_106_out, x2);
  not not_107 (not_107_out, x4);
  not not_108 (not_108_out, y2);
  not not_109 (not_109_out, y4);
  not not_110 (not_110_out, x2);
  not not_111 (not_111_out, x3);
  not not_112 (not_112_out, y1);
  not not_113 (not_113_out, y3);
  not not_114 (not_114_out, x2);
  not not_115 (not_115_out, x3);
  not not_116 (not_116_out, x4);
  not not_117 (not_117_out, y3);
  not not_118 (not_118_out, y4);
  not not_119 (not_119_out, x1);
  not not_120 (not_120_out, x3);
  not not_121 (not_121_out, x4);
  not not_122 (not_122_out, x1);
  not not_123 (not_123_out, x1);
  not not_124 (not_124_out, x1);
  not not_125 (not_125_out, x1);
  not not_126 (not_126_out, x1);
  not not_127 (not_127_out, y1);
  not not_128 (not_128_out, y2);
  not not_129 (not_129_out, y3);
  not not_130 (not_130_out, y4);
  not not_131 (not_131_out, x2);
  not not_132 (not_132_out, x3);
  not not_133 (not_133_out, y1);
  not not_134 (not_134_out, y2);
  not not_135 (not_135_out, y4);
  not not_136 (not_136_out, x2);
  not not_137 (not_137_out, y1);
  not not_138 (not_138_out, y3);
  not not_139 (not_139_out, x2);
  not not_140 (not_140_out, y1);
  not not_141 (not_141_out, y3);
  not not_142 (not_142_out, x3);
  not not_143 (not_143_out, y2);
  not not_144 (not_144_out, y3);
  not not_145 (not_145_out, y4);
  not not_146 (not_146_out, x1);
  not not_147 (not_147_out, x2);
  not not_148 (not_148_out, x1);
  not not_149 (not_149_out, x4);
  not not_150 (not_150_out, y1);
  not not_151 (not_151_out, y2);
  not not_152 (not_152_out, y3);
  not not_153 (not_153_out, x2);
  not not_154 (not_154_out, y1);
  not not_155 (not_155_out, y2);
  not not_156 (not_156_out, x2);
  not not_157 (not_157_out, y2);
  not not_158 (not_158_out, y1);
  not not_159 (not_159_out, y4);
  not not_160 (not_160_out, y2);
  not not_161 (not_161_out, y2);
  not not_162 (not_162_out, y1);
  not not_163 (not_163_out, y4);
  not not_164 (not_164_out, x1);
  not not_165 (not_165_out, x4);
  not not_166 (not_166_out, y1);
  not not_167 (not_167_out, x4);
  not not_168 (not_168_out, x1);
  not not_169 (not_169_out, x3);
  not not_170 (not_170_out, x1);
  not not_171 (not_171_out, y2);
  not not_172 (not_172_out, y4);
  not not_173 (not_173_out, x2);
  not not_174 (not_174_out, x4);
  and and_1 (and_1_out, not_1_out, not_2_out, not_3_out, x4);
  and and_2 (and_2_out, x3, x4);
  and and_3 (and_3_out, not_4_out, x2, x4);
  and and_4 (and_4_out, not_5_out, not_6_out, not_7_out, x1, not_8_out, not_9_out);
  and and_5 (and_5_out, x1, x4);
  and and_6 (and_6_out, y4, not_10_out, x4);
  and and_7 (and_7_out, y4, not_11_out, x3);
  and and_8 (and_8_out, not_12_out, not_13_out, y3, not_14_out, not_15_out, not_16_out);
  and and_9 (and_9_out, y3, not_17_out, not_18_out, not_19_out);
  and and_10 (and_10_out, y3, not_20_out, x3);
  and and_11 (and_11_out, not_21_out, y3, y4, not_22_out);
  and and_12 (and_12_out, y3, y4, not_23_out);
  and and_13 (and_13_out, not_24_out, not_25_out, y3, y4, x3);
  and and_14 (and_14_out, y2, x4);
  and and_15 (and_15_out, not_26_out, y2, not_27_out, not_28_out, x2, not_29_out);
  and and_16 (and_16_out, y2, not_30_out, y4, not_31_out);
  and and_17 (and_17_out, not_32_out, y2, y3, not_33_out, x2, x3);
  and and_18 (and_18_out, y1, not_34_out, not_35_out, not_36_out, x3);
  and and_19 (and_19_out, y1, not_37_out, y4, not_38_out);
  and and_20 (and_20_out, y1, y4, x4);
  and and_21 (and_21_out, y1, not_39_out, not_40_out, y4, x1, x3);
  and and_22 (and_22_out, y1, y3, not_41_out);
  and and_23 (and_23_out, y1, not_42_out, y3, y4, not_43_out);
  and and_24 (and_24_out, y1, y2, not_44_out, not_45_out, x1, x2, x3);
  and and_25 (and_25_out, not_46_out, not_47_out, not_48_out, not_49_out, not_50_out);
  and and_26 (and_26_out, not_51_out, not_52_out, not_53_out, not_54_out, not_55_out);
  and and_27 (and_27_out, not_56_out, not_57_out, not_58_out, not_59_out, not_60_out, not_61_out, x4);
  and and_28 (and_28_out, not_62_out, not_63_out, not_64_out, not_65_out, x3, not_66_out);
  and and_29 (and_29_out, not_67_out, not_68_out, x1, not_69_out, not_70_out);
  and and_30 (and_30_out, not_71_out, not_72_out, y3, y4, not_73_out, not_74_out);
  and and_31 (and_31_out, y2, x3, not_75_out);
  and and_32 (and_32_out, y2, y4, not_76_out);
  and and_33 (and_33_out, y2, y3, not_77_out);
  and and_34 (and_34_out, y1, not_78_out, not_79_out, not_80_out, x2, not_81_out, not_82_out);
  and and_35 (and_35_out, y1, y2, not_83_out);
  and and_36 (and_36_out, not_84_out, not_85_out, not_86_out, not_87_out, not_88_out, not_89_out);
  and and_37 (and_37_out, not_90_out, not_91_out, not_92_out, not_93_out, not_94_out, not_95_out);
  and and_38 (and_38_out, not_96_out, not_97_out, not_98_out, not_99_out, not_100_out);
  and and_39 (and_39_out, not_101_out, not_102_out, not_103_out, not_104_out, not_105_out, x3);
  and and_40 (and_40_out, y4, not_106_out, not_107_out);
  and and_41 (and_41_out, not_108_out, y3, not_109_out, not_110_out, not_111_out, x4);
  and and_42 (and_42_out, y3, x1);
  and and_43 (and_43_out, not_112_out, y2, not_113_out, not_114_out, not_115_out, not_116_out);
  and and_44 (and_44_out, y2, not_117_out, not_118_out, not_119_out, not_120_out, not_121_out);
  and and_45 (and_45_out, y1, not_122_out, x3, x4);
  and and_46 (and_46_out, y1, not_123_out, x2, x4);
  and and_47 (and_47_out, y1, not_124_out, x2, x3);
  and and_48 (and_48_out, y1, y4, not_125_out);
  and and_49 (and_49_out, y1, y3);
  and and_50 (and_50_out, y1, y2, not_126_out);
  and and_51 (and_51_out, not_127_out, not_128_out, not_129_out, not_130_out, not_131_out, not_132_out);
  and and_52 (and_52_out, not_133_out, not_134_out, not_135_out, not_136_out, x4);
  and and_53 (and_53_out, not_137_out, not_138_out, not_139_out, x4);
  and and_54 (and_54_out, not_140_out, not_141_out, not_142_out, x4);
  and and_55 (and_55_out, not_143_out, not_144_out, not_145_out, not_146_out, not_147_out, x4);
  and and_56 (and_56_out, not_148_out, x2, x3);
  and and_57 (and_57_out, x2, x3, not_149_out);
  and and_58 (and_58_out, not_150_out, not_151_out, not_152_out, x1, not_153_out);
  and and_59 (and_59_out, not_154_out, not_155_out, x1, not_156_out, x4);
  and and_60 (and_60_out, not_157_out, x1, x3);
  and and_61 (and_61_out, not_158_out, not_159_out, x1, x3, x4);
  and and_62 (and_62_out, not_160_out, y4, x3);
  and and_63 (and_63_out, not_161_out, y3, x3);
  and and_64 (and_64_out, not_162_out, y3, not_163_out, not_164_out, x2, not_165_out);
  and and_65 (and_65_out, not_166_out, y3, y4, x1, x3, not_167_out);
  and and_66 (and_66_out, y2, not_168_out, x2, x4);
  and and_67 (and_67_out, y2, x1, x2, not_169_out);
  and and_68 (and_68_out, y2, y4, not_170_out, x2);
  and and_69 (and_69_out, y2, y3, x2);
  and and_70 (and_70_out, y1, x2, x3);
  and and_71 (and_71_out, y1, not_171_out, y3, not_172_out, not_173_out, not_174_out);
  and and_72 (and_72_out, y1, y2, x2);
  or or_1 (B0, and_1_out, and_2_out, and_3_out, and_4_out, and_5_out, and_6_out, and_7_out, and_8_out, and_9_out, and_10_out, and_11_out, and_12_out, and_13_out, and_14_out, and_15_out, and_16_out, and_17_out, and_18_out, and_19_out, and_20_out, and_21_out, and_22_out, and_23_out, and_24_out);
  or or_2 (B1, and_25_out, and_26_out, and_27_out, and_28_out, and_29_out, and_30_out, and_31_out, and_32_out, and_33_out, and_34_out, and_35_out);
  or or_3 (B2, and_36_out, and_37_out, and_38_out, and_39_out, and_40_out, and_41_out, and_42_out, and_43_out, and_44_out, and_45_out, and_46_out, and_47_out, and_48_out, and_49_out, and_50_out);
  or or_4 (B3, and_51_out, and_52_out, and_53_out, and_54_out, and_55_out, and_56_out, and_57_out, and_58_out, and_59_out, and_60_out, and_61_out, and_62_out, and_63_out, and_64_out, and_65_out, and_66_out, and_67_out, and_68_out, and_69_out, and_70_out, and_71_out, and_72_out);
endmodule

module state_messages (
  input  POR,
  input  [4:0] Input_bus_1,
  input  [4:0] Input_bus_2,
  input  [4:0] Input_bus_3,
  input  [4:0] Input_bus_4,
  input  [4:0] Input_bus_5,
  input  [4:0] Input_bus_6,
  input  [4:0] Input_bus_7,
  input  [4:0] Input_bus_8,
  input  [4:0] Input_bus_9,
  input  [4:0] Input_bus_10,
  input  EN,
  output [29:0] Output_bus_1
);

  wire MSG_CLOCK_out, shift_register_1_p4;

  Clock #(.highDuration(56000), .lowDuration(56000)) MSG_CLOCK (.out(MSG_CLOCK_out));
  // Shift_Register #(.width(5), .length(10)) shift_register_1: pin names not known; wires that end beside it: POR, EN, MSG_CLOCK_out, shift_register_1_p4, Input_bus_1, Input_bus_2, Input_bus_3
  // Shift_Register #(.width(5), .length(6)) shift_register_2: pin names not known; wires that end beside it: Input_bus_4, Input_bus_5, Input_bus_6, Input_bus_7, Input_bus_8, Input_bus_9, Input_bus_10, POR, EN, MSG_CLOCK_out, shift_register_1_p4, {5{1'b1}}, shift_register_1_p4, Output_bus_1[4:0], Output_bus_1[9:5], Output_bus_1[14:10], Output_bus_1[19:15], Output_bus_1[24:20], Output_bus_1[29:25]
endmodule

module converter_4to5bits (
  input  [3:0] from_4bits,
  output [4:0] to_5bits
);


  assign to_5bits = {1'b0, from_4bits};
endmodule

module music_recorder (
  input  start_recorder,
  input  reset,
  input  data_ready,
  input  [4:0] data,
  input  play,
  input  CLOCK_TEMPO,
  input  CLOCK_CLK,
  output [4:0] Output_bus_1
);

  wire and_1_out, and_2_out, and_3_out, and_4_out, clock_1_out, or_1_out, or_2_out, shift_register_2_p1,
       shift_register_3_p1, t_ff_1_q;
  wire [4:0] multiplexer_1_out, undriven;

  Clock clock_1 (.out(clock_1_out));
  T_Flip_Flop t_ff_1 (.T(CLOCK_TEMPO), .clk(CLOCK_TEMPO), .Q(t_ff_1_q));  // open: Qn, reset, preset
  and and_1 (and_1_out, start_recorder, reset);
  and and_2 (and_2_out, data_ready, ~play);  // AND_Gate
  or or_1 (or_1_out, start_recorder, play);
  and and_3 (and_3_out, play, t_ff_1_q);
  and and_4 (and_4_out, play, CLOCK_TEMPO);
  or or_2 (or_2_out, reset, and_2_out, and_3_out);
  Multiplexer #(.width(5), .enable("false")) multiplexer_1 (
    .in0(data), .in1(undriven), .out(multiplexer_1_out), .sel(play));
  // Shift_Register #(.width(5), .length(32)) shift_register_1: pin names not known; wires that end beside it: multiplexer_1_out, {5{1'b1}}, {5{1'b1}}, {5{1'b1}}, {5{1'b1}}, {5{1'b1}}, {5{1'b1}}, 5'b00010, 5'b00010, 5'b00010, 5'b00010, 5'b00010, 5'b00010
  // Probe on multiplexer_1_out
  // Shift_Register #(.width(5), .length(32)) shift_register_2: pin names not known; wires that end beside it: shift_register_2_p1, {5{1'b1}}, {5{1'b1}}, {5{1'b1}}, {5{1'b1}}, {5{1'b1}}, {5{1'b1}}, {5{1'b1}}, {5{1'b1}}, {5{1'b1}}, {5{1'b1}}, {5{1'b1}}, {5{1'b1}}
  // Shift_Register #(.width(5), .length(32)) shift_register_3: pin names not known; wires that end beside it: shift_register_3_p1, 1'b0, and_1_out, or_1_out, or_2_out, shift_register_3_p1, {5{1'b1}}, {5{1'b1}}, {5{1'b1}}, {5{1'b1}}, {5{1'b1}}, {5{1'b1}}, {5{1'b1}}, {5{1'b1}}, {5{1'b1}}, {5{1'b1}}, {5{1'b1}}, {5{1'b1}}
  Multiplexer #(.width(5), .enable("false")) multiplexer_2 (
    .in0(undriven), .in1({5{1'b1}}), .out(Output_bus_1), .sel(and_4_out));
endmodule

module buzzer_sound (
  input  EN,
  input  signal_freq,
  output buzzer_signal
);

  and and_1 (buzzer_signal, EN, signal_freq);

  // Notes on the sheet:
  //   Buzzer sound (out)
endmodule

module let_it_be_song (
  input  play_load,
  input  CLOCK_TEMPO,
  output [4:0] OUT_MUSIC
);

  wire shift_register_2_p1, shift_register_3_p1, shift_register_4_p1, shift_register_5_p1,
       shift_register_6_p1, shift_register_7_p1, shift_register_8_p1, shift_register_9_p1,
       shift_register_10_p2, shift_register_11_p2;

  // Shift_Register #(.width(5), .length(32)) shift_register_1: pin names not known; wires that end beside it: {5{1'b1}}, {5{1'b1}}, {5{1'b1}}, {5{1'b1}}, {5{1'b1}}, {5{1'b1}}, {5{1'b1}}, {5{1'b1}}, {5{1'b1}}, {5{1'b1}}, {5{1'b1}}, {5{1'b1}}, {5{1'b1}}
  // Shift_Register #(.width(5), .length(32)) shift_register_2: pin names not known; wires that end beside it: shift_register_2_p1, 5'b00111, 5'b00111, 5'b00111, {5{1'b1}}, {5{1'b1}}, 5'b01000, 5'b01000, 5'b01000, {5{1'b1}}, {5{1'b1}}, 5'b01000, {5{1'b1}}
  // Shift_Register #(.width(5), .length(32)) shift_register_3: pin names not known; wires that end beside it: shift_register_3_p1, 5'b01010, 5'b01001, 5'b01001, {5{1'b1}}, {5{1'b1}}, 5'b01001, {5{1'b1}}, {5{1'b1}}, {5{1'b1}}, 5'b01001, 5'b01001, 5'b01001
  // Shift_Register #(.width(5), .length(32)) shift_register_4: pin names not known; wires that end beside it: shift_register_4_p1, 5'b01001, 5'b01001, 5'b01001, {5{1'b1}}, {5{1'b1}}, {5{1'b1}}, 5'b01011, 5'b01011, 5'b01011, {5{1'b1}}, {5{1'b1}}, {5{1'b1}}
  // Shift_Register #(.width(5), .length(32)) shift_register_5: pin names not known; wires that end beside it: shift_register_5_p1, 5'b00111, 5'b00111, 5'b00111, {5{1'b1}}, {5{1'b1}}, 5'b01000, 5'b01000, {5{1'b1}}, {5{1'b1}}, 5'b01001, {5{1'b1}}, {5{1'b1}}
  // Shift_Register #(.width(5), .length(32)) shift_register_6: pin names not known; wires that end beside it: shift_register_6_p1, {5{1'b1}}, 5'b01001, {5{1'b1}}, {5{1'b1}}, 5'b01010, 5'b01010, {5{1'b1}}, {5{1'b1}}, 5'b01001, 5'b01001, 5'b01001, {5{1'b1}}
  // Shift_Register #(.width(5), .length(32)) shift_register_7: pin names not known; wires that end beside it: shift_register_7_p1, {5{1'b1}}, {5{1'b1}}, 5'b01001, 5'b01001, {5{1'b1}}, {5{1'b1}}, 5'b01001, 5'b01001, {5{1'b1}}, {5{1'b1}}, 5'b01000, 5'b01000
  // Shift_Register #(.width(5), .length(32)) shift_register_8: pin names not known; wires that end beside it: shift_register_8_p1, {5{1'b1}}, {5{1'b1}}, 5'b00101, 5'b00101, {5{1'b1}}, {5{1'b1}}, 5'b00100, 5'b00100, {5{1'b1}}, {5{1'b1}}, 5'b00100, 5'b00100
  // Shift_Register #(.width(5), .length(32)) shift_register_9: pin names not known; wires that end beside it: shift_register_9_p1, 5'b01000, {5{1'b1}}, 5'b01001, {5{1'b1}}, {5{1'b1}}, 5'b01000, 5'b01000, 5'b01000, 5'b01000, {5{1'b1}}, {5{1'b1}}, 5'b01001
  // Shift_Register #(.width(5), .length(32)) shift_register_10: pin names not known; wires that end beside it: play_load, shift_register_10_p2, 5'b00111, 5'b00111, 5'b00111, {5{1'b1}}, {5{1'b1}}, 5'b00111, 5'b00111, {5{1'b1}}, {5{1'b1}}, 5'b01000, 5'b01000, {5{1'b1}}
  // Shift_Register #(.width(5), .length(32)) shift_register_11: pin names not known; wires that end beside it: CLOCK_TEMPO, shift_register_11_p2, {5{1'b1}}, 5'b00111, 5'b00111, {5{1'b1}}, {5{1'b1}}, 5'b00100, 5'b00100, {5{1'b1}}, {5{1'b1}}, 5'b00100, 5'b00100, {5{1'b1}}, play_load

  // Notes on the sheet:
  //   4ème
  //   3ème ligne
  //   do 2
  //   do 3
  //   2ème ligne
endmodule

module alarm_sound (
  input  EN_ALARM,
  input  CLOCK_TEMPO,
  output [4:0] frequency
);

  wire and_1_out;

  and and_1 (and_1_out, EN_ALARM, CLOCK_TEMPO);
  Multiplexer #(.width(5), .enable("false")) multiplexer_1 (
    .in0(5'b00101), .in1({5{1'b1}}), .out(frequency), .sel(and_1_out));

  // Notes on the sheet:
  //   Standard Alarm Sound
endmodule

module music_box (
  input  key_button_pressed,
  input  [3:0] key_button,
  input  rec,
  input  play_recorder,
  input  EN_alarm,
  input  play_song,
  output EN,
  output freq
);

  wire and_1_out, and_2_out, and_3_out, and_4_out, and_5_out, clock_1_out, clock_2_out, clock_3_out,
       clock_4_out, clock_5_out, clock_6_out, clock_7_out, clock_8_out, clock_9_out, clock_10_out,
       clock_11_out, clock_12_out, clock_13_out, clock_14_out, clock_15_out, clock_16_out, CLOCK_CLK_out,
       CLOCK_TEMPO_out, d_ff_1_q, d_ff_2_q, d_ff_3_q, not_1_out, not_2_out, not_3_out, not_4_out, not_5_out,
       not_6_out, not_7_out, not_8_out, not_9_out, not_10_out, not_11_out, not_12_out, s_r_ff_1_q;
  wire [1:0] or_1_out;
  wire [4:0] alarm_sound_1_frequency, converter_4to5bits_1_to_5bits, let_it_be_song_1_out_music,
       multiplexer_1_out, music_recorder_1_output_bus_1;

  Clock #(.highDuration(489), .lowDuration(489)) clock_1 (.out(clock_1_out));
  Clock #(.highDuration(436), .lowDuration(436)) clock_2 (.out(clock_2_out));
  Clock #(.highDuration(388), .lowDuration(388)) clock_3 (.out(clock_3_out));
  Clock #(.highDuration(365), .lowDuration(365)) clock_4 (.out(clock_4_out));
  Clock #(.highDuration(326), .lowDuration(326)) clock_5 (.out(clock_5_out));
  Clock #(.highDuration(291), .lowDuration(291)) clock_6 (.out(clock_6_out));
  Clock #(.highDuration(259), .lowDuration(259)) clock_7 (.out(clock_7_out));
  Clock #(.highDuration(245), .lowDuration(245)) clock_8 (.out(clock_8_out));
  Clock #(.highDuration(218), .lowDuration(218)) clock_9 (.out(clock_9_out));
  Clock #(.highDuration(194), .lowDuration(194)) clock_10 (.out(clock_10_out));
  Clock #(.highDuration(183), .lowDuration(183)) clock_11 (.out(clock_11_out));
  Clock #(.highDuration(163), .lowDuration(163)) clock_12 (.out(clock_12_out));
  Clock #(.highDuration(145), .lowDuration(145)) clock_13 (.out(clock_13_out));
  Clock #(.highDuration(130), .lowDuration(130)) clock_14 (.out(clock_14_out));
  Clock #(.highDuration(122), .lowDuration(122)) clock_15 (.out(clock_15_out));
  Clock #(.highDuration(109), .lowDuration(109)) clock_16 (.out(clock_16_out));
  // Probe on multiplexer_1_out
  Multiplexer #(.select(2), .width(5), .enable("false")) multiplexer_1 (
    .in0(converter_4to5bits_1_to_5bits), .in1(alarm_sound_1_frequency), .in2(music_recorder_1_output_bus_1),
    .in3(let_it_be_song_1_out_music), .out(multiplexer_1_out), .sel(or_1_out));
  // Probe on or_1_out
  not not_1 (not_1_out, play_recorder);
  not not_2 (not_2_out, EN_alarm);
  not not_3 (not_3_out, play_recorder);
  not not_4 (not_4_out, play_song);
  not not_5 (not_5_out, play_recorder);
  not not_6 (not_6_out, EN_alarm);
  not not_7 (not_7_out, EN_alarm);
  not not_8 (not_8_out, play_song);
  S_R_Flip_Flop #(.trigger("high")) s_r_ff_1 (
    .S(key_button_pressed), .R(CLOCK_TEMPO_out), .clk(1'b1), .Q(s_r_ff_1_q), .preset(key_button_pressed));  // open: reset, Qn
  Multiplexer #(.select(5), .enable("false")) multiplexer_2 (
    .in0(clock_1_out), .in1(clock_2_out), .in2(clock_3_out), .in3(clock_4_out), .in4(clock_5_out),
    .in5(clock_6_out), .in6(clock_7_out), .in7(clock_8_out), .in8(clock_9_out), .in9(clock_10_out),
    .in10(clock_11_out), .in11(clock_12_out), .in12(clock_13_out), .in13(clock_14_out), .in14(clock_15_out),
    .in15(clock_16_out), .in31(1'b0), .out(freq), .sel(multiplexer_1_out));  // open: in16, in17, in18, in19, in20, in21, in22, in23, in24, in25, in26, in27, in28, in29, in30
  converter_4to5bits converter_4to5bits_1 (.from_4bits(key_button), .to_5bits(converter_4to5bits_1_to_5bits));
  and and_1 (and_1_out, not_1_out, not_2_out, play_song);
  and and_2 (and_2_out, not_3_out, EN_alarm, not_4_out);
  and and_3 (and_3_out, not_5_out, not_6_out, play_song);
  and and_4 (and_4_out, play_recorder, not_7_out, not_8_out);
  or or_1 (or_1_out[0], and_1_out, and_2_out);
  or or_2 (or_1_out[1], and_3_out, and_4_out);
  or or_3 (EN, s_r_ff_1_q, EN_alarm, play_song, not_9_out);
  Clock #(.highDuration(10), .lowDuration(10)) CLOCK_CLK (.out(CLOCK_CLK_out));
  not not_9 (not_9_out, not_10_out);
  D_Flip_Flop d_ff_1 (.D(play_song), .clk(CLOCK_CLK_out), .Q(d_ff_1_q));  // open: Qn, preset, reset
  D_Flip_Flop d_ff_2 (.D(rec), .clk(CLOCK_CLK_out), .Q(d_ff_2_q));  // open: Qn, preset, reset
  not not_10 (not_10_out, d_ff_1_q);
  not not_11 (not_11_out, d_ff_2_q);
  and and_5 (and_5_out, not_11_out, rec);
  D_Flip_Flop d_ff_3 (.D(d_ff_1_q), .clk(CLOCK_CLK_out), .Q(d_ff_3_q));  // open: Qn, preset, reset
  not not_12 (not_12_out, d_ff_3_q);
  Clock #(.highDuration(12800), .lowDuration(12800)) CLOCK_TEMPO (.out(CLOCK_TEMPO_out));
  music_recorder music_recorder_1 (
    .start_recorder(rec), .reset(and_5_out), .data_ready(key_button_pressed),
    .data(converter_4to5bits_1_to_5bits), .play(play_recorder), .CLOCK_TEMPO(CLOCK_TEMPO_out),
    .CLOCK_CLK(CLOCK_CLK_out), .Output_bus_1(music_recorder_1_output_bus_1));
  alarm_sound alarm_sound_1 (.EN_ALARM(EN_alarm), .CLOCK_TEMPO(CLOCK_TEMPO_out), .frequency(alarm_sound_1_frequency));
  let_it_be_song let_it_be_song_1 (
    .play_load(not_12_out), .CLOCK_TEMPO(CLOCK_TEMPO_out), .OUT_MUSIC(let_it_be_song_1_out_music));

  // Notes on the sheet:
  //   0-Do
  //   1-Ré
  //   2-mi
  //   3-fa
  //   4-sol
  //   5-la
  //   6-si
  //   7-do
  //   8-re
  //   9-mi
  //   10-fa
  //   11-sol
  //   12-la
  //   13-si
  //   14-do
  //   15-re
  //   chaque touche à son propre son
  //   let it be
  //   song composed
endmodule

module converter_24to30 (
  input  [23:0] from_bits24,
  output [29:0] to_30bits
);


  assign to_30bits = {1'b0, from_bits24[23:20], 1'b0, from_bits24[19:16], 1'b0, from_bits24[15:12], 1'b0, from_bits24[11:8], 1'b0, from_bits24[7:4], 1'b0, from_bits24[3:0]};
endmodule

module time_setter (
  input  BTN,
  input  POR,
  input  TIME_CLOCK,
  input  SET_EN,
  input  [23:0] VALUE,
  input  [23:0] SET_VALUE,
  input  [29:0] SET_MSG,
  input  MSG_CLOCK,
  output SET_M_ENT_IMPULS,
  output SET_M_EN,
  output SET_TIME_IMPULS,
  output [29:0] SCR_OUT
);

  wire and_1_out, and_2_out, ImpulsOnRisingEdges_1_o, ImpulsOnRisingEdges_2_o;
  wire [23:0] multiplexer_1_out;
  wire [29:0] converter_24to30_1_to_30bits;

  Multiplexer #(.width(24), .enable("false")) multiplexer_1 (
    .in0(VALUE), .in1(SET_VALUE), .out(multiplexer_1_out), .sel(SET_M_EN));
  LongPush LongPush_1 (.I(BTN), .TICK_NUMBER(4'b0100), .TIME_CLOCK(TIME_CLOCK), .POR(POR), .O(SET_M_ENT_IMPULS));
  ImpulsOnRisingEdges ImpulsOnRisingEdges_1 (.I(BTN), .POR(POR), .CLOCK(TIME_CLOCK), .O(ImpulsOnRisingEdges_1_o));
  ImpulsOnRisingEdges ImpulsOnRisingEdges_2 (.I(and_1_out), .POR(POR), .CLOCK(TIME_CLOCK), .O(ImpulsOnRisingEdges_2_o));
  and and_1 (and_1_out, ImpulsOnRisingEdges_1_o, SET_M_EN);
  converter_24to30 converter_24to30_1 (.from_bits24(multiplexer_1_out), .to_30bits(converter_24to30_1_to_30bits));
  S_R_Flip_Flop #(.trigger("low")) s_r_ff_1 (
    .S(SET_M_ENT_IMPULS), .R(and_1_out), .clk(1'b0), .Q(SET_M_EN), .reset(POR));  // open: Qn, preset
  Multiplexer #(.width(30), .enable("false")) multiplexer_2 (
    .in0(converter_24to30_1_to_30bits), .in1(SET_MSG), .out(SCR_OUT), .sel(and_2_out));
  and and_2 (and_2_out, SET_M_EN, MSG_CLOCK);
  and and_3 (SET_TIME_IMPULS, SET_EN, ImpulsOnRisingEdges_2_o);
endmodule
