// Logisim project Pave_numerique_virtuel.circ as structural Verilog: 1 circuit, main circuit main
module main (
  input  in_1,
  input  in_2,
  input  in_3,
  input  in_4,
  output out_5,
  output out_6,
  output out_7,
  output out_8
);

  wire button_1_out, button_2_out, button_3_out, button_4_out, button_5_out, button_6_out, button_7_out,
       button_8_out, button_9_out, button_10_out, button_11_out, button_12_out, button_13_out, button_14_out,
       button_15_out, button_16_out, or_1_out, or_2_out, or_3_out, or_4_out, or_5_out, or_6_out, or_7_out,
       or_8_out, or_9_out, or_10_out, or_11_out, or_12_out, or_13_out, or_14_out, or_15_out, or_16_out,
       or_17_out, or_18_out, or_19_out, or_20_out, Y1, Y2, Y3, Y4;

  Button button_1 (.out(button_1_out));
  or or_1 (or_1_out, ~button_1_out, out_8);  // OR_Gate
  Button button_2 (.out(button_2_out));
  or or_2 (or_2_out, ~button_2_out, out_8);  // OR_Gate
  Button button_3 (.out(button_3_out));
  or or_3 (or_3_out, ~button_3_out, out_8);  // OR_Gate
  Button button_4 (.out(button_4_out));
  or or_4 (or_4_out, ~button_4_out, out_8);  // OR_Gate
  Button button_5 (.out(button_5_out));
  or or_5 (or_5_out, ~button_5_out, out_7);  // OR_Gate
  Button button_6 (.out(button_6_out));
  or or_6 (or_6_out, ~button_6_out, out_7);  // OR_Gate
  Button button_7 (.out(button_7_out));
  or or_7 (or_7_out, ~button_7_out, out_7);  // OR_Gate
  Button button_8 (.out(button_8_out));
  or or_8 (or_8_out, ~button_8_out, out_7);  // OR_Gate
  Button button_9 (.out(button_9_out));
  or or_9 (or_9_out, ~button_9_out, out_6);  // OR_Gate
  Button button_10 (.out(button_10_out));
  or or_10 (or_10_out, ~button_10_out, out_6);  // OR_Gate
  Button button_11 (.out(button_11_out));
  or or_11 (or_11_out, ~button_11_out, out_6);  // OR_Gate
  Button button_12 (.out(button_12_out));
  or or_12 (or_12_out, ~button_12_out, out_6);  // OR_Gate
  Button button_13 (.out(button_13_out));
  or or_13 (or_13_out, ~button_13_out, out_5);  // OR_Gate
  Button button_14 (.out(button_14_out));
  or or_14 (or_14_out, ~button_14_out, out_5);  // OR_Gate
  Button button_15 (.out(button_15_out));
  or or_15 (or_15_out, ~button_15_out, out_5);  // OR_Gate
  Button button_16 (.out(button_16_out));
  or or_16 (or_16_out, ~button_16_out, out_5);  // OR_Gate
  not not_1 (Y1, or_17_out);
  or or_17 (or_17_out, ~or_13_out, ~or_9_out, ~or_5_out, ~or_1_out);  // OR_Gate
  not not_2 (Y2, or_18_out);
  or or_18 (or_18_out, ~or_14_out, ~or_10_out, ~or_6_out, ~or_2_out);  // OR_Gate
  or or_19 (or_19_out, ~or_15_out, ~or_11_out, ~or_7_out, ~or_3_out);  // OR_Gate
  not not_3 (Y3, or_19_out);
  or or_20 (or_20_out, ~or_16_out, ~or_12_out, ~or_8_out, ~or_4_out);  // OR_Gate
  not not_4 (Y4, or_20_out);

  // Other names for the same wires on the sheet: X1 = out_5; X2 = out_6; X3 = out_7; X4 = out_8

  // Notes on the sheet:
  //   Pavé numérique virtuel
  //   Circuit ici entre les 2
endmodule
