// Logisim project ee110_hexddec_pavenum.circ.xml.circ as structural Verilog: 10 circuits, main circuit hexddec_example
module hexddec_example (
  input  RESET,
  input  y1,
  input  y2,
  input  y3,
  input  y4,
  output x1,
  output x2,
  output x3,
  output x4,
  output data_ready
);

  wire button_1_out, button_2_out, button_3_out, button_4_out, button_5_out, button_6_out, button_7_out,
       button_8_out, button_9_out, button_10_out, button_11_out, button_12_out, button_13_out, button_14_out,
       button_15_out, button_16_out, column_debouncer_ch0_dout, column_debouncer_ch1_dout,
       column_debouncer_ch2_dout, column_debouncer_ch3_dout, ddec01_a, ddec01_b, ddec01_c, ddec01_d,
       ddec01_decpt, ddec01_e, ddec01_f, ddec01_g, FSM_main_output_1, FSM_main_output_2, FSM_main_output_3,
       FSM_main_output_4, or_1_out, or_2_out, or_3_out, or_4_out, or_5_out, or_6_out, or_7_out, or_8_out,
       or_9_out, or_10_out, or_11_out, or_12_out, or_13_out, or_14_out, or_15_out, or_16_out, or_17_out,
       or_18_out, or_19_out, or_20_out, or_21_out, result_register_output_1, result_register_output_2,
       result_register_output_3, result_register_output_4, result_register_output_5,
       result_register_output_6, result_register_output_7, result_register_output_8,
       state0_logic_hp_s0_detect, state1_logic_hp_s0_detect, state2_logic_hp_s2_data_ready,
       state3_logic_timer_out, X1_t, X2_t, X3_t, X4_t, Y1_t, Y2_t, Y3_t, Y4_t;

  Button button_1 (.out(button_1_out));
  Button button_2 (.out(button_2_out));
  Button button_3 (.out(button_3_out));
  Button button_4 (.out(button_4_out));
  Button button_5 (.out(button_5_out));
  or or_1 (or_1_out, ~button_1_out, X4_t);  // OR_Gate
  Button button_6 (.out(button_6_out));
  or or_2 (or_2_out, ~button_2_out, X4_t);  // OR_Gate
  Button button_7 (.out(button_7_out));
  or or_3 (or_3_out, ~button_3_out, X4_t);  // OR_Gate
  Button button_8 (.out(button_8_out));
  or or_4 (or_4_out, ~button_4_out, X4_t);  // OR_Gate
  Button button_9 (.out(button_9_out));
  or or_5 (or_5_out, ~button_5_out, X3_t);  // OR_Gate
  Button button_10 (.out(button_10_out));
  or or_6 (or_6_out, ~button_6_out, X3_t);  // OR_Gate
  Button button_11 (.out(button_11_out));
  or or_7 (or_7_out, ~button_7_out, X3_t);  // OR_Gate
  Button button_12 (.out(button_12_out));
  or or_8 (or_8_out, ~button_8_out, X3_t);  // OR_Gate
  Button button_13 (.out(button_13_out));
  or or_9 (or_9_out, ~button_9_out, X2_t);  // OR_Gate
  Button button_14 (.out(button_14_out));
  or or_10 (or_10_out, ~button_10_out, X2_t);  // OR_Gate
  Button button_15 (.out(button_15_out));
  or or_11 (or_11_out, ~button_11_out, X2_t);  // OR_Gate
  Button button_16 (.out(button_16_out));
  or or_12 (or_12_out, ~button_12_out, X2_t);  // OR_Gate
  Clock sysclk ();  // open: out
  Clock #(.highDuration(10), .lowDuration(10)) clk_256 ();  // open: out
  Clock #(.highDuration(100), .lowDuration(100)) clk_16 ();  // open: out
  or or_13 (or_13_out, ~button_13_out, X1_t);  // OR_Gate
  or or_14 (or_14_out, ~or_13_out, ~or_9_out, ~or_5_out, ~or_1_out);  // OR_Gate
  or or_15 (or_15_out, ~button_14_out, X1_t);  // OR_Gate
  or or_16 (or_16_out, ~or_15_out, ~or_10_out, ~or_6_out, ~or_2_out);  // OR_Gate
  or or_17 (or_17_out, ~button_15_out, X1_t);  // OR_Gate
  or or_18 (or_18_out, ~or_17_out, ~or_11_out, ~or_7_out, ~or_3_out);  // OR_Gate
  or or_19 (or_19_out, ~button_16_out, X1_t);  // OR_Gate
  or or_20 (or_20_out, ~or_19_out, ~or_12_out, ~or_8_out, ~or_4_out);  // OR_Gate
  not not_1 (Y1_t, or_14_out);
  not not_2 (Y2_t, or_16_out);
  not not_3 (Y3_t, or_18_out);
  not not_4 (Y4_t, or_20_out);
  FSM_full FSM_main (
    .i01_Hpulse(state3_logic_timer_out), .i02_Hpulse(state3_logic_timer_out),
    .i03_Hpulse(state3_logic_timer_out), .Input_1(state3_logic_timer_out), .RESET(RESET),
    .Output_1(FSM_main_output_1), .Output_2(FSM_main_output_2), .Output_3(FSM_main_output_3),
    .Output_4(FSM_main_output_4));
  debounce_4 column_debouncer (
    .ch0(Y1_t), .ch1(Y2_t), .ch2(Y3_t), .ch3(Y4_t), .RESET(RESET), .ch0_dout(column_debouncer_ch0_dout),
    .ch1_dout(column_debouncer_ch1_dout), .ch2_dout(column_debouncer_ch2_dout),
    .ch3_dout(column_debouncer_ch3_dout));
  register_8bit result_register (
    .clk01(state0_logic_hp_s0_detect), .clk02(state1_logic_hp_s0_detect), .RESET(RESET),
    .b0(column_debouncer_ch0_dout), .b1(column_debouncer_ch1_dout), .b2(column_debouncer_ch2_dout),
    .b3(column_debouncer_ch3_dout), .b4(x1), .b5(x2), .b6(x3), .b7(x4), .Output_1(result_register_output_1),
    .Output_2(result_register_output_2), .Output_3(result_register_output_3),
    .Output_4(result_register_output_4), .Output_5(result_register_output_5),
    .Output_6(result_register_output_6), .Output_7(result_register_output_7),
    .Output_8(result_register_output_8));
  state_0 state0_logic (
    .S0(FSM_main_output_1), .RESET(RESET), .y1(column_debouncer_ch0_dout), .y2(column_debouncer_ch1_dout),
    .y3(column_debouncer_ch2_dout), .y4(column_debouncer_ch3_dout), .HP_S0_detect(state0_logic_hp_s0_detect));
  state_1_to_be_completed state1_logic (
    .s1(FSM_main_output_2), .RESET(RESET), .y1(column_debouncer_ch0_dout), .y2(column_debouncer_ch1_dout),
    .y3(column_debouncer_ch2_dout), .y4(column_debouncer_ch3_dout), .HP_S0_detect(state1_logic_hp_s0_detect),
    .coldriver0(x1), .coldriver1(x2), .coldriver2(x3), .coldriver3(x4));
  state_2 state2_logic (.s2(FSM_main_output_3), .RESET(RESET), .HP_S2_data_ready(state2_logic_hp_s2_data_ready));
  state_3 state3_logic (.s3(FSM_main_output_4), .RESET(RESET), .timer_out(state3_logic_timer_out));
  or or_21 (or_21_out, state3_logic_timer_out, RESET);
  D_Flip_Flop d_ff_1 (
    .D(1'b0), .clk(1'b0), .Q(data_ready), .preset(state2_logic_hp_s2_data_ready), .reset(or_21_out));  // open: Qn
  displ_dec_to_be_completed ddec01 (
    .p0(result_register_output_1), .p1(result_register_output_2), .p2(result_register_output_3),
    .p3(result_register_output_4), .p4(result_register_output_5), .p5(result_register_output_6),
    .p6(result_register_output_7), .p7(result_register_output_8), .g(ddec01_g), .f(ddec01_f), .a(ddec01_a),
    .b(ddec01_b), .c(ddec01_c), .d(ddec01_d), .e(ddec01_e), .decpt(ddec01_decpt));
  _7_Segment_Display L_7_Segment_Display_1 (
    .g(ddec01_g), .f(ddec01_f), .a(ddec01_a), .b(ddec01_b), .e(ddec01_e), .d(ddec01_d), .c(ddec01_c),
    .dp(ddec01_decpt));
endmodule

module FSM_full (
  input  i01_Hpulse,
  input  i02_Hpulse,
  input  i03_Hpulse,
  input  Input_1,
  input  RESET,
  output Output_1,
  output Output_2,
  output Output_3,
  output Output_4
);

  wire or_1_out;

  Clock sysclk ();  // open: out
  or or_1 (or_1_out, i01_Hpulse, i02_Hpulse, i03_Hpulse, Input_1);
  D_Flip_Flop d_ff_1 (.D(Output_4), .clk(or_1_out), .Q(Output_1), .preset(RESET));  // open: Qn, reset
  D_Flip_Flop d_ff_2 (.D(Output_1), .clk(or_1_out), .Q(Output_2), .reset(RESET));  // open: Qn, preset
  D_Flip_Flop d_ff_3 (.D(Output_2), .clk(or_1_out), .Q(Output_3), .reset(RESET));  // open: Qn, preset
  D_Flip_Flop d_ff_4 (.D(Output_3), .clk(or_1_out), .Q(Output_4), .reset(RESET));  // open: Qn, preset

  // Notes on the sheet:
  //   Transition logic
  //   (active on a positive pulse)
  //   A Moore finite-state machine and its decoder are optimized into a simplified circuit presented here
  //   Counter and decoder
  //   (optimized/simplified into one circuit)
endmodule

module state_0 (
  input  S0,
  input  RESET,
  input  y1,
  input  y2,
  input  y3,
  input  y4,
  output HP_S0_detect
);

  wire and_1_out, and_2_out, clk_256_out, d_ff_1_q, d_ff_2_q, d_ff_3_q, not_1_out, or_1_out, xor_1_out;

  Clock sysclk ();  // open: out
  Clock #(.highDuration(10), .lowDuration(10)) clk_256 (.out(clk_256_out));
  not not_1 (not_1_out, S0);
  or or_1 (or_1_out, not_1_out, RESET);
  and and_1 (and_1_out, y1, y2, y3, y4);
  D_Flip_Flop d_ff_1 (.D(and_1_out), .clk(clk_256_out), .Q(d_ff_1_q), .reset(or_1_out));  // open: Qn, preset
  xor xor_1 (xor_1_out, and_1_out, d_ff_1_q);
  D_Flip_Flop d_ff_2 (.D(and_2_out), .clk(clk_256_out), .Q(d_ff_2_q), .reset(or_1_out));  // open: Qn, preset
  and and_2 (and_2_out, xor_1_out, d_ff_1_q);
  D_Flip_Flop d_ff_3 (.D(d_ff_2_q), .clk(clk_256_out), .Q(d_ff_3_q), .reset(or_1_out));  // open: Qn, preset
  xor xor_2 (HP_S0_detect, d_ff_2_q, d_ff_3_q);
endmodule

module state_1_to_be_completed (
  input  s1,
  input  RESET,
  input  y1,
  input  y2,
  input  y3,
  input  y4,
  output HP_S0_detect,
  output coldriver0,
  output coldriver1,
  output coldriver2,
  output coldriver3
);

  wire and_1_out, and_2_out, and_3_out, and_4_out, button_1_out, button_2_out, button_3_out, button_4_out,
       button_5_out, button_6_out, button_7_out, button_8_out, button_9_out, button_10_out, button_11_out,
       button_12_out, button_13_out, button_14_out, button_15_out, button_16_out, clk_16_out, clk_256_out,
       d_ff_2_qn, d_ff_3_q, d_ff_3_qn, d_ff_4_q, d_ff_5_q, d_ff_6_q, d_ff_7_q, d_ff_8_q, d_ff_9_q, d_ff_10_q,
       d_ff_10_qn, not_1_out, not_2_out, not_3_out, not_4_out, not_5_out, or_1_out, or_2_out, or_3_out,
       or_4_out, or_5_out, or_6_out, or_7_out, or_8_out, or_9_out, or_10_out, or_11_out, or_12_out,
       or_13_out, or_14_out, or_15_out, or_16_out, or_17_out, or_18_out, or_19_out, or_20_out, or_21_out,
       or_22_out, undriven, undriven_2, undriven_3, undriven_4, undriven_5, xor_1_out, xor_2_out, xor_4_out;

  Button button_1 (.out(button_1_out));
  or or_1 (or_1_out, ~button_1_out, undriven);  // OR_Gate
  Button button_2 (.out(button_2_out));
  or or_2 (or_2_out, ~button_2_out, undriven);  // OR_Gate
  Button button_3 (.out(button_3_out));
  or or_3 (or_3_out, ~button_3_out, undriven);  // OR_Gate
  Button button_4 (.out(button_4_out));
  or or_4 (or_4_out, ~button_4_out, undriven);  // OR_Gate
  Button button_5 (.out(button_5_out));
  or or_5 (or_5_out, ~button_5_out, undriven_2);  // OR_Gate
  Button button_6 (.out(button_6_out));
  or or_6 (or_6_out, ~button_6_out, undriven_2);  // OR_Gate
  Button button_7 (.out(button_7_out));
  or or_7 (or_7_out, ~button_7_out, undriven_2);  // OR_Gate
  Button button_8 (.out(button_8_out));
  or or_8 (or_8_out, ~button_8_out, undriven_2);  // OR_Gate
  Button button_9 (.out(button_9_out));
  or or_9 (or_9_out, ~button_9_out, undriven_3);  // OR_Gate
  Button button_10 (.out(button_10_out));
  or or_10 (or_10_out, ~button_10_out, undriven_3);  // OR_Gate
  Button button_11 (.out(button_11_out));
  or or_11 (or_11_out, ~button_11_out, undriven_3);  // OR_Gate
  Button button_12 (.out(button_12_out));
  or or_12 (or_12_out, ~button_12_out, undriven_3);  // OR_Gate
  Button button_13 (.out(button_13_out));
  or or_13 (or_13_out, ~button_13_out, undriven_4);  // OR_Gate
  Button button_14 (.out(button_14_out));
  or or_14 (or_14_out, ~button_14_out, undriven_4);  // OR_Gate
  Button button_15 (.out(button_15_out));
  or or_15 (or_15_out, ~button_15_out, undriven_4);  // OR_Gate
  Button button_16 (.out(button_16_out));
  or or_16 (or_16_out, ~button_16_out, undriven_4);  // OR_Gate
  not not_1 (not_1_out, or_17_out);
  or or_17 (or_17_out, ~or_13_out, ~or_9_out, ~or_5_out, ~or_1_out);  // OR_Gate
  or or_18 (or_18_out, ~or_14_out, ~or_10_out, ~or_6_out, ~or_2_out);  // OR_Gate
  not not_2 (not_2_out, or_18_out);
  not not_3 (not_3_out, or_19_out);
  or or_19 (or_19_out, ~or_15_out, ~or_11_out, ~or_7_out, ~or_3_out);  // OR_Gate
  or or_20 (or_20_out, ~or_16_out, ~or_12_out, ~or_8_out, ~or_4_out);  // OR_Gate
  not not_4 (not_4_out, or_20_out);
  Clock #(.highDuration(100), .lowDuration(100)) clk_16 (.out(clk_16_out));
  Clock sysclk ();  // open: out
  not not_5 (not_5_out, s1);
  Clock #(.highDuration(10), .lowDuration(10)) clk_256 (.out(clk_256_out));
  or or_21 (or_21_out, not_5_out, RESET);
  and and_1 (and_1_out, not_1_out, not_2_out, not_3_out, not_4_out);
  and and_2 (and_2_out, d_ff_10_q, clk_16_out);
  D_Flip_Flop d_ff_1 (
    .D(undriven_5), .clk(and_2_out), .Qn(coldriver0), .preset(or_21_out), .reset(xor_2_out));  // open: Q
  D_Flip_Flop d_ff_2 (.D(s1), .clk(clk_256_out), .Qn(d_ff_2_qn), .reset(or_21_out));  // open: Q, preset
  D_Flip_Flop d_ff_3 (
    .D(and_1_out), .clk(clk_256_out), .Q(d_ff_3_q), .Qn(d_ff_3_qn), .reset(or_22_out));  // open: preset
  or or_22 (or_22_out, or_21_out, d_ff_10_qn);
  D_Flip_Flop d_ff_4 (.D(and_3_out), .clk(clk_256_out), .Q(d_ff_4_q), .reset(or_21_out));  // open: Qn, preset
  and and_3 (and_3_out, s1, d_ff_2_qn);
  xor xor_1 (xor_1_out, and_1_out, d_ff_3_q);
  D_Flip_Flop d_ff_5 (.D(and_4_out), .clk(clk_256_out), .Q(d_ff_5_q), .reset(or_22_out));  // open: Qn, preset
  and and_4 (and_4_out, xor_1_out, d_ff_3_q);
  D_Flip_Flop d_ff_6 (.D(d_ff_4_q), .clk(clk_256_out), .Q(d_ff_6_q), .reset(or_21_out));  // open: Qn, preset
  D_Flip_Flop d_ff_7 (.D(d_ff_5_q), .clk(clk_256_out), .Q(d_ff_7_q), .reset(or_22_out));  // open: Qn, preset
  xor xor_2 (xor_2_out, d_ff_4_q, d_ff_6_q);
  D_Flip_Flop d_ff_8 (.D(d_ff_6_q), .clk(clk_256_out), .Q(d_ff_8_q), .reset(or_21_out));  // open: Qn, preset
  D_Flip_Flop d_ff_9 (.D(d_ff_8_q), .clk(clk_256_out), .Q(d_ff_9_q), .reset(or_21_out));  // open: Qn, preset
  xor xor_3 (HP_S0_detect, d_ff_5_q, d_ff_7_q);
  xor xor_4 (xor_4_out, d_ff_8_q, d_ff_9_q);
  D_Flip_Flop d_ff_10 (.Q(d_ff_10_q), .Qn(d_ff_10_qn), .preset(xor_4_out), .reset(or_21_out));  // open: D, clk

  assign coldriver1 = coldriver0;
  assign coldriver2 = coldriver0;
  assign coldriver3 = coldriver0;

  // Notes on the sheet:
  //   Pavé numérique virtuel
  //   Your bubble-counter at this location
endmodule

module state_2 (
  input  s2,
  input  RESET,
  output HP_S2_data_ready
);

  wire clk_256_out, d_ff_1_q, d_ff_2_q, d_ff_3_q, not_1_out, or_1_out;

  Clock sysclk ();  // open: out
  Clock #(.highDuration(10), .lowDuration(10)) clk_256 (.out(clk_256_out));
  not not_1 (not_1_out, s2);
  or or_1 (or_1_out, not_1_out, RESET);
  D_Flip_Flop d_ff_1 (.D(1'b0), .clk(clk_256_out), .Q(d_ff_1_q), .preset(or_1_out));  // open: Qn, reset
  D_Flip_Flop d_ff_2 (.D(d_ff_1_q), .clk(clk_256_out), .Q(d_ff_2_q), .reset(or_1_out));  // open: Qn, preset
  D_Flip_Flop d_ff_3 (.D(d_ff_2_q), .clk(clk_256_out), .Q(d_ff_3_q), .reset(or_1_out));  // open: Qn, preset
  xor xor_1 (HP_S2_data_ready, d_ff_2_q, d_ff_3_q);
endmodule

module state_3 (
  input  s3,
  input  RESET,
  output timer_out
);

  wire clk_256_out, not_1_out, or_1_out;

  Clock sysclk ();  // open: out
  Clock #(.highDuration(10), .lowDuration(10)) clk_256 (.out(clk_256_out));
  not not_1 (not_1_out, s3);
  or or_1 (or_1_out, not_1_out, RESET);
  Counter counter_1 (.clr(or_1_out), .clk(clk_256_out), .carry(timer_out));  // open: load, up, count, D, Q
endmodule

module three_level_digfilter (
  input  button_in,
  input  RESET,
  output Output_1
);

  wire and_1_out, and_2_out, clk_256_out, d_ff_1_q, d_ff_2_q, d_ff_3_q, d_ff_4_q;

  Clock sysclk ();  // open: out
  Clock clk_256 (.out(clk_256_out));
  D_Flip_Flop d_ff_1 (.D(button_in), .clk(clk_256_out), .Q(d_ff_1_q), .reset(RESET));  // open: Qn, preset
  D_Flip_Flop d_ff_2 (.D(d_ff_1_q), .clk(clk_256_out), .Q(d_ff_2_q), .reset(RESET));  // open: Qn, preset
  D_Flip_Flop d_ff_3 (.D(d_ff_2_q), .clk(clk_256_out), .Q(d_ff_3_q), .reset(RESET));  // open: Qn, preset
  D_Flip_Flop d_ff_4 (.D(d_ff_3_q), .clk(clk_256_out), .Q(d_ff_4_q), .reset(RESET));  // open: Qn, preset
  J_K_Flip_Flop j_k_ff_1 (.J(and_1_out), .K(and_2_out), .clk(clk_256_out), .Q(Output_1));  // open: Qn, preset, reset
  and and_1 (and_1_out, d_ff_2_q, d_ff_3_q, d_ff_4_q);
  and and_2 (and_2_out, ~d_ff_4_q, ~d_ff_3_q, ~d_ff_2_q);  // AND_Gate
endmodule

module debounce_4 (
  input  ch0,
  input  ch1,
  input  ch2,
  input  ch3,
  input  RESET,
  output ch0_dout,
  output ch1_dout,
  output ch2_dout,
  output ch3_dout
);

  Clock sysclk ();  // open: out
  three_level_digfilter debounce_ch0 (.button_in(ch0), .RESET(RESET), .Output_1(ch0_dout));
  three_level_digfilter debounce_ch1 (.button_in(ch1), .RESET(RESET), .Output_1(ch1_dout));
  three_level_digfilter debounce_ch2 (.button_in(ch2), .RESET(RESET), .Output_1(ch2_dout));
  three_level_digfilter debounce_ch3 (.button_in(ch3), .RESET(RESET), .Output_1(ch3_dout));
endmodule

module register_8bit (
  input  clk01,
  input  clk02,
  input  RESET,
  input  b0,
  input  b1,
  input  b2,
  input  b3,
  input  b4,
  input  b5,
  input  b6,
  input  b7,
  output Output_1,
  output Output_2,
  output Output_3,
  output Output_4,
  output Output_5,
  output Output_6,
  output Output_7,
  output Output_8
);

  Clock sysclk ();  // open: out
  D_Flip_Flop d_ff_1 (.D(b0), .clk(clk01), .Q(Output_1), .preset(RESET));  // open: Qn, reset
  D_Flip_Flop d_ff_2 (.D(b1), .clk(clk01), .Q(Output_2), .reset(RESET));  // open: Qn, preset
  D_Flip_Flop d_ff_3 (.D(b2), .clk(clk01), .Q(Output_3), .reset(RESET));  // open: Qn, preset
  D_Flip_Flop d_ff_4 (.D(b3), .clk(clk01), .Q(Output_4), .reset(RESET));  // open: Qn, preset
  D_Flip_Flop d_ff_5 (.D(b4), .clk(clk02), .Q(Output_5), .reset(RESET));  // open: Qn, preset
  D_Flip_Flop d_ff_6 (.D(b5), .clk(clk02), .Q(Output_6), .reset(RESET));  // open: Qn, preset
  D_Flip_Flop d_ff_7 (.D(b6), .clk(clk02), .Q(Output_7), .reset(RESET));  // open: Qn, preset
  D_Flip_Flop d_ff_8 (.D(b7), .clk(clk02), .Q(Output_8), .reset(RESET));  // open: Qn, preset
endmodule

module displ_dec_to_be_completed (
  input  p0,
  input  p1,
  input  p2,
  input  p3,
  input  p4,
  input  p5,
  input  p6,
  input  p7,
  output g,
  output f,
  output a,
  output b,
  output c,
  output d,
  output e,
  output decpt
);


  assign a = p2;
  assign b = p3;
  assign c = p4;
  assign d = p5;
  assign decpt = p7;
  assign e = p6;
  assign f = p1;
  assign g = p0;

  // Notes on the sheet:
  //   Decoder must be developed
endmodule
