// Logisim project Decodeur.circ as structural Verilog: 2 circuits, main circuit main
module main (
);

  wire a, b, c, d, dipswitch_1_p1, dipswitch_1_p2, dipswitch_1_p3, dipswitch_1_p4, e, f, g, h;

  // DipSwitch dipswitch_1: pin names not known; wires that end beside it: dipswitch_1_p1, dipswitch_1_p2, dipswitch_1_p3, dipswitch_1_p4
  decodeur7seg decodeur7seg_1 (
    .W(dipswitch_1_p1), .X(dipswitch_1_p2), .Y(dipswitch_1_p3), .Z(dipswitch_1_p4), .a(a), .b(b), .c(c),
    .d(d), .e(e), .f(f), .g(g));
  _7_Segment_Display u_7_segment_display_1 (.g(g), .f(f), .a(a), .b(b), .e(e), .d(d), .c(c), .dp(h));

  // Notes on the sheet:
  //   MSB
  //   LSB
endmodule

module decodeur7seg (
  input  W,
  input  X,
  input  Y,
  input  Z,
  output a,
  output b,
  output c,
  output d,
  output e,
  output f,
  output g
);

  wire and_1_out, and_2_out, and_3_out, and_4_out, and_5_out, and_6_out, and_7_out, and_8_out, and_9_out,
       and_10_out, and_11_out, and_12_out, and_13_out, and_14_out, and_15_out, and_16_out, and_17_out,
       and_18_out, and_19_out, and_20_out, and_21_out, and_22_out, and_23_out, and_24_out, and_25_out,
       and_26_out, and_27_out, and_28_out, and_29_out, and_30_out, and_31_out, and_32_out, and_33_out,
       and_34_out, and_35_out, and_36_out, not_1_out, not_2_out, not_3_out, not_4_out;

  not not_1 (not_1_out, W);
  not not_2 (not_2_out, X);
  not not_3 (not_3_out, Y);
  not not_4 (not_4_out, Z);
  and and_1 (and_1_out, not_2_out, not_4_out);
  and and_2 (and_2_out, not_1_out, Y);
  and and_3 (and_3_out, not_1_out, X, Z);
  and and_4 (and_4_out, X, Y);
  and and_5 (and_5_out, W, not_2_out, not_3_out);
  and and_6 (and_6_out, W, not_4_out);
  and and_7 (and_7_out, not_1_out, not_2_out);
  and and_8 (and_8_out, not_1_out, not_3_out, not_4_out);
  and and_9 (and_9_out, not_2_out, not_4_out);
  and and_10 (and_10_out, not_1_out, Y, Z);
  and and_11 (and_11_out, W, not_3_out, Z);
  and and_12 (and_12_out, not_1_out, not_3_out);
  and and_13 (and_13_out, not_1_out, Z);
  and and_14 (and_14_out, not_3_out, Z);
  and and_15 (and_15_out, not_1_out, X);
  and and_16 (and_16_out, W, not_2_out);
  and and_17 (and_17_out, not_1_out, not_2_out, not_4_out);
  and and_18 (and_18_out, not_1_out, Y, not_4_out);
  and and_19 (and_19_out, not_2_out, Y, Z);
  and and_20 (and_20_out, X, not_3_out, Z);
  and and_21 (and_21_out, W, not_3_out);
  and and_22 (and_22_out, W, X, not_4_out);
  and and_23 (and_23_out, not_2_out, not_4_out);
  and and_24 (and_24_out, Y, not_4_out);
  and and_25 (and_25_out, W, Y);
  and and_26 (and_26_out, W, X);
  and and_27 (and_27_out, not_3_out, not_4_out);
  and and_28 (and_28_out, not_1_out, X, not_3_out);
  and and_29 (and_29_out, X, not_4_out);
  and and_30 (and_30_out, W, not_2_out);
  and and_31 (and_31_out, W, Y);
  and and_32 (and_32_out, not_2_out, Y);
  and and_33 (and_33_out, Y, not_4_out);
  and and_34 (and_34_out, not_1_out, X, not_3_out);
  and and_35 (and_35_out, W, not_2_out);
  and and_36 (and_36_out, W, Z);
  or or_1 (a, and_1_out, and_2_out, and_3_out, and_4_out, and_5_out, and_6_out);
  or or_2 (b, and_7_out, and_8_out, and_9_out, and_10_out, and_11_out);
  or or_3 (c, and_12_out, and_13_out, and_14_out, and_15_out, and_16_out);
  or or_4 (d, and_17_out, and_18_out, and_19_out, and_20_out, and_21_out, and_22_out);
  or or_5 (e, and_23_out, and_24_out, and_25_out, and_26_out);
  or or_6 (f, and_27_out, and_28_out, and_29_out, and_30_out, and_31_out);
  or or_7 (g, and_32_out, and_33_out, and_34_out, and_35_out, and_36_out);
endmodule
