// Logisim project ALU.circ as structural Verilog: 5 circuits, main circuit additionneur
module additionneur (
  input  A3,
  input  A2,
  input  A1,
  input  A0,
  input  B3,
  input  B2,
  input  B1,
  input  B0,
  output C0,
  output C1,
  output C2,
  output C3,
  output carry
);

  wire adder_1_cout, adder_2_cout, adder_3_cout;

  Adder #(.width(1)) adder_1 (.a(A0), .b(B0), .out(C0), .cin(1'b0), .cout(adder_1_cout));
  Adder #(.width(1)) adder_2 (.a(A1), .b(B1), .out(C1), .cin(adder_1_cout), .cout(adder_2_cout));
  Adder #(.width(1)) adder_3 (.a(A2), .b(B2), .out(C2), .cin(adder_2_cout), .cout(adder_3_cout));
  Adder #(.width(1)) adder_4 (.a(A3), .b(B3), .out(C3), .cin(adder_3_cout), .cout(carry));
endmodule

module main (
);

  wire a, a1, a2, additionneur_1_c0, additionneur_1_c1, additionneur_1_c2, additionneur_1_c3, b, b1, b2, c,
       c1, c2, d, d1, d2, e, e1, e2, f, f1, f2, g, g1, g2, h, h1, h2;
  wire [3:0] dipswitch_1_p1, dipswitch_2_p1, soustracteur_1_c, undriven;

  // DipSwitch #(.number(4)) dipswitch_1: pin names not known; wires that end beside it: dipswitch_1_p1[0], dipswitch_1_p1[1], dipswitch_1_p1[2], dipswitch_1_p1[3]
  // DipSwitch #(.number(4)) dipswitch_2: pin names not known; wires that end beside it: dipswitch_2_p1[0], dipswitch_2_p1[1], dipswitch_2_p1[2], dipswitch_2_p1[3]
  decodeur7segment decodeur7segment_1 (
    .W(dipswitch_1_p1[0]), .X(dipswitch_1_p1[1]), .Y(dipswitch_1_p1[2]), .Z(dipswitch_1_p1[3]), .a(a), .b(b),
    .c(c), .d(d), .e(e), .f(f), .g(g));
  decodeur7segment decodeur7segment_2 (
    .W(undriven[0]), .X(undriven[1]), .Y(undriven[2]), .Z(undriven[3]), .a(a), .b(b), .c(c), .d(d), .e(e),
    .f(f), .g(g));
  _7_Segment_Display u_7_segment_display_1 (.g(g), .f(f), .a(a), .b(b), .e(e), .d(d), .c(c), .dp(h));
  _7_Segment_Display u_7_segment_display_2 (.g(g), .f(f), .a(a), .b(b), .e(e), .d(d), .c(c), .dp(h));
  additionneur additionneur_1 (
    .C0(additionneur_1_c0), .C1(additionneur_1_c1), .C2(additionneur_1_c2), .C3(additionneur_1_c3), .carry(h1));  // open: A3, A2, A1, A0, B3, B2, B1, B0
  soustracteur soustracteur_1 (.A(dipswitch_2_p1), .C(soustracteur_1_c), .underlfow(h2));  // open: B
  decodeur7segment decodeur7segment_3 (
    .W(additionneur_1_c0), .X(additionneur_1_c1), .Y(additionneur_1_c2), .Z(additionneur_1_c3), .a(a1),
    .b(b1), .c(c1), .d(d1), .e(e1), .f(f1), .g(g1));
  decodeur7segment decodeur7segment_4 (
    .W(soustracteur_1_c[0]), .X(soustracteur_1_c[1]), .Y(soustracteur_1_c[2]), .Z(soustracteur_1_c[3]),
    .a(a2), .b(b2), .c(c2), .d(d2), .e(e2), .f(f2), .g(g2));
  _7_Segment_Display u_7_segment_display_3 (.g(g1), .f(f1), .a(a1), .b(b1), .e(e1), .d(d1), .c(c1), .dp(h1));
  _7_Segment_Display u_7_segment_display_4 (.g(g2), .f(f2), .a(a2), .b(b2), .e(e2), .d(d2), .c(c2), .dp(h2));
endmodule

module soustracteur (
  input  [3:0] A,
  input  [3:0] B,
  output [3:0] C,
  output underlfow
);

  wire subtractor_1_bout, subtractor_2_bout, subtractor_3_bout;

  Subtractor #(.width(1)) subtractor_1 (.a(A[0]), .b(B[0]), .out(C[0]), .bin(1'b0), .bout(subtractor_1_bout));
  Subtractor #(.width(1)) subtractor_2 (
    .a(A[1]), .b(B[1]), .out(C[1]), .bin(subtractor_1_bout), .bout(subtractor_2_bout));
  Subtractor #(.width(1)) subtractor_3 (
    .a(A[2]), .b(B[2]), .out(C[2]), .bin(subtractor_2_bout), .bout(subtractor_3_bout));
  Subtractor #(.width(1)) subtractor_4 (.a(A[3]), .b(B[3]), .out(C[3]), .bin(subtractor_3_bout), .bout(underlfow));
endmodule

module soustracteur2 (
  input  [3:0] A,
  input  [3:0] B,
  output [3:0] C,
  output underlfow
);

  wire and_1_out, and_2_out, and_3_out, and_4_out, and_5_out, and_6_out, and_7_out, and_8_out, and_9_out,
       and_10_out, and_11_out, and_12_out, and_13_out, and_14_out, and_15_out, and_16_out, and_17_out,
       and_18_out, and_19_out, and_20_out, and_21_out, and_22_out, and_23_out, and_24_out, and_25_out,
       and_26_out, and_27_out, and_28_out, and_29_out, and_30_out, and_31_out, and_32_out, and_33_out,
       and_34_out, and_35_out, and_36_out, and_37_out, and_38_out, and_39_out, and_40_out, and_41_out,
       and_42_out, and_43_out, and_44_out, and_45_out, and_46_out, and_47_out, and_48_out, and_49_out,
       and_50_out, and_51_out, and_52_out, and_53_out, and_54_out, and_55_out, and_56_out, and_57_out,
       and_58_out, and_59_out, and_60_out, and_61_out, and_62_out, and_63_out, and_64_out, and_65_out,
       and_66_out, and_67_out, and_68_out, and_69_out, and_70_out, and_71_out, and_72_out, and_73_out,
       and_74_out, and_75_out, not_1_out, not_2_out, not_3_out, not_4_out, not_5_out, not_6_out, not_7_out,
       not_8_out;

  not not_1 (not_1_out, A[3]);
  not not_2 (not_2_out, A[2]);
  not not_3 (not_3_out, A[1]);
  not not_4 (not_4_out, A[0]);
  not not_5 (not_5_out, B[3]);
  not not_6 (not_6_out, B[2]);
  not not_7 (not_7_out, B[1]);
  not not_8 (not_8_out, B[0]);
  and and_1 (and_1_out, not_1_out, not_2_out, not_3_out, not_4_out, not_5_out, B[0]);
  and and_2 (and_2_out, not_1_out, not_2_out, not_3_out, not_5_out, B[1]);
  and and_3 (and_3_out, not_1_out, not_2_out, not_4_out, not_5_out, B[1], B[0]);
  and and_4 (and_4_out, not_1_out, not_2_out, not_5_out, B[2]);
  and and_5 (and_5_out, not_1_out, not_3_out, not_4_out, not_5_out, B[2], B[0]);
  and and_6 (and_6_out, not_1_out, not_3_out, not_5_out, B[2], B[1]);
  and and_7 (and_7_out, not_1_out, not_4_out, not_5_out, B[2], B[1], B[0]);
  and and_8 (and_8_out, not_1_out, B[3], not_6_out, not_7_out, not_8_out);
  and and_9 (and_9_out, not_1_out, A[0], B[3], not_6_out, not_7_out);
  and and_10 (and_10_out, not_1_out, A[1], B[3], not_6_out, not_7_out);
  and and_11 (and_11_out, not_1_out, A[1], B[3], not_6_out, not_8_out);
  and and_12 (and_12_out, not_1_out, A[1], A[0], B[3], not_6_out);
  and and_13 (and_13_out, not_1_out, A[2], B[3], not_6_out);
  and and_14 (and_14_out, not_1_out, A[2], B[3], not_7_out, not_8_out);
  and and_15 (and_15_out, not_1_out, A[2], A[0], B[3], not_7_out);
  and and_16 (and_16_out, not_1_out, A[2], A[1], B[3], not_7_out);
  and and_17 (and_17_out, not_1_out, A[2], A[1], B[3], not_8_out);
  and and_18 (and_18_out, not_1_out, A[2], A[1], A[0], B[3]);
  and and_19 (and_19_out, A[3], not_5_out, not_6_out, not_7_out, not_8_out);
  and and_20 (and_20_out, A[3], not_2_out, not_3_out, not_4_out, B[3], B[0]);
  and and_21 (and_21_out, A[3], not_2_out, not_3_out, B[3], B[1]);
  and and_22 (and_22_out, A[3], not_2_out, not_4_out, B[3], B[1], B[0]);
  and and_23 (and_23_out, A[3], not_2_out, B[3], B[2]);
  and and_24 (and_24_out, A[3], not_3_out, not_4_out, B[3], B[2], B[0]);
  and and_25 (and_25_out, A[3], not_3_out, B[3], B[2], B[1]);
  and and_26 (and_26_out, A[3], not_4_out, B[3], B[2], B[1], B[0]);
  and and_27 (and_27_out, A[3], A[0], not_5_out, not_6_out, not_7_out);
  and and_28 (and_28_out, A[3], A[1], not_5_out, not_6_out, not_7_out);
  and and_29 (and_29_out, A[3], A[1], not_5_out, not_6_out, not_8_out);
  and and_30 (and_30_out, A[3], A[1], A[0], not_5_out, not_6_out);
  and and_31 (and_31_out, A[3], A[2], not_5_out, not_6_out);
  and and_32 (and_32_out, A[3], A[2], not_5_out, not_7_out, not_8_out);
  and and_33 (and_33_out, A[3], A[2], A[0], not_5_out, not_7_out);
  and and_34 (and_34_out, A[3], A[2], A[1], not_5_out, not_7_out);
  and and_35 (and_35_out, A[3], A[2], A[1], not_5_out, not_8_out);
  and and_36 (and_36_out, A[3], A[2], A[1], A[0], not_5_out);
  and and_37 (and_37_out, not_2_out, not_3_out, not_4_out, not_6_out, B[0]);
  and and_38 (and_38_out, not_2_out, not_3_out, not_6_out, B[1]);
  and and_39 (and_39_out, not_2_out, not_4_out, not_6_out, B[1], B[0]);
  and and_40 (and_40_out, not_2_out, B[2], not_7_out, not_8_out);
  and and_41 (and_41_out, not_2_out, A[0], B[2], not_7_out);
  and and_42 (and_42_out, not_2_out, A[1], B[2], not_7_out);
  and and_43 (and_43_out, not_2_out, A[1], B[2], not_8_out);
  and and_44 (and_44_out, not_2_out, A[1], A[0], B[2]);
  and and_45 (and_45_out, A[2], not_6_out, not_7_out, not_8_out);
  and and_46 (and_46_out, A[2], not_3_out, not_4_out, B[2], B[0]);
  and and_47 (and_47_out, A[2], not_3_out, B[2], B[1]);
  and and_48 (and_48_out, A[2], not_4_out, B[2], B[1], B[0]);
  and and_49 (and_49_out, A[2], A[0], not_6_out, not_7_out);
  and and_50 (and_50_out, A[2], A[1], not_6_out, not_7_out);
  and and_51 (and_51_out, A[2], A[1], not_6_out, not_8_out);
  and and_52 (and_52_out, A[2], A[1], A[0], not_6_out);
  and and_53 (and_53_out, not_3_out, not_4_out, not_7_out, B[0]);
  and and_54 (and_54_out, not_3_out, B[1], not_8_out);
  and and_55 (and_55_out, not_3_out, A[0], B[1]);
  and and_56 (and_56_out, A[1], not_7_out, not_8_out);
  and and_57 (and_57_out, A[1], not_4_out, B[1], B[0]);
  and and_58 (and_58_out, A[1], A[0], not_7_out);
  and and_59 (and_59_out, not_4_out, B[0]);
  and and_60 (and_60_out, A[0], not_8_out);
  and and_61 (and_61_out, not_1_out, not_2_out, not_3_out, not_4_out, B[0]);
  and and_62 (and_62_out, not_1_out, not_2_out, not_3_out, B[1]);
  and and_63 (and_63_out, not_1_out, not_2_out, not_4_out, B[1], B[0]);
  and and_64 (and_64_out, not_1_out, not_2_out, B[2]);
  and and_65 (and_65_out, not_1_out, not_3_out, not_4_out, B[2], B[0]);
  and and_66 (and_66_out, not_1_out, not_3_out, B[2], B[1]);
  and and_67 (and_67_out, not_1_out, not_4_out, B[2], B[1], B[0]);
  and and_68 (and_68_out, not_1_out, B[3]);
  and and_69 (and_69_out, not_2_out, not_3_out, not_4_out, B[3], B[0]);
  and and_70 (and_70_out, not_2_out, not_3_out, B[3], B[1]);
  and and_71 (and_71_out, not_2_out, not_4_out, B[3], B[1], B[0]);
  and and_72 (and_72_out, not_2_out, B[3], B[2]);
  and and_73 (and_73_out, not_3_out, not_4_out, B[3], B[2], B[0]);
  and and_74 (and_74_out, not_3_out, B[3], B[2], B[1]);
  and and_75 (and_75_out, not_4_out, B[3], B[2], B[1], B[0]);
  or or_1 (C[2], and_37_out, and_38_out, and_39_out, and_40_out, and_41_out, and_42_out, and_43_out, and_44_out, and_45_out, and_46_out, and_47_out, and_48_out, and_49_out, and_50_out, and_51_out, and_52_out);
  or or_2 (C[1], and_53_out, and_54_out, and_55_out, and_56_out, and_57_out, and_58_out);
  or or_3 (C[0], and_59_out, and_60_out);
  or or_4 (underlfow, and_61_out, and_62_out, and_63_out, and_64_out, and_65_out, and_66_out, and_67_out, and_68_out, and_69_out, and_70_out, and_71_out, and_72_out, and_73_out, and_74_out, and_75_out);
  or or_5 (C[3], and_1_out, and_2_out, and_3_out, and_4_out, and_5_out, and_6_out, and_7_out, and_8_out, and_9_out, and_10_out, and_11_out, and_12_out, and_13_out, and_14_out, and_15_out, and_16_out, and_17_out, and_18_out, and_19_out, and_20_out, and_21_out, and_22_out, and_23_out, and_24_out, and_25_out, and_26_out, and_27_out, and_28_out, and_29_out, and_30_out, and_31_out, and_32_out, and_33_out, and_34_out, and_35_out, and_36_out);
endmodule

module decodeur7segment (
  input  W,
  input  X,
  input  Y,
  input  Z,
  output a,
  output b,
  output c,
  output d,
  output e,
  output f,
  output g
);

  wire and_1_out, and_2_out, and_3_out, and_4_out, and_5_out, and_6_out, and_7_out, and_8_out, and_9_out,
       and_10_out, and_11_out, and_12_out, and_13_out, and_14_out, and_15_out, and_16_out, and_17_out,
       and_18_out, and_19_out, and_20_out, and_21_out, and_22_out, and_23_out, and_24_out, and_25_out,
       and_26_out, and_27_out, and_28_out, and_29_out, and_30_out, and_31_out, and_32_out, and_33_out,
       and_34_out, and_35_out, and_36_out, not_1_out, not_2_out, not_3_out, not_4_out;

  not not_1 (not_1_out, W);
  not not_2 (not_2_out, X);
  not not_3 (not_3_out, Y);
  not not_4 (not_4_out, Z);
  and and_1 (and_1_out, not_2_out, not_4_out);
  and and_2 (and_2_out, not_1_out, Y);
  and and_3 (and_3_out, not_1_out, X, Z);
  and and_4 (and_4_out, X, Y);
  and and_5 (and_5_out, W, not_2_out, not_3_out);
  and and_6 (and_6_out, W, not_4_out);
  and and_7 (and_7_out, not_1_out, not_2_out);
  and and_8 (and_8_out, not_1_out, not_3_out, not_4_out);
  and and_9 (and_9_out, not_2_out, not_4_out);
  and and_10 (and_10_out, not_1_out, Y, Z);
  and and_11 (and_11_out, W, not_3_out, Z);
  and and_12 (and_12_out, not_1_out, not_3_out);
  and and_13 (and_13_out, not_1_out, Z);
  and and_14 (and_14_out, not_3_out, Z);
  and and_15 (and_15_out, not_1_out, X);
  and and_16 (and_16_out, W, not_2_out);
  and and_17 (and_17_out, not_1_out, not_2_out, not_4_out);
  and and_18 (and_18_out, not_1_out, Y, not_4_out);
  and and_19 (and_19_out, not_2_out, Y, Z);
  and and_20 (and_20_out, X, not_3_out, Z);
  and and_21 (and_21_out, W, not_3_out);
  and and_22 (and_22_out, W, X, not_4_out);
  and and_23 (and_23_out, not_2_out, not_4_out);
  and and_24 (and_24_out, Y, not_4_out);
  and and_25 (and_25_out, W, Y);
  and and_26 (and_26_out, W, X);
  and and_27 (and_27_out, not_3_out, not_4_out);
  and and_28 (and_28_out, not_1_out, X, not_3_out);
  and and_29 (and_29_out, X, not_4_out);
  and and_30 (and_30_out, W, not_2_out);
  and and_31 (and_31_out, W, Y);
  and and_32 (and_32_out, not_2_out, Y);
  and and_33 (and_33_out, Y, not_4_out);
  and and_34 (and_34_out, not_1_out, X, not_3_out);
  and and_35 (and_35_out, W, not_2_out);
  and and_36 (and_36_out, W, Z);
  or or_1 (a, and_1_out, and_2_out, and_3_out, and_4_out, and_5_out, and_6_out);
  or or_2 (b, and_7_out, and_8_out, and_9_out, and_10_out, and_11_out);
  or or_3 (c, and_12_out, and_13_out, and_14_out, and_15_out, and_16_out);
  or or_4 (d, and_17_out, and_18_out, and_19_out, and_20_out, and_21_out, and_22_out);
  or or_5 (e, and_23_out, and_24_out, and_25_out, and_26_out);
  or or_6 (f, and_27_out, and_28_out, and_29_out, and_30_out, and_31_out);
  or or_7 (g, and_32_out, and_33_out, and_34_out, and_35_out, and_36_out);
endmodule
